// Logisim project cpu24（理想）.circ as structural Verilog: 24 circuits, main circuit ◇单周期MIPS
module \单周期MIPS  (
  output RegWrite,
  output MemWrite,
  output [31:0] PC,
  output [31:0] IR,
  output [31:0] RDin,
  output [31:0] MDin
);

  wire and_1_out, and_2_out, and_3_out, and_4_out, and_5_out, and_6_out, and_11_out, and_12_out, and_13_out,
       and_14_out, B_JMP, CLK, comparator_1_gt, comparator_2_eq, d_ff_1_q, d_ff_2_q, d_ff_3_q, d_ff_4_qn,
       d_ff_5_qn, d_ff_6_qn, decoder_1_out0, decoder_1_out1, decoder_1_out2, EPC, ERET, Go, IE, IE_q, INM,
       INM1, INM2, INM3, IR1, IR1_num, IR1_over, IR2, IR2_num, IR2_over, IR3, IR3_num, IR3_over, IR_star,
       MFC0, mips_alu_1_equal, MTC0, multiplexer_10_out, multiplexer_15_out, not_1_out, or_5_out, or_6_out,
       or_7_out, or_8_out, or_9_out, or_10_out, priority_encoder_1_gs, run, SignedExt, W1, W2, W3,
       \单周期硬布线控制器_1_alu_src , \单周期硬布线控制器_1_beq , \单周期硬布线控制器_1_blez , \单周期硬布线控制器_1_bne , \单周期硬布线控制器_1_jr ,
       \单周期硬布线控制器_1_lhu , \单周期硬布线控制器_1_memtoreg , \单周期硬布线控制器_1_syscall ;
  wire [0:0] \单周期硬布线控制器_1_jal , \单周期硬布线控制器_1_regdst ;
  wire [1:0] or_4_out, priority_encoder_1_out;
  wire [3:0] \单周期硬布线控制器_1_alu_op ;
  wire [4:0] multiplexer_4_out, multiplexer_5_out, multiplexer_6_out;
  wire [15:0] bitselector_1_out, \总周期数 ;
  wire [27:0] O_PC;
  wire [31:0] B_PC, bit_extender_1_out, bit_extender_2_out, bit_extender_3_out, EPC_DA, IR_PC, JR_PC,
       LedData, MFC0_DA, mips_alu_1_result, multiplexer_2_out, multiplexer_8_out, multiplexer_11_out,
       multiplexer_12_out, multiplexer_13_out, multiplexer_14_out, PC_q, ram_1_data, shifter_1_out;
  wire [31:28] J_PC;

  Clock #(.highDuration(1), .lowDuration(1)) clock_1 (.out(CLK));
  Button _1 (.out(IR1));
  Button _2 (.out(IR2));
  Button _3 (.out(IR3));
  Button \u_继续运行  (.out(Go));
  LED #(.active("true")) led_1 (.in(W1));
  LED #(.active("true")) led_2 (.in(W2));
  LED #(.active("true")) led_3 (.in(W3));
  D_Flip_Flop #(.trigger("rising"), .Pre_Clr_Positions("LEGACY"), .NegatePresetClear("false"), .enable("true"), .NewFFLayout("false")) d_ff_1 (
    .clk(IR1), .D(1'b1), .Q(d_ff_1_q), .reset(IR1_num));  // open: Qn, preset, en
  or or_1 (W1, IR1_num, d_ff_1_q);
  D_Flip_Flop #(.trigger("rising"), .Pre_Clr_Positions("LEGACY"), .NegatePresetClear("false"), .enable("true"), .NewFFLayout("false")) d_ff_2 (
    .clk(IR2), .D(1'b1), .Q(d_ff_2_q), .reset(IR2_num));  // open: Qn, preset, en
  or or_2 (W2, IR2_num, d_ff_2_q);
  D_Flip_Flop #(.trigger("rising"), .Pre_Clr_Positions("LEGACY"), .NegatePresetClear("false"), .enable("true"), .NewFFLayout("false")) d_ff_3 (
    .clk(IR3), .D(1'b1), .Q(d_ff_3_q), .reset(IR3_num));  // open: Qn, preset, en
  or or_3 (W3, IR3_num, d_ff_3_q);
  Hex_Digit_Display hex_digit_display_1 (.value(LedData[27:24]));  // open: dp
  Hex_Digit_Display hex_digit_display_2 (.value(LedData[31:28]));  // open: dp
  or or_4 (or_4_out[0], \单周期硬布线控制器_1_jr , B_JMP);
  Multiplexer #(.select(2), .width(32), .disabled("Z"), .enable("false")) multiplexer_1 (
    .in0({J_PC, O_PC}), .in1(B_PC), .in2({J_PC, IR[25:0], 2'b00}), .in3(JR_PC), .out(PC), .sel(or_4_out));
  or or_5 (or_5_out, d_ff_3_q, IR3_num);
  Hex_Digit_Display hex_digit_display_3 (.value(LedData[19:16]));  // open: dp
  Hex_Digit_Display hex_digit_display_4 (.value(LedData[23:20]));  // open: dp
  Multiplexer #(.select(2), .width(32), .disabled("Z"), .enable("false")) multiplexer_2 (
    .in0(PC), .in1(EPC_DA), .in2(IR_PC), .in3(EPC_DA), .out(multiplexer_2_out), .sel({IR_star, ERET}));
  or or_6 (or_6_out, d_ff_1_q, IR1_num);
  and and_1 (and_1_out, or_6_out, ~IR1_over);  // AND_Gate
  or or_7 (or_7_out, d_ff_2_q, IR2_num);
  and and_2 (and_2_out, or_7_out, ~IR2_over);  // AND_Gate
  and and_3 (and_3_out, or_5_out, ~IR3_over);  // AND_Gate
  Hex_Digit_Display hex_digit_display_5 (.value(LedData[11:8]));  // open: dp
  Hex_Digit_Display hex_digit_display_6 (.value(LedData[15:12]));  // open: dp
  Register #(.width(32), .trigger("rising"), .Select("low")) u_PC (
    .D(multiplexer_2_out), .en(run), .Q(PC_q), .clk(CLK));  // open: clr
  D_Flip_Flop #(.trigger("rising"), .Pre_Clr_Positions("LEGACY"), .NegatePresetClear("false"), .enable("true"), .NewFFLayout("false")) u_IR1 (
    .clk(CLK), .D(and_1_out), .Q(IR1_num));  // open: Qn, preset, en, reset
  D_Flip_Flop #(.trigger("rising"), .Pre_Clr_Positions("LEGACY"), .NegatePresetClear("false"), .enable("true"), .NewFFLayout("false")) u_IR2 (
    .clk(CLK), .D(and_2_out), .Q(IR2_num));  // open: Qn, preset, en, reset
  D_Flip_Flop #(.trigger("rising"), .Pre_Clr_Positions("LEGACY"), .NegatePresetClear("false"), .enable("true"), .NewFFLayout("false")) u_IR3 (
    .clk(CLK), .D(and_3_out), .Q(IR3_num));  // open: Qn, preset, en, reset
  Hex_Digit_Display hex_digit_display_7 (.value(LedData[7:4]));  // open: dp
  Hex_Digit_Display hex_digit_display_8 (.value(LedData[3:0]));  // open: dp
  // Probe on \总周期数 
  Adder #(.width(32)) adder_1 (.a(PC_q), .b(32'h4), .out({J_PC, O_PC}));  // open: cin, cout
  ROM #(.addrWidth(10), .dataWidth(32), .Select("high")) rom_1 (.addr(PC_q[11:2]), .data(IR));
  Demultiplexer #(.select(2), .width(1), .tristate("false"), .disabled("Z"), .enable("false")) demultiplexer_1 (
    .out1(IE), .out2(EPC), .out3(INM), .in(MTC0), .sel(IR[12:11]));  // open: out0
  and and_4 (and_4_out, IR1_num, d_ff_4_qn);
  D_Flip_Flop #(.trigger("rising"), .Pre_Clr_Positions("LEGACY"), .NegatePresetClear("false"), .enable("true"), .NewFFLayout("false")) d_ff_4 (
    .clk(CLK), .D(MDin[0]), .Q(INM1), .Qn(d_ff_4_qn), .en(INM));  // open: preset, reset
  \单周期硬布线控制器  \u_单周期硬布线控制器_1  (
    .OP(IR[31:26]), .Func(IR[5:0]), .MF(IR[25:21]), .ALU_OP(\单周期硬布线控制器_1_alu_op ),
    .MemToReg(\单周期硬布线控制器_1_memtoreg ), .MemWrite(MemWrite), .ALU_SRC(\单周期硬布线控制器_1_alu_src ),
    .RegWrite(RegWrite), .SysCALL(\单周期硬布线控制器_1_syscall ), .SignedExt(SignedExt),
    .RegDst(\单周期硬布线控制器_1_regdst [0]), .Beq(\单周期硬布线控制器_1_beq ), .Bne(\单周期硬布线控制器_1_bne ),
    .JR(\单周期硬布线控制器_1_jr ), .JMP(or_4_out[1]), .JAL(\单周期硬布线控制器_1_jal [0]), .MFC0(MFC0), .MTC0(MTC0),
    .ERET(ERET), .BLEZ(\单周期硬布线控制器_1_blez ), .LHU(\单周期硬布线控制器_1_lhu ));  // open: R1_used, R2_used
  and and_5 (and_5_out, IR2_num, d_ff_5_qn);
  D_Flip_Flop #(.trigger("rising"), .Pre_Clr_Positions("LEGACY"), .NegatePresetClear("false"), .enable("true"), .NewFFLayout("false")) d_ff_5 (
    .clk(CLK), .D(MDin[1]), .Q(INM2), .Qn(d_ff_5_qn), .en(INM));  // open: preset, reset
  Multiplexer #(.select(1), .width(32), .disabled("Z"), .enable("false")) multiplexer_3 (
    .in0(EPC_DA), .in1({{29{1'b0}}, INM3, INM2, INM1}), .out(MFC0_DA), .sel(IR[11]));
  Multiplexer #(.select(1), .width(5), .disabled("Z"), .enable("false")) multiplexer_4 (
    .in0(IR[25:21]), .in1(5'b00010), .out(multiplexer_4_out), .sel(\单周期硬布线控制器_1_syscall ));
  Multiplexer #(.select(1), .width(5), .disabled("Z"), .enable("false")) multiplexer_5 (
    .in0(IR[20:16]), .in1(5'b00100), .out(multiplexer_5_out), .sel(\单周期硬布线控制器_1_syscall ));
  Multiplexer #(.select(2), .width(5), .disabled("Z"), .enable("false")) multiplexer_6 (
    .in0(IR[20:16]), .in1(IR[15:11]), .in2({5{1'b1}}), .out(multiplexer_6_out),
    .sel({\单周期硬布线控制器_1_jal [0], \单周期硬布线控制器_1_regdst [0]}));  // open: in3
  Multiplexer #(.select(2), .width(32), .disabled("Z"), .enable("false")) multiplexer_7 (
    .in0(multiplexer_13_out), .in1({J_PC, O_PC}), .in2(MFC0_DA), .in3(MFC0_DA), .out(RDin),
    .sel({MFC0, \单周期硬布线控制器_1_jal [0]}));
  and and_6 (and_6_out, IR3_num, d_ff_6_qn);
  or or_8 (or_8_out, MFC0, RegWrite);
  assign bit_extender_1_out = {{16{1'b0}}, IR[15:0]};  // Bit_Extender bit_extender_1
  assign bit_extender_2_out = {{16{IR[15]}}, IR[15:0]};  // Bit_Extender bit_extender_2
  Priority_Encoder #(.select(2), .disabled("Z")) priority_encoder_1 (
    .in0(and_4_out), .in1(and_5_out), .in2(and_6_out), .in3(1'b0), .out(priority_encoder_1_out),
    .gs(priority_encoder_1_gs));  // open: en_out, en_in
  D_Flip_Flop #(.trigger("rising"), .Pre_Clr_Positions("LEGACY"), .NegatePresetClear("false"), .enable("true"), .NewFFLayout("false")) d_ff_6 (
    .clk(CLK), .D(MDin[2]), .Q(INM3), .Qn(d_ff_6_qn), .en(INM));  // open: preset, reset
  not not_1 (not_1_out, MDin[0]);
  MIPS_Regifile mips_regifile_1 (
    .Din(RDin), .Clk(CLK), .R1(JR_PC), .R2(MDin), .WE(or_8_out), .W_num(multiplexer_6_out),
    .R1_num(multiplexer_4_out), .R2_num(multiplexer_5_out));
  Multiplexer #(.select(1), .width(32), .disabled("Z"), .enable("false")) multiplexer_8 (
    .in0(bit_extender_1_out), .in1(bit_extender_2_out), .out(multiplexer_8_out), .sel(SignedExt));
  Multiplexer #(.select(2), .width(32), .disabled("Z"), .enable("false")) multiplexer_9 (
    .in0(32'hc), .in1(32'hf8), .in2(32'h164), .out(IR_PC), .sel(priority_encoder_1_out));  // open: in3
  Decoder #(.select(2), .tristate("false"), .disabled("Z"), .enable("false")) decoder_1 (
    .out0(decoder_1_out0), .out1(decoder_1_out1), .out2(decoder_1_out2), .sel(priority_encoder_1_out));  // open: out3
  Multiplexer #(.select(1), .width(1), .disabled("Z"), .enable("false")) multiplexer_10 (
    .in0(1'b0), .in1(not_1_out), .out(multiplexer_10_out), .sel(IE));
  Comparator #(.width(32), .mode("twosComplement")) comparator_1 (
    .a(JR_PC), .b({32{1'b0}}), .gt(comparator_1_gt));  // open: eq, lt
  Multiplexer #(.select(1), .width(32), .disabled("Z"), .enable("false")) multiplexer_11 (
    .in0(MDin), .in1(multiplexer_8_out), .out(multiplexer_11_out), .sel(\单周期硬布线控制器_1_alu_src ));
  Shifter #(.width(32), .shift("ll")) shifter_1 (.in(multiplexer_8_out), .\dist (5'b00010), .out(shifter_1_out));
  and and_7 (IR1_over, decoder_1_out0, ERET);
  and and_8 (IR2_over, decoder_1_out1, ERET);
  and and_9 (IR3_over, decoder_1_out2, ERET);
  and and_10 (IR_star, priority_encoder_1_gs, IE_q);
  D_Flip_Flop #(.trigger("rising"), .Pre_Clr_Positions("LEGACY"), .NegatePresetClear("false"), .enable("true"), .NewFFLayout("false")) u_IE (
    .clk(CLK), .D(multiplexer_10_out), .Q(IE_q), .preset(ERET), .en(or_9_out));  // open: Qn, reset
  or or_9 (or_9_out, ERET, IE, IR_star);
  MIPS_ALU mips_alu_1 (
    .X(JR_PC), .Y(multiplexer_11_out), .AluOP(\单周期硬布线控制器_1_alu_op ), .Equal(mips_alu_1_equal),
    .Result(mips_alu_1_result), .shamt(IR[10:6]));  // open: Result_2
  Adder #(.width(32)) adder_2 (.a(shifter_1_out), .b({J_PC, O_PC}), .out(B_PC));  // open: cin, cout
  and and_11 (and_11_out, IR_star, ~ERET);  // AND_Gate
  and and_12 (and_12_out, mips_alu_1_equal, \单周期硬布线控制器_1_beq );
  and and_13 (and_13_out, \单周期硬布线控制器_1_bne , ~mips_alu_1_equal);  // AND_Gate
  and and_14 (and_14_out, \单周期硬布线控制器_1_blez , ~comparator_1_gt);  // AND_Gate
  Multiplexer #(.select(1), .width(32), .disabled("Z"), .enable("false")) multiplexer_12 (
    .in0(PC), .in1(MDin), .out(multiplexer_12_out), .sel(EPC));
  Register #(.width(32), .trigger("rising"), .Select("low")) register_1 (
    .D(multiplexer_12_out), .en(or_10_out), .Q(EPC_DA), .clk(CLK));  // open: clr
  or or_10 (or_10_out, EPC, and_11_out);
  or or_11 (B_JMP, and_12_out, and_13_out, and_14_out);
  RAM #(.addrWidth(10), .dataWidth(32), .bus("separate"), .Select("high")) ram_1 (
    .addr(mips_alu_1_result[11:2]), .din(MDin), .data(ram_1_data), .str(MemWrite), .clk(CLK));  // open: sel, ld, clr
  BitSelector #(.width(32), .group(16)) bitselector_1 (.in(ram_1_data), .out(bitselector_1_out));  // open: sel
  Multiplexer #(.select(1), .width(32), .disabled("Z"), .enable("false")) multiplexer_13 (
    .in0(mips_alu_1_result), .in1(multiplexer_14_out), .out(multiplexer_13_out), .sel(\单周期硬布线控制器_1_memtoreg ));
  Multiplexer #(.select(1), .width(32), .disabled("Z"), .enable("false")) multiplexer_14 (
    .in0(ram_1_data), .in1(bit_extender_3_out), .out(multiplexer_14_out), .sel(\单周期硬布线控制器_1_lhu ));
  assign bit_extender_3_out = {{16{1'b0}}, bitselector_1_out};  // Bit_Extender bit_extender_3
  Counter #(.width(16), .max('hffff), .ongoal("stay"), .trigger("rising"), .behavior("old")) counter_1 (
    .count(run), .Q(\总周期数 ), .clk(CLK));  // open: load, D, carry, clr, preset
  Multiplexer #(.select(1), .width(1), .disabled("Z"), .enable("false")) multiplexer_15 (
    .in0(1'b0), .in1(comparator_2_eq), .out(multiplexer_15_out), .sel(\单周期硬布线控制器_1_syscall ));
  Comparator #(.width(32), .mode("twosComplement")) comparator_2 (
    .a(JR_PC), .b(32'h22), .eq(comparator_2_eq));  // open: gt, lt
  or or_12 (run, ~\单周期硬布线控制器_1_syscall , multiplexer_15_out, Go);  // OR_Gate
  Register #(.width(32), .trigger("rising"), .Select("low")) register_2 (
    .D(MDin), .en(multiplexer_15_out), .Q(LedData), .clk(CLK));  // open: clr

  // Other names for the same wires on the sheet: a0[31:0] = MDin; IR_DA[31:0] = MDin; J_PC[27:2] = IR[25:0];
  //   rd[4:0] = IR[15:11]; O_PC[31:28] = J_PC

  // Notes on the sheet:
  //   中断源
  //   中断等待指示
  //   总复位信号应将除ROM以外所有存储组件全部清零
  //   数码管输出
  //   Reset 
  //   Reset 
  //   Reset 
  //   数码管输出应该用寄存器锁存，否则显示数据只能一闪而过
  //   指令存储器
  //   指令字
  //   contents of rom_1 (hex, n*v repeats v):
  //   201d0ffc 40800800 8000c74 afb60000 23bdfffc afb50000 23bdfffc afb40000 23bdfffc afb30000 23bdfffc
  //   afb00000 23bdfffc afa20000 23bdfffc afa40000 23bdfffc 40041000 afa40000 23bdfffc 40041800 afa40000
  //   23bdfffc 20040001 40841800 40800800 20160001 20140006 20150001 168020 108100 2149825 132020 20020022
  //   c 1600fffa 295a022 1680fff7 20040001 40840800 23bd0004 8fa40000 40841800 23bd0004 8fa40000 40841000
  //   23bd0004 8fa40000 23bd0004 8fa20000 23bd0004 8fb00000 23bd0004 8fb30000 23bd0004 8fb40000 23bd0004
  //   8fb50000 23bd0004 8fb60000 42000018 c afb60000 23bdfffc afb50000 23bdfffc afb40000 23bdfffc afb30000
  //   23bdfffc afb00000 23bdfffc afa20000 23bdfffc afa40000 23bdfffc 40041000 afa40000 23bdfffc 40041800
  //   afa40000 23bdfffc 20040003 40841800 40800800 20160002 20140006 20150001 8000c1d afb60000 23bdfffc
  //   afb50000 23bdfffc afb40000 23bdfffc afb30000 23bdfffc afb00000 23bdfffc afa20000 23bdfffc afa40000
  //   23bdfffc 40041000 afa40000 23bdfffc 40041800 afa40000 23bdfffc 20040007 40841800 40800800 20160003
  //   20140006 20150001 8000c1d 20082000 20020022 82020 c 2108ffff 1500fffc 2002000a c
  //   OP
  //   OP
  //   Func
  //   Func
  //   MF
  //   rs
  //   rt
  //   rd
  //   AluOP
  //   MemToReg
  //   MemWrite
  //   AluSrcB
  //   RegWrite
  //   Syscall
  //   Signedext
  //   RegDst
  //   BEQ
  //   BNE
  //   JR
  //   JMP
  //   JAL
  //   MFC0
  //   MTC0
  //   ERET
  //   LHU
  //   BLEZ
  //   为方便自动评测，需要输出PC，IR，寄存器文件写入端口RDin，内存写入端口MDin等信号
  //   中断屏蔽寄存器
  //   中断向量
endmodule

// 硬布线控制器
module \单周期硬布线控制器  (
  input  [5:0] OP,
  input  [5:0] Func,
  input  [4:0] MF,
  output [3:0] ALU_OP,
  output MemToReg,
  output MemWrite,
  output ALU_SRC,
  output RegWrite,
  output SysCALL,
  output SignedExt,
  output RegDst,
  output Beq,
  output Bne,
  output JR,
  output JMP,
  output JAL,
  output MFC0,
  output MTC0,
  output ERET,
  output LHU,
  output BLEZ,
  output R1_used,
  output R2_used
);

  \运算器控制器  \u_运算器控制器_1  (
    .OP0(OP[0]), .OP1(OP[1]), .OP2(OP[2]), .OP3(OP[3]), .OP4(OP[4]), .OP5(OP[5]), .F0(Func[0]), .F1(Func[1]),
    .F2(Func[2]), .F3(Func[3]), .F4(Func[4]), .F5(Func[5]), .S0(ALU_OP[0]), .S1(ALU_OP[1]), .S2(ALU_OP[2]),
    .S3(ALU_OP[3]));
  \控制信号生成  \u_控制信号生成_1  (
    .OP0(OP[0]), .OP1(OP[1]), .OP2(OP[2]), .OP3(OP[3]), .OP4(OP[4]), .OP5(OP[5]), .F0(Func[0]), .F1(Func[1]),
    .F2(Func[2]), .F3(Func[3]), .F4(Func[4]), .F5(Func[5]), .MF0(MF[0]), .MF1(MF[1]), .MF2(MF[2]),
    .MF3(MF[3]), .MF4(MF[4]), .MemToReg(MemToReg), .MemWrite(MemWrite), .ALU_SRC(ALU_SRC),
    .RegWrite(RegWrite), .SysCALL(SysCALL), .SignedExt(SignedExt), .RegDst(RegDst), .BEQ(Beq), .BNE(Bne),
    .JR(JR), .JUMP(JMP), .JAL(JAL), .MFC0(MFC0), .MTC0(MTC0), .ERET(ERET), .LHU(LHU), .BLEZ(BLEZ));
  \寄存器使用情况  \u_寄存器使用情况_1  (
    .OP0(OP[0]), .OP1(OP[1]), .OP2(OP[2]), .OP3(OP[3]), .OP4(OP[4]), .OP5(OP[5]), .F0(Func[0]), .F1(Func[1]),
    .F2(Func[2]), .F3(Func[3]), .F4(Func[4]), .F5(Func[5]), .R1_used(R1_used), .R2_used(R2_used));

  // Other names for the same wires on the sheet: OP_CODE[5:0] = OP

  // Notes on the sheet:
  //   控制信号生成，产生数据通路需要的其他控制信号
  //   运算器控制器，根据指令生成运算器功能选择信号
endmodule

// 运算器信号生成
module \运算器控制器  (
  input  OP0,
  input  OP1,
  input  OP2,
  input  OP3,
  input  OP4,
  input  OP5,
  input  F0,
  input  F1,
  input  F2,
  input  F3,
  input  F4,
  input  F5,
  output S0,
  output S1,
  output S2,
  output S3
);

  wire and_1_out, and_2_out, and_3_out, and_4_out, and_5_out, and_6_out, and_7_out, and_8_out, and_9_out,
       and_10_out, and_11_out, and_12_out, and_13_out, and_14_out, and_15_out, and_16_out, and_17_out,
       and_18_out, and_19_out, and_20_out, and_21_out, and_22_out, and_23_out, and_24_out, and_25_out,
       and_26_out, and_27_out, and_28_out, and_29_out, and_30_out, and_31_out, and_32_out, and_33_out,
       and_34_out, and_35_out, and_36_out, and_37_out, and_38_out, and_39_out, and_40_out, and_41_out,
       not_1_out, not_2_out, not_3_out, not_4_out, not_5_out, not_6_out, not_7_out, not_8_out, not_9_out,
       not_10_out, not_11_out, not_12_out, not_13_out, not_14_out, not_15_out, not_16_out, not_17_out,
       not_18_out, not_19_out, not_20_out, not_21_out, not_22_out, not_23_out, not_24_out, not_25_out,
       not_26_out, not_27_out, not_28_out, not_29_out, not_30_out, not_31_out, not_32_out, not_33_out,
       not_34_out, not_35_out, not_36_out, not_37_out, not_38_out, not_39_out, not_40_out, not_41_out,
       not_42_out, not_43_out, not_44_out, not_45_out, not_46_out, not_47_out, not_48_out, not_49_out,
       not_50_out, not_51_out, not_52_out, not_53_out, not_54_out, not_55_out, not_56_out, not_57_out,
       not_58_out, not_59_out, not_60_out, not_61_out, not_62_out, not_63_out, not_64_out, not_65_out,
       not_66_out, not_67_out, not_68_out, not_69_out, not_70_out, not_71_out, not_72_out, not_73_out,
       not_74_out, not_75_out, not_76_out, not_77_out, not_78_out, not_79_out, not_80_out, not_81_out,
       not_82_out, not_83_out, not_84_out, not_85_out, not_86_out, not_87_out, not_88_out, not_89_out,
       not_90_out, not_91_out, not_92_out, not_93_out, not_94_out, not_95_out, not_96_out, not_97_out,
       not_98_out, not_99_out, not_100_out, not_101_out, not_102_out, not_103_out, not_104_out, not_105_out,
       not_106_out, not_107_out, not_108_out, not_109_out, not_110_out, not_111_out, not_112_out,
       not_113_out, not_114_out, not_115_out, not_116_out, not_117_out, not_118_out, not_119_out,
       not_120_out, not_121_out, not_122_out, not_123_out, not_124_out, not_125_out, not_126_out,
       not_127_out, not_128_out, not_129_out, not_130_out, not_131_out, not_132_out, not_133_out,
       not_134_out, not_135_out, not_136_out, not_137_out, not_138_out, not_139_out, not_140_out,
       not_141_out, not_142_out, not_143_out, not_144_out, not_145_out, not_146_out, not_147_out,
       not_148_out, not_149_out, not_150_out, not_151_out, not_152_out, not_153_out, not_154_out,
       not_155_out, not_156_out, not_157_out, not_158_out, not_159_out, not_160_out, not_161_out,
       not_162_out, not_163_out, not_164_out, not_165_out, not_166_out, not_167_out, not_168_out,
       not_169_out, not_170_out, not_171_out, not_172_out, not_173_out, not_174_out, not_175_out,
       not_176_out, not_177_out, not_178_out, not_179_out, not_180_out, not_181_out, not_182_out,
       not_183_out, not_184_out, not_185_out, not_186_out, not_187_out, not_188_out, not_189_out,
       not_190_out, not_191_out, not_192_out, not_193_out, not_194_out, not_195_out, not_196_out,
       not_197_out, not_198_out, not_199_out, not_200_out, not_201_out, not_202_out, not_203_out,
       not_204_out, not_205_out, not_206_out, not_207_out, not_208_out, not_209_out, not_210_out,
       not_211_out, not_212_out, not_213_out, not_214_out, not_215_out, not_216_out, not_217_out,
       not_218_out, not_219_out, not_220_out, not_221_out, not_222_out, not_223_out, not_224_out,
       not_225_out, not_226_out, not_227_out, not_228_out, not_229_out, not_230_out, not_231_out,
       not_232_out, not_233_out, not_234_out, not_235_out, not_236_out, not_237_out, not_238_out,
       not_239_out, not_240_out, not_241_out, not_242_out, not_243_out, not_244_out, not_245_out,
       not_246_out, not_247_out, not_248_out, not_249_out, not_250_out, not_251_out, not_252_out,
       not_253_out, not_254_out, not_255_out, not_256_out, not_257_out, not_258_out, not_259_out,
       not_260_out, not_261_out, not_262_out, not_263_out, not_264_out, not_265_out, not_266_out,
       not_267_out, not_268_out, not_269_out;

  not not_1 (not_1_out, OP5);
  not not_2 (not_2_out, OP4);
  not not_3 (not_3_out, OP3);
  not not_4 (not_4_out, OP2);
  not not_5 (not_5_out, OP1);
  not not_6 (not_6_out, OP0);
  not not_7 (not_7_out, F5);
  not not_8 (not_8_out, F4);
  not not_9 (not_9_out, F3);
  not not_10 (not_10_out, F2);
  not not_11 (not_11_out, OP5);
  not not_12 (not_12_out, OP4);
  not not_13 (not_13_out, OP3);
  not not_14 (not_14_out, OP2);
  not not_15 (not_15_out, OP1);
  not not_16 (not_16_out, OP0);
  not not_17 (not_17_out, F4);
  not not_18 (not_18_out, F3);
  not not_19 (not_19_out, F2);
  not not_20 (not_20_out, F1);
  not not_21 (not_21_out, F0);
  not not_22 (not_22_out, OP5);
  not not_23 (not_23_out, OP4);
  not not_24 (not_24_out, OP3);
  not not_25 (not_25_out, OP2);
  not not_26 (not_26_out, OP1);
  not not_27 (not_27_out, OP0);
  not not_28 (not_28_out, F4);
  not not_29 (not_29_out, F3);
  not not_30 (not_30_out, F2);
  not not_31 (not_31_out, F1);
  not not_32 (not_32_out, OP5);
  not not_33 (not_33_out, OP4);
  not not_34 (not_34_out, OP3);
  not not_35 (not_35_out, OP2);
  not not_36 (not_36_out, OP1);
  not not_37 (not_37_out, OP0);
  not not_38 (not_38_out, F4);
  not not_39 (not_39_out, F3);
  not not_40 (not_40_out, F1);
  not not_41 (not_41_out, F0);
  not not_42 (not_42_out, OP5);
  not not_43 (not_43_out, OP4);
  not not_44 (not_44_out, OP3);
  not not_45 (not_45_out, OP2);
  not not_46 (not_46_out, OP1);
  not not_47 (not_47_out, OP0);
  not not_48 (not_48_out, F4);
  not not_49 (not_49_out, F2);
  not not_50 (not_50_out, F0);
  not not_51 (not_51_out, OP5);
  not not_52 (not_52_out, OP4);
  not not_53 (not_53_out, OP2);
  not not_54 (not_54_out, OP1);
  not not_55 (not_55_out, OP0);
  not not_56 (not_56_out, OP5);
  not not_57 (not_57_out, OP4);
  not not_58 (not_58_out, OP1);
  not not_59 (not_59_out, OP0);
  not not_60 (not_60_out, OP5);
  not not_61 (not_61_out, OP4);
  not not_62 (not_62_out, OP2);
  not not_63 (not_63_out, OP1);
  not not_64 (not_64_out, OP5);
  not not_65 (not_65_out, OP4);
  not not_66 (not_66_out, OP2);
  not not_67 (not_67_out, OP0);
  not not_68 (not_68_out, OP4);
  not not_69 (not_69_out, OP3);
  not not_70 (not_70_out, OP2);
  not not_71 (not_71_out, OP4);
  not not_72 (not_72_out, OP2);
  not not_73 (not_73_out, OP5);
  not not_74 (not_74_out, OP4);
  not not_75 (not_75_out, OP2);
  not not_76 (not_76_out, OP4);
  not not_77 (not_77_out, OP3);
  not not_78 (not_78_out, OP1);
  not not_79 (not_79_out, OP5);
  not not_80 (not_80_out, OP4);
  not not_81 (not_81_out, OP3);
  not not_82 (not_82_out, OP2);
  not not_83 (not_83_out, OP1);
  not not_84 (not_84_out, OP0);
  not not_85 (not_85_out, F5);
  not not_86 (not_86_out, F4);
  not not_87 (not_87_out, F3);
  not not_88 (not_88_out, F2);
  not not_89 (not_89_out, F0);
  not not_90 (not_90_out, OP5);
  not not_91 (not_91_out, OP4);
  not not_92 (not_92_out, OP3);
  not not_93 (not_93_out, OP2);
  not not_94 (not_94_out, OP1);
  not not_95 (not_95_out, OP0);
  not not_96 (not_96_out, F4);
  not not_97 (not_97_out, F3);
  not not_98 (not_98_out, F2);
  not not_99 (not_99_out, F0);
  not not_100 (not_100_out, OP5);
  not not_101 (not_101_out, OP4);
  not not_102 (not_102_out, OP3);
  not not_103 (not_103_out, OP2);
  not not_104 (not_104_out, OP1);
  not not_105 (not_105_out, OP0);
  not not_106 (not_106_out, F4);
  not not_107 (not_107_out, F3);
  not not_108 (not_108_out, F1);
  not not_109 (not_109_out, F0);
  not not_110 (not_110_out, OP5);
  not not_111 (not_111_out, OP4);
  not not_112 (not_112_out, OP3);
  not not_113 (not_113_out, OP2);
  not not_114 (not_114_out, OP1);
  not not_115 (not_115_out, OP0);
  not not_116 (not_116_out, F4);
  not not_117 (not_117_out, F3);
  not not_118 (not_118_out, OP5);
  not not_119 (not_119_out, OP4);
  not not_120 (not_120_out, OP3);
  not not_121 (not_121_out, OP2);
  not not_122 (not_122_out, OP1);
  not not_123 (not_123_out, OP0);
  not not_124 (not_124_out, F4);
  not not_125 (not_125_out, F2);
  not not_126 (not_126_out, F0);
  not not_127 (not_127_out, OP5);
  not not_128 (not_128_out, OP4);
  not not_129 (not_129_out, OP1);
  not not_130 (not_130_out, OP0);
  not not_131 (not_131_out, OP5);
  not not_132 (not_132_out, OP4);
  not not_133 (not_133_out, OP2);
  not not_134 (not_134_out, OP0);
  not not_135 (not_135_out, OP5);
  not not_136 (not_136_out, OP4);
  not not_137 (not_137_out, OP3);
  not not_138 (not_138_out, OP2);
  not not_139 (not_139_out, OP1);
  not not_140 (not_140_out, OP0);
  not not_141 (not_141_out, F4);
  not not_142 (not_142_out, F3);
  not not_143 (not_143_out, F2);
  not not_144 (not_144_out, OP5);
  not not_145 (not_145_out, OP4);
  not not_146 (not_146_out, OP2);
  not not_147 (not_147_out, OP5);
  not not_148 (not_148_out, OP4);
  not not_149 (not_149_out, OP3);
  not not_150 (not_150_out, OP2);
  not not_151 (not_151_out, OP1);
  not not_152 (not_152_out, OP0);
  not not_153 (not_153_out, F4);
  not not_154 (not_154_out, F3);
  not not_155 (not_155_out, F2);
  not not_156 (not_156_out, F1);
  not not_157 (not_157_out, F0);
  not not_158 (not_158_out, OP5);
  not not_159 (not_159_out, OP4);
  not not_160 (not_160_out, OP3);
  not not_161 (not_161_out, OP2);
  not not_162 (not_162_out, OP1);
  not not_163 (not_163_out, OP0);
  not not_164 (not_164_out, F4);
  not not_165 (not_165_out, F3);
  not not_166 (not_166_out, F2);
  not not_167 (not_167_out, F1);
  not not_168 (not_168_out, OP5);
  not not_169 (not_169_out, OP4);
  not not_170 (not_170_out, OP3);
  not not_171 (not_171_out, OP2);
  not not_172 (not_172_out, OP1);
  not not_173 (not_173_out, OP0);
  not not_174 (not_174_out, F4);
  not not_175 (not_175_out, F3);
  not not_176 (not_176_out, F2);
  not not_177 (not_177_out, F0);
  not not_178 (not_178_out, OP5);
  not not_179 (not_179_out, OP4);
  not not_180 (not_180_out, OP3);
  not not_181 (not_181_out, OP2);
  not not_182 (not_182_out, OP1);
  not not_183 (not_183_out, OP0);
  not not_184 (not_184_out, F4);
  not not_185 (not_185_out, F3);
  not not_186 (not_186_out, F1);
  not not_187 (not_187_out, F0);
  not not_188 (not_188_out, OP5);
  not not_189 (not_189_out, OP4);
  not not_190 (not_190_out, OP3);
  not not_191 (not_191_out, OP2);
  not not_192 (not_192_out, OP1);
  not not_193 (not_193_out, OP0);
  not not_194 (not_194_out, F4);
  not not_195 (not_195_out, F2);
  not not_196 (not_196_out, OP5);
  not not_197 (not_197_out, OP4);
  not not_198 (not_198_out, OP2);
  not not_199 (not_199_out, OP1);
  not not_200 (not_200_out, OP0);
  not not_201 (not_201_out, OP5);
  not not_202 (not_202_out, OP4);
  not not_203 (not_203_out, OP1);
  not not_204 (not_204_out, OP0);
  not not_205 (not_205_out, OP5);
  not not_206 (not_206_out, OP4);
  not not_207 (not_207_out, OP2);
  not not_208 (not_208_out, OP1);
  not not_209 (not_209_out, OP4);
  not not_210 (not_210_out, OP3);
  not not_211 (not_211_out, OP2);
  not not_212 (not_212_out, OP4);
  not not_213 (not_213_out, OP2);
  not not_214 (not_214_out, OP5);
  not not_215 (not_215_out, OP4);
  not not_216 (not_216_out, OP3);
  not not_217 (not_217_out, OP2);
  not not_218 (not_218_out, OP1);
  not not_219 (not_219_out, OP0);
  not not_220 (not_220_out, F4);
  not not_221 (not_221_out, F3);
  not not_222 (not_222_out, F2);
  not not_223 (not_223_out, OP4);
  not not_224 (not_224_out, OP3);
  not not_225 (not_225_out, OP1);
  not not_226 (not_226_out, OP5);
  not not_227 (not_227_out, OP4);
  not not_228 (not_228_out, OP3);
  not not_229 (not_229_out, OP2);
  not not_230 (not_230_out, OP1);
  not not_231 (not_231_out, OP0);
  not not_232 (not_232_out, F4);
  not not_233 (not_233_out, F3);
  not not_234 (not_234_out, F1);
  not not_235 (not_235_out, OP5);
  not not_236 (not_236_out, OP4);
  not not_237 (not_237_out, OP3);
  not not_238 (not_238_out, OP2);
  not not_239 (not_239_out, OP1);
  not not_240 (not_240_out, OP0);
  not not_241 (not_241_out, F4);
  not not_242 (not_242_out, F3);
  not not_243 (not_243_out, OP5);
  not not_244 (not_244_out, OP4);
  not not_245 (not_245_out, OP3);
  not not_246 (not_246_out, OP2);
  not not_247 (not_247_out, OP1);
  not not_248 (not_248_out, OP0);
  not not_249 (not_249_out, F4);
  not not_250 (not_250_out, F2);
  not not_251 (not_251_out, F0);
  not not_252 (not_252_out, OP5);
  not not_253 (not_253_out, OP4);
  not not_254 (not_254_out, OP3);
  not not_255 (not_255_out, OP2);
  not not_256 (not_256_out, OP1);
  not not_257 (not_257_out, OP0);
  not not_258 (not_258_out, F4);
  not not_259 (not_259_out, F2);
  not not_260 (not_260_out, OP5);
  not not_261 (not_261_out, OP4);
  not not_262 (not_262_out, OP2);
  not not_263 (not_263_out, OP0);
  not not_264 (not_264_out, OP5);
  not not_265 (not_265_out, OP4);
  not not_266 (not_266_out, OP1);
  not not_267 (not_267_out, OP5);
  not not_268 (not_268_out, OP4);
  not not_269 (not_269_out, OP2);
  and and_1 (and_1_out, not_1_out, not_2_out, not_3_out, not_4_out, not_5_out, not_6_out, not_7_out, not_8_out, not_9_out, not_10_out, F1, F0);
  and and_2 (and_2_out, not_11_out, not_12_out, not_13_out, not_14_out, not_15_out, not_16_out, F5, not_17_out, not_18_out, not_19_out, not_20_out, not_21_out);
  and and_3 (and_3_out, not_22_out, not_23_out, not_24_out, not_25_out, not_26_out, not_27_out, F5, not_28_out, not_29_out, not_30_out, not_31_out, F0);
  and and_4 (and_4_out, not_32_out, not_33_out, not_34_out, not_35_out, not_36_out, not_37_out, F5, not_38_out, not_39_out, F2, not_40_out, not_41_out);
  and and_5 (and_5_out, not_42_out, not_43_out, not_44_out, not_45_out, not_46_out, not_47_out, F5, not_48_out, F3, not_49_out, F1, not_50_out);
  and and_6 (and_6_out, not_51_out, not_52_out, OP3, not_53_out, not_54_out, not_55_out);
  and and_7 (and_7_out, not_56_out, not_57_out, OP3, OP2, not_58_out, not_59_out);
  and and_8 (and_8_out, not_60_out, not_61_out, OP3, not_62_out, not_63_out, OP0);
  and and_9 (and_9_out, not_64_out, not_65_out, OP3, not_66_out, OP1, not_67_out);
  and and_10 (and_10_out, OP5, not_68_out, not_69_out, not_70_out, OP1, OP0);
  and and_11 (and_11_out, OP5, not_71_out, OP3, not_72_out, OP1, OP0);
  and and_12 (and_12_out, not_73_out, not_74_out, OP3, not_75_out, OP1, OP0);
  and and_13 (and_13_out, OP5, not_76_out, not_77_out, OP2, not_78_out, OP0);
  and and_14 (and_14_out, not_79_out, not_80_out, not_81_out, not_82_out, not_83_out, not_84_out, not_85_out, not_86_out, not_87_out, not_88_out, F1, not_89_out);
  and and_15 (and_15_out, not_90_out, not_91_out, not_92_out, not_93_out, not_94_out, not_95_out, F5, not_96_out, not_97_out, not_98_out, F1, not_99_out);
  and and_16 (and_16_out, not_100_out, not_101_out, not_102_out, not_103_out, not_104_out, not_105_out, F5, not_106_out, not_107_out, F2, not_108_out, not_109_out);
  and and_17 (and_17_out, not_110_out, not_111_out, not_112_out, not_113_out, not_114_out, not_115_out, F5, not_116_out, not_117_out, F2, F1, F0);
  and and_18 (and_18_out, not_118_out, not_119_out, not_120_out, not_121_out, not_122_out, not_123_out, F5, not_124_out, F3, not_125_out, F1, not_126_out);
  and and_19 (and_19_out, not_127_out, not_128_out, OP3, OP2, not_129_out, not_130_out);
  and and_20 (and_20_out, not_131_out, not_132_out, OP3, not_133_out, OP1, not_134_out);
  and and_21 (and_21_out, not_135_out, not_136_out, not_137_out, not_138_out, not_139_out, not_140_out, F5, not_141_out, not_142_out, not_143_out, F1, F0);
  and and_22 (and_22_out, not_144_out, not_145_out, OP3, not_146_out, OP1, OP0);
  and and_23 (and_23_out, not_147_out, not_148_out, not_149_out, not_150_out, not_151_out, not_152_out, F5, not_153_out, not_154_out, not_155_out, not_156_out, not_157_out);
  and and_24 (and_24_out, not_158_out, not_159_out, not_160_out, not_161_out, not_162_out, not_163_out, F5, not_164_out, not_165_out, not_166_out, not_167_out, F0);
  and and_25 (and_25_out, not_168_out, not_169_out, not_170_out, not_171_out, not_172_out, not_173_out, F5, not_174_out, not_175_out, not_176_out, F1, not_177_out);
  and and_26 (and_26_out, not_178_out, not_179_out, not_180_out, not_181_out, not_182_out, not_183_out, F5, not_184_out, not_185_out, F2, not_186_out, not_187_out);
  and and_27 (and_27_out, not_188_out, not_189_out, not_190_out, not_191_out, not_192_out, not_193_out, F5, not_194_out, F3, not_195_out, F1, F0);
  and and_28 (and_28_out, not_196_out, not_197_out, OP3, not_198_out, not_199_out, not_200_out);
  and and_29 (and_29_out, not_201_out, not_202_out, OP3, OP2, not_203_out, not_204_out);
  and and_30 (and_30_out, not_205_out, not_206_out, OP3, not_207_out, not_208_out, OP0);
  and and_31 (and_31_out, OP5, not_209_out, not_210_out, not_211_out, OP1, OP0);
  and and_32 (and_32_out, OP5, not_212_out, OP3, not_213_out, OP1, OP0);
  and and_33 (and_33_out, not_214_out, not_215_out, not_216_out, not_217_out, not_218_out, not_219_out, F5, not_220_out, not_221_out, not_222_out, F1, F0);
  and and_34 (and_34_out, OP5, not_223_out, not_224_out, OP2, not_225_out, OP0);
  and and_35 (and_35_out, not_226_out, not_227_out, not_228_out, not_229_out, not_230_out, not_231_out, F5, not_232_out, not_233_out, F2, not_234_out, F0);
  and and_36 (and_36_out, not_235_out, not_236_out, not_237_out, not_238_out, not_239_out, not_240_out, F5, not_241_out, not_242_out, F2, F1, F0);
  and and_37 (and_37_out, not_243_out, not_244_out, not_245_out, not_246_out, not_247_out, not_248_out, F5, not_249_out, F3, not_250_out, F1, not_251_out);
  and and_38 (and_38_out, not_252_out, not_253_out, not_254_out, not_255_out, not_256_out, not_257_out, F5, not_258_out, F3, not_259_out, F1, F0);
  and and_39 (and_39_out, not_260_out, not_261_out, OP3, not_262_out, OP1, not_263_out);
  and and_40 (and_40_out, not_264_out, not_265_out, OP3, OP2, not_266_out, OP0);
  and and_41 (and_41_out, not_267_out, not_268_out, OP3, not_269_out, OP1, OP0);
  or or_1 (S1, and_14_out, and_15_out, and_16_out, and_17_out, and_18_out, and_19_out, and_20_out, and_21_out, and_22_out);
  or or_2 (S3, and_35_out, and_36_out, and_37_out, and_38_out, and_39_out, and_40_out, and_41_out);
  or or_3 (S0, and_1_out, and_2_out, and_3_out, and_4_out, and_5_out, and_6_out, and_7_out, and_8_out, and_9_out, and_10_out, and_11_out, and_12_out, and_13_out);
  or or_4 (S2, and_23_out, and_24_out, and_25_out, and_26_out, and_27_out, and_28_out, and_29_out, and_30_out, and_31_out, and_32_out, and_33_out, and_34_out);
endmodule

// 控制信号生成
module \控制信号生成  (
  input  OP0,
  input  OP1,
  input  OP2,
  input  OP3,
  input  OP4,
  input  OP5,
  input  F0,
  input  F1,
  input  F2,
  input  F3,
  input  F4,
  input  F5,
  input  MF0,
  input  MF1,
  input  MF2,
  input  MF3,
  input  MF4,
  output MemToReg,
  output MemWrite,
  output ALU_SRC,
  output RegWrite,
  output SysCALL,
  output SignedExt,
  output RegDst,
  output BEQ,
  output BNE,
  output JR,
  output JUMP,
  output JAL,
  output MFC0,
  output MTC0,
  output ERET,
  output LHU,
  output BLEZ
);

  wire and_1_out, and_2_out, and_4_out, and_5_out, and_6_out, and_7_out, and_8_out, and_9_out, and_10_out,
       and_11_out, and_12_out, and_13_out, and_14_out, and_15_out, and_16_out, and_17_out, and_18_out,
       and_19_out, and_20_out, and_21_out, and_22_out, and_23_out, and_24_out, and_25_out, and_26_out,
       and_27_out, and_28_out, and_29_out, and_30_out, and_31_out, and_32_out, and_33_out, and_35_out,
       and_36_out, and_37_out, and_38_out, and_39_out, and_40_out, and_41_out, and_42_out, and_43_out,
       and_44_out, and_45_out, and_46_out, and_47_out, and_48_out, and_49_out, and_50_out, and_51_out,
       and_52_out, and_53_out, and_54_out, and_55_out, and_56_out, and_60_out, and_61_out, not_1_out,
       not_2_out, not_3_out, not_4_out, not_5_out, not_6_out, not_7_out, not_8_out, not_9_out, not_10_out,
       not_11_out, not_12_out, not_13_out, not_14_out, not_15_out, not_16_out, not_17_out, not_18_out,
       not_19_out, not_20_out, not_21_out, not_22_out, not_23_out, not_24_out, not_25_out, not_26_out,
       not_27_out, not_28_out, not_29_out, not_30_out, not_31_out, not_32_out, not_33_out, not_34_out,
       not_35_out, not_36_out, not_37_out, not_38_out, not_39_out, not_40_out, not_41_out, not_42_out,
       not_43_out, not_44_out, not_45_out, not_46_out, not_47_out, not_48_out, not_49_out, not_50_out,
       not_51_out, not_52_out, not_53_out, not_54_out, not_55_out, not_56_out, not_57_out, not_58_out,
       not_59_out, not_60_out, not_61_out, not_62_out, not_63_out, not_64_out, not_65_out, not_66_out,
       not_67_out, not_68_out, not_69_out, not_70_out, not_71_out, not_72_out, not_73_out, not_74_out,
       not_75_out, not_76_out, not_77_out, not_78_out, not_79_out, not_80_out, not_81_out, not_82_out,
       not_83_out, not_84_out, not_85_out, not_86_out, not_87_out, not_88_out, not_89_out, not_90_out,
       not_91_out, not_92_out, not_93_out, not_94_out, not_95_out, not_96_out, not_97_out, not_98_out,
       not_99_out, not_100_out, not_101_out, not_102_out, not_103_out, not_104_out, not_105_out, not_106_out,
       not_107_out, not_108_out, not_109_out, not_110_out, not_111_out, not_112_out, not_113_out,
       not_114_out, not_115_out, not_116_out, not_117_out, not_118_out, not_119_out, not_120_out,
       not_121_out, not_122_out, not_123_out, not_124_out, not_125_out, not_126_out, not_127_out,
       not_128_out, not_129_out, not_130_out, not_131_out, not_132_out, not_133_out, not_134_out,
       not_135_out, not_136_out, not_137_out, not_138_out, not_139_out, not_140_out, not_141_out,
       not_142_out, not_143_out, not_144_out, not_145_out, not_146_out, not_147_out, not_148_out,
       not_149_out, not_150_out, not_151_out, not_152_out, not_153_out, not_154_out, not_155_out,
       not_156_out, not_157_out, not_158_out, not_159_out, not_160_out, not_161_out, not_162_out,
       not_163_out, not_164_out, not_165_out, not_166_out, not_167_out, not_168_out, not_169_out,
       not_170_out, not_171_out, not_172_out, not_173_out, not_174_out, not_175_out, not_176_out,
       not_177_out, not_178_out, not_179_out, not_180_out, not_181_out, not_182_out, not_183_out,
       not_184_out, not_185_out, not_186_out, not_187_out, not_188_out, not_189_out, not_190_out,
       not_191_out, not_192_out, not_193_out, not_194_out, not_195_out, not_196_out, not_197_out,
       not_198_out, not_199_out, not_200_out, not_201_out, not_202_out, not_203_out, not_204_out,
       not_205_out, not_206_out, not_207_out, not_208_out, not_209_out, not_210_out, not_211_out,
       not_212_out, not_213_out, not_214_out, not_215_out, not_216_out, not_217_out, not_218_out,
       not_219_out, not_220_out, not_221_out, not_222_out, not_223_out, not_224_out, not_225_out,
       not_226_out, not_227_out, not_228_out, not_229_out, not_230_out, not_231_out, not_232_out,
       not_233_out, not_234_out, not_235_out, not_236_out, not_237_out, not_238_out, not_239_out,
       not_240_out, not_241_out, not_242_out, not_243_out, not_244_out, not_245_out, not_246_out,
       not_247_out, not_248_out, not_249_out, not_250_out, not_251_out, not_252_out, not_253_out,
       not_254_out, not_255_out, not_256_out, not_257_out, not_258_out, not_259_out, not_260_out,
       not_261_out, not_262_out, not_263_out, not_264_out, not_265_out, not_266_out, not_267_out,
       not_268_out, not_269_out, not_270_out, not_271_out, not_272_out, not_273_out, not_274_out,
       not_275_out, not_276_out, not_277_out, not_278_out, not_279_out, not_280_out, not_281_out,
       not_282_out, not_283_out, not_284_out, not_285_out, not_286_out, not_287_out, not_288_out,
       not_289_out, not_290_out, not_291_out, not_292_out, not_293_out, not_294_out, not_295_out,
       not_296_out, not_297_out, not_298_out, not_299_out, not_300_out, not_301_out, not_302_out,
       not_303_out, not_304_out, not_305_out, not_306_out, not_307_out, not_308_out, not_309_out,
       not_310_out, not_311_out, not_312_out, not_313_out, not_314_out, not_315_out, not_316_out,
       not_317_out, not_318_out, not_319_out, not_320_out, not_321_out, not_322_out, not_323_out,
       not_324_out, not_325_out, not_326_out, not_327_out, not_328_out, not_329_out, not_330_out,
       not_331_out, not_332_out, not_333_out, not_334_out, not_335_out, not_336_out, not_337_out,
       not_338_out, not_339_out, not_340_out, not_341_out, not_342_out, not_343_out, not_344_out,
       not_345_out, not_346_out, not_347_out, not_348_out, not_349_out, not_350_out, not_351_out,
       not_352_out, not_353_out, not_354_out, not_355_out, not_356_out, not_357_out, not_358_out,
       not_359_out, not_360_out, not_361_out, not_362_out, not_363_out, not_364_out, not_365_out,
       not_366_out, not_367_out, not_368_out, not_369_out, not_370_out, not_371_out, not_372_out,
       not_373_out, not_374_out, not_375_out, not_376_out, not_377_out, not_378_out, not_379_out,
       not_380_out, not_381_out, not_382_out, not_383_out, not_384_out, not_385_out, not_386_out,
       not_387_out, not_388_out, not_389_out, not_390_out, not_391_out, not_392_out, not_393_out,
       not_394_out, not_395_out, not_396_out, not_397_out, not_398_out, not_399_out, not_400_out,
       not_401_out, not_402_out, not_403_out, not_404_out, not_405_out, not_406_out, not_407_out,
       not_408_out, not_409_out, not_410_out, not_411_out, not_412_out, not_413_out, not_414_out,
       not_415_out, not_416_out, not_417_out, not_418_out, not_419_out, not_420_out, not_421_out,
       not_422_out, not_423_out, not_424_out, not_425_out, not_426_out;

  not not_1 (not_1_out, OP4);
  not not_2 (not_2_out, OP3);
  not not_3 (not_3_out, OP2);
  not not_4 (not_4_out, OP4);
  not not_5 (not_5_out, OP3);
  not not_6 (not_6_out, OP1);
  not not_7 (not_7_out, OP4);
  not not_8 (not_8_out, OP2);
  not not_9 (not_9_out, OP5);
  not not_10 (not_10_out, OP4);
  not not_11 (not_11_out, OP2);
  not not_12 (not_12_out, OP1);
  not not_13 (not_13_out, OP0);
  not not_14 (not_14_out, OP5);
  not not_15 (not_15_out, OP4);
  not not_16 (not_16_out, OP1);
  not not_17 (not_17_out, OP0);
  not not_18 (not_18_out, OP5);
  not not_19 (not_19_out, OP4);
  not not_20 (not_20_out, OP2);
  not not_21 (not_21_out, OP1);
  not not_22 (not_22_out, OP5);
  not not_23 (not_23_out, OP4);
  not not_24 (not_24_out, OP2);
  not not_25 (not_25_out, OP0);
  not not_26 (not_26_out, OP5);
  not not_27 (not_27_out, OP4);
  not not_28 (not_28_out, OP1);
  not not_29 (not_29_out, OP4);
  not not_30 (not_30_out, OP3);
  not not_31 (not_31_out, OP2);
  not not_32 (not_32_out, OP4);
  not not_33 (not_33_out, OP2);
  not not_34 (not_34_out, OP5);
  not not_35 (not_35_out, OP4);
  not not_36 (not_36_out, OP2);
  not not_37 (not_37_out, OP4);
  not not_38 (not_38_out, OP3);
  not not_39 (not_39_out, OP1);
  not not_40 (not_40_out, OP5);
  not not_41 (not_41_out, OP4);
  not not_42 (not_42_out, OP3);
  not not_43 (not_43_out, OP2);
  not not_44 (not_44_out, OP1);
  not not_45 (not_45_out, OP0);
  not not_46 (not_46_out, F5);
  not not_47 (not_47_out, F4);
  not not_48 (not_48_out, F3);
  not not_49 (not_49_out, F2);
  not not_50 (not_50_out, F1);
  not not_51 (not_51_out, F0);
  not not_52 (not_52_out, OP5);
  not not_53 (not_53_out, OP4);
  not not_54 (not_54_out, OP3);
  not not_55 (not_55_out, OP2);
  not not_56 (not_56_out, OP1);
  not not_57 (not_57_out, OP0);
  not not_58 (not_58_out, F5);
  not not_59 (not_59_out, F4);
  not not_60 (not_60_out, F3);
  not not_61 (not_61_out, F2);
  not not_62 (not_62_out, OP5);
  not not_63 (not_63_out, OP4);
  not not_64 (not_64_out, OP3);
  not not_65 (not_65_out, OP2);
  not not_66 (not_66_out, OP1);
  not not_67 (not_67_out, OP0);
  not not_68 (not_68_out, F5);
  not not_69 (not_69_out, F4);
  not not_70 (not_70_out, F3);
  not not_71 (not_71_out, F2);
  not not_72 (not_72_out, F0);
  not not_73 (not_73_out, OP5);
  not not_74 (not_74_out, OP4);
  not not_75 (not_75_out, OP3);
  not not_76 (not_76_out, OP2);
  not not_77 (not_77_out, OP1);
  not not_78 (not_78_out, OP0);
  not not_79 (not_79_out, F4);
  not not_80 (not_80_out, F3);
  not not_81 (not_81_out, F2);
  not not_82 (not_82_out, F1);
  not not_83 (not_83_out, F0);
  not not_84 (not_84_out, OP5);
  not not_85 (not_85_out, OP4);
  not not_86 (not_86_out, OP3);
  not not_87 (not_87_out, OP2);
  not not_88 (not_88_out, OP1);
  not not_89 (not_89_out, OP0);
  not not_90 (not_90_out, F4);
  not not_91 (not_91_out, F3);
  not not_92 (not_92_out, F2);
  not not_93 (not_93_out, F1);
  not not_94 (not_94_out, OP5);
  not not_95 (not_95_out, OP4);
  not not_96 (not_96_out, OP3);
  not not_97 (not_97_out, OP2);
  not not_98 (not_98_out, OP1);
  not not_99 (not_99_out, OP0);
  not not_100 (not_100_out, F4);
  not not_101 (not_101_out, F3);
  not not_102 (not_102_out, F2);
  not not_103 (not_103_out, F0);
  not not_104 (not_104_out, OP5);
  not not_105 (not_105_out, OP4);
  not not_106 (not_106_out, OP3);
  not not_107 (not_107_out, OP2);
  not not_108 (not_108_out, OP1);
  not not_109 (not_109_out, OP0);
  not not_110 (not_110_out, F4);
  not not_111 (not_111_out, F3);
  not not_112 (not_112_out, F1);
  not not_113 (not_113_out, F0);
  not not_114 (not_114_out, OP5);
  not not_115 (not_115_out, OP4);
  not not_116 (not_116_out, OP3);
  not not_117 (not_117_out, OP2);
  not not_118 (not_118_out, OP1);
  not not_119 (not_119_out, OP0);
  not not_120 (not_120_out, F4);
  not not_121 (not_121_out, F3);
  not not_122 (not_122_out, F1);
  not not_123 (not_123_out, OP5);
  not not_124 (not_124_out, OP4);
  not not_125 (not_125_out, OP3);
  not not_126 (not_126_out, OP2);
  not not_127 (not_127_out, OP1);
  not not_128 (not_128_out, OP0);
  not not_129 (not_129_out, F4);
  not not_130 (not_130_out, F3);
  not not_131 (not_131_out, OP5);
  not not_132 (not_132_out, OP4);
  not not_133 (not_133_out, OP3);
  not not_134 (not_134_out, OP2);
  not not_135 (not_135_out, OP1);
  not not_136 (not_136_out, OP0);
  not not_137 (not_137_out, F4);
  not not_138 (not_138_out, F2);
  not not_139 (not_139_out, F0);
  not not_140 (not_140_out, OP5);
  not not_141 (not_141_out, OP4);
  not not_142 (not_142_out, OP3);
  not not_143 (not_143_out, OP2);
  not not_144 (not_144_out, OP1);
  not not_145 (not_145_out, OP0);
  not not_146 (not_146_out, F4);
  not not_147 (not_147_out, F2);
  not not_148 (not_148_out, OP5);
  not not_149 (not_149_out, OP4);
  not not_150 (not_150_out, OP3);
  not not_151 (not_151_out, OP2);
  not not_152 (not_152_out, OP5);
  not not_153 (not_153_out, OP4);
  not not_154 (not_154_out, OP2);
  not not_155 (not_155_out, OP1);
  not not_156 (not_156_out, OP0);
  not not_157 (not_157_out, OP5);
  not not_158 (not_158_out, OP4);
  not not_159 (not_159_out, OP1);
  not not_160 (not_160_out, OP0);
  not not_161 (not_161_out, OP5);
  not not_162 (not_162_out, OP4);
  not not_163 (not_163_out, OP2);
  not not_164 (not_164_out, OP1);
  not not_165 (not_165_out, OP5);
  not not_166 (not_166_out, OP4);
  not not_167 (not_167_out, OP2);
  not not_168 (not_168_out, OP0);
  not not_169 (not_169_out, OP5);
  not not_170 (not_170_out, OP4);
  not not_171 (not_171_out, OP1);
  not not_172 (not_172_out, OP4);
  not not_173 (not_173_out, OP3);
  not not_174 (not_174_out, OP2);
  not not_175 (not_175_out, OP5);
  not not_176 (not_176_out, OP4);
  not not_177 (not_177_out, OP3);
  not not_178 (not_178_out, OP2);
  not not_179 (not_179_out, OP1);
  not not_180 (not_180_out, OP0);
  not not_181 (not_181_out, F4);
  not not_182 (not_182_out, F3);
  not not_183 (not_183_out, F2);
  not not_184 (not_184_out, OP5);
  not not_185 (not_185_out, OP4);
  not not_186 (not_186_out, OP2);
  not not_187 (not_187_out, OP4);
  not not_188 (not_188_out, OP3);
  not not_189 (not_189_out, OP1);
  not not_190 (not_190_out, OP0);
  not not_191 (not_191_out, OP1);
  not not_192 (not_192_out, OP2);
  not not_193 (not_193_out, OP3);
  not not_194 (not_194_out, OP4);
  not not_195 (not_195_out, OP5);
  not not_196 (not_196_out, F0);
  not not_197 (not_197_out, F1);
  not not_198 (not_198_out, F4);
  not not_199 (not_199_out, F5);
  not not_200 (not_200_out, OP5);
  not not_201 (not_201_out, OP4);
  not not_202 (not_202_out, OP3);
  not not_203 (not_203_out, OP1);
  not not_204 (not_204_out, OP0);
  not not_205 (not_205_out, OP5);
  not not_206 (not_206_out, OP4);
  not not_207 (not_207_out, OP3);
  not not_208 (not_208_out, OP1);
  not not_209 (not_209_out, OP5);
  not not_210 (not_210_out, OP4);
  not not_211 (not_211_out, OP2);
  not not_212 (not_212_out, OP1);
  not not_213 (not_213_out, OP0);
  not not_214 (not_214_out, OP5);
  not not_215 (not_215_out, OP4);
  not not_216 (not_216_out, OP2);
  not not_217 (not_217_out, OP1);
  not not_218 (not_218_out, OP5);
  not not_219 (not_219_out, OP4);
  not not_220 (not_220_out, OP2);
  not not_221 (not_221_out, OP0);
  not not_222 (not_222_out, OP4);
  not not_223 (not_223_out, OP3);
  not not_224 (not_224_out, OP2);
  not not_225 (not_225_out, OP4);
  not not_226 (not_226_out, OP2);
  not not_227 (not_227_out, OP5);
  not not_228 (not_228_out, OP4);
  not not_229 (not_229_out, OP2);
  not not_230 (not_230_out, OP4);
  not not_231 (not_231_out, OP3);
  not not_232 (not_232_out, OP1);
  not not_233 (not_233_out, OP5);
  not not_234 (not_234_out, OP4);
  not not_235 (not_235_out, OP3);
  not not_236 (not_236_out, OP0);
  not not_237 (not_237_out, OP5);
  not not_238 (not_238_out, OP4);
  not not_239 (not_239_out, OP3);
  not not_240 (not_240_out, OP2);
  not not_241 (not_241_out, OP1);
  not not_242 (not_242_out, OP0);
  not not_243 (not_243_out, F5);
  not not_244 (not_244_out, F4);
  not not_245 (not_245_out, F3);
  not not_246 (not_246_out, F2);
  not not_247 (not_247_out, F1);
  not not_248 (not_248_out, F0);
  not not_249 (not_249_out, OP5);
  not not_250 (not_250_out, OP4);
  not not_251 (not_251_out, OP3);
  not not_252 (not_252_out, OP2);
  not not_253 (not_253_out, OP1);
  not not_254 (not_254_out, OP0);
  not not_255 (not_255_out, F5);
  not not_256 (not_256_out, F4);
  not not_257 (not_257_out, F3);
  not not_258 (not_258_out, F2);
  not not_259 (not_259_out, OP5);
  not not_260 (not_260_out, OP4);
  not not_261 (not_261_out, OP3);
  not not_262 (not_262_out, OP2);
  not not_263 (not_263_out, OP1);
  not not_264 (not_264_out, OP0);
  not not_265 (not_265_out, F5);
  not not_266 (not_266_out, F4);
  not not_267 (not_267_out, F3);
  not not_268 (not_268_out, F2);
  not not_269 (not_269_out, F0);
  not not_270 (not_270_out, OP5);
  not not_271 (not_271_out, OP4);
  not not_272 (not_272_out, OP3);
  not not_273 (not_273_out, OP2);
  not not_274 (not_274_out, OP1);
  not not_275 (not_275_out, OP0);
  not not_276 (not_276_out, F4);
  not not_277 (not_277_out, F3);
  not not_278 (not_278_out, F2);
  not not_279 (not_279_out, F1);
  not not_280 (not_280_out, F0);
  not not_281 (not_281_out, OP5);
  not not_282 (not_282_out, OP4);
  not not_283 (not_283_out, OP3);
  not not_284 (not_284_out, OP2);
  not not_285 (not_285_out, OP1);
  not not_286 (not_286_out, OP0);
  not not_287 (not_287_out, F4);
  not not_288 (not_288_out, F3);
  not not_289 (not_289_out, F2);
  not not_290 (not_290_out, F1);
  not not_291 (not_291_out, OP5);
  not not_292 (not_292_out, OP4);
  not not_293 (not_293_out, OP3);
  not not_294 (not_294_out, OP2);
  not not_295 (not_295_out, OP1);
  not not_296 (not_296_out, OP0);
  not not_297 (not_297_out, F4);
  not not_298 (not_298_out, F3);
  not not_299 (not_299_out, F2);
  not not_300 (not_300_out, F0);
  not not_301 (not_301_out, OP5);
  not not_302 (not_302_out, OP4);
  not not_303 (not_303_out, OP3);
  not not_304 (not_304_out, OP2);
  not not_305 (not_305_out, OP1);
  not not_306 (not_306_out, OP0);
  not not_307 (not_307_out, F4);
  not not_308 (not_308_out, F3);
  not not_309 (not_309_out, F1);
  not not_310 (not_310_out, F0);
  not not_311 (not_311_out, OP5);
  not not_312 (not_312_out, OP4);
  not not_313 (not_313_out, OP3);
  not not_314 (not_314_out, OP2);
  not not_315 (not_315_out, OP1);
  not not_316 (not_316_out, OP0);
  not not_317 (not_317_out, F4);
  not not_318 (not_318_out, F3);
  not not_319 (not_319_out, F1);
  not not_320 (not_320_out, OP5);
  not not_321 (not_321_out, OP4);
  not not_322 (not_322_out, OP3);
  not not_323 (not_323_out, OP2);
  not not_324 (not_324_out, OP1);
  not not_325 (not_325_out, OP0);
  not not_326 (not_326_out, F4);
  not not_327 (not_327_out, F3);
  not not_328 (not_328_out, OP5);
  not not_329 (not_329_out, OP4);
  not not_330 (not_330_out, OP3);
  not not_331 (not_331_out, OP2);
  not not_332 (not_332_out, OP1);
  not not_333 (not_333_out, OP0);
  not not_334 (not_334_out, F4);
  not not_335 (not_335_out, F2);
  not not_336 (not_336_out, F0);
  not not_337 (not_337_out, OP5);
  not not_338 (not_338_out, OP4);
  not not_339 (not_339_out, OP3);
  not not_340 (not_340_out, OP2);
  not not_341 (not_341_out, OP1);
  not not_342 (not_342_out, OP0);
  not not_343 (not_343_out, F4);
  not not_344 (not_344_out, F2);
  not not_345 (not_345_out, OP5);
  not not_346 (not_346_out, OP4);
  not not_347 (not_347_out, OP3);
  not not_348 (not_348_out, OP2);
  not not_349 (not_349_out, OP1);
  not not_350 (not_350_out, OP0);
  not not_351 (not_351_out, F4);
  not not_352 (not_352_out, F3);
  not not_353 (not_353_out, F2);
  not not_354 (not_354_out, OP0);
  not not_355 (not_355_out, OP1);
  not not_356 (not_356_out, OP3);
  not not_357 (not_357_out, OP4);
  not not_358 (not_358_out, OP5);
  not not_359 (not_359_out, OP1);
  not not_360 (not_360_out, OP3);
  not not_361 (not_361_out, OP4);
  not not_362 (not_362_out, OP5);
  not not_363 (not_363_out, OP0);
  not not_364 (not_364_out, OP1);
  not not_365 (not_365_out, OP2);
  not not_366 (not_366_out, OP3);
  not not_367 (not_367_out, OP4);
  not not_368 (not_368_out, OP5);
  not not_369 (not_369_out, F0);
  not not_370 (not_370_out, F1);
  not not_371 (not_371_out, F2);
  not not_372 (not_372_out, F4);
  not not_373 (not_373_out, F5);
  not not_374 (not_374_out, OP0);
  not not_375 (not_375_out, OP2);
  not not_376 (not_376_out, OP3);
  not not_377 (not_377_out, OP4);
  not not_378 (not_378_out, OP5);
  not not_379 (not_379_out, F0);
  not not_380 (not_380_out, F1);
  not not_381 (not_381_out, F2);
  not not_382 (not_382_out, F4);
  not not_383 (not_383_out, F5);
  not not_384 (not_384_out, OP2);
  not not_385 (not_385_out, OP3);
  not not_386 (not_386_out, OP4);
  not not_387 (not_387_out, OP5);
  not not_388 (not_388_out, OP2);
  not not_389 (not_389_out, OP3);
  not not_390 (not_390_out, OP4);
  not not_391 (not_391_out, OP5);
  not not_392 (not_392_out, OP5);
  not not_393 (not_393_out, OP3);
  not not_394 (not_394_out, OP2);
  not not_395 (not_395_out, OP1);
  not not_396 (not_396_out, OP0);
  not not_397 (not_397_out, MF4);
  not not_398 (not_398_out, MF3);
  not not_399 (not_399_out, MF2);
  not not_400 (not_400_out, MF1);
  not not_401 (not_401_out, MF0);
  not not_402 (not_402_out, OP5);
  not not_403 (not_403_out, OP3);
  not not_404 (not_404_out, OP2);
  not not_405 (not_405_out, OP1);
  not not_406 (not_406_out, OP0);
  not not_407 (not_407_out, MF4);
  not not_408 (not_408_out, MF3);
  not not_409 (not_409_out, MF1);
  not not_410 (not_410_out, MF0);
  not not_411 (not_411_out, OP5);
  not not_412 (not_412_out, OP3);
  not not_413 (not_413_out, OP2);
  not not_414 (not_414_out, OP1);
  not not_415 (not_415_out, OP0);
  not not_416 (not_416_out, F5);
  not not_417 (not_417_out, F2);
  not not_418 (not_418_out, F1);
  not not_419 (not_419_out, F0);
  not not_420 (not_420_out, OP4);
  not not_421 (not_421_out, OP3);
  not not_422 (not_422_out, OP1);
  not not_423 (not_423_out, OP5);
  not not_424 (not_424_out, OP4);
  not not_425 (not_425_out, OP3);
  not not_426 (not_426_out, OP0);
  and and_1 (and_1_out, OP5, not_1_out, not_2_out, not_3_out, OP1, OP0);
  and and_2 (and_2_out, OP5, not_4_out, not_5_out, OP2, not_6_out, OP0);
  and and_3 (MemWrite, OP5, not_7_out, OP3, not_8_out, OP1, OP0);
  and and_4 (and_4_out, not_9_out, not_10_out, OP3, not_11_out, not_12_out, not_13_out);
  and and_5 (and_5_out, not_14_out, not_15_out, OP3, OP2, not_16_out, not_17_out);
  and and_6 (and_6_out, not_18_out, not_19_out, OP3, not_20_out, not_21_out, OP0);
  and and_7 (and_7_out, not_22_out, not_23_out, OP3, not_24_out, OP1, not_25_out);
  and and_8 (and_8_out, not_26_out, not_27_out, OP3, OP2, not_28_out, OP0);
  and and_9 (and_9_out, OP5, not_29_out, not_30_out, not_31_out, OP1, OP0);
  and and_10 (and_10_out, OP5, not_32_out, OP3, not_33_out, OP1, OP0);
  and and_11 (and_11_out, not_34_out, not_35_out, OP3, not_36_out, OP1, OP0);
  and and_12 (and_12_out, OP5, not_37_out, not_38_out, OP2, not_39_out, OP0);
  and and_13 (and_13_out, not_40_out, not_41_out, not_42_out, not_43_out, not_44_out, not_45_out, not_46_out, not_47_out, not_48_out, not_49_out, not_50_out, not_51_out);
  and and_14 (and_14_out, not_52_out, not_53_out, not_54_out, not_55_out, not_56_out, not_57_out, not_58_out, not_59_out, not_60_out, not_61_out, F1, F0);
  and and_15 (and_15_out, not_62_out, not_63_out, not_64_out, not_65_out, not_66_out, not_67_out, not_68_out, not_69_out, not_70_out, not_71_out, F1, not_72_out);
  and and_16 (and_16_out, not_73_out, not_74_out, not_75_out, not_76_out, not_77_out, not_78_out, F5, not_79_out, not_80_out, not_81_out, not_82_out, not_83_out);
  and and_17 (and_17_out, not_84_out, not_85_out, not_86_out, not_87_out, not_88_out, not_89_out, F5, not_90_out, not_91_out, not_92_out, not_93_out, F0);
  and and_18 (and_18_out, not_94_out, not_95_out, not_96_out, not_97_out, not_98_out, not_99_out, F5, not_100_out, not_101_out, not_102_out, F1, not_103_out);
  and and_19 (and_19_out, not_104_out, not_105_out, not_106_out, not_107_out, not_108_out, not_109_out, F5, not_110_out, not_111_out, F2, not_112_out, not_113_out);
  and and_20 (and_20_out, not_114_out, not_115_out, not_116_out, not_117_out, not_118_out, not_119_out, F5, not_120_out, not_121_out, F2, not_122_out, F0);
  and and_21 (and_21_out, not_123_out, not_124_out, not_125_out, not_126_out, not_127_out, not_128_out, F5, not_129_out, not_130_out, F2, F1, F0);
  and and_22 (and_22_out, not_131_out, not_132_out, not_133_out, not_134_out, not_135_out, not_136_out, F5, not_137_out, F3, not_138_out, F1, not_139_out);
  and and_23 (and_23_out, not_140_out, not_141_out, not_142_out, not_143_out, not_144_out, not_145_out, F5, not_146_out, F3, not_147_out, F1, F0);
  and and_24 (and_24_out, not_148_out, not_149_out, not_150_out, not_151_out, OP1, OP0);
  and and_25 (and_25_out, not_152_out, not_153_out, OP3, not_154_out, not_155_out, not_156_out);
  and and_26 (and_26_out, not_157_out, not_158_out, OP3, OP2, not_159_out, not_160_out);
  and and_27 (and_27_out, not_161_out, not_162_out, OP3, not_163_out, not_164_out, OP0);
  and and_28 (and_28_out, not_165_out, not_166_out, OP3, not_167_out, OP1, not_168_out);
  and and_29 (and_29_out, not_169_out, not_170_out, OP3, OP2, not_171_out, OP0);
  and and_30 (and_30_out, OP5, not_172_out, not_173_out, not_174_out, OP1, OP0);
  and and_31 (and_31_out, not_175_out, not_176_out, not_177_out, not_178_out, not_179_out, not_180_out, F5, not_181_out, not_182_out, not_183_out, F1, F0);
  and and_32 (and_32_out, not_184_out, not_185_out, OP3, not_186_out, OP1, OP0);
  and and_33 (and_33_out, OP5, not_187_out, not_188_out, OP2, not_189_out, OP0);
  and and_34 (SysCALL, not_190_out, not_191_out, not_192_out, not_193_out, not_194_out, not_195_out, not_196_out, not_197_out, F2, F3, not_198_out, not_199_out);
  and and_35 (and_35_out, not_200_out, not_201_out, not_202_out, OP2, not_203_out, not_204_out);
  and and_36 (and_36_out, not_205_out, not_206_out, not_207_out, OP2, not_208_out, OP0);
  and and_37 (and_37_out, not_209_out, not_210_out, OP3, not_211_out, not_212_out, not_213_out);
  and and_38 (and_38_out, not_214_out, not_215_out, OP3, not_216_out, not_217_out, OP0);
  and and_39 (and_39_out, not_218_out, not_219_out, OP3, not_220_out, OP1, not_221_out);
  and and_40 (and_40_out, OP5, not_222_out, not_223_out, not_224_out, OP1, OP0);
  and and_41 (and_41_out, OP5, not_225_out, OP3, not_226_out, OP1, OP0);
  and and_42 (and_42_out, not_227_out, not_228_out, OP3, not_229_out, OP1, OP0);
  and and_43 (and_43_out, OP5, not_230_out, not_231_out, OP2, not_232_out, OP0);
  and and_44 (and_44_out, not_233_out, not_234_out, not_235_out, OP2, OP1, not_236_out);
  and and_45 (and_45_out, not_237_out, not_238_out, not_239_out, not_240_out, not_241_out, not_242_out, not_243_out, not_244_out, not_245_out, not_246_out, not_247_out, not_248_out);
  and and_46 (and_46_out, not_249_out, not_250_out, not_251_out, not_252_out, not_253_out, not_254_out, not_255_out, not_256_out, not_257_out, not_258_out, F1, F0);
  and and_47 (and_47_out, not_259_out, not_260_out, not_261_out, not_262_out, not_263_out, not_264_out, not_265_out, not_266_out, not_267_out, not_268_out, F1, not_269_out);
  and and_48 (and_48_out, not_270_out, not_271_out, not_272_out, not_273_out, not_274_out, not_275_out, F5, not_276_out, not_277_out, not_278_out, not_279_out, not_280_out);
  and and_49 (and_49_out, not_281_out, not_282_out, not_283_out, not_284_out, not_285_out, not_286_out, F5, not_287_out, not_288_out, not_289_out, not_290_out, F0);
  and and_50 (and_50_out, not_291_out, not_292_out, not_293_out, not_294_out, not_295_out, not_296_out, F5, not_297_out, not_298_out, not_299_out, F1, not_300_out);
  and and_51 (and_51_out, not_301_out, not_302_out, not_303_out, not_304_out, not_305_out, not_306_out, F5, not_307_out, not_308_out, F2, not_309_out, not_310_out);
  and and_52 (and_52_out, not_311_out, not_312_out, not_313_out, not_314_out, not_315_out, not_316_out, F5, not_317_out, not_318_out, F2, not_319_out, F0);
  and and_53 (and_53_out, not_320_out, not_321_out, not_322_out, not_323_out, not_324_out, not_325_out, F5, not_326_out, not_327_out, F2, F1, F0);
  and and_54 (and_54_out, not_328_out, not_329_out, not_330_out, not_331_out, not_332_out, not_333_out, F5, not_334_out, F3, not_335_out, F1, not_336_out);
  and and_55 (and_55_out, not_337_out, not_338_out, not_339_out, not_340_out, not_341_out, not_342_out, F5, not_343_out, F3, not_344_out, F1, F0);
  and and_56 (and_56_out, not_345_out, not_346_out, not_347_out, not_348_out, not_349_out, not_350_out, F5, not_351_out, not_352_out, not_353_out, F1, F0);
  and and_57 (BEQ, not_354_out, not_355_out, OP2, not_356_out, not_357_out, not_358_out);
  and and_58 (BNE, OP0, not_359_out, OP2, not_360_out, not_361_out, not_362_out);
  and and_59 (JR, not_363_out, not_364_out, not_365_out, not_366_out, not_367_out, not_368_out, not_369_out, not_370_out, not_371_out, F3, not_372_out, not_373_out);
  and and_60 (and_60_out, not_374_out, not_375_out, not_376_out, not_377_out, not_378_out, not_379_out, not_380_out, not_381_out, F3, not_382_out, not_383_out);
  and and_61 (and_61_out, OP1, not_384_out, not_385_out, not_386_out, not_387_out);
  and and_62 (JAL, OP0, OP1, not_388_out, not_389_out, not_390_out, not_391_out);
  and and_63 (MFC0, not_392_out, OP4, not_393_out, not_394_out, not_395_out, not_396_out, not_397_out, not_398_out, not_399_out, not_400_out, not_401_out);
  and and_64 (MTC0, not_402_out, OP4, not_403_out, not_404_out, not_405_out, not_406_out, not_407_out, not_408_out, MF2, not_409_out, not_410_out);
  and and_65 (ERET, not_411_out, OP4, not_412_out, not_413_out, not_414_out, not_415_out, not_416_out, F4, F3, not_417_out, not_418_out, not_419_out, MF4);
  and and_66 (LHU, OP5, not_420_out, not_421_out, OP2, not_422_out, OP0);
  and and_67 (BLEZ, not_423_out, not_424_out, not_425_out, OP2, OP1, not_426_out);
  or or_1 (MemToReg, and_1_out, and_2_out);
  or or_2 (ALU_SRC, and_4_out, and_5_out, and_6_out, and_7_out, and_8_out, and_9_out, and_10_out, and_11_out, and_12_out);
  or or_3 (SignedExt, and_35_out, and_36_out, and_37_out, and_38_out, and_39_out, and_40_out, and_41_out, and_42_out, and_43_out, and_44_out);
  or or_4 (JUMP, and_60_out, and_61_out);
  or or_5 (RegWrite, and_13_out, and_14_out, and_15_out, and_16_out, and_17_out, and_18_out, and_19_out, and_20_out, and_21_out, and_22_out, and_23_out, and_24_out, and_25_out, and_26_out, and_27_out, and_28_out, and_29_out, and_30_out, and_31_out, and_32_out, and_33_out);
  or or_6 (RegDst, and_45_out, and_46_out, and_47_out, and_48_out, and_49_out, and_50_out, and_51_out, and_52_out, and_53_out, and_54_out, and_55_out, and_56_out);
endmodule

module \理想流水线  (
  output RegWrite,
  output MemWrite,
  output [31:0] IF_PC,
  output [31:0] ID_PC,
  output [31:0] EX_PC,
  output [31:0] M_PC,
  output [31:0] WB_PC,
  output [31:0] RDin,
  output [31:0] MDin,
  output [31:0] LedData
);

  wire and_1_out, and_2_out, and_3_out, B_JMP, CLK, comparator_1_gt, comparator_2_eq, Go, IR1, IR2, IR3, JAL,
       JMP, JR, mips_alu_1_equal, multiplexer_6_out, or_3_out, RegDst, RST, run, signedext, stall, Syscall,
       W1, W2, W3, \单周期硬布线控制器_1_eret , \单周期硬布线控制器_1_mfc0 , \单周期硬布线控制器_1_mtc0 ;
  wire [0:0] mem_wb_1_wb_2, or_1_out;
  wire [1:0] id_ex_1_mem_2, \单周期硬布线控制器_1_memwrite ;
  wire [1:1] ex_mem_1_mem_2;
  wire [3:0] id_ex_1_ex_2, \单周期硬布线控制器_1_alu_op ;
  wire [4:0] ex_mem_1_wb_2, id_ex_1_ir_2_2, id_ex_1_wb_2, multiplexer_2_out, multiplexer_3_out, W_num,
       \单周期硬布线控制器_1_memtoreg ;
  wire [9:4] id_ex_1_ex_2_2, \单周期硬布线控制器_1_alu_src ;
  wire [15:0] bitselector_1_out, \LoadUse次数 , \总周期数 , \插入气泡数 , \无条件分支数 , \条件分支成功数 ;
  wire [27:2] J_PC;
  wire [31:0] a0, adder_2_out, adder_4_out, B_PC, bit_extender_1_out, bit_extender_2_out, bit_extender_3_out,
       ex_mem_1_a0_2, ex_mem_1_alu_2, ex_mem_1_ir_2, ex_mem_1_v0_2, id_ex_1_b_2, id_ex_1_imm_2, id_ex_1_ir_2,
       JR_PC, mem_wb_1_alu_2, mem_wb_1_ir_2, mem_wb_1_md_2, mips_alu_1_result, mips_regifile_1_r1,
       mips_regifile_1_r2, multiplexer_1_out, multiplexer_4_out, multiplexer_5_out, multiplexer_7_out, O_PC,
       ram_1_data, rom_1_data, shifter_1_out, v0;
  wire [31:26] if_id_1_ir_2;

  Button \u_总复位  (.out(RST));
  Button _1 (.out(IR1));
  Button _2 (.out(IR2));
  Button _3 (.out(IR3));
  Button \u_继续运行  (.out(Go));
  LED #(.active("true")) led_1 (.in(W1));
  LED #(.active("true")) led_2 (.in(W2));
  LED #(.active("true")) led_3 (.in(W3));
  Hex_Digit_Display hex_digit_display_1 (.value(LedData[31:28]));  // open: dp
  or or_1 (or_1_out[0], JR, B_JMP);
  Multiplexer #(.select(2), .width(32), .disabled("Z"), .enable("false")) multiplexer_1 (
    .in0(O_PC), .in1(B_PC), .in2({ID_PC[31:28], J_PC, 2'b00}), .in3(JR_PC), .out(multiplexer_1_out),
    .sel({JMP, or_1_out[0]}));
  Hex_Digit_Display hex_digit_display_2 (.value(LedData[23:20]));  // open: dp
  Hex_Digit_Display hex_digit_display_3 (.value(LedData[27:24]));  // open: dp
  Register #(.width(32), .trigger("rising"), .Select("low")) PC (
    .D(multiplexer_1_out), .en(run), .Q(IF_PC), .clk(CLK));  // open: clr
  Hex_Digit_Display hex_digit_display_4 (.value(LedData[15:12]));  // open: dp
  Hex_Digit_Display hex_digit_display_5 (.value(LedData[19:16]));  // open: dp
  Adder #(.width(32)) adder_1 (.a(IF_PC), .b(32'h4), .out(O_PC));  // open: cin, cout
  Hex_Digit_Display hex_digit_display_6 (.value(LedData[11:8]));  // open: dp
  Hex_Digit_Display hex_digit_display_7 (.value(LedData[7:4]));  // open: dp
  Clock #(.highDuration(1), .lowDuration(1)) clock_1 (.out(CLK));
  ROM #(.addrWidth(10), .dataWidth(32), .Select("high")) rom_1 (.addr(IF_PC[11:2]), .data(rom_1_data));
  Hex_Digit_Display hex_digit_display_8 (.value(LedData[3:0]));  // open: dp
  IF_ID if_id_1 (
    .IR(rom_1_data), .PC(IF_PC), .IR_2({if_id_1_ir_2, J_PC}), .PC_2(ID_PC), .\清零 (RST), .CLK(CLK),
    .\使能_低电平有效 (stall));  // open: BHT, BHT_2
  // Probe on \总周期数 
  // Probe on \无条件分支数 
  // Probe on \条件分支成功数 
  // Probe on \插入气泡数 
  // Probe on \LoadUse次数 
  \单周期硬布线控制器  \u_单周期硬布线控制器_1  (
    .OP(if_id_1_ir_2), .Func(J_PC[7:2]), .MF(J_PC[27:23]), .ALU_OP(\单周期硬布线控制器_1_alu_op ),
    .MemToReg(\单周期硬布线控制器_1_memtoreg [0]), .MemWrite(\单周期硬布线控制器_1_memwrite [0]),
    .ALU_SRC(\单周期硬布线控制器_1_alu_src [4]), .RegWrite(\单周期硬布线控制器_1_memtoreg [1]),
    .SysCALL(\单周期硬布线控制器_1_memtoreg [2]), .SignedExt(signedext), .RegDst(\单周期硬布线控制器_1_memtoreg [3]),
    .Beq(\单周期硬布线控制器_1_alu_src [5]), .Bne(\单周期硬布线控制器_1_alu_src [6]), .JR(\单周期硬布线控制器_1_alu_src [7]),
    .JMP(\单周期硬布线控制器_1_alu_src [8]), .JAL(\单周期硬布线控制器_1_memtoreg [4]), .MFC0(\单周期硬布线控制器_1_mfc0 ),
    .MTC0(\单周期硬布线控制器_1_mtc0 ), .ERET(\单周期硬布线控制器_1_eret ), .BLEZ(\单周期硬布线控制器_1_alu_src [9]),
    .LHU(\单周期硬布线控制器_1_memwrite [1]));  // open: R1_used, R2_used
  Multiplexer #(.select(1), .width(5), .disabled("Z"), .enable("false")) multiplexer_2 (
    .in0(J_PC[27:23]), .in1(5'b00010), .out(multiplexer_2_out), .sel(\单周期硬布线控制器_1_memtoreg [2]));
  Multiplexer #(.select(1), .width(5), .disabled("Z"), .enable("false")) multiplexer_3 (
    .in0(J_PC[22:18]), .in1(5'b00100), .out(multiplexer_3_out), .sel(\单周期硬布线控制器_1_memtoreg [2]));
  // Probe on IF_PC[11:0]
  assign bit_extender_1_out = {{16{1'b0}}, J_PC[17:2]};  // Bit_Extender bit_extender_1
  assign bit_extender_2_out = {{16{J_PC[17]}}, J_PC[17:2]};  // Bit_Extender bit_extender_2
  // Probe on EX_PC[11:0]
  // Probe on ID_PC[11:0]
  MIPS_Regifile mips_regifile_1 (
    .Din(RDin), .Clk(CLK), .R1(mips_regifile_1_r1), .R2(mips_regifile_1_r2), .WE(RegWrite), .W_num(W_num),
    .R1_num(multiplexer_2_out), .R2_num(multiplexer_3_out));
  // Probe on M_PC[11:0]
  ID_EX id_ex_1 (
    .WB(\单周期硬布线控制器_1_memtoreg ), .MEM(\单周期硬布线控制器_1_memwrite ),
    .EX({\单周期硬布线控制器_1_alu_src , \单周期硬布线控制器_1_alu_op }), .IR({if_id_1_ir_2, J_PC}), .PC(ID_PC),
    .A(mips_regifile_1_r1), .B(mips_regifile_1_r2), .IMM(multiplexer_4_out), .WB_2(id_ex_1_wb_2),
    .MEM_2(id_ex_1_mem_2), .EX_2({id_ex_1_ex_2_2[9], JMP, JR, id_ex_1_ex_2_2[6:4], id_ex_1_ex_2}),
    .IR_2({id_ex_1_ir_2[31:11], id_ex_1_ir_2_2, id_ex_1_ir_2[5:0]}), .PC_2(EX_PC), .A_2(JR_PC),
    .B_2(id_ex_1_b_2), .IMM_2(id_ex_1_imm_2), .\清零 (RST), .CLK(CLK), .\使能_低电平有效 (stall));  // open: A_EX_hazard, A_EX_hazard_2, MF, MF_2, B_MFC0_hazard, B_MFC0_hazard_2, BHT, BHT_2
  Multiplexer #(.select(1), .width(32), .disabled("Z"), .enable("false")) multiplexer_4 (
    .in0(bit_extender_1_out), .in1(bit_extender_2_out), .out(multiplexer_4_out), .sel(signedext));
  // Probe on WB_PC[11:0]
  Adder #(.width(32)) adder_2 (.a(EX_PC), .b(32'h4), .out(adder_2_out));  // open: cin, cout
  Counter #(.width(16), .max('hffff), .ongoal("stay"), .trigger("rising"), .behavior("old")) counter_1 (
    .count(run), .Q(\总周期数 ), .clk(CLK));  // open: load, D, carry, clr, preset
  Comparator #(.width(32), .mode("twosComplement")) comparator_1 (
    .a(JR_PC), .b({32{1'b0}}), .gt(comparator_1_gt));  // open: eq, lt
  Multiplexer #(.select(1), .width(32), .disabled("Z"), .enable("false")) multiplexer_5 (
    .in0(id_ex_1_b_2), .in1(id_ex_1_imm_2), .out(multiplexer_5_out), .sel(id_ex_1_ex_2_2[4]));
  and and_1 (and_1_out, ~comparator_1_gt, id_ex_1_ex_2_2[9]);  // AND_Gate
  and and_2 (and_2_out, id_ex_1_ex_2_2[5], mips_alu_1_equal);
  and and_3 (and_3_out, id_ex_1_ex_2_2[6], ~mips_alu_1_equal);  // AND_Gate
  MIPS_ALU mips_alu_1 (
    .X(JR_PC), .Y(multiplexer_5_out), .AluOP(id_ex_1_ex_2), .Equal(mips_alu_1_equal),
    .Result(mips_alu_1_result), .shamt(id_ex_1_ir_2_2));  // open: Result_2
  Shifter #(.width(32), .shift("ll")) shifter_1 (.in(id_ex_1_imm_2), .\dist (5'b00010), .out(shifter_1_out));
  Adder #(.width(32)) adder_3 (.a(shifter_1_out), .b(adder_2_out), .out(B_PC));  // open: cin, cout
  or or_2 (B_JMP, and_1_out, and_2_out, and_3_out);
  Multiplexer #(.select(1), .width(1), .disabled("Z"), .enable("false")) multiplexer_6 (
    .in0(1'b0), .in1(comparator_2_eq), .out(multiplexer_6_out), .sel(Syscall));
  Comparator #(.width(32), .mode("twosComplement")) comparator_2 (
    .a(v0), .b(32'h22), .eq(comparator_2_eq));  // open: gt, lt
  EX_MEM ex_mem_1 (
    .WB(id_ex_1_wb_2), .MEM(id_ex_1_mem_2), .IR({id_ex_1_ir_2[31:11], id_ex_1_ir_2_2, id_ex_1_ir_2[5:0]}),
    .PC(EX_PC), .B(id_ex_1_b_2), .ALU(mips_alu_1_result), .WB_2(ex_mem_1_wb_2),
    .MEM_2({ex_mem_1_mem_2[1], MemWrite}), .IR_2(ex_mem_1_ir_2), .PC_2(M_PC), .B_2(MDin),
    .ALU_2(ex_mem_1_alu_2), .\清零 (RST), .CLK(CLK), .\使能_低电平有效 (stall), .V0(JR_PC), .V0_2(ex_mem_1_v0_2),
    .a0(id_ex_1_b_2), .a0_2(ex_mem_1_a0_2));  // open: MFC0, MEC0
  or or_3 (or_3_out, ~Syscall, multiplexer_6_out, Go);  // OR_Gate
  D_Flip_Flop #(.trigger("falling"), .Pre_Clr_Positions("LEGACY"), .NegatePresetClear("false"), .enable("true"), .NewFFLayout("false")) d_ff_1 (
    .clk(or_3_out), .D(1'b1), .Q(stall), .Qn(run));  // open: preset, en, reset
  Register #(.width(32), .trigger("rising"), .Select("low")) register_1 (
    .D(a0), .en(multiplexer_6_out), .Q(LedData), .clk(CLK));  // open: clr
  RAM #(.addrWidth(10), .dataWidth(32), .bus("separate"), .Select("high")) ram_1 (
    .addr(ex_mem_1_alu_2[11:2]), .din(MDin), .data(ram_1_data), .str(MemWrite), .clk(CLK));  // open: sel, ld, clr
  BitSelector #(.width(32), .group(16)) bitselector_1 (.in(ram_1_data), .out(bitselector_1_out));  // open: sel
  Multiplexer #(.select(1), .width(32), .disabled("Z"), .enable("false")) multiplexer_7 (
    .in0(ram_1_data), .in1(bit_extender_3_out), .out(multiplexer_7_out), .sel(ex_mem_1_mem_2[1]));
  assign bit_extender_3_out = {{16{1'b0}}, bitselector_1_out};  // Bit_Extender bit_extender_3
  MEM_WB mem_wb_1 (
    .WB(ex_mem_1_wb_2), .IR(ex_mem_1_ir_2), .PC(M_PC), .ALU(ex_mem_1_alu_2), .MD(multiplexer_7_out),
    .WB_2({JAL, RegDst, Syscall, RegWrite, mem_wb_1_wb_2[0]}), .IR_2(mem_wb_1_ir_2), .PC_2(WB_PC),
    .ALU_2(mem_wb_1_alu_2), .MD_2(mem_wb_1_md_2), .\清零 (RST), .CLK(CLK), .\使能_低电平有效 (stall),
    .v0(ex_mem_1_v0_2), .v0_2(v0), .a0(ex_mem_1_a0_2), .a0_2(a0));  // open: MFC0, MFC0_2
  Multiplexer #(.select(2), .width(5), .disabled("Z"), .enable("false")) multiplexer_8 (
    .in0(mem_wb_1_ir_2[20:16]), .in1(mem_wb_1_ir_2[15:11]), .in2({5{1'b1}}), .in3({5{1'b1}}), .out(W_num),
    .sel({JAL, RegDst}));
  Adder #(.width(32)) adder_4 (.a(WB_PC), .b(32'h4), .out(adder_4_out));  // open: cin, cout
  Multiplexer #(.select(2), .width(32), .disabled("Z"), .enable("false")) multiplexer_9 (
    .in0(mem_wb_1_alu_2), .in1(mem_wb_1_md_2), .in2(adder_4_out), .in3(adder_4_out), .out(RDin),
    .sel({JAL, mem_wb_1_wb_2[0]}));

  // Other names for the same wires on the sheet: J_PC[31:28] = ID_PC[31:28]; MEM_PC[31:0] = M_PC

  // Notes on the sheet:
  //   中断源
  //   中断等待指示
  //   数码管输出
  //   指令存储器
  //   contents of rom_1 (hex, n*v repeats v):
  //   20100000 20110000 20120000 20130000 36100000 36310001 36520002 36730003 ae100000 ae110004 ae120008
  //   ae13000c 2002000a 20110000 20120000 20130000 c
  //   OP
  //   Func
  //   MF
  //   rs
  //   rt
  //   AluOP
  //   MemToReg
  //   MemWrite
  //   AluSrcB
  //   RegWrite
  //   Syscall
  //   Signedext
  //   RegDst
  //   BEQ
  //   BNE
  //   JR
  //   JMP
  //   JAL
  //   MFC0
  //   MTC0
  //   ERET
  //   LHU
  //   BLEZ
  //   流水调试日志用
  //   为方便自动评测，需要输出流水线各段保存的PC值，注意是PC不是PC+4，另外ID段寄存器写入信息，Mem段内存写入信息也要输出
endmodule

module \气泡流水线  (
  output RegWrite,
  output MemWrite,
  output [31:0] IF_PC,
  output [31:0] ID_PC,
  output [31:0] EX_PC,
  output [31:0] M_PC,
  output [31:0] WB_PC,
  output [31:0] RDin,
  output [31:0] MDin,
  output [31:0] LedData
);

  wire and_1_out, and_2_out, and_3_out, and_4_out, B_JMP, brench_hazard, CLK, comparator_1_gt,
       comparator_2_eq, DATA_hazard, Go, IR1, IR2, IR3, JAL, JMP, JR, mips_alu_1_equal, multiplexer_2_out,
       multiplexer_8_out, or_2_out, or_3_out, or_4_out, R1_U, R2_U, RegDst, RST, run, signedext, stall,
       Syscall, W1, W2, W3, \单周期硬布线控制器_1_eret , \单周期硬布线控制器_1_mfc0 , \单周期硬布线控制器_1_mtc0 ,
       \数据相关检测_1_a_ex_hazard , \数据相关检测_1_a_mem_hazard , \数据相关检测_1_b_ex_hazard , \数据相关检测_1_b_mem_hazard ;
  wire [0:0] mem_wb_1_wb_2, or_1_out;
  wire [1:0] id_ex_1_mem_2, \单周期硬布线控制器_1_memwrite ;
  wire [1:1] ex_mem_1_mem_2;
  wire [3:0] id_ex_1_ex_2, \单周期硬布线控制器_1_alu_op ;
  wire [4:0] ex_mem_1_ir_2_2, ex_mem_1_ir_2_3, ex_mem_1_wb_2, id_ex_1_wb_2, R1_num, R2_num, W_num,
       \单周期硬布线控制器_1_memtoreg ;
  wire [9:4] id_ex_1_ex_2_2, \单周期硬布线控制器_1_alu_src ;
  wire [15:0] bitselector_1_out, \LoadUse次数 , N1, N2, \总周期数 , \插入气泡数 , \无条件分支数 , \条件分支成功数 ;
  wire [27:2] J_PC;
  wire [31:0] a0, adder_2_out, adder_4_out, B_PC, bit_extender_1_out, bit_extender_2_out, bit_extender_3_out,
       ex_mem_1_a0_2, ex_mem_1_alu_2, ex_mem_1_ir_2, ex_mem_1_v0_2, id_ex_1_b_2, id_ex_1_imm_2, if_id_1_ir_2,
       IR, JR_PC, mem_wb_1_alu_2, mem_wb_1_ir_2, mem_wb_1_md_2, mips_alu_1_result, mips_regifile_1_r1,
       mips_regifile_1_r2, multiplexer_1_out, multiplexer_5_out, multiplexer_6_out, multiplexer_7_out, O_PC,
       ram_1_data, shifter_1_out, v0;
  wire [31:26] id_ex_1_ir_2;

  Clock #(.highDuration(1), .lowDuration(1)) clock_1 (.out(CLK));
  Button _1 (.out(IR1));
  Button _2 (.out(IR2));
  Button _3 (.out(IR3));
  Button \u_总复位  (.out(RST));
  Button \u_继续运行  (.out(Go));
  LED #(.active("true")) led_1 (.in(W1));
  LED #(.active("true")) led_2 (.in(W2));
  LED #(.active("true")) led_3 (.in(W3));
  Hex_Digit_Display hex_digit_display_1 (.value(LedData[31:28]));  // open: dp
  or or_1 (or_1_out[0], JR, B_JMP);
  Multiplexer #(.select(2), .width(32), .disabled("Z"), .enable("false")) multiplexer_1 (
    .in0(O_PC), .in1(B_PC), .in2({EX_PC[31:28], J_PC, 2'b00}), .in3(JR_PC), .out(multiplexer_1_out),
    .sel({JMP, or_1_out[0]}));
  Multiplexer #(.select(1), .width(1), .disabled("Z"), .enable("false")) multiplexer_2 (
    .in0(run), .in1(1'b0), .out(multiplexer_2_out), .sel(DATA_hazard));
  Hex_Digit_Display hex_digit_display_2 (.value(LedData[27:24]));  // open: dp
  Hex_Digit_Display hex_digit_display_3 (.value(LedData[23:20]));  // open: dp
  Register #(.width(32), .trigger("rising"), .Select("low")) PC (
    .D(multiplexer_1_out), .en(multiplexer_2_out), .Q(IF_PC), .clk(CLK));  // open: clr
  Hex_Digit_Display hex_digit_display_4 (.value(LedData[19:16]));  // open: dp
  Hex_Digit_Display hex_digit_display_5 (.value(LedData[15:12]));  // open: dp
  Adder #(.width(32)) adder_1 (.a(IF_PC), .b(32'h4), .out(O_PC));  // open: cin, cout
  Hex_Digit_Display hex_digit_display_6 (.value(LedData[7:4]));  // open: dp
  Hex_Digit_Display hex_digit_display_7 (.value(LedData[11:8]));  // open: dp
  // Probe on \总周期数 
  Counter #(.width(16), .max('hffff), .ongoal("stay"), .trigger("rising"), .behavior("old")) counter_1 (
    .count(or_2_out), .Q(N1), .clk(CLK));  // open: load, D, carry, clr, preset
  ROM #(.addrWidth(10), .dataWidth(32), .Select("high")) rom_1 (.addr(IF_PC[11:2]), .data(IR));
  Hex_Digit_Display hex_digit_display_8 (.value(LedData[3:0]));  // open: dp
  or or_2 (or_2_out, RST, brench_hazard);
  IF_ID if_id_1 (
    .IR(IR), .PC(IF_PC), .IR_2(if_id_1_ir_2), .PC_2(ID_PC), .\清零 (or_2_out), .CLK(CLK), .\使能_低电平有效 (or_3_out));  // open: BHT, BHT_2
  or or_3 (or_3_out, stall, DATA_hazard);
  \单周期硬布线控制器  \u_单周期硬布线控制器_1  (
    .OP(if_id_1_ir_2[31:26]), .Func(if_id_1_ir_2[5:0]), .MF(if_id_1_ir_2[25:21]),
    .ALU_OP(\单周期硬布线控制器_1_alu_op ), .MemToReg(\单周期硬布线控制器_1_memtoreg [0]),
    .MemWrite(\单周期硬布线控制器_1_memwrite [0]), .ALU_SRC(\单周期硬布线控制器_1_alu_src [4]),
    .RegWrite(\单周期硬布线控制器_1_memtoreg [1]), .SysCALL(\单周期硬布线控制器_1_memtoreg [2]), .SignedExt(signedext),
    .RegDst(\单周期硬布线控制器_1_memtoreg [3]), .Beq(\单周期硬布线控制器_1_alu_src [5]), .Bne(\单周期硬布线控制器_1_alu_src [6]),
    .JR(\单周期硬布线控制器_1_alu_src [7]), .JMP(\单周期硬布线控制器_1_alu_src [8]), .JAL(\单周期硬布线控制器_1_memtoreg [4]),
    .MFC0(\单周期硬布线控制器_1_mfc0 ), .MTC0(\单周期硬布线控制器_1_mtc0 ), .ERET(\单周期硬布线控制器_1_eret ),
    .BLEZ(\单周期硬布线控制器_1_alu_src [9]), .LHU(\单周期硬布线控制器_1_memwrite [1]), .R1_used(R1_U), .R2_used(R2_U));
  Multiplexer #(.select(1), .width(5), .disabled("Z"), .enable("false")) multiplexer_3 (
    .in0(if_id_1_ir_2[25:21]), .in1(5'b00010), .out(R1_num), .sel(\单周期硬布线控制器_1_memtoreg [2]));
  Multiplexer #(.select(1), .width(5), .disabled("Z"), .enable("false")) multiplexer_4 (
    .in0(if_id_1_ir_2[20:16]), .in1(5'b00100), .out(R2_num), .sel(\单周期硬布线控制器_1_memtoreg [2]));
  // Probe on \总周期数 
  // Probe on \无条件分支数 
  // Probe on \条件分支成功数 
  // Probe on \插入气泡数 
  // Probe on \LoadUse次数 
  assign bit_extender_1_out = {{16{1'b0}}, if_id_1_ir_2[15:0]};  // Bit_Extender bit_extender_1
  assign bit_extender_2_out = {{16{if_id_1_ir_2[15]}}, if_id_1_ir_2[15:0]};  // Bit_Extender bit_extender_2
  // Probe on IF_PC[11:0]
  // Probe on ID_PC[11:0]
  Counter #(.width(16), .max('hffff), .ongoal("stay"), .trigger("rising"), .behavior("old")) counter_2 (
    .count(and_1_out), .Q(N2), .clk(CLK));  // open: load, D, carry, clr, preset
  and and_1 (and_1_out, run, or_4_out);
  MIPS_Regifile mips_regifile_1 (
    .Din(RDin), .Clk(CLK), .R1(mips_regifile_1_r1), .R2(mips_regifile_1_r2), .WE(RegWrite), .W_num(W_num),
    .R1_num(R1_num), .R2_num(R2_num));
  // Probe on EX_PC[11:0]
  or or_4 (or_4_out, RST, DATA_hazard, brench_hazard);
  ID_EX id_ex_1 (
    .WB(\单周期硬布线控制器_1_memtoreg ), .MEM(\单周期硬布线控制器_1_memwrite ),
    .EX({\单周期硬布线控制器_1_alu_src , \单周期硬布线控制器_1_alu_op }), .IR(if_id_1_ir_2), .PC(ID_PC),
    .A(mips_regifile_1_r1), .B(mips_regifile_1_r2), .IMM(multiplexer_5_out), .WB_2(id_ex_1_wb_2),
    .MEM_2(id_ex_1_mem_2), .EX_2({id_ex_1_ex_2_2[9], JMP, JR, id_ex_1_ex_2_2[6:4], id_ex_1_ex_2}),
    .IR_2({id_ex_1_ir_2, J_PC}), .PC_2(EX_PC), .A_2(JR_PC), .B_2(id_ex_1_b_2), .IMM_2(id_ex_1_imm_2),
    .\清零 (or_4_out), .CLK(CLK), .\使能_低电平有效 (stall));  // open: A_EX_hazard, A_EX_hazard_2, MF, MF_2, B_MFC0_hazard, B_MFC0_hazard_2, BHT, BHT_2
  Multiplexer #(.select(1), .width(32), .disabled("Z"), .enable("false")) multiplexer_5 (
    .in0(bit_extender_1_out), .in1(bit_extender_2_out), .out(multiplexer_5_out), .sel(signedext));
  // Probe on WB_PC[11:0]
  // Probe on M_PC[11:0]
  Adder #(.width(32)) adder_2 (.a(EX_PC), .b(32'h4), .out(adder_2_out));  // open: cin, cout
  or or_5 (brench_hazard, JR, B_JMP, JMP);
  Comparator #(.width(32), .mode("twosComplement")) comparator_1 (
    .a(JR_PC), .b({32{1'b0}}), .gt(comparator_1_gt));  // open: eq, lt
  Multiplexer #(.select(1), .width(32), .disabled("Z"), .enable("false")) multiplexer_6 (
    .in0(id_ex_1_b_2), .in1(id_ex_1_imm_2), .out(multiplexer_6_out), .sel(id_ex_1_ex_2_2[4]));
  and and_2 (and_2_out, ~comparator_1_gt, id_ex_1_ex_2_2[9]);  // AND_Gate
  and and_3 (and_3_out, id_ex_1_ex_2_2[5], mips_alu_1_equal);
  and and_4 (and_4_out, id_ex_1_ex_2_2[6], ~mips_alu_1_equal);  // AND_Gate
  MIPS_ALU mips_alu_1 (
    .X(JR_PC), .Y(multiplexer_6_out), .AluOP(id_ex_1_ex_2), .Equal(mips_alu_1_equal),
    .Result(mips_alu_1_result), .shamt(J_PC[12:8]));  // open: Result_2
  Shifter #(.width(32), .shift("ll")) shifter_1 (.in(id_ex_1_imm_2), .\dist (5'b00010), .out(shifter_1_out));
  Adder #(.width(32)) adder_3 (.a(shifter_1_out), .b(adder_2_out), .out(B_PC));  // open: cin, cout
  or or_6 (B_JMP, and_2_out, and_3_out, and_4_out);
  or or_7 (DATA_hazard, \数据相关检测_1_a_ex_hazard , \数据相关检测_1_b_ex_hazard , \数据相关检测_1_b_mem_hazard , \数据相关检测_1_a_mem_hazard );
  \数据相关检测  \u_数据相关检测_1  (
    .EX_JAL(id_ex_1_wb_2[4]), .R1_used(R1_U), .EX_rt_num(J_PC[22:18]), .EX_rd_num(J_PC[17:13]),
    .MEM_rt_num(ex_mem_1_ir_2_3), .MEM_rd_num(ex_mem_1_ir_2_2), .MEM_JAL(ex_mem_1_wb_2[4]), .R2_used(R2_U),
    .EX_RegDst(id_ex_1_wb_2[3]), .EX_RegWrite(id_ex_1_wb_2[1]), .A_EX_hazard(\数据相关检测_1_a_ex_hazard ),
    .A_MEM_hazard(\数据相关检测_1_a_mem_hazard ), .MEM_RegDst(ex_mem_1_wb_2[3]), .MEM_RegWrite(ex_mem_1_wb_2[1]),
    .R1_num(R1_num), .R2_num(R2_num), .B_EX_hazard(\数据相关检测_1_b_ex_hazard ),
    .B_MEM_hazard(\数据相关检测_1_b_mem_hazard ), .EX_MFC0(1'b0));  // open: MFC0_hazard
  EX_MEM ex_mem_1 (
    .WB(id_ex_1_wb_2), .MEM(id_ex_1_mem_2), .IR({id_ex_1_ir_2, J_PC}), .PC(EX_PC), .B(id_ex_1_b_2),
    .ALU(mips_alu_1_result), .WB_2(ex_mem_1_wb_2), .MEM_2({ex_mem_1_mem_2[1], MemWrite}),
    .IR_2({ex_mem_1_ir_2[31:21], ex_mem_1_ir_2_3, ex_mem_1_ir_2_2, ex_mem_1_ir_2[10:0]}), .PC_2(M_PC),
    .B_2(MDin), .ALU_2(ex_mem_1_alu_2), .\清零 (RST), .CLK(CLK), .\使能_低电平有效 (stall), .V0(JR_PC),
    .V0_2(ex_mem_1_v0_2), .a0(id_ex_1_b_2), .a0_2(ex_mem_1_a0_2));  // open: MFC0, MEC0
  Counter #(.width(16), .max('hffff), .ongoal("stay"), .trigger("rising"), .behavior("old")) counter_3 (
    .count(run), .Q(\总周期数 ), .clk(CLK));  // open: load, D, carry, clr, preset
  RAM #(.addrWidth(10), .dataWidth(32), .bus("separate"), .Select("high")) ram_1 (
    .addr(ex_mem_1_alu_2[11:2]), .din(MDin), .data(ram_1_data), .str(MemWrite), .clk(CLK));  // open: sel, ld, clr
  Multiplexer #(.select(1), .width(32), .disabled("Z"), .enable("false")) multiplexer_7 (
    .in0(ram_1_data), .in1(bit_extender_3_out), .out(multiplexer_7_out), .sel(ex_mem_1_mem_2[1]));
  assign bit_extender_3_out = {{16{1'b0}}, bitselector_1_out};  // Bit_Extender bit_extender_3
  BitSelector #(.width(32), .group(16)) bitselector_1 (.in(ram_1_data), .out(bitselector_1_out));  // open: sel
  MEM_WB mem_wb_1 (
    .WB(ex_mem_1_wb_2), .IR({ex_mem_1_ir_2[31:21], ex_mem_1_ir_2_3, ex_mem_1_ir_2_2, ex_mem_1_ir_2[10:0]}),
    .PC(M_PC), .ALU(ex_mem_1_alu_2), .MD(multiplexer_7_out),
    .WB_2({JAL, RegDst, Syscall, RegWrite, mem_wb_1_wb_2[0]}), .IR_2(mem_wb_1_ir_2), .PC_2(WB_PC),
    .ALU_2(mem_wb_1_alu_2), .MD_2(mem_wb_1_md_2), .\清零 (RST), .CLK(CLK), .\使能_低电平有效 (stall),
    .v0(ex_mem_1_v0_2), .v0_2(v0), .a0(ex_mem_1_a0_2), .a0_2(a0));  // open: MFC0, MFC0_2
  Multiplexer #(.select(1), .width(1), .disabled("Z"), .enable("false")) multiplexer_8 (
    .in0(1'b0), .in1(comparator_2_eq), .out(multiplexer_8_out), .sel(Syscall));
  Comparator #(.width(32), .mode("twosComplement")) comparator_2 (
    .a(v0), .b(32'h22), .eq(comparator_2_eq));  // open: gt, lt
  Adder #(.width(32)) adder_4 (.a(WB_PC), .b(32'h4), .out(adder_4_out));  // open: cin, cout
  not not_1 (stall, run);
  or or_8 (run, ~Syscall, multiplexer_8_out, Go);  // OR_Gate
  Adder #(.width(16)) adder_5 (.a(N2), .b(N1), .out(\插入气泡数 ));  // open: cin, cout
  Multiplexer #(.select(2), .width(5), .disabled("Z"), .enable("false")) multiplexer_9 (
    .in0(mem_wb_1_ir_2[20:16]), .in1(mem_wb_1_ir_2[15:11]), .in2({5{1'b1}}), .in3({5{1'b1}}), .out(W_num),
    .sel({JAL, RegDst}));
  Register #(.width(32), .trigger("rising"), .Select("low")) register_1 (
    .D(a0), .en(multiplexer_8_out), .Q(LedData), .clk(CLK));  // open: clr
  Multiplexer #(.select(2), .width(32), .disabled("Z"), .enable("false")) multiplexer_10 (
    .in0(mem_wb_1_alu_2), .in1(mem_wb_1_md_2), .in2(adder_4_out), .in3(adder_4_out), .out(RDin),
    .sel({JAL, mem_wb_1_wb_2[0]}));
  Counter #(.width(16), .max('hffff), .ongoal("stay"), .trigger("rising"), .behavior("old")) counter_4 (
    .count(B_JMP), .Q(\条件分支成功数 ), .clk(CLK));  // open: load, D, carry, clr, preset
  Counter #(.width(16), .max('hffff), .ongoal("stay"), .trigger("rising"), .behavior("old")) counter_5 (
    .count(JMP), .Q(\无条件分支数 ), .clk(CLK));  // open: load, D, carry, clr, preset

  // Other names for the same wires on the sheet: J_PC[31:28] = EX_PC[31:28]; MEM_PC[31:0] = M_PC; PC[31:0] = IF_PC

  // Notes on the sheet:
  //   中断源
  //   中断等待指示
  //   总复位信号应将除ROM以外所有存储组件全部清零
  //   数码管输出
  //   指令存储器
  //   数码管输出应该用寄存器锁存，否则显示数据只能一闪而过
  //   contents of rom_1 (hex, n*v repeats v):
  //   20110001 8000c05 20110001 20120002 20130003 8000c09 20110001 20120002 20130003 8000c0d 20110001
  //   20120002 20130003 8000c11 20110001 20120002 20130003 c000cf1 20100001 20110001 118fc0 112020
  //   20020022 c 118882 12200001 8000c15 112020 20020022 c 20110001 118880 112020 20020022 c 12200001
  //   8000c1f 20110001 118fc0 112020 20020022 c 1188c3 112020 20020022 c 118903 112020 20020022 c 118903
  //   112020 20020022 c 118903 112020 20020022 c 118903 112020 20020022 c 118903 112020 20020022 c 118903
  //   112020 20020022 c 118903 112020 20020022 c 20100001 109fc0 139fc3 8021 2012000c 24160003 26100001
  //   3210000f 20080008 20090001 139900 2709825 132020 20020022 c 1094022 1500fff9 22100001 2018000f
  //   2188024 108700 20080008 20090001 139902 2709825 132021 20020022 c 1094022 1500fff9 108702 2c9b022
  //   12c00001 8000c50 4020 1084027 84400 3508ffff 82021 20020022 c 2010ffff 20110000 ae300000 22100001
  //   22310004 ae300000 22100001 22310004 ae300000 22100001 22310004 ae300000 22100001 22310004 ae300000
  //   22100001 22310004 ae300000 22100001 22310004 ae300000 22100001 22310004 ae300000 22100001 22310004
  //   ae300000 22100001 22310004 ae300000 22100001 22310004 ae300000 22100001 22310004 ae300000 22100001
  //   22310004 ae300000 22100001 22310004 ae300000 22100001 22310004 ae300000 22100001 22310004 ae300000
  //   22100001 22310004 22100001 8020 2011003c 8e130000 8e340000 274402a 11000002 ae330000 ae140000
  //   2231fffc 1611fff8 102020 20020022 c 22100004 2011003c 1611fff2 20020032 c 20080001 20110010 112020
  //   20020022 c 200b0020 2288823 112020 20020022 c 216bffff 1560fffa 2002000a c 2008ffff 20090000
  //   20111997 112020 20020022 c 2288820 2e291949 1120fffa 2002000a c 20090000 200b0010 34118483 20120404
  //   118c00 129400 36318281 22520404 ad310000 2328820 21290004 216bffff 1560fffb 200b0020 20090000
  //   95310000 112020 20020022 c 21290002 216bffff 1560fff9 2002000a c 2011fff1 112020 20020022 c 22310001
  //   1a20fffb 2002000a c 20100000 22100001 102020 20020022 c 22100002 102020 20020022 c 22100003 102020
  //   20020022 c 22100004 102020 20020022 c 22100005 102020 20020022 c 22100006 102020 20020022 c 22100007
  //   102020 20020022 c 22100008 102020 20020022 20020022 c 3e00008
  //   OP
  //   Func
  //   MF
  //   rs
  //   rt
  //   AluOP
  //   MemToReg
  //   MemWrite
  //   AluSrcB
  //   RegWrite
  //   Syscall
  //   Signedext
  //   RegDst
  //   BEQ
  //   BNE
  //   JR
  //   JMP
  //   JAL
  //   MFC0
  //   MTC0
  //   ERET
  //   LHU
  //   BLEZ
  //   流水调试日志用
  //   为方便自动评测，需要输出流水线各段保存的PC值，注意是PC不是PC+4，另外ID段寄存器写入信息，Mem段内存写入信息也要输出
endmodule
module \重定向流水线  (
  output RegWrite,
  output MemWrite,
  output [31:0] IF_PC,
  output [31:0] ID_PC,
  output [31:0] EX_PC,
  output [31:0] M_PC,
  output [31:0] WB_PC,
  output [31:0] RDin,
  output [31:0] MDin,
  output [31:0] LedData
);

  wire A_EX_hazard, and_1_out, and_3_out, and_4_out, and_5_out, and_6_out, and_7_out, and_8_out, and_9_out,
       and_10_out, and_15_out, and_16_out, and_17_out, and_18_out, and_19_out, B_EX_hazard, B_JMP, B_TYPE,
       brench_hazard, CLK, comparator_1_eq, comparator_2_gt, comparator_3_eq, comparator_4_eq, d_ff_1_q,
       d_ff_2_q, d_ff_3_q, d_ff_4_qn, d_ff_5_qn, d_ff_6_qn, data_hazard, decoder_1_out0, decoder_1_out1,
       decoder_1_out2, EPC, ERET, EX_M2R, FAIL, fail_t, Go, IE, IE_q, INM, INM1, INM2, INM3, IR1, IR1_num,
       IR1_over, IR2, IR2_num, IR2_over, IR3, IR3_num, IR3_over, IR_star, IRready, J_TYPE, JAL, JMP, JR,
       LoadUse, MEM_M2R, MEM_rd0, MFC0, MFC0_hazard, mips_alu_1_equal, MTC0, multiplexer_5_out,
       multiplexer_8_out, multiplexer_15_out, multiplexer_25_out, not_1_out, not_2_out, not_3_out, or_4_out,
       or_5_out, or_6_out, or_8_out, or_9_out, or_10_out, or_11_out, or_13_out, or_14_out, or_15_out,
       or_18_out, or_19_out, or_20_out, priority_encoder_1_gs, R1_U, R2_U, rd_sel, RegDst, RST, run,
       signedext, stall, Syscall, W1, W2, W3, WB_M2R;
  wire [0:0] bht_1_miss, id_ex_1_bht_2;
  wire [1:0] bht_1_bhtresult, ex_mem_1_mec0, id_ex_1_bht_2_2, id_ex_1_mem_2, multiplexer_12_out,
       multiplexer_13_out, \new , priority_encoder_1_out, \单周期硬布线控制器_1_memwrite , \预测更新_1_new ;
  wire [1:1] ex_mem_1_mem_2;
  wire [2:0] bht_1_change, id_ex_1_mf_2, \单周期硬布线控制器_1_mfc0 ;
  wire [3:0] id_ex_1_a_ex_hazard_2, replace;
  wire [3:2] hazard;
  wire [4:0] ex_mem_1_ir_2_3, R1_num, R2_num, rd, W_num, \单周期硬布线控制器_1_memtoreg ;
  wire [4:1] ex_mem_1_ir_2_2, ex_mem_1_wb_2, id_ex_1_wb_2;
  wire [5:0] if_id_1_bht_2;
  wire [9:0] id_ex_1_ex_2, \单周期硬布线控制器_1_alu_op ;
  wire [15:0] bitselector_1_out, \LoadUse次数 , N1, N2, \总周期数 , \插入气泡数 , \无条件分支数 , \条件分支成功数 ;
  wire [27:2] J_PC;
  wire [31:0] a0, adder_4_out, AIM_PC, B_PC, bht_1_for_pc, bit_extender_1_out, bit_extender_2_out,
       bit_extender_3_out, EPC_DA, ex_mem_1_a0_2, ex_mem_1_ir_2, ex_mem_1_v0_2, id_ex_1_a_2, id_ex_1_b_2,
       id_ex_1_imm_2, if_id_1_ir_2, IR, IR_DA, IR_PC, JR_PC, MEM_ALU, mem_wb_1_ir_2, MFC0_DA,
       mips_alu_1_result, mips_regifile_1_r1, mips_regifile_1_r2, multiplexer_1_out, multiplexer_2_out,
       multiplexer_3_out, multiplexer_4_out, multiplexer_9_out, multiplexer_17_out, multiplexer_18_out,
       multiplexer_20_out, multiplexer_21_out, multiplexer_23_out, O_PC, ram_1_data, RIGHT_PC, shifter_1_out,
       v0, WB_ALU, WB_MD, Y_PC;
  wire [31:26] id_ex_1_ir_2;

  Clock #(.highDuration(1), .lowDuration(1)) clock_1 (.out(CLK));
  Button _1 (.out(IR1));
  Button _2 (.out(IR2));
  Button _3 (.out(IR3));
  Button \u_继续运行  (.out(Go));
  LED #(.active("true")) led_1 (.in(W1));
  LED #(.active("true")) led_2 (.in(W2));
  LED #(.active("true")) led_3 (.in(W3));
  Button \u_总复位  (.out(RST));
  Hex_Digit_Display hex_digit_display_1 (.value(LedData[31:28]));  // open: dp
  Multiplexer #(.select(1), .width(32), .disabled("Z"), .enable("false")) multiplexer_1 (
    .in0(O_PC), .in1(JR_PC), .out(multiplexer_1_out), .sel(JR));
  Hex_Digit_Display hex_digit_display_2 (.value(LedData[27:24]));  // open: dp
  Hex_Digit_Display hex_digit_display_3 (.value(LedData[23:20]));  // open: dp
  Multiplexer #(.select(1), .width(32), .disabled("Z"), .enable("false")) multiplexer_2 (
    .in0(multiplexer_1_out), .in1(bht_1_for_pc), .out(multiplexer_2_out), .sel(bht_1_bhtresult[1]));
  or or_1 (W1, IR1_num, d_ff_1_q);
  or or_2 (W2, IR2_num, d_ff_2_q);
  or or_3 (W3, IR3_num, d_ff_3_q);
  Hex_Digit_Display hex_digit_display_4 (.value(LedData[19:16]));  // open: dp
  Hex_Digit_Display hex_digit_display_5 (.value(LedData[15:12]));  // open: dp
  Multiplexer #(.select(1), .width(32), .disabled("Z"), .enable("false")) multiplexer_3 (
    .in0(multiplexer_2_out), .in1(RIGHT_PC), .out(multiplexer_3_out), .sel(FAIL));
  D_Flip_Flop #(.trigger("rising"), .Pre_Clr_Positions("LEGACY"), .NegatePresetClear("false"), .enable("true"), .NewFFLayout("false")) d_ff_1 (
    .clk(IR1), .D(1'b1), .Q(d_ff_1_q), .reset(IR1_num));  // open: Qn, preset, en
  D_Flip_Flop #(.trigger("rising"), .Pre_Clr_Positions("LEGACY"), .NegatePresetClear("false"), .enable("true"), .NewFFLayout("false")) d_ff_2 (
    .clk(IR2), .D(1'b1), .Q(d_ff_2_q), .reset(IR2_num));  // open: Qn, preset, en
  D_Flip_Flop #(.trigger("rising"), .Pre_Clr_Positions("LEGACY"), .NegatePresetClear("false"), .enable("true"), .NewFFLayout("false")) d_ff_3 (
    .clk(IR3), .D(1'b1), .Q(d_ff_3_q), .reset(IR3_num));  // open: Qn, preset, en
  Hex_Digit_Display hex_digit_display_6 (.value(LedData[7:4]));  // open: dp
  Hex_Digit_Display hex_digit_display_7 (.value(LedData[11:8]));  // open: dp
  and and_1 (and_1_out, JR, JMP);
  Register #(.width(32), .trigger("rising"), .Select("low")) PC (
    .D(multiplexer_4_out), .en(multiplexer_5_out), .Q(IF_PC), .clk(CLK));  // open: clr
  Multiplexer #(.select(2), .width(32), .disabled("Z"), .enable("false")) multiplexer_4 (
    .in0(multiplexer_3_out), .in1(EPC_DA), .in2(IR_PC), .in3(EPC_DA), .out(multiplexer_4_out),
    .sel({IRready, ERET}));
  Multiplexer #(.select(1), .width(1), .disabled("Z"), .enable("false")) multiplexer_5 (
    .in0(run), .in1(1'b0), .out(multiplexer_5_out), .sel(LoadUse));
  or or_4 (or_4_out, d_ff_1_q, IR1_num);
  or or_5 (or_5_out, d_ff_2_q, IR2_num);
  or or_6 (or_6_out, d_ff_3_q, IR3_num);
  Hex_Digit_Display hex_digit_display_8 (.value(LedData[3:0]));  // open: dp
  // Probe on \总周期数 
  and and_2 (FAIL, and_3_out, ~comparator_1_eq);  // AND_Gate
  or or_7 (brench_hazard, and_1_out, FAIL);
  and and_3 (and_3_out, replace[3], fail_t);
  and and_4 (and_4_out, or_4_out, ~IR1_over);  // AND_Gate
  and and_5 (and_5_out, or_5_out, ~IR2_over);  // AND_Gate
  and and_6 (and_6_out, or_6_out, ~IR3_over);  // AND_Gate
  Comparator #(.width(32), .mode("twosComplement")) comparator_1 (
    .a(RIGHT_PC), .b(ID_PC), .eq(comparator_1_eq));  // open: gt, lt
  BHT bht_1 (
    .CLK(CLK), .PC(IF_PC), .\new (\new ), .replace(replace), .BHTresult(bht_1_bhtresult),
    .FOR_PC(bht_1_for_pc), .change(bht_1_change), .AIM_PC(AIM_PC), .IN_PC(EX_PC), .miss(bht_1_miss[0]));
  Adder #(.width(32)) adder_1 (.a(IF_PC), .b(32'h4), .out(O_PC));  // open: cin, cout
  D_Flip_Flop #(.trigger("rising"), .Pre_Clr_Positions("LEGACY"), .NegatePresetClear("false"), .enable("true"), .NewFFLayout("false")) u_IR1 (
    .clk(CLK), .D(and_4_out), .Q(IR1_num));  // open: Qn, preset, en, reset
  D_Flip_Flop #(.trigger("rising"), .Pre_Clr_Positions("LEGACY"), .NegatePresetClear("false"), .enable("true"), .NewFFLayout("false")) u_IR2 (
    .clk(CLK), .D(and_5_out), .Q(IR2_num));  // open: Qn, preset, en, reset
  D_Flip_Flop #(.trigger("rising"), .Pre_Clr_Positions("LEGACY"), .NegatePresetClear("false"), .enable("true"), .NewFFLayout("false")) u_IR3 (
    .clk(CLK), .D(and_6_out), .Q(IR3_num));  // open: Qn, preset, en, reset
  // Probe on \总周期数 
  // Probe on \无条件分支数 
  // Probe on \条件分支成功数 
  // Probe on \插入气泡数 
  // Probe on \LoadUse次数 
  ROM #(.addrWidth(10), .dataWidth(32), .Select("high")) rom_1 (.addr(IF_PC[11:2]), .data(IR));
  or or_8 (or_8_out, ERET, RST, brench_hazard, IRready);
  IF_ID if_id_1 (
    .IR(IR), .PC(IF_PC), .IR_2(if_id_1_ir_2), .PC_2(ID_PC), .\清零 (or_8_out), .CLK(CLK),
    .\使能_低电平有效 (or_9_out), .BHT({bht_1_bhtresult, bht_1_change, bht_1_miss[0]}), .BHT_2(if_id_1_bht_2));
  or or_9 (or_9_out, stall, LoadUse);
  // Probe on ID_PC[11:0]
  // Probe on IF_PC[11:0]
  Demultiplexer #(.select(2), .width(1), .tristate("false"), .disabled("Z"), .enable("false")) demultiplexer_1 (
    .out1(IE), .out2(EPC), .out3(INM), .in(MTC0), .sel(J_PC[14:13]));  // open: out0
  and and_7 (and_7_out, IR1_num, d_ff_4_qn);
  D_Flip_Flop #(.trigger("rising"), .Pre_Clr_Positions("LEGACY"), .NegatePresetClear("false"), .enable("true"), .NewFFLayout("false")) d_ff_4 (
    .clk(CLK), .D(IR_DA[0]), .Q(INM1), .Qn(d_ff_4_qn), .en(INM));  // open: preset, reset
  // Probe on M_PC[11:0]
  // Probe on EX_PC[11:0]
  \单周期硬布线控制器  \u_单周期硬布线控制器_1  (
    .OP(if_id_1_ir_2[31:26]), .Func(if_id_1_ir_2[5:0]), .MF(if_id_1_ir_2[25:21]),
    .ALU_OP(\单周期硬布线控制器_1_alu_op [3:0]), .MemToReg(\单周期硬布线控制器_1_memtoreg [0]),
    .MemWrite(\单周期硬布线控制器_1_memwrite [0]), .ALU_SRC(\单周期硬布线控制器_1_alu_op [4]),
    .RegWrite(\单周期硬布线控制器_1_memtoreg [1]), .SysCALL(\单周期硬布线控制器_1_memtoreg [2]), .SignedExt(signedext),
    .RegDst(\单周期硬布线控制器_1_memtoreg [3]), .Beq(\单周期硬布线控制器_1_alu_op [5]), .Bne(\单周期硬布线控制器_1_alu_op [6]),
    .JR(\单周期硬布线控制器_1_alu_op [7]), .JMP(\单周期硬布线控制器_1_alu_op [8]), .JAL(\单周期硬布线控制器_1_memtoreg [4]),
    .MFC0(\单周期硬布线控制器_1_mfc0 [0]), .MTC0(\单周期硬布线控制器_1_mfc0 [1]), .ERET(\单周期硬布线控制器_1_mfc0 [2]),
    .BLEZ(\单周期硬布线控制器_1_alu_op [9]), .LHU(\单周期硬布线控制器_1_memwrite [1]), .R1_used(R1_U), .R2_used(R2_U));
  // Probe on WB_PC[11:0]
  Multiplexer #(.select(1), .width(5), .disabled("Z"), .enable("false")) multiplexer_6 (
    .in0(if_id_1_ir_2[25:21]), .in1(5'b00010), .out(R1_num), .sel(\单周期硬布线控制器_1_memtoreg [2]));
  Multiplexer #(.select(1), .width(5), .disabled("Z"), .enable("false")) multiplexer_7 (
    .in0(if_id_1_ir_2[20:16]), .in1(5'b00100), .out(R2_num), .sel(\单周期硬布线控制器_1_memtoreg [2]));
  or or_10 (or_10_out, MFC0, RegWrite);
  MIPS_Regifile mips_regifile_1 (
    .Din(RDin), .Clk(CLK), .R1(mips_regifile_1_r1), .R2(mips_regifile_1_r2), .WE(or_10_out), .W_num(W_num),
    .R1_num(R1_num), .R2_num(R2_num));
  assign bit_extender_1_out = {{16{1'b0}}, if_id_1_ir_2[15:0]};  // Bit_Extender bit_extender_1
  assign bit_extender_2_out = {{16{if_id_1_ir_2[15]}}, if_id_1_ir_2[15:0]};  // Bit_Extender bit_extender_2
  Multiplexer #(.select(1), .width(1), .disabled("Z"), .enable("false")) multiplexer_8 (
    .in0(rd[0]), .in1(MEM_rd0), .out(multiplexer_8_out), .sel(rd_sel));
  and and_8 (and_8_out, IR2_num, d_ff_5_qn);
  D_Flip_Flop #(.trigger("rising"), .Pre_Clr_Positions("LEGACY"), .NegatePresetClear("false"), .enable("true"), .NewFFLayout("false")) d_ff_5 (
    .clk(CLK), .D(IR_DA[1]), .Q(INM2), .Qn(d_ff_5_qn), .en(INM));  // open: preset, reset
  Multiplexer #(.select(1), .width(32), .disabled("Z"), .enable("false")) multiplexer_9 (
    .in0(bit_extender_1_out), .in1(bit_extender_2_out), .out(multiplexer_9_out), .sel(signedext));
  Multiplexer #(.select(1), .width(32), .disabled("Z"), .enable("false")) multiplexer_10 (
    .in0(EPC_DA), .in1({{29{1'b0}}, INM3, INM2, INM1}), .out(MFC0_DA), .sel(multiplexer_8_out));
  Multiplexer #(.select(1), .width(2), .disabled("Z"), .enable("false")) multiplexer_11 (
    .in0(\预测更新_1_new ), .in1(multiplexer_13_out), .out(\new ), .sel(id_ex_1_bht_2[0]));
  or or_11 (or_11_out, ERET, RST, LoadUse, brench_hazard, IRready);
  ID_EX id_ex_1 (
    .WB(\单周期硬布线控制器_1_memtoreg ), .MEM(\单周期硬布线控制器_1_memwrite ), .EX(\单周期硬布线控制器_1_alu_op ), .IR(if_id_1_ir_2),
    .PC(ID_PC), .A(mips_regifile_1_r1), .B(mips_regifile_1_r2), .IMM(multiplexer_9_out),
    .WB_2({id_ex_1_wb_2, EX_M2R}), .MEM_2(id_ex_1_mem_2),
    .EX_2({id_ex_1_ex_2[9], JMP, JR, id_ex_1_ex_2[6:0]}), .IR_2({id_ex_1_ir_2, J_PC}), .PC_2(EX_PC),
    .A_2(id_ex_1_a_2), .B_2(id_ex_1_b_2), .IMM_2(id_ex_1_imm_2), .\清零 (or_11_out), .CLK(CLK),
    .\使能_低电平有效 (stall), .A_EX_hazard({hazard, B_EX_hazard, A_EX_hazard}),
    .A_EX_hazard_2(id_ex_1_a_ex_hazard_2), .MF(\单周期硬布线控制器_1_mfc0 ),
    .MF_2({id_ex_1_mf_2[2], MTC0, id_ex_1_mf_2[0]}), .B_MFC0_hazard(MFC0_hazard), .B_MFC0_hazard_2(rd_sel),
    .BHT(if_id_1_bht_2), .BHT_2({id_ex_1_bht_2_2, replace[2:0], id_ex_1_bht_2[0]}));
  and and_9 (and_9_out, IR3_num, d_ff_6_qn);
  D_Flip_Flop #(.trigger("rising"), .Pre_Clr_Positions("LEGACY"), .NegatePresetClear("false"), .enable("true"), .NewFFLayout("false")) d_ff_6 (
    .clk(CLK), .D(IR_DA[2]), .Q(INM3), .Qn(d_ff_6_qn), .en(INM));  // open: preset, reset
  Multiplexer #(.select(1), .width(2), .disabled("Z"), .enable("false")) multiplexer_12 (
    .in0(2'b10), .in1(2'b10), .out(multiplexer_12_out), .sel(and_10_out));
  Multiplexer #(.select(1), .width(2), .disabled("Z"), .enable("false")) multiplexer_13 (
    .in0(multiplexer_12_out), .in1(2'b10), .out(multiplexer_13_out), .sel(J_TYPE));
  \预测更新  \u_预测更新_1  (.B_result(not_2_out), .History(id_ex_1_bht_2_2), .New(\预测更新_1_new ));
  Adder #(.width(32)) adder_2 (.a(EX_PC), .b(32'h4), .out(Y_PC));  // open: cin, cout
  Multiplexer #(.select(2), .width(32), .disabled("Z"), .enable("false")) multiplexer_14 (
    .in0(32'hc), .in1(32'hf8), .in2(32'h164), .out(IR_PC), .sel(priority_encoder_1_out));  // open: in3
  Decoder #(.select(2), .tristate("false"), .disabled("Z"), .enable("false")) decoder_1 (
    .out0(decoder_1_out0), .out1(decoder_1_out1), .out2(decoder_1_out2), .sel(priority_encoder_1_out));  // open: out3
  Priority_Encoder #(.select(2), .disabled("Z")) priority_encoder_1 (
    .in0(and_7_out), .in1(and_8_out), .in2(and_9_out), .in3(1'b0), .out(priority_encoder_1_out),
    .gs(priority_encoder_1_gs));  // open: en_out, en_in
  not not_1 (not_1_out, IR_DA[0]);
  and and_10 (and_10_out, B_JMP, B_TYPE);
  xor xor_1 (fail_t, or_14_out, id_ex_1_bht_2_2[1]);
  not not_2 (not_2_out, fail_t);
  or or_12 (replace[3], J_TYPE, B_TYPE);
  B_J_TYPE b_j_type_1 (.OP5_1(id_ex_1_ir_2[31:27]), .B_TYPE(B_TYPE), .J_TYPE(J_TYPE));
  and and_11 (IR1_over, decoder_1_out0, ERET);
  and and_12 (IR2_over, decoder_1_out1, ERET);
  and and_13 (IR3_over, decoder_1_out2, ERET);
  and and_14 (IR_star, priority_encoder_1_gs, IE_q);
  Multiplexer #(.select(1), .width(1), .disabled("Z"), .enable("false")) multiplexer_15 (
    .in0(1'b0), .in1(not_1_out), .out(multiplexer_15_out), .sel(IE));
  or or_13 (or_13_out, ERET, IE, IRready);
  or or_14 (or_14_out, B_JMP, and_15_out);
  Multiplexer #(.select(1), .width(32), .disabled("Z"), .enable("false")) multiplexer_16 (
    .in0({EX_PC[31:28], J_PC, 2'b00}), .in1(B_PC), .out(AIM_PC), .sel(B_TYPE));
  \数据重定向  \u_数据重定向_1  (
    .hazard(id_ex_1_a_ex_hazard_2), .A(id_ex_1_a_2), .MEM_ALU(MEM_ALU), .WB_ALU(WB_ALU), .WB_MD(WB_MD),
    .B(id_ex_1_b_2), .MFC0_DA(MFC0_DA), .A_2(JR_PC), .WB_M2R(WB_M2R), .MEM_M2R(MEM_M2R), .B_2(IR_DA),
    .MFC0_hazard(rd_sel));
  D_Flip_Flop #(.trigger("rising"), .Pre_Clr_Positions("LEGACY"), .NegatePresetClear("false"), .enable("true"), .NewFFLayout("false")) u_IE (
    .clk(CLK), .D(multiplexer_15_out), .Q(IE_q), .preset(ERET), .en(or_13_out));  // open: Qn, reset
  Multiplexer #(.select(1), .width(32), .disabled("Z"), .enable("false")) multiplexer_17 (
    .in0(Y_PC), .in1({EX_PC[31:28], J_PC, 2'b00}), .out(multiplexer_17_out), .sel(J_TYPE));
  and and_15 (and_15_out, JMP, ~JR);  // AND_Gate
  Comparator #(.width(32), .mode("twosComplement")) comparator_2 (
    .a(JR_PC), .b({32{1'b0}}), .gt(comparator_2_gt));  // open: eq, lt
  Multiplexer #(.select(1), .width(32), .disabled("Z"), .enable("false")) multiplexer_18 (
    .in0(M_PC), .in1(IR_DA), .out(multiplexer_18_out), .sel(EPC));
  or or_15 (or_15_out, EPC, and_16_out);
  and and_16 (and_16_out, IRready, ~ERET);  // AND_Gate
  Multiplexer #(.select(1), .width(32), .disabled("Z"), .enable("false")) multiplexer_19 (
    .in0(multiplexer_17_out), .in1(B_PC), .out(RIGHT_PC), .sel(B_JMP));
  Multiplexer #(.select(1), .width(32), .disabled("Z"), .enable("false")) multiplexer_20 (
    .in0(IR_DA), .in1(id_ex_1_imm_2), .out(multiplexer_20_out), .sel(id_ex_1_ex_2[4]));
  Register #(.width(32), .trigger("rising"), .Select("low")) register_1 (
    .D(multiplexer_18_out), .en(or_15_out), .Q(EPC_DA), .clk(CLK));  // open: clr
  and and_17 (and_17_out, ~comparator_2_gt, id_ex_1_ex_2[9]);  // AND_Gate
  and and_18 (and_18_out, id_ex_1_ex_2[5], mips_alu_1_equal);
  and and_19 (and_19_out, id_ex_1_ex_2[6], ~mips_alu_1_equal);  // AND_Gate
  MIPS_ALU mips_alu_1 (
    .X(JR_PC), .Y(multiplexer_20_out), .AluOP(id_ex_1_ex_2[3:0]), .Equal(mips_alu_1_equal),
    .Result(mips_alu_1_result), .shamt(J_PC[12:8]));  // open: Result_2
  Shifter #(.width(32), .shift("ll")) shifter_1 (.in(id_ex_1_imm_2), .\dist (5'b00010), .out(shifter_1_out));
  or or_16 (B_JMP, and_17_out, and_18_out, and_19_out);
  Adder #(.width(32)) adder_3 (.a(shifter_1_out), .b(Y_PC), .out(B_PC));  // open: cin, cout
  or or_17 (data_hazard, A_EX_hazard, B_EX_hazard, hazard[3], hazard[2]);
  \数据相关检测  \u_数据相关检测_1  (
    .EX_JAL(id_ex_1_wb_2[4]), .R1_used(R1_U), .EX_rt_num(J_PC[22:18]), .EX_rd_num(J_PC[17:13]),
    .MEM_rt_num(ex_mem_1_ir_2_3), .MEM_rd_num({ex_mem_1_ir_2_2, MEM_rd0}), .MEM_JAL(ex_mem_1_wb_2[4]),
    .R2_used(R2_U), .EX_RegDst(id_ex_1_wb_2[3]), .EX_RegWrite(id_ex_1_wb_2[1]), .A_EX_hazard(A_EX_hazard),
    .A_MEM_hazard(hazard[2]), .MEM_RegDst(ex_mem_1_wb_2[3]), .MEM_RegWrite(ex_mem_1_wb_2[1]),
    .R1_num(R1_num), .R2_num(R2_num), .B_EX_hazard(B_EX_hazard), .B_MEM_hazard(hazard[3]),
    .EX_MFC0(id_ex_1_mf_2[0]), .MFC0_hazard(MFC0_hazard));
  or or_18 (or_18_out, IRready, RST, ERET);
  EX_MEM ex_mem_1 (
    .WB({id_ex_1_wb_2, EX_M2R}), .MEM(id_ex_1_mem_2), .IR({id_ex_1_ir_2, J_PC}), .PC(EX_PC), .B(IR_DA),
    .ALU(mips_alu_1_result), .WB_2({ex_mem_1_wb_2, MEM_M2R}), .MEM_2({ex_mem_1_mem_2[1], MemWrite}),
    .IR_2({ex_mem_1_ir_2[31:21], ex_mem_1_ir_2_3, ex_mem_1_ir_2_2, MEM_rd0, ex_mem_1_ir_2[10:0]}),
    .PC_2(M_PC), .B_2(MDin), .ALU_2(MEM_ALU), .\清零 (or_18_out), .CLK(CLK), .\使能_低电平有效 (stall), .V0(JR_PC),
    .V0_2(ex_mem_1_v0_2), .a0(IR_DA), .a0_2(ex_mem_1_a0_2), .MFC0({id_ex_1_mf_2[2], id_ex_1_mf_2[0]}),
    .MEC0(ex_mem_1_mec0));
  RAM #(.addrWidth(10), .dataWidth(32), .bus("separate"), .Select("high")) ram_1 (
    .addr(MEM_ALU[11:2]), .din(MDin), .data(ram_1_data), .str(MemWrite), .clk(CLK));  // open: sel, ld, clr
  Counter #(.width(16), .max('hffff), .ongoal("stay"), .trigger("rising"), .behavior("old")) counter_1 (
    .count(run), .Q(\总周期数 ), .clk(CLK));  // open: load, D, carry, clr, preset
  BitSelector #(.width(32), .group(16)) bitselector_1 (.in(ram_1_data), .out(bitselector_1_out));  // open: sel
  or or_19 (or_19_out, IRready, RST, ERET);
  Multiplexer #(.select(1), .width(32), .disabled("Z"), .enable("false")) multiplexer_21 (
    .in0(ram_1_data), .in1(bit_extender_3_out), .out(multiplexer_21_out), .sel(ex_mem_1_mem_2[1]));
  assign bit_extender_3_out = {{16{1'b0}}, bitselector_1_out};  // Bit_Extender bit_extender_3
  Counter #(.width(16), .max('hffff), .ongoal("stay"), .trigger("rising"), .behavior("old")) counter_2 (
    .count(B_JMP), .Q(\条件分支成功数 ), .clk(CLK));  // open: load, D, carry, clr, preset
  Counter #(.width(16), .max('hffff), .ongoal("stay"), .trigger("rising"), .behavior("old")) counter_3 (
    .count(JMP), .Q(\无条件分支数 ), .clk(CLK));  // open: load, D, carry, clr, preset
  MEM_WB mem_wb_1 (
    .WB({ex_mem_1_wb_2, MEM_M2R}),
    .IR({ex_mem_1_ir_2[31:21], ex_mem_1_ir_2_3, ex_mem_1_ir_2_2, MEM_rd0, ex_mem_1_ir_2[10:0]}), .PC(M_PC),
    .ALU(MEM_ALU), .MD(multiplexer_21_out), .WB_2({JAL, RegDst, Syscall, RegWrite, WB_M2R}),
    .IR_2({mem_wb_1_ir_2[31:16], rd, mem_wb_1_ir_2[10:0]}), .PC_2(WB_PC), .ALU_2(WB_ALU), .MD_2(WB_MD),
    .\清零 (or_19_out), .CLK(CLK), .\使能_低电平有效 (stall), .v0(ex_mem_1_v0_2), .v0_2(v0), .a0(ex_mem_1_a0_2),
    .a0_2(a0), .MFC0(ex_mem_1_mec0), .MFC0_2({ERET, MFC0}));
  Comparator #(.width(32), .mode("twosComplement")) comparator_3 (
    .a({32{1'b0}}),
    .b({ex_mem_1_ir_2[31:21], ex_mem_1_ir_2_3, ex_mem_1_ir_2_2, MEM_rd0, ex_mem_1_ir_2[10:0]}),
    .eq(comparator_3_eq));  // open: gt, lt
  Multiplexer #(.select(2), .width(5), .disabled("Z"), .enable("false")) multiplexer_22 (
    .in0(mem_wb_1_ir_2[20:16]), .in1(rd), .in2({5{1'b1}}), .in3({5{1'b1}}), .out(W_num), .sel({JAL, RegDst}));
  Adder #(.width(32)) adder_4 (.a(WB_PC), .b(32'h4), .out(adder_4_out));  // open: cin, cout
  not not_3 (not_3_out, comparator_3_eq);
  Multiplexer #(.select(2), .width(32), .disabled("Z"), .enable("false")) multiplexer_23 (
    .in0(WB_ALU), .in1(WB_MD), .in2(adder_4_out), .in3(adder_4_out), .out(multiplexer_23_out),
    .sel({JAL, WB_M2R}));
  or or_20 (or_20_out, A_EX_hazard, B_EX_hazard);
  and and_20 (IRready, IR_star, not_3_out);
  and and_21 (LoadUse, or_20_out, EX_M2R);
  Multiplexer #(.select(1), .width(32), .disabled("Z"), .enable("false")) multiplexer_24 (
    .in0(multiplexer_23_out), .in1(MFC0_DA), .out(RDin), .sel(MFC0));
  Counter #(.width(16), .max('hffff), .ongoal("stay"), .trigger("rising"), .behavior("old")) counter_4 (
    .count(LoadUse), .Q(\LoadUse次数 ), .clk(CLK));  // open: load, D, carry, clr, preset
  Comparator #(.width(32), .mode("twosComplement")) comparator_4 (
    .a(v0), .b(32'h22), .eq(comparator_4_eq));  // open: gt, lt
  or or_21 (run, ~Syscall, multiplexer_25_out, Go);  // OR_Gate
  Multiplexer #(.select(1), .width(1), .disabled("Z"), .enable("false")) multiplexer_25 (
    .in0(1'b0), .in1(comparator_4_eq), .out(multiplexer_25_out), .sel(Syscall));
  not not_4 (stall, run);
  Register #(.width(32), .trigger("rising"), .Select("low")) register_2 (
    .D(a0), .en(multiplexer_25_out), .Q(LedData), .clk(CLK));  // open: clr
  Adder #(.width(16)) adder_5 (.a(N2), .b(N1), .out(\插入气泡数 ));  // open: cin, cout
  Counter #(.width(16), .max('hffff), .ongoal("stay"), .trigger("rising"), .behavior("old")) counter_5 (
    .count(brench_hazard), .Q(N2), .clk(CLK));  // open: load, D, carry, clr, preset
  Counter #(.width(16), .max('hffff), .ongoal("stay"), .trigger("rising"), .behavior("old")) counter_6 (
    .count(brench_hazard), .Q(N1), .clk(CLK));  // open: load, D, carry, clr, preset

  // Other names for the same wires on the sheet: hazard[1:0] = {B_EX_hazard, A_EX_hazard}; rd_mtc0[4:0] = J_PC[17:13];
  //   J_PC[31:28] = EX_PC[31:28]; MEM_PC[31:0] = M_PC; PC[31:0] = M_PC

  // Notes on the sheet:
  //   中断源
  //   中断等待指示
  //   总复位信号应将除ROM以外所有存储组件全部清零
  //   数码管输出
  //   数码管输出应该用寄存器锁存，否则显示数据只能一闪而过
  //   Reset 
  //   Reset 
  //   Reset 
  //   指令存储器
  //   contents of rom_1 (hex, n*v repeats v):
  //   20110001 8000c05 20110001 20120002 20130003 8000c09 20110001 20120002 20130003 8000c0d 20110001
  //   20120002 20130003 8000c11 20110001 20120002 20130003 c000cb8 20100001 20110001 118fc0 112020
  //   20020022 c 118882 12200001 8000c15 112020 20020022 c 20110001 118880 112020 20020022 c 12200001
  //   8000c1f 20110001 118fc0 112020 20020022 c 1188c3 112020 20020022 c 118903 112020 20020022 c 118903
  //   112020 20020022 c 118903 112020 20020022 c 118903 112020 20020022 c 118903 112020 20020022 c 118903
  //   112020 20020022 c 118903 112020 20020022 c 20100001 109fc0 139fc3 8021 2012000c 24160003 26100001
  //   3210000f 20080008 20090001 139900 2709825 132020 20020022 c 1094022 1500fff9 22100001 2018000f
  //   2188024 108700 20080008 20090001 139902 2709825 132021 20020022 c 1094022 1500fff9 108702 2c9b022
  //   12c00001 8000c50 4020 1084027 84400 3508ffff 82021 20020022 c 2010ffff 20110000 ae300000 22100001
  //   22310004 ae300000 22100001 22310004 ae300000 22100001 22310004 ae300000 22100001 22310004 ae300000
  //   22100001 22310004 ae300000 22100001 22310004 ae300000 22100001 22310004 ae300000 22100001 22310004
  //   ae300000 22100001 22310004 ae300000 22100001 22310004 ae300000 22100001 22310004 ae300000 22100001
  //   22310004 ae300000 22100001 22310004 ae300000 22100001 22310004 ae300000 22100001 22310004 ae300000
  //   22100001 22310004 22100001 8020 2011003c 8e130000 8e340000 274402a 11000002 ae330000 ae140000
  //   2231fffc 1611fff8 102020 20020022 c 22100004 2011003c 1611fff2 20020032 c 20100000 22100001 102020
  //   20020022 c 22100002 102020 20020022 c 22100003 102020 20020022 c 22100004 102020 20020022 c 22100005
  //   102020 20020022 c 22100006 102020 20020022 c 22100007 102020 20020022 c 22100008 102020 20020022
  //   20020022 c 3e00008
  //   OP
  //   Func
  //   MF
  //   rs
  //   rt
  //   AluOP
  //   MemToReg
  //   MemWrite
  //   AluSrcB
  //   RegWrite
  //   Syscall
  //   Signedext
  //   RegDst
  //   BEQ
  //   BNE
  //   JR
  //   JMP
  //   JAL
  //   MFC0
  //   MTC0
  //   ERET
  //   LHU
  //   BLEZ
  //   流水调试日志用
  //   中断屏蔽寄存器
  //   中断向量
  //   为方便自动评测，需要输出流水线各段保存的PC值，注意是PC不是PC+4，另外ID段寄存器写入信息，Mem段内存写入信息也要输出
endmodule

module IF_ID (
  input  [5:0] BHT,
  input  [31:0] IR,
  input  [31:0] PC,
  input  \清零 ,
  input  CLK,
  input  \使能_低电平有效 ,
  output [5:0] BHT_2,
  output [31:0] IR_2,
  output [31:0] PC_2
);

  wire not_1_out;
  wire [5:0] multiplexer_1_out;
  wire [31:0] multiplexer_2_out, multiplexer_3_out;

  Multiplexer #(.select(1), .width(6), .disabled("Z"), .enable("false")) multiplexer_1 (
    .in0(BHT), .in1({6{1'b0}}), .out(multiplexer_1_out), .sel(\清零 ));
  Multiplexer #(.select(1), .width(32), .disabled("Z"), .enable("false")) multiplexer_2 (
    .in0(IR), .in1({32{1'b0}}), .out(multiplexer_2_out), .sel(\清零 ));
  Multiplexer #(.select(1), .width(32), .disabled("Z"), .enable("false")) multiplexer_3 (
    .in0(PC), .in1({32{1'b0}}), .out(multiplexer_3_out), .sel(\清零 ));
  not not_1 (not_1_out, \使能_低电平有效 );
  Register #(.width(6), .trigger("rising"), .Select("low")) register_1 (
    .D(multiplexer_1_out), .en(not_1_out), .Q(BHT_2), .clk(CLK));  // open: clr
  Register #(.width(32), .trigger("rising"), .Select("low")) register_2 (
    .D(multiplexer_2_out), .en(not_1_out), .Q(IR_2), .clk(CLK));  // open: clr
  Register #(.width(32), .trigger("rising"), .Select("low")) register_3 (
    .D(multiplexer_3_out), .en(not_1_out), .Q(PC_2), .clk(CLK));  // open: clr
endmodule

module ID_EX (
  input  [5:0] BHT,
  input  B_MFC0_hazard,
  input  [2:0] MF,
  input  [3:0] A_EX_hazard,
  input  [4:0] WB,
  input  [1:0] MEM,
  input  [9:0] EX,
  input  [31:0] IR,
  input  [31:0] PC,
  input  [31:0] A,
  input  [31:0] B,
  input  [31:0] IMM,
  input  \清零 ,
  input  CLK,
  input  \使能_低电平有效 ,
  output [5:0] BHT_2,
  output B_MFC0_hazard_2,
  output [2:0] MF_2,
  output [3:0] A_EX_hazard_2,
  output [4:0] WB_2,
  output [1:0] MEM_2,
  output [9:0] EX_2,
  output [31:0] IR_2,
  output [31:0] PC_2,
  output [31:0] A_2,
  output [31:0] B_2,
  output [31:0] IMM_2
);

  wire multiplexer_2_out, not_1_out;
  wire [1:0] multiplexer_6_out;
  wire [2:0] multiplexer_3_out;
  wire [3:0] multiplexer_4_out;
  wire [4:0] multiplexer_5_out;
  wire [5:0] multiplexer_1_out;
  wire [9:0] multiplexer_7_out;
  wire [31:0] multiplexer_8_out, multiplexer_9_out, multiplexer_10_out, multiplexer_11_out,
       multiplexer_12_out;

  Multiplexer #(.select(1), .width(6), .disabled("Z"), .enable("false")) multiplexer_1 (
    .in0(BHT), .in1({6{1'b0}}), .out(multiplexer_1_out), .sel(\清零 ));
  Multiplexer #(.select(1), .width(1), .disabled("Z"), .enable("false")) multiplexer_2 (
    .in0(B_MFC0_hazard), .in1(1'b0), .out(multiplexer_2_out), .sel(\清零 ));
  Multiplexer #(.select(1), .width(3), .disabled("Z"), .enable("false")) multiplexer_3 (
    .in0(MF), .in1(3'b000), .out(multiplexer_3_out), .sel(\清零 ));
  Multiplexer #(.select(1), .width(4), .disabled("Z"), .enable("false")) multiplexer_4 (
    .in0(A_EX_hazard), .in1(4'b0000), .out(multiplexer_4_out), .sel(\清零 ));
  Multiplexer #(.select(1), .width(5), .disabled("Z"), .enable("false")) multiplexer_5 (
    .in0(WB), .in1({5{1'b0}}), .out(multiplexer_5_out), .sel(\清零 ));
  Multiplexer #(.select(1), .width(2), .disabled("Z"), .enable("false")) multiplexer_6 (
    .in0(MEM), .in1(2'b00), .out(multiplexer_6_out), .sel(\清零 ));
  Multiplexer #(.select(1), .width(10), .disabled("Z"), .enable("false")) multiplexer_7 (
    .in0(EX), .in1({10{1'b0}}), .out(multiplexer_7_out), .sel(\清零 ));
  Multiplexer #(.select(1), .width(32), .disabled("Z"), .enable("false")) multiplexer_8 (
    .in0(IR), .in1({32{1'b0}}), .out(multiplexer_8_out), .sel(\清零 ));
  Multiplexer #(.select(1), .width(32), .disabled("Z"), .enable("false")) multiplexer_9 (
    .in0(PC), .in1({32{1'b0}}), .out(multiplexer_9_out), .sel(\清零 ));
  Multiplexer #(.select(1), .width(32), .disabled("Z"), .enable("false")) multiplexer_10 (
    .in0(A), .in1({32{1'b0}}), .out(multiplexer_10_out), .sel(\清零 ));
  Multiplexer #(.select(1), .width(32), .disabled("Z"), .enable("false")) multiplexer_11 (
    .in0(B), .in1({32{1'b0}}), .out(multiplexer_11_out), .sel(\清零 ));
  Multiplexer #(.select(1), .width(32), .disabled("Z"), .enable("false")) multiplexer_12 (
    .in0(IMM), .in1({32{1'b0}}), .out(multiplexer_12_out), .sel(\清零 ));
  not not_1 (not_1_out, \使能_低电平有效 );
  Register #(.width(6), .trigger("rising"), .Select("low")) register_1 (
    .D(multiplexer_1_out), .en(not_1_out), .Q(BHT_2), .clk(CLK));  // open: clr
  Register #(.width(1), .trigger("rising"), .Select("low")) register_2 (
    .D(multiplexer_2_out), .en(not_1_out), .Q(B_MFC0_hazard_2), .clk(CLK));  // open: clr
  Register #(.width(3), .trigger("rising"), .Select("low")) register_3 (
    .D(multiplexer_3_out), .en(not_1_out), .Q(MF_2), .clk(CLK));  // open: clr
  Register #(.width(4), .trigger("rising"), .Select("low")) register_4 (
    .D(multiplexer_4_out), .en(not_1_out), .Q(A_EX_hazard_2), .clk(CLK));  // open: clr
  Register #(.width(5), .trigger("rising"), .Select("low")) register_5 (
    .D(multiplexer_5_out), .en(not_1_out), .Q(WB_2), .clk(CLK));  // open: clr
  Register #(.width(2), .trigger("rising"), .Select("low")) register_6 (
    .D(multiplexer_6_out), .en(not_1_out), .Q(MEM_2), .clk(CLK));  // open: clr
  Register #(.width(10), .trigger("rising"), .Select("low")) register_7 (
    .D(multiplexer_7_out), .en(not_1_out), .Q(EX_2), .clk(CLK));  // open: clr
  Register #(.width(32), .trigger("rising"), .Select("low")) register_8 (
    .D(multiplexer_8_out), .en(not_1_out), .Q(IR_2), .clk(CLK));  // open: clr
  Register #(.width(32), .trigger("rising"), .Select("low")) register_9 (
    .D(multiplexer_9_out), .en(not_1_out), .Q(PC_2), .clk(CLK));  // open: clr
  Register #(.width(32), .trigger("rising"), .Select("low")) register_10 (
    .D(multiplexer_10_out), .en(not_1_out), .Q(A_2), .clk(CLK));  // open: clr
  Register #(.width(32), .trigger("rising"), .Select("low")) register_11 (
    .D(multiplexer_11_out), .en(not_1_out), .Q(B_2), .clk(CLK));  // open: clr
  Register #(.width(32), .trigger("rising"), .Select("low")) register_12 (
    .D(multiplexer_12_out), .en(not_1_out), .Q(IMM_2), .clk(CLK));  // open: clr
endmodule

module EX_MEM (
  input  [4:0] WB,
  input  [1:0] MEM,
  input  [1:0] MFC0,
  input  [31:0] IR,
  input  [31:0] PC,
  input  [31:0] B,
  input  [31:0] ALU,
  input  [31:0] V0,
  input  [31:0] a0,
  input  \清零 ,
  input  CLK,
  input  \使能_低电平有效 ,
  output [4:0] WB_2,
  output [1:0] MEM_2,
  output [1:0] MEC0,
  output [31:0] IR_2,
  output [31:0] PC_2,
  output [31:0] B_2,
  output [31:0] ALU_2,
  output [31:0] V0_2,
  output [31:0] a0_2
);

  wire not_1_out;
  wire [1:0] multiplexer_2_out, multiplexer_3_out;
  wire [4:0] multiplexer_1_out;
  wire [31:0] multiplexer_4_out, multiplexer_5_out, multiplexer_6_out, multiplexer_7_out, multiplexer_8_out,
       multiplexer_9_out;

  Multiplexer #(.select(1), .width(5), .disabled("Z"), .enable("false")) multiplexer_1 (
    .in0(WB), .in1({5{1'b0}}), .out(multiplexer_1_out), .sel(\清零 ));
  Multiplexer #(.select(1), .width(2), .disabled("Z"), .enable("false")) multiplexer_2 (
    .in0(MEM), .in1(2'b00), .out(multiplexer_2_out), .sel(\清零 ));
  Multiplexer #(.select(1), .width(2), .disabled("Z"), .enable("false")) multiplexer_3 (
    .in0(MFC0), .in1(2'b00), .out(multiplexer_3_out), .sel(\清零 ));
  Multiplexer #(.select(1), .width(32), .disabled("Z"), .enable("false")) multiplexer_4 (
    .in0(IR), .in1({32{1'b0}}), .out(multiplexer_4_out), .sel(\清零 ));
  Multiplexer #(.select(1), .width(32), .disabled("Z"), .enable("false")) multiplexer_5 (
    .in0(PC), .in1({32{1'b0}}), .out(multiplexer_5_out), .sel(\清零 ));
  Multiplexer #(.select(1), .width(32), .disabled("Z"), .enable("false")) multiplexer_6 (
    .in0(B), .in1({32{1'b0}}), .out(multiplexer_6_out), .sel(\清零 ));
  Multiplexer #(.select(1), .width(32), .disabled("Z"), .enable("false")) multiplexer_7 (
    .in0(ALU), .in1({32{1'b0}}), .out(multiplexer_7_out), .sel(\清零 ));
  Multiplexer #(.select(1), .width(32), .disabled("Z"), .enable("false")) multiplexer_8 (
    .in0(V0), .in1({32{1'b0}}), .out(multiplexer_8_out), .sel(\清零 ));
  Multiplexer #(.select(1), .width(32), .disabled("Z"), .enable("false")) multiplexer_9 (
    .in0(a0), .in1({32{1'b0}}), .out(multiplexer_9_out), .sel(\清零 ));
  not not_1 (not_1_out, \使能_低电平有效 );
  Register #(.width(5), .trigger("rising"), .Select("low")) register_1 (
    .D(multiplexer_1_out), .en(not_1_out), .Q(WB_2), .clk(CLK));  // open: clr
  Register #(.width(2), .trigger("rising"), .Select("low")) register_2 (
    .D(multiplexer_2_out), .en(not_1_out), .Q(MEM_2), .clk(CLK));  // open: clr
  Register #(.width(2), .trigger("rising"), .Select("low")) register_3 (
    .D(multiplexer_3_out), .en(not_1_out), .Q(MEC0), .clk(CLK));  // open: clr
  Register #(.width(32), .trigger("rising"), .Select("low")) register_4 (
    .D(multiplexer_4_out), .en(not_1_out), .Q(IR_2), .clk(CLK));  // open: clr
  Register #(.width(32), .trigger("rising"), .Select("low")) register_5 (
    .D(multiplexer_5_out), .en(not_1_out), .Q(PC_2), .clk(CLK));  // open: clr
  Register #(.width(32), .trigger("rising"), .Select("low")) register_6 (
    .D(multiplexer_6_out), .en(not_1_out), .Q(B_2), .clk(CLK));  // open: clr
  Register #(.width(32), .trigger("rising"), .Select("low")) register_7 (
    .D(multiplexer_7_out), .en(not_1_out), .Q(ALU_2), .clk(CLK));  // open: clr
  Register #(.width(32), .trigger("rising"), .Select("low")) register_8 (
    .D(multiplexer_8_out), .en(not_1_out), .Q(V0_2), .clk(CLK));  // open: clr
  Register #(.width(32), .trigger("rising"), .Select("low")) register_9 (
    .D(multiplexer_9_out), .en(not_1_out), .Q(a0_2), .clk(CLK));  // open: clr
endmodule

module MEM_WB (
  input  [4:0] WB,
  input  [1:0] MFC0,
  input  [31:0] IR,
  input  [31:0] PC,
  input  [31:0] ALU,
  input  [31:0] MD,
  input  [31:0] v0,
  input  [31:0] a0,
  input  \清零 ,
  input  CLK,
  input  \使能_低电平有效 ,
  output [4:0] WB_2,
  output [1:0] MFC0_2,
  output [31:0] IR_2,
  output [31:0] PC_2,
  output [31:0] ALU_2,
  output [31:0] MD_2,
  output [31:0] v0_2,
  output [31:0] a0_2
);

  wire not_1_out;
  wire [1:0] multiplexer_2_out;
  wire [4:0] multiplexer_1_out;
  wire [31:0] multiplexer_3_out, multiplexer_4_out, multiplexer_5_out, multiplexer_6_out, multiplexer_7_out,
       multiplexer_8_out;

  Multiplexer #(.select(1), .width(5), .disabled("Z"), .enable("false")) multiplexer_1 (
    .in0(WB), .in1({5{1'b0}}), .out(multiplexer_1_out), .sel(\清零 ));
  Multiplexer #(.select(1), .width(2), .disabled("Z"), .enable("false")) multiplexer_2 (
    .in0(MFC0), .in1(2'b00), .out(multiplexer_2_out), .sel(\清零 ));
  Multiplexer #(.select(1), .width(32), .disabled("Z"), .enable("false")) multiplexer_3 (
    .in0(IR), .in1({32{1'b0}}), .out(multiplexer_3_out), .sel(\清零 ));
  Multiplexer #(.select(1), .width(32), .disabled("Z"), .enable("false")) multiplexer_4 (
    .in0(PC), .in1({32{1'b0}}), .out(multiplexer_4_out), .sel(\清零 ));
  Multiplexer #(.select(1), .width(32), .disabled("Z"), .enable("false")) multiplexer_5 (
    .in0(ALU), .in1({32{1'b0}}), .out(multiplexer_5_out), .sel(\清零 ));
  Multiplexer #(.select(1), .width(32), .disabled("Z"), .enable("false")) multiplexer_6 (
    .in0(MD), .in1({32{1'b0}}), .out(multiplexer_6_out), .sel(\清零 ));
  Multiplexer #(.select(1), .width(32), .disabled("Z"), .enable("false")) multiplexer_7 (
    .in0(v0), .in1({32{1'b0}}), .out(multiplexer_7_out), .sel(\清零 ));
  Multiplexer #(.select(1), .width(32), .disabled("Z"), .enable("false")) multiplexer_8 (
    .in0(a0), .in1({32{1'b0}}), .out(multiplexer_8_out), .sel(\清零 ));
  not not_1 (not_1_out, \使能_低电平有效 );
  Register #(.width(5), .trigger("rising"), .Select("low")) register_1 (
    .D(multiplexer_1_out), .en(not_1_out), .Q(WB_2), .clk(CLK));  // open: clr
  Register #(.width(2), .trigger("rising"), .Select("low")) register_2 (
    .D(multiplexer_2_out), .en(not_1_out), .Q(MFC0_2), .clk(CLK));  // open: clr
  Register #(.width(32), .trigger("rising"), .Select("low")) register_3 (
    .D(multiplexer_3_out), .en(not_1_out), .Q(IR_2), .clk(CLK));  // open: clr
  Register #(.width(32), .trigger("rising"), .Select("low")) register_4 (
    .D(multiplexer_4_out), .en(not_1_out), .Q(PC_2), .clk(CLK));  // open: clr
  Register #(.width(32), .trigger("rising"), .Select("low")) register_5 (
    .D(multiplexer_5_out), .en(not_1_out), .Q(ALU_2), .clk(CLK));  // open: clr
  Register #(.width(32), .trigger("rising"), .Select("low")) register_6 (
    .D(multiplexer_6_out), .en(not_1_out), .Q(MD_2), .clk(CLK));  // open: clr
  Register #(.width(32), .trigger("rising"), .Select("low")) register_7 (
    .D(multiplexer_7_out), .en(not_1_out), .Q(v0_2), .clk(CLK));  // open: clr
  Register #(.width(32), .trigger("rising"), .Select("low")) register_8 (
    .D(multiplexer_8_out), .en(not_1_out), .Q(a0_2), .clk(CLK));  // open: clr
endmodule

module \寄存器使用情况  (
  input  OP0,
  input  OP1,
  input  OP2,
  input  OP3,
  input  OP4,
  input  OP5,
  input  F0,
  input  F1,
  input  F2,
  input  F3,
  input  F4,
  input  F5,
  output R1_used,
  output R2_used
);

  wire and_1_out, and_2_out, and_3_out, and_4_out, and_5_out, and_6_out, and_7_out, and_8_out, and_9_out,
       and_10_out, and_11_out, and_12_out, and_13_out, and_14_out, and_15_out, and_16_out, and_17_out,
       and_18_out, and_19_out, and_20_out, and_21_out, and_22_out, and_23_out, and_24_out, and_25_out,
       and_26_out, and_27_out, and_28_out, and_29_out, and_30_out, and_31_out, and_32_out, and_33_out,
       and_34_out, and_35_out, and_36_out, and_37_out, and_38_out, and_39_out, and_40_out, not_1_out,
       not_2_out, not_3_out, not_4_out, not_5_out, not_6_out, not_7_out, not_8_out, not_9_out, not_10_out,
       not_11_out, not_12_out, not_13_out, not_14_out, not_15_out, not_16_out, not_17_out, not_18_out,
       not_19_out, not_20_out, not_21_out, not_22_out, not_23_out, not_24_out, not_25_out, not_26_out,
       not_27_out, not_28_out, not_29_out, not_30_out, not_31_out, not_32_out, not_33_out, not_34_out,
       not_35_out, not_36_out, not_37_out, not_38_out, not_39_out, not_40_out, not_41_out, not_42_out,
       not_43_out, not_44_out, not_45_out, not_46_out, not_47_out, not_48_out, not_49_out, not_50_out,
       not_51_out, not_52_out, not_53_out, not_54_out, not_55_out, not_56_out, not_57_out, not_58_out,
       not_59_out, not_60_out, not_61_out, not_62_out, not_63_out, not_64_out, not_65_out, not_66_out,
       not_67_out, not_68_out, not_69_out, not_70_out, not_71_out, not_72_out, not_73_out, not_74_out,
       not_75_out, not_76_out, not_77_out, not_78_out, not_79_out, not_80_out, not_81_out, not_82_out,
       not_83_out, not_84_out, not_85_out, not_86_out, not_87_out, not_88_out, not_89_out, not_90_out,
       not_91_out, not_92_out, not_93_out, not_94_out, not_95_out, not_96_out, not_97_out, not_98_out,
       not_99_out, not_100_out, not_101_out, not_102_out, not_103_out, not_104_out, not_105_out, not_106_out,
       not_107_out, not_108_out, not_109_out, not_110_out, not_111_out, not_112_out, not_113_out,
       not_114_out, not_115_out, not_116_out, not_117_out, not_118_out, not_119_out, not_120_out,
       not_121_out, not_122_out, not_123_out, not_124_out, not_125_out, not_126_out, not_127_out,
       not_128_out, not_129_out, not_130_out, not_131_out, not_132_out, not_133_out, not_134_out,
       not_135_out, not_136_out, not_137_out, not_138_out, not_139_out, not_140_out, not_141_out,
       not_142_out, not_143_out, not_144_out, not_145_out, not_146_out, not_147_out, not_148_out,
       not_149_out, not_150_out, not_151_out, not_152_out, not_153_out, not_154_out, not_155_out,
       not_156_out, not_157_out, not_158_out, not_159_out, not_160_out, not_161_out, not_162_out,
       not_163_out, not_164_out, not_165_out, not_166_out, not_167_out, not_168_out, not_169_out,
       not_170_out, not_171_out, not_172_out, not_173_out, not_174_out, not_175_out, not_176_out,
       not_177_out, not_178_out, not_179_out, not_180_out, not_181_out, not_182_out, not_183_out,
       not_184_out, not_185_out, not_186_out, not_187_out, not_188_out, not_189_out, not_190_out,
       not_191_out, not_192_out, not_193_out, not_194_out, not_195_out, not_196_out, not_197_out,
       not_198_out, not_199_out, not_200_out, not_201_out, not_202_out, not_203_out, not_204_out,
       not_205_out, not_206_out, not_207_out, not_208_out, not_209_out, not_210_out, not_211_out,
       not_212_out, not_213_out, not_214_out, not_215_out, not_216_out, not_217_out, not_218_out,
       not_219_out, not_220_out, not_221_out, not_222_out, not_223_out, not_224_out, not_225_out,
       not_226_out, not_227_out, not_228_out, not_229_out, not_230_out, not_231_out, not_232_out,
       not_233_out, not_234_out, not_235_out, not_236_out, not_237_out, not_238_out, not_239_out,
       not_240_out, not_241_out, not_242_out, not_243_out, not_244_out, not_245_out, not_246_out,
       not_247_out, not_248_out, not_249_out, not_250_out, not_251_out, not_252_out, not_253_out,
       not_254_out, not_255_out, not_256_out, not_257_out, not_258_out, not_259_out, not_260_out,
       not_261_out, not_262_out, not_263_out, not_264_out, not_265_out, not_266_out, not_267_out,
       not_268_out, not_269_out, not_270_out, not_271_out, not_272_out, not_273_out, not_274_out,
       not_275_out, not_276_out, not_277_out, not_278_out, not_279_out, not_280_out, not_281_out,
       not_282_out, not_283_out, not_284_out, not_285_out, not_286_out, not_287_out, not_288_out,
       not_289_out, not_290_out, not_291_out, not_292_out;

  not not_1 (not_1_out, OP5);
  not not_2 (not_2_out, OP4);
  not not_3 (not_3_out, OP3);
  not not_4 (not_4_out, OP2);
  not not_5 (not_5_out, OP1);
  not not_6 (not_6_out, OP0);
  not not_7 (not_7_out, F4);
  not not_8 (not_8_out, F3);
  not not_9 (not_9_out, F2);
  not not_10 (not_10_out, F1);
  not not_11 (not_11_out, F0);
  not not_12 (not_12_out, OP5);
  not not_13 (not_13_out, OP4);
  not not_14 (not_14_out, OP3);
  not not_15 (not_15_out, OP2);
  not not_16 (not_16_out, OP1);
  not not_17 (not_17_out, OP0);
  not not_18 (not_18_out, F4);
  not not_19 (not_19_out, F3);
  not not_20 (not_20_out, F2);
  not not_21 (not_21_out, F1);
  not not_22 (not_22_out, OP5);
  not not_23 (not_23_out, OP4);
  not not_24 (not_24_out, OP3);
  not not_25 (not_25_out, OP2);
  not not_26 (not_26_out, OP1);
  not not_27 (not_27_out, OP0);
  not not_28 (not_28_out, F4);
  not not_29 (not_29_out, F3);
  not not_30 (not_30_out, F2);
  not not_31 (not_31_out, F0);
  not not_32 (not_32_out, OP5);
  not not_33 (not_33_out, OP4);
  not not_34 (not_34_out, OP3);
  not not_35 (not_35_out, OP2);
  not not_36 (not_36_out, OP1);
  not not_37 (not_37_out, OP0);
  not not_38 (not_38_out, F4);
  not not_39 (not_39_out, F3);
  not not_40 (not_40_out, F1);
  not not_41 (not_41_out, F0);
  not not_42 (not_42_out, OP5);
  not not_43 (not_43_out, OP4);
  not not_44 (not_44_out, OP3);
  not not_45 (not_45_out, OP2);
  not not_46 (not_46_out, OP1);
  not not_47 (not_47_out, OP0);
  not not_48 (not_48_out, F4);
  not not_49 (not_49_out, F3);
  not not_50 (not_50_out, F1);
  not not_51 (not_51_out, OP5);
  not not_52 (not_52_out, OP4);
  not not_53 (not_53_out, OP3);
  not not_54 (not_54_out, OP2);
  not not_55 (not_55_out, OP1);
  not not_56 (not_56_out, OP0);
  not not_57 (not_57_out, F4);
  not not_58 (not_58_out, F3);
  not not_59 (not_59_out, OP5);
  not not_60 (not_60_out, OP4);
  not not_61 (not_61_out, OP3);
  not not_62 (not_62_out, OP2);
  not not_63 (not_63_out, OP1);
  not not_64 (not_64_out, OP0);
  not not_65 (not_65_out, F4);
  not not_66 (not_66_out, F2);
  not not_67 (not_67_out, F0);
  not not_68 (not_68_out, OP5);
  not not_69 (not_69_out, OP4);
  not not_70 (not_70_out, OP3);
  not not_71 (not_71_out, OP2);
  not not_72 (not_72_out, OP1);
  not not_73 (not_73_out, OP0);
  not not_74 (not_74_out, F4);
  not not_75 (not_75_out, F2);
  not not_76 (not_76_out, OP5);
  not not_77 (not_77_out, OP4);
  not not_78 (not_78_out, OP3);
  not not_79 (not_79_out, OP2);
  not not_80 (not_80_out, OP1);
  not not_81 (not_81_out, OP0);
  not not_82 (not_82_out, F5);
  not not_83 (not_83_out, F4);
  not not_84 (not_84_out, F2);
  not not_85 (not_85_out, F1);
  not not_86 (not_86_out, F0);
  not not_87 (not_87_out, OP5);
  not not_88 (not_88_out, OP4);
  not not_89 (not_89_out, OP3);
  not not_90 (not_90_out, OP2);
  not not_91 (not_91_out, OP1);
  not not_92 (not_92_out, OP0);
  not not_93 (not_93_out, F5);
  not not_94 (not_94_out, F4);
  not not_95 (not_95_out, F1);
  not not_96 (not_96_out, F0);
  not not_97 (not_97_out, OP5);
  not not_98 (not_98_out, OP4);
  not not_99 (not_99_out, OP3);
  not not_100 (not_100_out, OP1);
  not not_101 (not_101_out, OP0);
  not not_102 (not_102_out, OP5);
  not not_103 (not_103_out, OP4);
  not not_104 (not_104_out, OP3);
  not not_105 (not_105_out, OP1);
  not not_106 (not_106_out, OP5);
  not not_107 (not_107_out, OP4);
  not not_108 (not_108_out, OP2);
  not not_109 (not_109_out, OP1);
  not not_110 (not_110_out, OP0);
  not not_111 (not_111_out, OP5);
  not not_112 (not_112_out, OP4);
  not not_113 (not_113_out, OP1);
  not not_114 (not_114_out, OP0);
  not not_115 (not_115_out, OP5);
  not not_116 (not_116_out, OP4);
  not not_117 (not_117_out, OP2);
  not not_118 (not_118_out, OP1);
  not not_119 (not_119_out, OP5);
  not not_120 (not_120_out, OP4);
  not not_121 (not_121_out, OP2);
  not not_122 (not_122_out, OP0);
  not not_123 (not_123_out, OP5);
  not not_124 (not_124_out, OP4);
  not not_125 (not_125_out, OP1);
  not not_126 (not_126_out, OP4);
  not not_127 (not_127_out, OP3);
  not not_128 (not_128_out, OP2);
  not not_129 (not_129_out, OP4);
  not not_130 (not_130_out, OP2);
  not not_131 (not_131_out, OP5);
  not not_132 (not_132_out, OP4);
  not not_133 (not_133_out, OP3);
  not not_134 (not_134_out, OP2);
  not not_135 (not_135_out, OP1);
  not not_136 (not_136_out, OP0);
  not not_137 (not_137_out, F4);
  not not_138 (not_138_out, F3);
  not not_139 (not_139_out, F2);
  not not_140 (not_140_out, OP5);
  not not_141 (not_141_out, OP4);
  not not_142 (not_142_out, OP2);
  not not_143 (not_143_out, OP4);
  not not_144 (not_144_out, OP3);
  not not_145 (not_145_out, OP1);
  not not_146 (not_146_out, OP5);
  not not_147 (not_147_out, OP4);
  not not_148 (not_148_out, OP3);
  not not_149 (not_149_out, OP0);
  not not_150 (not_150_out, OP5);
  not not_151 (not_151_out, OP4);
  not not_152 (not_152_out, OP3);
  not not_153 (not_153_out, OP2);
  not not_154 (not_154_out, OP1);
  not not_155 (not_155_out, OP0);
  not not_156 (not_156_out, F5);
  not not_157 (not_157_out, F4);
  not not_158 (not_158_out, F3);
  not not_159 (not_159_out, F2);
  not not_160 (not_160_out, F1);
  not not_161 (not_161_out, F0);
  not not_162 (not_162_out, OP5);
  not not_163 (not_163_out, OP4);
  not not_164 (not_164_out, OP3);
  not not_165 (not_165_out, OP2);
  not not_166 (not_166_out, OP1);
  not not_167 (not_167_out, OP0);
  not not_168 (not_168_out, F5);
  not not_169 (not_169_out, F4);
  not not_170 (not_170_out, F3);
  not not_171 (not_171_out, F2);
  not not_172 (not_172_out, OP5);
  not not_173 (not_173_out, OP4);
  not not_174 (not_174_out, OP3);
  not not_175 (not_175_out, OP2);
  not not_176 (not_176_out, OP1);
  not not_177 (not_177_out, OP0);
  not not_178 (not_178_out, F5);
  not not_179 (not_179_out, F4);
  not not_180 (not_180_out, F3);
  not not_181 (not_181_out, F2);
  not not_182 (not_182_out, F0);
  not not_183 (not_183_out, OP5);
  not not_184 (not_184_out, OP4);
  not not_185 (not_185_out, OP3);
  not not_186 (not_186_out, OP2);
  not not_187 (not_187_out, OP1);
  not not_188 (not_188_out, OP0);
  not not_189 (not_189_out, F4);
  not not_190 (not_190_out, F3);
  not not_191 (not_191_out, F2);
  not not_192 (not_192_out, F1);
  not not_193 (not_193_out, F0);
  not not_194 (not_194_out, OP5);
  not not_195 (not_195_out, OP4);
  not not_196 (not_196_out, OP3);
  not not_197 (not_197_out, OP2);
  not not_198 (not_198_out, OP1);
  not not_199 (not_199_out, OP0);
  not not_200 (not_200_out, F4);
  not not_201 (not_201_out, F3);
  not not_202 (not_202_out, F2);
  not not_203 (not_203_out, F1);
  not not_204 (not_204_out, OP5);
  not not_205 (not_205_out, OP4);
  not not_206 (not_206_out, OP3);
  not not_207 (not_207_out, OP2);
  not not_208 (not_208_out, OP1);
  not not_209 (not_209_out, OP0);
  not not_210 (not_210_out, F4);
  not not_211 (not_211_out, F3);
  not not_212 (not_212_out, F2);
  not not_213 (not_213_out, F0);
  not not_214 (not_214_out, OP5);
  not not_215 (not_215_out, OP4);
  not not_216 (not_216_out, OP3);
  not not_217 (not_217_out, OP2);
  not not_218 (not_218_out, OP1);
  not not_219 (not_219_out, OP0);
  not not_220 (not_220_out, F4);
  not not_221 (not_221_out, F3);
  not not_222 (not_222_out, F1);
  not not_223 (not_223_out, F0);
  not not_224 (not_224_out, OP5);
  not not_225 (not_225_out, OP4);
  not not_226 (not_226_out, OP3);
  not not_227 (not_227_out, OP2);
  not not_228 (not_228_out, OP1);
  not not_229 (not_229_out, OP0);
  not not_230 (not_230_out, F4);
  not not_231 (not_231_out, F3);
  not not_232 (not_232_out, F1);
  not not_233 (not_233_out, OP5);
  not not_234 (not_234_out, OP4);
  not not_235 (not_235_out, OP3);
  not not_236 (not_236_out, OP2);
  not not_237 (not_237_out, OP1);
  not not_238 (not_238_out, OP0);
  not not_239 (not_239_out, F4);
  not not_240 (not_240_out, F3);
  not not_241 (not_241_out, OP5);
  not not_242 (not_242_out, OP4);
  not not_243 (not_243_out, OP3);
  not not_244 (not_244_out, OP2);
  not not_245 (not_245_out, OP1);
  not not_246 (not_246_out, OP0);
  not not_247 (not_247_out, F4);
  not not_248 (not_248_out, F2);
  not not_249 (not_249_out, F0);
  not not_250 (not_250_out, OP5);
  not not_251 (not_251_out, OP4);
  not not_252 (not_252_out, OP3);
  not not_253 (not_253_out, OP2);
  not not_254 (not_254_out, OP1);
  not not_255 (not_255_out, OP0);
  not not_256 (not_256_out, F4);
  not not_257 (not_257_out, F2);
  not not_258 (not_258_out, OP5);
  not not_259 (not_259_out, OP4);
  not not_260 (not_260_out, OP3);
  not not_261 (not_261_out, OP2);
  not not_262 (not_262_out, OP1);
  not not_263 (not_263_out, OP0);
  not not_264 (not_264_out, F5);
  not not_265 (not_265_out, F4);
  not not_266 (not_266_out, F1);
  not not_267 (not_267_out, F0);
  not not_268 (not_268_out, OP5);
  not not_269 (not_269_out, OP4);
  not not_270 (not_270_out, OP3);
  not not_271 (not_271_out, OP1);
  not not_272 (not_272_out, OP0);
  not not_273 (not_273_out, OP5);
  not not_274 (not_274_out, OP4);
  not not_275 (not_275_out, OP3);
  not not_276 (not_276_out, OP1);
  not not_277 (not_277_out, OP4);
  not not_278 (not_278_out, OP2);
  not not_279 (not_279_out, OP5);
  not not_280 (not_280_out, OP3);
  not not_281 (not_281_out, OP2);
  not not_282 (not_282_out, OP1);
  not not_283 (not_283_out, OP0);
  not not_284 (not_284_out, OP5);
  not not_285 (not_285_out, OP4);
  not not_286 (not_286_out, OP3);
  not not_287 (not_287_out, OP2);
  not not_288 (not_288_out, OP1);
  not not_289 (not_289_out, OP0);
  not not_290 (not_290_out, F4);
  not not_291 (not_291_out, F3);
  not not_292 (not_292_out, F2);
  and and_1 (and_1_out, not_1_out, not_2_out, not_3_out, not_4_out, not_5_out, not_6_out, F5, not_7_out, not_8_out, not_9_out, not_10_out, not_11_out);
  and and_2 (and_2_out, not_12_out, not_13_out, not_14_out, not_15_out, not_16_out, not_17_out, F5, not_18_out, not_19_out, not_20_out, not_21_out, F0);
  and and_3 (and_3_out, not_22_out, not_23_out, not_24_out, not_25_out, not_26_out, not_27_out, F5, not_28_out, not_29_out, not_30_out, F1, not_31_out);
  and and_4 (and_4_out, not_32_out, not_33_out, not_34_out, not_35_out, not_36_out, not_37_out, F5, not_38_out, not_39_out, F2, not_40_out, not_41_out);
  and and_5 (and_5_out, not_42_out, not_43_out, not_44_out, not_45_out, not_46_out, not_47_out, F5, not_48_out, not_49_out, F2, not_50_out, F0);
  and and_6 (and_6_out, not_51_out, not_52_out, not_53_out, not_54_out, not_55_out, not_56_out, F5, not_57_out, not_58_out, F2, F1, F0);
  and and_7 (and_7_out, not_59_out, not_60_out, not_61_out, not_62_out, not_63_out, not_64_out, F5, not_65_out, F3, not_66_out, F1, not_67_out);
  and and_8 (and_8_out, not_68_out, not_69_out, not_70_out, not_71_out, not_72_out, not_73_out, F5, not_74_out, F3, not_75_out, F1, F0);
  and and_9 (and_9_out, not_76_out, not_77_out, not_78_out, not_79_out, not_80_out, not_81_out, not_82_out, not_83_out, F3, not_84_out, not_85_out, not_86_out);
  and and_10 (and_10_out, not_87_out, not_88_out, not_89_out, not_90_out, not_91_out, not_92_out, not_93_out, not_94_out, F3, F2, not_95_out, not_96_out);
  and and_11 (and_11_out, not_97_out, not_98_out, not_99_out, OP2, not_100_out, not_101_out);
  and and_12 (and_12_out, not_102_out, not_103_out, not_104_out, OP2, not_105_out, OP0);
  and and_13 (and_13_out, not_106_out, not_107_out, OP3, not_108_out, not_109_out, not_110_out);
  and and_14 (and_14_out, not_111_out, not_112_out, OP3, OP2, not_113_out, not_114_out);
  and and_15 (and_15_out, not_115_out, not_116_out, OP3, not_117_out, not_118_out, OP0);
  and and_16 (and_16_out, not_119_out, not_120_out, OP3, not_121_out, OP1, not_122_out);
  and and_17 (and_17_out, not_123_out, not_124_out, OP3, OP2, not_125_out, OP0);
  and and_18 (and_18_out, OP5, not_126_out, not_127_out, not_128_out, OP1, OP0);
  and and_19 (and_19_out, OP5, not_129_out, OP3, not_130_out, OP1, OP0);
  and and_20 (and_20_out, not_131_out, not_132_out, not_133_out, not_134_out, not_135_out, not_136_out, F5, not_137_out, not_138_out, not_139_out, F1, F0);
  and and_21 (and_21_out, not_140_out, not_141_out, OP3, not_142_out, OP1, OP0);
  and and_22 (and_22_out, OP5, not_143_out, not_144_out, OP2, not_145_out, OP0);
  and and_23 (and_23_out, not_146_out, not_147_out, not_148_out, OP2, OP1, not_149_out);
  and and_24 (and_24_out, not_150_out, not_151_out, not_152_out, not_153_out, not_154_out, not_155_out, not_156_out, not_157_out, not_158_out, not_159_out, not_160_out, not_161_out);
  and and_25 (and_25_out, not_162_out, not_163_out, not_164_out, not_165_out, not_166_out, not_167_out, not_168_out, not_169_out, not_170_out, not_171_out, F1, F0);
  and and_26 (and_26_out, not_172_out, not_173_out, not_174_out, not_175_out, not_176_out, not_177_out, not_178_out, not_179_out, not_180_out, not_181_out, F1, not_182_out);
  and and_27 (and_27_out, not_183_out, not_184_out, not_185_out, not_186_out, not_187_out, not_188_out, F5, not_189_out, not_190_out, not_191_out, not_192_out, not_193_out);
  and and_28 (and_28_out, not_194_out, not_195_out, not_196_out, not_197_out, not_198_out, not_199_out, F5, not_200_out, not_201_out, not_202_out, not_203_out, F0);
  and and_29 (and_29_out, not_204_out, not_205_out, not_206_out, not_207_out, not_208_out, not_209_out, F5, not_210_out, not_211_out, not_212_out, F1, not_213_out);
  and and_30 (and_30_out, not_214_out, not_215_out, not_216_out, not_217_out, not_218_out, not_219_out, F5, not_220_out, not_221_out, F2, not_222_out, not_223_out);
  and and_31 (and_31_out, not_224_out, not_225_out, not_226_out, not_227_out, not_228_out, not_229_out, F5, not_230_out, not_231_out, F2, not_232_out, F0);
  and and_32 (and_32_out, not_233_out, not_234_out, not_235_out, not_236_out, not_237_out, not_238_out, F5, not_239_out, not_240_out, F2, F1, F0);
  and and_33 (and_33_out, not_241_out, not_242_out, not_243_out, not_244_out, not_245_out, not_246_out, F5, not_247_out, F3, not_248_out, F1, not_249_out);
  and and_34 (and_34_out, not_250_out, not_251_out, not_252_out, not_253_out, not_254_out, not_255_out, F5, not_256_out, F3, not_257_out, F1, F0);
  and and_35 (and_35_out, not_258_out, not_259_out, not_260_out, not_261_out, not_262_out, not_263_out, not_264_out, not_265_out, F3, F2, not_266_out, not_267_out);
  and and_36 (and_36_out, not_268_out, not_269_out, not_270_out, OP2, not_271_out, not_272_out);
  and and_37 (and_37_out, not_273_out, not_274_out, not_275_out, OP2, not_276_out, OP0);
  and and_38 (and_38_out, OP5, not_277_out, OP3, not_278_out, OP1, OP0);
  and and_39 (and_39_out, not_279_out, OP4, not_280_out, not_281_out, not_282_out, not_283_out);
  and and_40 (and_40_out, not_284_out, not_285_out, not_286_out, not_287_out, not_288_out, not_289_out, F5, not_290_out, not_291_out, not_292_out, F1, F0);
  or or_1 (R1_used, and_1_out, and_2_out, and_3_out, and_4_out, and_5_out, and_6_out, and_7_out, and_8_out, and_9_out, and_10_out, and_11_out, and_12_out, and_13_out, and_14_out, and_15_out, and_16_out, and_17_out, and_18_out, and_19_out, and_20_out, and_21_out, and_22_out, and_23_out);
  or or_2 (R2_used, and_24_out, and_25_out, and_26_out, and_27_out, and_28_out, and_29_out, and_30_out, and_31_out, and_32_out, and_33_out, and_34_out, and_35_out, and_36_out, and_37_out, and_38_out, and_39_out, and_40_out);
endmodule

module \数据相关检测  (
  input  EX_JAL,
  input  EX_RegDst,
  input  [4:0] R1_num,
  input  R1_used,
  input  EX_RegWrite,
  input  [4:0] EX_rt_num,
  input  [4:0] EX_rd_num,
  input  EX_MFC0,
  input  [4:0] MEM_rt_num,
  input  [4:0] MEM_rd_num,
  input  MEM_JAL,
  input  MEM_RegDst,
  input  R2_used,
  input  MEM_RegWrite,
  input  [4:0] R2_num,
  output A_EX_hazard,
  output B_EX_hazard,
  output MFC0_hazard,
  output A_MEM_hazard,
  output B_MEM_hazard
);

  wire comparator_1_eq, comparator_2_eq, comparator_3_eq, comparator_4_eq, comparator_5_eq, comparator_6_eq,
       multiplexer_3_out, multiplexer_4_out, multiplexer_5_out, multiplexer_6_out, multiplexer_8_out;
  wire [4:0] multiplexer_1_out, multiplexer_2_out;

  Multiplexer #(.select(2), .width(5), .disabled("Z"), .enable("false")) multiplexer_1 (
    .in0(EX_rt_num), .in1(EX_rd_num), .in2({5{1'b1}}), .out(multiplexer_1_out), .sel({EX_JAL, EX_RegDst}));  // open: in3
  Multiplexer #(.select(2), .width(5), .disabled("Z"), .enable("false")) multiplexer_2 (
    .in0(MEM_rt_num), .in1(MEM_rd_num), .in2({5{1'b1}}), .out(multiplexer_2_out), .sel({MEM_JAL, MEM_RegDst}));  // open: in3
  Comparator #(.width(5), .mode("twosComplement")) comparator_1 (
    .a(R1_num), .b({5{1'b0}}), .eq(comparator_1_eq));  // open: gt, lt
  Comparator #(.width(5), .mode("twosComplement")) comparator_2 (
    .a(multiplexer_1_out), .b(R1_num), .eq(comparator_2_eq));  // open: gt, lt
  Comparator #(.width(5), .mode("twosComplement")) comparator_3 (
    .a(multiplexer_1_out), .b(R2_num), .eq(comparator_3_eq));  // open: gt, lt
  Comparator #(.width(5), .mode("twosComplement")) comparator_4 (
    .a(multiplexer_2_out), .b(R1_num), .eq(comparator_4_eq));  // open: gt, lt
  Comparator #(.width(5), .mode("twosComplement")) comparator_5 (
    .a(multiplexer_2_out), .b(R2_num), .eq(comparator_5_eq));  // open: gt, lt
  Comparator #(.width(5), .mode("twosComplement")) comparator_6 (
    .a(R2_num), .b({5{1'b0}}), .eq(comparator_6_eq));  // open: gt, lt
  Multiplexer #(.select(1), .width(1), .disabled("Z"), .enable("false")) multiplexer_3 (
    .in0(comparator_2_eq), .in1(1'b0), .out(multiplexer_3_out), .sel(comparator_1_eq));
  Multiplexer #(.select(1), .width(1), .disabled("Z"), .enable("false")) multiplexer_4 (
    .in0(comparator_3_eq), .in1(1'b0), .out(multiplexer_4_out), .sel(comparator_6_eq));
  Multiplexer #(.select(1), .width(1), .disabled("Z"), .enable("false")) multiplexer_5 (
    .in0(comparator_4_eq), .in1(1'b0), .out(multiplexer_5_out), .sel(comparator_1_eq));
  Multiplexer #(.select(1), .width(1), .disabled("Z"), .enable("false")) multiplexer_6 (
    .in0(comparator_5_eq), .in1(1'b0), .out(multiplexer_6_out), .sel(comparator_6_eq));
  Multiplexer #(.select(2), .width(1), .disabled("Z"), .enable("false")) multiplexer_7 (
    .in0(1'b0), .in1(1'b0), .in2(1'b0), .in3(multiplexer_3_out), .out(A_EX_hazard),
    .sel({R1_used, EX_RegWrite}));
  Multiplexer #(.select(2), .width(1), .disabled("Z"), .enable("false")) multiplexer_8 (
    .in0(1'b0), .in1(1'b0), .in2(1'b0), .in3(multiplexer_4_out), .out(multiplexer_8_out),
    .sel({R2_used, EX_RegWrite}));
  Multiplexer #(.select(2), .width(1), .disabled("Z"), .enable("false")) multiplexer_9 (
    .in0(1'b0), .in1(1'b0), .in2(1'b0), .in3(multiplexer_4_out), .out(MFC0_hazard), .sel({R2_used, EX_MFC0}));
  Multiplexer #(.select(2), .width(1), .disabled("Z"), .enable("false")) multiplexer_10 (
    .in0(1'b0), .in1(1'b0), .in2(1'b0), .in3(multiplexer_5_out), .out(A_MEM_hazard),
    .sel({R1_used, MEM_RegWrite}));
  Multiplexer #(.select(2), .width(1), .disabled("Z"), .enable("false")) multiplexer_11 (
    .in0(1'b0), .in1(1'b0), .in2(1'b0), .in3(multiplexer_6_out), .out(B_MEM_hazard),
    .sel({R2_used, MEM_RegWrite}));
  or or_1 (B_EX_hazard, multiplexer_8_out, MFC0_hazard);
endmodule

// 数据重定向
module \数据重定向  (
  input  [3:0] hazard,
  input  [31:0] A,
  input  [31:0] MEM_ALU,
  input  [31:0] WB_ALU,
  input  [31:0] WB_MD,
  input  WB_M2R,
  input  MEM_M2R,
  input  [31:0] B,
  input  [31:0] MFC0_DA,
  input  MFC0_hazard,
  output [31:0] A_2,
  output [31:0] B_2
);

  wire and_3_out, and_4_out, and_5_out, and_6_out;
  wire [1:0] or_1_out, or_2_out;
  wire [31:0] multiplexer_1_out;

  Multiplexer #(.select(1), .width(32), .disabled("Z"), .enable("false")) multiplexer_1 (
    .in0(MEM_ALU), .in1(MFC0_DA), .out(multiplexer_1_out), .sel(MFC0_hazard));
  and and_1 (or_1_out[1], hazard[2], ~hazard[0]);  // AND_Gate
  and and_2 (or_2_out[1], hazard[3], ~hazard[1]);  // AND_Gate
  Multiplexer #(.select(2), .width(32), .disabled("Z"), .enable("false")) multiplexer_2 (
    .in0(A), .in1(MEM_ALU), .in2(WB_ALU), .in3(WB_MD), .out(A_2), .sel(or_1_out));
  or or_1 (or_1_out[0], and_4_out, and_3_out);
  and and_3 (and_3_out, hazard[2], WB_M2R);
  and and_4 (and_4_out, hazard[0], ~MEM_M2R);  // AND_Gate
  Multiplexer #(.select(2), .width(32), .disabled("Z"), .enable("false")) multiplexer_3 (
    .in0(B), .in1(multiplexer_1_out), .in2(WB_ALU), .in3(WB_MD), .out(B_2), .sel(or_2_out));
  or or_2 (or_2_out[0], and_5_out, and_6_out);
  and and_5 (and_5_out, hazard[1], ~MEM_M2R);  // AND_Gate
  and and_6 (and_6_out, hazard[3], WB_M2R);

  // Other names for the same wires on the sheet: A_EX_hazard = hazard[0]; B_EX_hazard = hazard[1];
  //   A_MEM_hazard = hazard[2]; B_MEM_hazard = hazard[3]
endmodule

// BHT
module BHT (
  input  CLK,
  input  [31:0] PC,
  input  [31:0] AIM_PC,
  input  [31:0] IN_PC,
  input  [1:0] \new ,
  input  [3:0] replace,
  output [1:0] BHTresult,
  output [31:0] FOR_PC,
  output miss,
  output [2:0] change
);

  wire and_1_out, and_2_out, and_3_out, and_4_out, and_5_out, and_6_out, and_7_out, and_8_out,
       comparator_1_eq, comparator_2_eq, comparator_3_eq, comparator_4_eq, comparator_5_eq, comparator_6_eq,
       comparator_7_eq, comparator_8_eq, comparator_9_lt, comparator_10_lt, comparator_11_lt,
       comparator_12_lt, comparator_13_lt, comparator_14_lt, comparator_15_lt, hit, hit1, hit2, hit3, hit4,
       hit5, hit6, hit7, hit8, not_1_out, not_2_out, not_3_out, not_4_out, not_5_out, not_6_out, not_8_out,
       or_1_out, or_2_out, or_3_out, or_4_out, or_5_out, or_6_out, or_7_out, or_8_out, V1, V2, V3, V4, V5,
       V6, V7, V8, write1, write2, write3, write4, write5, write6, write7, write8;
  wire [1:0] History, \分支预测历史_2_q , \分支预测历史_3_q , \分支预测历史_4_q , \分支预测历史_5_q , \分支预测历史_6_q , \分支预测历史_7_q ,
       \分支预测历史_8_q , \分支预测历史_q ;
  wire [2:0] multiplexer_3_out, multiplexer_5_out, multiplexer_7_out, multiplexer_9_out, multiplexer_10_out,
       multiplexer_13_out, multiplexer_14_out, priority_encoder_1_out;
  wire [31:0] adder_1_out, C1, C2, C3, C4, C5, C6, C7, C8, FOR_PC_t, multiplexer_2_out, multiplexer_4_out,
       multiplexer_6_out, multiplexer_8_out, multiplexer_11_out, multiplexer_12_out, PC1, PC2, PC3, PC4, PC5,
       PC6, PC7, PC8, \分支目标地址_2_q , \分支目标地址_3_q , \分支目标地址_4_q , \分支目标地址_5_q , \分支目标地址_6_q , \分支目标地址_7_q ,
       \分支目标地址_8_q , \分支目标地址_q ;

  Register #(.width(1), .trigger("rising"), .Select("low")) valid (
    .D(1'b1), .en(write1), .Q(V1), .clk(CLK));  // open: clr
  Register #(.width(1), .trigger("rising"), .Select("low")) valid_2 (
    .D(1'b1), .en(write2), .Q(V2), .clk(CLK));  // open: clr
  Register #(.width(1), .trigger("rising"), .Select("low")) valid_3 (
    .D(1'b1), .en(write3), .Q(V3), .clk(CLK));  // open: clr
  Register #(.width(1), .trigger("rising"), .Select("low")) valid_4 (
    .D(1'b1), .en(write4), .Q(V4), .clk(CLK));  // open: clr
  Register #(.width(1), .trigger("rising"), .Select("low")) valid_5 (
    .D(1'b1), .en(write5), .Q(V5), .clk(CLK));  // open: clr
  Register #(.width(1), .trigger("rising"), .Select("low")) valid_6 (
    .D(1'b1), .en(write6), .Q(V6), .clk(CLK));  // open: clr
  Register #(.width(1), .trigger("rising"), .Select("low")) valid_7 (
    .D(1'b1), .en(write7), .Q(V7), .clk(CLK));  // open: clr
  Register #(.width(1), .trigger("rising"), .Select("low")) valid_8 (
    .D(1'b1), .en(write8), .Q(V8), .clk(CLK));  // open: clr
  Register #(.width(32), .trigger("rising"), .Select("low")) \u_分支指令地址  (
    .D(IN_PC), .en(write1), .Q(PC1), .clk(CLK));  // open: clr
  Register #(.width(32), .trigger("rising"), .Select("low")) \u_分支指令地址_2  (
    .D(IN_PC), .en(write2), .Q(PC2), .clk(CLK));  // open: clr
  Register #(.width(32), .trigger("rising"), .Select("low")) \u_分支指令地址_3  (
    .D(IN_PC), .en(write3), .Q(PC3), .clk(CLK));  // open: clr
  Register #(.width(32), .trigger("rising"), .Select("low")) \u_分支指令地址_4  (
    .D(IN_PC), .en(write4), .Q(PC4), .clk(CLK));  // open: clr
  Register #(.width(32), .trigger("rising"), .Select("low")) \u_分支指令地址_5  (
    .D(IN_PC), .en(write5), .Q(PC5), .clk(CLK));  // open: clr
  Register #(.width(32), .trigger("rising"), .Select("low")) \u_分支指令地址_6  (
    .D(IN_PC), .en(write6), .Q(PC6), .clk(CLK));  // open: clr
  Register #(.width(32), .trigger("rising"), .Select("low")) \u_分支指令地址_7  (
    .D(IN_PC), .en(write7), .Q(PC7), .clk(CLK));  // open: clr
  Register #(.width(32), .trigger("rising"), .Select("low")) \u_分支指令地址_8  (
    .D(IN_PC), .en(write8), .Q(PC8), .clk(CLK));  // open: clr
  Register #(.width(2), .trigger("rising"), .Select("low")) \u_分支预测历史  (
    .D(\new ), .en(write1), .Q(\分支预测历史_q ), .clk(CLK));  // open: clr
  Register #(.width(2), .trigger("rising"), .Select("low")) \u_分支预测历史_2  (
    .D(\new ), .en(write2), .Q(\分支预测历史_2_q ), .clk(CLK));  // open: clr
  Register #(.width(2), .trigger("rising"), .Select("low")) \u_分支预测历史_3  (
    .D(\new ), .en(write3), .Q(\分支预测历史_3_q ), .clk(CLK));  // open: clr
  Register #(.width(2), .trigger("rising"), .Select("low")) \u_分支预测历史_4  (
    .D(\new ), .en(write4), .Q(\分支预测历史_4_q ), .clk(CLK));  // open: clr
  Register #(.width(2), .trigger("rising"), .Select("low")) \u_分支预测历史_5  (
    .D(\new ), .en(write5), .Q(\分支预测历史_5_q ), .clk(CLK));  // open: clr
  Register #(.width(2), .trigger("rising"), .Select("low")) \u_分支预测历史_6  (
    .D(\new ), .en(write6), .Q(\分支预测历史_6_q ), .clk(CLK));  // open: clr
  Register #(.width(2), .trigger("rising"), .Select("low")) \u_分支预测历史_7  (
    .D(\new ), .en(write7), .Q(\分支预测历史_7_q ), .clk(CLK));  // open: clr
  Register #(.width(2), .trigger("rising"), .Select("low")) \u_分支预测历史_8  (
    .D(\new ), .en(write8), .Q(\分支预测历史_8_q ), .clk(CLK));  // open: clr
  assign History = hit1 ? \分支预测历史_q  : 2'bz;  // Controlled_Buffer controlled_buffer_1
  assign History = hit2 ? \分支预测历史_2_q  : 2'bz;  // Controlled_Buffer controlled_buffer_2
  assign History = hit3 ? \分支预测历史_3_q  : 2'bz;  // Controlled_Buffer controlled_buffer_3
  assign History = hit4 ? \分支预测历史_4_q  : 2'bz;  // Controlled_Buffer controlled_buffer_4
  assign History = hit5 ? \分支预测历史_5_q  : 2'bz;  // Controlled_Buffer controlled_buffer_5
  assign History = hit6 ? \分支预测历史_6_q  : 2'bz;  // Controlled_Buffer controlled_buffer_6
  assign History = hit7 ? \分支预测历史_7_q  : 2'bz;  // Controlled_Buffer controlled_buffer_7
  assign History = hit8 ? \分支预测历史_8_q  : 2'bz;  // Controlled_Buffer controlled_buffer_8
  Counter #(.width(32), .max('hffffffff), .ongoal("wrap"), .trigger("rising"), .behavior("old")) count (
    .load(or_1_out), .D({32{1'b0}}), .Q(C1), .clk(CLK));  // open: count, carry, clr, preset
  Counter #(.width(32), .max('hffffffff), .ongoal("wrap"), .trigger("rising"), .behavior("old")) count_2 (
    .load(or_2_out), .D({32{1'b0}}), .Q(C2), .clk(CLK));  // open: count, carry, clr, preset
  Counter #(.width(32), .max('hffffffff), .ongoal("wrap"), .trigger("rising"), .behavior("old")) count_3 (
    .load(or_3_out), .D({32{1'b0}}), .Q(C3), .clk(CLK));  // open: count, carry, clr, preset
  Counter #(.width(32), .max('hffffffff), .ongoal("wrap"), .trigger("rising"), .behavior("old")) count_4 (
    .load(or_4_out), .D({32{1'b0}}), .Q(C4), .clk(CLK));  // open: count, carry, clr, preset
  Counter #(.width(32), .max('hffffffff), .ongoal("wrap"), .trigger("rising"), .behavior("old")) count_5 (
    .load(or_5_out), .D({32{1'b0}}), .Q(C5), .clk(CLK));  // open: count, carry, clr, preset
  Counter #(.width(32), .max('hffffffff), .ongoal("wrap"), .trigger("rising"), .behavior("old")) count_6 (
    .load(or_6_out), .D({32{1'b0}}), .Q(C6), .clk(CLK));  // open: count, carry, clr, preset
  Counter #(.width(32), .max('hffffffff), .ongoal("wrap"), .trigger("rising"), .behavior("old")) count_7 (
    .load(or_7_out), .D({32{1'b0}}), .Q(C7), .clk(CLK));  // open: count, carry, clr, preset
  Counter #(.width(32), .max('hffffffff), .ongoal("wrap"), .trigger("rising"), .behavior("old")) count_8 (
    .load(or_8_out), .D({32{1'b0}}), .Q(C8), .clk(CLK));  // open: count, carry, clr, preset
  or or_1 (or_1_out, write1, hit1);
  or or_2 (or_2_out, write2, hit2);
  or or_3 (or_3_out, write3, hit3);
  or or_4 (or_4_out, write4, hit4);
  or or_5 (or_5_out, write5, hit5);
  or or_6 (or_6_out, write6, hit6);
  or or_7 (or_7_out, write7, hit7);
  or or_8 (or_8_out, write8, hit8);
  Register #(.width(32), .trigger("rising"), .Select("low")) \u_分支目标地址  (
    .D(AIM_PC), .en(write1), .Q(\分支目标地址_q ), .clk(CLK));  // open: clr
  Register #(.width(32), .trigger("rising"), .Select("low")) \u_分支目标地址_2  (
    .D(AIM_PC), .en(write2), .Q(\分支目标地址_2_q ), .clk(CLK));  // open: clr
  Register #(.width(32), .trigger("rising"), .Select("low")) \u_分支目标地址_3  (
    .D(AIM_PC), .en(write3), .Q(\分支目标地址_3_q ), .clk(CLK));  // open: clr
  Register #(.width(32), .trigger("rising"), .Select("low")) \u_分支目标地址_4  (
    .D(AIM_PC), .en(write4), .Q(\分支目标地址_4_q ), .clk(CLK));  // open: clr
  Register #(.width(32), .trigger("rising"), .Select("low")) \u_分支目标地址_5  (
    .D(AIM_PC), .en(write5), .Q(\分支目标地址_5_q ), .clk(CLK));  // open: clr
  Register #(.width(32), .trigger("rising"), .Select("low")) \u_分支目标地址_6  (
    .D(AIM_PC), .en(write6), .Q(\分支目标地址_6_q ), .clk(CLK));  // open: clr
  Register #(.width(32), .trigger("rising"), .Select("low")) \u_分支目标地址_7  (
    .D(AIM_PC), .en(write7), .Q(\分支目标地址_7_q ), .clk(CLK));  // open: clr
  Register #(.width(32), .trigger("rising"), .Select("low")) \u_分支目标地址_8  (
    .D(AIM_PC), .en(write8), .Q(\分支目标地址_8_q ), .clk(CLK));  // open: clr
  assign FOR_PC_t = hit1 ? \分支目标地址_q  : 32'bz;  // Controlled_Buffer controlled_buffer_9
  assign FOR_PC_t = hit2 ? \分支目标地址_2_q  : 32'bz;  // Controlled_Buffer controlled_buffer_10
  assign FOR_PC_t = hit3 ? \分支目标地址_3_q  : 32'bz;  // Controlled_Buffer controlled_buffer_11
  assign FOR_PC_t = hit4 ? \分支目标地址_4_q  : 32'bz;  // Controlled_Buffer controlled_buffer_12
  assign FOR_PC_t = hit5 ? \分支目标地址_5_q  : 32'bz;  // Controlled_Buffer controlled_buffer_13
  assign FOR_PC_t = hit6 ? \分支目标地址_6_q  : 32'bz;  // Controlled_Buffer controlled_buffer_14
  assign FOR_PC_t = hit7 ? \分支目标地址_7_q  : 32'bz;  // Controlled_Buffer controlled_buffer_15
  assign FOR_PC_t = hit8 ? \分支目标地址_8_q  : 32'bz;  // Controlled_Buffer controlled_buffer_16
  Comparator #(.width(32), .mode("twosComplement")) comparator_1 (
    .a(PC1), .b(PC), .eq(comparator_1_eq));  // open: gt, lt
  Comparator #(.width(32), .mode("twosComplement")) comparator_2 (
    .a(PC2), .b(PC), .eq(comparator_2_eq));  // open: gt, lt
  Comparator #(.width(32), .mode("twosComplement")) comparator_3 (
    .a(PC3), .b(PC), .eq(comparator_3_eq));  // open: gt, lt
  Comparator #(.width(32), .mode("twosComplement")) comparator_4 (
    .a(PC4), .b(PC), .eq(comparator_4_eq));  // open: gt, lt
  Comparator #(.width(32), .mode("twosComplement")) comparator_5 (
    .a(PC5), .b(PC), .eq(comparator_5_eq));  // open: gt, lt
  Comparator #(.width(32), .mode("twosComplement")) comparator_6 (
    .a(PC6), .b(PC), .eq(comparator_6_eq));  // open: gt, lt
  Comparator #(.width(32), .mode("twosComplement")) comparator_7 (
    .a(PC7), .b(PC), .eq(comparator_7_eq));  // open: gt, lt
  Comparator #(.width(32), .mode("twosComplement")) comparator_8 (
    .a(PC8), .b(PC), .eq(comparator_8_eq));  // open: gt, lt
  Comparator #(.width(32), .mode("unsigned")) comparator_9 (.a(C1), .b(C2), .lt(comparator_9_lt));  // open: gt, eq
  not not_1 (not_1_out, comparator_9_lt);
  Comparator #(.width(32), .mode("unsigned")) comparator_10 (.a(C3), .b(C4), .lt(comparator_10_lt));  // open: gt, eq
  not not_2 (not_2_out, comparator_10_lt);
  Comparator #(.width(32), .mode("unsigned")) comparator_11 (.a(C5), .b(C6), .lt(comparator_11_lt));  // open: gt, eq
  not not_3 (not_3_out, comparator_11_lt);
  Comparator #(.width(32), .mode("unsigned")) comparator_12 (.a(C7), .b(C8), .lt(comparator_12_lt));  // open: gt, eq
  not not_4 (not_4_out, comparator_12_lt);
  Multiplexer #(.select(1), .width(2), .disabled("Z"), .enable("false")) multiplexer_1 (
    .in0(2'b01), .in1(History), .out(BHTresult), .sel(hit));
  and and_1 (and_1_out, comparator_1_eq, V1);
  and and_2 (and_2_out, comparator_2_eq, V2);
  and and_3 (and_3_out, comparator_3_eq, V3);
  and and_4 (and_4_out, comparator_4_eq, V4);
  and and_5 (and_5_out, comparator_5_eq, V5);
  and and_6 (and_6_out, comparator_6_eq, V6);
  and and_7 (and_7_out, comparator_7_eq, V7);
  and and_8 (and_8_out, comparator_8_eq, V8);
  Multiplexer #(.select(1), .width(32), .disabled("Z"), .enable("false")) multiplexer_2 (
    .in0(C2), .in1(C1), .out(multiplexer_2_out), .sel(not_1_out));
  Multiplexer #(.select(1), .width(3), .disabled("Z"), .enable("false")) multiplexer_3 (
    .in0(3'b001), .in1(3'b000), .out(multiplexer_3_out), .sel(not_1_out));
  Multiplexer #(.select(1), .width(32), .disabled("Z"), .enable("false")) multiplexer_4 (
    .in0(C4), .in1(C3), .out(multiplexer_4_out), .sel(not_2_out));
  Multiplexer #(.select(1), .width(3), .disabled("Z"), .enable("false")) multiplexer_5 (
    .in0(3'b011), .in1(3'b010), .out(multiplexer_5_out), .sel(not_2_out));
  Multiplexer #(.select(1), .width(32), .disabled("Z"), .enable("false")) multiplexer_6 (
    .in0(C6), .in1(C5), .out(multiplexer_6_out), .sel(not_3_out));
  Multiplexer #(.select(1), .width(3), .disabled("Z"), .enable("false")) multiplexer_7 (
    .in0(3'b101), .in1(3'b100), .out(multiplexer_7_out), .sel(not_3_out));
  Multiplexer #(.select(1), .width(32), .disabled("Z"), .enable("false")) multiplexer_8 (
    .in0(C8), .in1(C7), .out(multiplexer_8_out), .sel(not_4_out));
  Multiplexer #(.select(1), .width(3), .disabled("Z"), .enable("false")) multiplexer_9 (
    .in0(3'b111), .in1(3'b110), .out(multiplexer_9_out), .sel(not_4_out));
  Decoder #(.select(3), .tristate("false"), .disabled(0), .enable("true")) decoder_1 (
    .out0(hit1), .out1(hit2), .out2(hit3), .out3(hit4), .out4(hit5), .out5(hit6), .out6(hit7), .out7(hit8),
    .sel(priority_encoder_1_out), .en(hit));
  Priority_Encoder #(.select(3), .disabled("Z")) priority_encoder_1 (
    .in0(and_1_out), .in1(and_2_out), .in2(and_3_out), .in3(and_4_out), .in4(and_5_out), .in5(and_6_out),
    .in6(and_7_out), .in7(and_8_out), .out(priority_encoder_1_out), .gs(hit));  // open: en_out, en_in
  Comparator #(.width(32), .mode("unsigned")) comparator_13 (
    .a(multiplexer_2_out), .b(multiplexer_4_out), .lt(comparator_13_lt));  // open: gt, eq
  not not_5 (not_5_out, comparator_13_lt);
  Comparator #(.width(32), .mode("unsigned")) comparator_14 (
    .a(multiplexer_6_out), .b(multiplexer_8_out), .lt(comparator_14_lt));  // open: gt, eq
  not not_6 (not_6_out, comparator_14_lt);
  not not_7 (miss, hit);
  Multiplexer #(.select(1), .width(3), .disabled("Z"), .enable("false")) multiplexer_10 (
    .in0(multiplexer_5_out), .in1(multiplexer_3_out), .out(multiplexer_10_out), .sel(not_5_out));
  Multiplexer #(.select(1), .width(32), .disabled("Z"), .enable("false")) multiplexer_11 (
    .in0(multiplexer_4_out), .in1(multiplexer_2_out), .out(multiplexer_11_out), .sel(not_5_out));
  Multiplexer #(.select(1), .width(32), .disabled("Z"), .enable("false")) multiplexer_12 (
    .in0(multiplexer_8_out), .in1(multiplexer_6_out), .out(multiplexer_12_out), .sel(not_6_out));
  Multiplexer #(.select(1), .width(3), .disabled("Z"), .enable("false")) multiplexer_13 (
    .in0(multiplexer_9_out), .in1(multiplexer_7_out), .out(multiplexer_13_out), .sel(not_6_out));
  Comparator #(.width(32), .mode("unsigned")) comparator_15 (
    .a(multiplexer_11_out), .b(multiplexer_12_out), .lt(comparator_15_lt));  // open: gt, eq
  not not_8 (not_8_out, comparator_15_lt);
  Multiplexer #(.select(1), .width(3), .disabled("Z"), .enable("false")) multiplexer_14 (
    .in0(multiplexer_13_out), .in1(multiplexer_10_out), .out(multiplexer_14_out), .sel(not_8_out));
  Decoder #(.select(3), .tristate("false"), .disabled(0), .enable("true")) decoder_2 (
    .out0(write1), .out1(write2), .out2(write3), .out3(write4), .out4(write5), .out5(write6), .out6(write7),
    .out7(write8), .sel(replace[2:0]), .en(replace[3]));
  Multiplexer #(.select(1), .width(3), .disabled("Z"), .enable("false")) multiplexer_15 (
    .in0(priority_encoder_1_out), .in1(multiplexer_14_out), .out(change), .sel(miss));
  Adder #(.width(32)) adder_1 (.a(PC), .b(32'h4), .out(adder_1_out));  // open: cin, cout
  Multiplexer #(.select(1), .width(32), .disabled("Z"), .enable("false")) multiplexer_16 (
    .in0(adder_1_out), .in1(FOR_PC_t), .out(FOR_PC), .sel(hit));

  // Notes on the sheet:
  //   1
  //   2
  //   3
  //   4
  //   5
  //   6
  //   7
  //   8
  //   需要向后传递让EX更新
  //   归并比较计数器最大值位置，该位置执行写入或更新
endmodule

// 预测更新
module \预测更新  (
  input  B_result,
  input  [1:0] History,
  output [1:0] New
);

  wire and_1_out, and_2_out, and_3_out, and_4_out, not_1_out, not_2_out, not_3_out, not_4_out, not_5_out;

  not not_1 (not_1_out, History[0]);
  not not_2 (not_2_out, B_result);
  not not_3 (not_3_out, History[0]);
  not not_4 (not_4_out, History[1]);
  not not_5 (not_5_out, History[0]);
  and and_1 (and_1_out, History[1], not_1_out);
  and and_2 (and_2_out, B_result, History[0]);
  and and_3 (and_3_out, not_2_out, History[1], not_3_out);
  and and_4 (and_4_out, B_result, not_4_out, not_5_out);
  or or_1 (New[1], and_1_out, and_2_out);
  or or_2 (New[0], and_3_out, and_4_out);
endmodule

// B_J
module B_J_TYPE (
  input  [4:0] OP5_1,
  output J_TYPE,
  output B_TYPE
);

  wire and_1_out, and_3_out, not_1_out, not_2_out, not_3_out, not_4_out, not_5_out, not_6_out, not_7_out,
       not_8_out, not_9_out, not_10_out, not_11_out;

  not not_1 (not_1_out, OP5_1[4]);
  not not_2 (not_2_out, OP5_1[3]);
  not not_3 (not_3_out, OP5_1[2]);
  not not_4 (not_4_out, OP5_1[0]);
  not not_5 (not_5_out, OP5_1[4]);
  not not_6 (not_6_out, OP5_1[3]);
  not not_7 (not_7_out, OP5_1[2]);
  not not_8 (not_8_out, OP5_1[1]);
  not not_9 (not_9_out, OP5_1[4]);
  not not_10 (not_10_out, OP5_1[3]);
  not not_11 (not_11_out, OP5_1[2]);
  and and_1 (and_1_out, not_1_out, not_2_out, not_3_out, OP5_1[1], not_4_out);
  and and_2 (J_TYPE, not_5_out, not_6_out, not_7_out, not_8_out, OP5_1[0]);
  and and_3 (and_3_out, not_9_out, not_10_out, not_11_out, OP5_1[1], OP5_1[0]);
  or or_1 (B_TYPE, and_1_out, and_3_out);
endmodule

module \单周期MIPS_2  (
  output RegWrite,
  output MemWrite,
  output [31:0] PC,
  output [31:0] IR,
  output [31:0] RDin,
  output [31:0] MDin
);

  wire and_1_out, and_2_out, B_JMP, CLK, comparator_1_eq, Go, IR1, IR2, IR3, mips_alu_1_equal,
       multiplexer_9_out, not_1_out, run, SignedExt, W1, W2, W3, \单周期硬布线控制器_1_alu_src , \单周期硬布线控制器_1_beq ,
       \单周期硬布线控制器_1_bne , \单周期硬布线控制器_1_jr , \单周期硬布线控制器_1_memtoreg , \单周期硬布线控制器_1_syscall ;
  wire [1:0] or_1_out, \单周期硬布线控制器_1_regdst ;
  wire [3:0] \单周期硬布线控制器_1_alu_op ;
  wire [4:0] multiplexer_2_out, multiplexer_3_out, multiplexer_4_out;
  wire [15:0] \总周期数 ;
  wire [31:0] B_PC, bit_extender_1_out, bit_extender_2_out, JR_PC, LedData, mips_alu_1_result,
       multiplexer_1_out, multiplexer_6_out, multiplexer_7_out, multiplexer_8_out, O_PC, ram_1_data,
       shifter_1_out;

  Clock #(.highDuration(1), .lowDuration(1)) clock_1 (.out(CLK));
  Button _1 (.out(IR1));
  Button _2 (.out(IR2));
  Button _3 (.out(IR3));
  or or_1 (or_1_out[0], \单周期硬布线控制器_1_jr , B_JMP);
  Multiplexer #(.select(2), .width(32), .disabled("Z"), .enable("false")) multiplexer_1 (
    .in0(O_PC), .in1(B_PC), .in2({4'b0000, IR[25:0], 2'b00}), .in3(JR_PC), .out(multiplexer_1_out),
    .sel(or_1_out));
  Button \u_继续运行  (.out(Go));
  LED #(.active("true")) led_1 (.in(W1));
  LED #(.active("true")) led_2 (.in(W2));
  LED #(.active("true")) led_3 (.in(W3));
  Register #(.width(32), .trigger("rising"), .Select("low")) u_PC (
    .D(multiplexer_1_out), .en(run), .Q(PC), .clk(CLK));  // open: clr
  Hex_Digit_Display hex_digit_display_1 (.value(LedData[27:24]));  // open: dp
  Hex_Digit_Display hex_digit_display_2 (.value(LedData[31:28]));  // open: dp
  Adder #(.width(32)) adder_1 (.a(PC), .b(32'h4), .out(O_PC));  // open: cin, cout
  Hex_Digit_Display hex_digit_display_3 (.value(LedData[19:16]));  // open: dp
  Hex_Digit_Display hex_digit_display_4 (.value(LedData[23:20]));  // open: dp
  ROM #(.addrWidth(10), .dataWidth(32), .Select("high")) rom_1 (.addr(PC[11:2]), .data(IR));
  Hex_Digit_Display hex_digit_display_5 (.value(LedData[11:8]));  // open: dp
  Hex_Digit_Display hex_digit_display_6 (.value(LedData[15:12]));  // open: dp
  Hex_Digit_Display hex_digit_display_7 (.value(LedData[7:4]));  // open: dp
  Hex_Digit_Display hex_digit_display_8 (.value(LedData[3:0]));  // open: dp
  // Probe on \总周期数 
  \单周期硬布线控制器_2  \u_单周期硬布线控制器_1  (
    .Func(IR[5:0]), .OP(IR[31:26]), .ALU_OP(\单周期硬布线控制器_1_alu_op ), .MemToReg(\单周期硬布线控制器_1_memtoreg ),
    .MemWrite(MemWrite), .ALU_SRC(\单周期硬布线控制器_1_alu_src ), .RegWrite(RegWrite),
    .SysCALL(\单周期硬布线控制器_1_syscall ), .SignedExt(SignedExt), .RegDst(\单周期硬布线控制器_1_regdst [0]),
    .JR(\单周期硬布线控制器_1_jr ), .JMP(or_1_out[1]), .Beq(\单周期硬布线控制器_1_beq ), .JAL(\单周期硬布线控制器_1_regdst [1]),
    .Bne(\单周期硬布线控制器_1_bne ));
  Multiplexer #(.select(1), .width(5), .disabled("Z"), .enable("false")) multiplexer_2 (
    .in0(IR[25:21]), .in1(5'b00010), .out(multiplexer_2_out), .sel(\单周期硬布线控制器_1_syscall ));
  Multiplexer #(.select(1), .width(5), .disabled("Z"), .enable("false")) multiplexer_3 (
    .in0(IR[20:16]), .in1(5'b00100), .out(multiplexer_3_out), .sel(\单周期硬布线控制器_1_syscall ));
  Multiplexer #(.select(2), .width(5), .disabled("Z"), .enable("false")) multiplexer_4 (
    .in0(IR[20:16]), .in1(IR[15:11]), .in2({5{1'b1}}), .out(multiplexer_4_out), .sel(\单周期硬布线控制器_1_regdst ));  // open: in3
  Multiplexer #(.select(1), .width(32), .disabled("Z"), .enable("false")) multiplexer_5 (
    .in0(multiplexer_8_out), .in1(O_PC), .out(RDin), .sel(\单周期硬布线控制器_1_regdst [1]));
  assign bit_extender_1_out = {{16{1'b0}}, IR[15:0]};  // Bit_Extender bit_extender_1
  assign bit_extender_2_out = {{16{IR[15]}}, IR[15:0]};  // Bit_Extender bit_extender_2
  MIPS_Regifile mips_regifile_1 (
    .Din(RDin), .Clk(CLK), .R1(JR_PC), .R2(MDin), .WE(RegWrite), .W_num(multiplexer_4_out),
    .R1_num(multiplexer_2_out), .R2_num(multiplexer_3_out));
  Multiplexer #(.select(1), .width(32), .disabled("Z"), .enable("false")) multiplexer_6 (
    .in0(bit_extender_1_out), .in1(bit_extender_2_out), .out(multiplexer_6_out), .sel(SignedExt));
  Multiplexer #(.select(1), .width(32), .disabled("Z"), .enable("false")) multiplexer_7 (
    .in0(MDin), .in1(multiplexer_6_out), .out(multiplexer_7_out), .sel(\单周期硬布线控制器_1_alu_src ));
  Shifter #(.width(32), .shift("ll")) shifter_1 (.in(multiplexer_6_out), .\dist (5'b00010), .out(shifter_1_out));
  not not_1 (not_1_out, mips_alu_1_equal);
  MIPS_ALU mips_alu_1 (
    .X(JR_PC), .Y(multiplexer_7_out), .AluOP(\单周期硬布线控制器_1_alu_op ), .Equal(mips_alu_1_equal),
    .Result(mips_alu_1_result), .shamt(IR[10:6]));  // open: Result_2
  Adder #(.width(32)) adder_2 (.a(shifter_1_out), .b(O_PC), .out(B_PC));  // open: cin, cout
  and and_1 (and_1_out, mips_alu_1_equal, \单周期硬布线控制器_1_beq );
  or or_2 (B_JMP, and_1_out, and_2_out);
  and and_2 (and_2_out, not_1_out, \单周期硬布线控制器_1_bne );
  RAM #(.addrWidth(10), .dataWidth(32), .bus("separate"), .Select("high")) ram_1 (
    .addr(mips_alu_1_result[11:2]), .din(MDin), .data(ram_1_data), .str(MemWrite), .clk(CLK));  // open: sel, ld, clr
  Multiplexer #(.select(1), .width(32), .disabled("Z"), .enable("false")) multiplexer_8 (
    .in0(mips_alu_1_result), .in1(ram_1_data), .out(multiplexer_8_out), .sel(\单周期硬布线控制器_1_memtoreg ));
  Counter #(.width(16), .max('hffff), .ongoal("stay"), .trigger("rising"), .behavior("old")) counter_1 (
    .count(run), .Q(\总周期数 ), .clk(CLK));  // open: load, D, carry, clr, preset
  Multiplexer #(.select(1), .width(1), .disabled("Z"), .enable("false")) multiplexer_9 (
    .in0(1'b0), .in1(comparator_1_eq), .out(multiplexer_9_out), .sel(\单周期硬布线控制器_1_syscall ));
  Comparator #(.width(32), .mode("twosComplement")) comparator_1 (
    .a(JR_PC), .b(32'h22), .eq(comparator_1_eq));  // open: gt, lt
  or or_3 (run, ~\单周期硬布线控制器_1_syscall , multiplexer_9_out, Go);  // OR_Gate
  Register #(.width(32), .trigger("rising"), .Select("low")) register_1 (
    .D(MDin), .en(multiplexer_9_out), .Q(LedData), .clk(CLK));  // open: clr

  // Other names for the same wires on the sheet: a0[31:0] = MDin; J_PC[27:2] = IR[25:0]

  // Notes on the sheet:
  //   中断源
  //   中断等待指示
  //   总复位信号应将除ROM以外所有存储组件全部清零
  //   指令存储器
  //   contents of rom_1 (hex, n*v repeats v):
  //   20110001 8000c05 20110001 20120002 20130003 8000c09 20110001 20120002 20130003 8000c0d 20110001
  //   20120002 20130003 8000c11 20110001 20120002 20130003 c000cb8 20100001 20110001 118fc0 112020
  //   20020022 c 118882 12200001 8000c15 112020 20020022 c 20110001 118880 112020 20020022 c 12200001
  //   8000c1f 20110001 118fc0 112020 20020022 c 1188c3 112020 20020022 c 118903 112020 20020022 c 118903
  //   112020 20020022 c 118903 112020 20020022 c 118903 112020 20020022 c 118903 112020 20020022 c 118903
  //   112020 20020022 c 118903 112020 20020022 c 20100001 109fc0 139fc3 8021 2012000c 24160003 26100001
  //   3210000f 20080008 20090001 139900 2709825 132020 20020022 c 1094022 1500fff9 22100001 2018000f
  //   2188024 108700 20080008 20090001 139902 2709825 132021 20020022 c 1094022 1500fff9 108702 2c9b022
  //   12c00001 8000c50 4020 1084027 84400 3508ffff 82021 20020022 c 2010ffff 20110000 ae300000 22100001
  //   22310004 ae300000 22100001 22310004 ae300000 22100001 22310004 ae300000 22100001 22310004 ae300000
  //   22100001 22310004 ae300000 22100001 22310004 ae300000 22100001 22310004 ae300000 22100001 22310004
  //   ae300000 22100001 22310004 ae300000 22100001 22310004 ae300000 22100001 22310004 ae300000 22100001
  //   22310004 ae300000 22100001 22310004 ae300000 22100001 22310004 ae300000 22100001 22310004 ae300000
  //   22100001 22310004 22100001 8020 2011003c 8e130000 8e340000 274402a 11000002 ae330000 ae140000
  //   2231fffc 1611fff8 102020 20020022 c 22100004 2011003c 1611fff2 2002000a c 20100000 22100001 102020
  //   20020022 c 22100002 102020 20020022 c 22100003 102020 20020022 c 22100004 102020 20020022 c 22100005
  //   102020 20020022 c 22100006 102020 20020022 c 22100007 102020 20020022 c 22100008 102020 20020022
  //   20020022 c 3e00008
  //   数码管输出
  //   OP
  //   rs
  //   指令字
  //   rt
  //   rd
  //   数码管输出应该用寄存器锁存，否则显示数据只能一闪而过
  //   JMP
  //   JR
  //   OP
  //   Func
  //   Func
  //   Beq
  //   Bne
  //   MemToReg
  //   MemWrite
  //   AluOP
  //   AluSrcB
  //   RegWrite
  //   JAL
  //   RegDst
  //   Syscall
  //   为方便自动评测，需要输出PC，IR，寄存器文件写入端口RDin，内存写入端口MDin等信号
endmodule

// 单周期硬布线控制器
module \单周期硬布线控制器_2  (
  input  [5:0] OP,
  input  [5:0] Func,
  output [3:0] ALU_OP,
  output MemToReg,
  output MemWrite,
  output ALU_SRC,
  output RegWrite,
  output SysCALL,
  output SignedExt,
  output RegDst,
  output Beq,
  output Bne,
  output JR,
  output JMP,
  output JAL
);

  \运算控制器自动生成  \u_运算控制器自动生成_1  (
    .OP0(OP[0]), .OP1(OP[1]), .OP2(OP[2]), .OP3(OP[3]), .OP4(OP[4]), .OP5(OP[5]), .F0(Func[0]), .F1(Func[1]),
    .F2(Func[2]), .F3(Func[3]), .F4(Func[4]), .F5(Func[5]), .S0(ALU_OP[0]), .S1(ALU_OP[1]), .S2(ALU_OP[2]),
    .S3(ALU_OP[3]));
  \控制信号自动生成  \u_控制信号自动生成_1  (
    .OP0(OP[0]), .OP1(OP[1]), .OP2(OP[2]), .OP3(OP[3]), .OP4(OP[4]), .OP5(OP[5]), .F0(Func[0]), .F1(Func[1]),
    .F2(Func[2]), .F3(Func[3]), .F4(Func[4]), .F5(Func[5]), .MemToReg(MemToReg), .MemWrite(MemWrite),
    .ALU_SRC(ALU_SRC), .RegWrite(RegWrite), .SysCALL(SysCALL), .SignedExt(SignedExt), .RegDst(RegDst),
    .BEQ(Beq), .BNE(Bne), .JR(JR), .JUMP(JMP), .JAL(JAL));

  // Other names for the same wires on the sheet: OP_CODE[5:0] = OP

  // Notes on the sheet:
  //   运算器控制器，根据指令生成运算器功能选择信号
  //   控制信号生成，产生数据通路需要的其他控制信号
endmodule
// 运算器控制器
module \运算控制器自动生成  (
  input  OP0,
  input  OP1,
  input  OP2,
  input  OP3,
  input  OP4,
  input  OP5,
  input  F0,
  input  F1,
  input  F2,
  input  F3,
  input  F4,
  input  F5,
  output S0,
  output S1,
  output S2,
  output S3
);

  wire and_1_out, and_2_out, and_3_out, and_4_out, and_5_out, and_6_out, and_7_out, and_8_out, and_9_out,
       and_10_out, and_11_out, and_12_out, and_13_out, and_14_out, and_15_out, and_16_out, and_17_out,
       and_18_out, and_19_out, and_20_out, and_21_out, and_22_out, and_23_out, and_24_out, and_25_out,
       and_26_out, and_27_out, and_28_out, and_29_out, and_30_out, and_31_out, and_32_out, and_33_out,
       and_34_out, not_1_out, not_2_out, not_3_out, not_4_out, not_5_out, not_6_out, not_7_out, not_8_out,
       not_9_out, not_10_out, not_11_out, not_12_out, not_13_out, not_14_out, not_15_out, not_16_out,
       not_17_out, not_18_out, not_19_out, not_20_out, not_21_out, not_22_out, not_23_out, not_24_out,
       not_25_out, not_26_out, not_27_out, not_28_out, not_29_out, not_30_out, not_31_out, not_32_out,
       not_33_out, not_34_out, not_35_out, not_36_out, not_37_out, not_38_out, not_39_out, not_40_out,
       not_41_out, not_42_out, not_43_out, not_44_out, not_45_out, not_46_out, not_47_out, not_48_out,
       not_49_out, not_50_out, not_51_out, not_52_out, not_53_out, not_54_out, not_55_out, not_56_out,
       not_57_out, not_58_out, not_59_out, not_60_out, not_61_out, not_62_out, not_63_out, not_64_out,
       not_65_out, not_66_out, not_67_out, not_68_out, not_69_out, not_70_out, not_71_out, not_72_out,
       not_73_out, not_74_out, not_75_out, not_76_out, not_77_out, not_78_out, not_79_out, not_80_out,
       not_81_out, not_82_out, not_83_out, not_84_out, not_85_out, not_86_out, not_87_out, not_88_out,
       not_89_out, not_90_out, not_91_out, not_92_out, not_93_out, not_94_out, not_95_out, not_96_out,
       not_97_out, not_98_out, not_99_out, not_100_out, not_101_out, not_102_out, not_103_out, not_104_out,
       not_105_out, not_106_out, not_107_out, not_108_out, not_109_out, not_110_out, not_111_out,
       not_112_out, not_113_out, not_114_out, not_115_out, not_116_out, not_117_out, not_118_out,
       not_119_out, not_120_out, not_121_out, not_122_out, not_123_out, not_124_out, not_125_out,
       not_126_out, not_127_out, not_128_out, not_129_out, not_130_out, not_131_out, not_132_out,
       not_133_out, not_134_out, not_135_out, not_136_out, not_137_out, not_138_out, not_139_out,
       not_140_out, not_141_out, not_142_out, not_143_out, not_144_out, not_145_out, not_146_out,
       not_147_out, not_148_out, not_149_out, not_150_out, not_151_out, not_152_out, not_153_out,
       not_154_out, not_155_out, not_156_out, not_157_out, not_158_out, not_159_out, not_160_out,
       not_161_out, not_162_out, not_163_out, not_164_out, not_165_out, not_166_out, not_167_out,
       not_168_out, not_169_out, not_170_out, not_171_out, not_172_out, not_173_out, not_174_out,
       not_175_out, not_176_out, not_177_out, not_178_out, not_179_out, not_180_out, not_181_out,
       not_182_out, not_183_out, not_184_out, not_185_out, not_186_out, not_187_out, not_188_out,
       not_189_out, not_190_out, not_191_out, not_192_out, not_193_out, not_194_out, not_195_out,
       not_196_out, not_197_out, not_198_out, not_199_out, not_200_out, not_201_out, not_202_out,
       not_203_out, not_204_out, not_205_out, not_206_out, not_207_out, not_208_out, not_209_out,
       not_210_out, not_211_out, not_212_out, not_213_out, not_214_out, not_215_out, not_216_out,
       not_217_out, not_218_out, not_219_out, not_220_out, not_221_out, not_222_out, not_223_out,
       not_224_out, not_225_out, not_226_out, not_227_out, not_228_out, not_229_out, not_230_out,
       not_231_out, not_232_out, not_233_out, not_234_out, not_235_out, not_236_out;

  not not_1 (not_1_out, OP5);
  not not_2 (not_2_out, OP4);
  not not_3 (not_3_out, OP3);
  not not_4 (not_4_out, OP2);
  not not_5 (not_5_out, OP1);
  not not_6 (not_6_out, OP0);
  not not_7 (not_7_out, F5);
  not not_8 (not_8_out, F4);
  not not_9 (not_9_out, F3);
  not not_10 (not_10_out, F2);
  not not_11 (not_11_out, OP5);
  not not_12 (not_12_out, OP4);
  not not_13 (not_13_out, OP3);
  not not_14 (not_14_out, OP2);
  not not_15 (not_15_out, OP1);
  not not_16 (not_16_out, OP0);
  not not_17 (not_17_out, F4);
  not not_18 (not_18_out, F3);
  not not_19 (not_19_out, F2);
  not not_20 (not_20_out, F1);
  not not_21 (not_21_out, F0);
  not not_22 (not_22_out, OP5);
  not not_23 (not_23_out, OP4);
  not not_24 (not_24_out, OP3);
  not not_25 (not_25_out, OP2);
  not not_26 (not_26_out, OP1);
  not not_27 (not_27_out, OP0);
  not not_28 (not_28_out, F4);
  not not_29 (not_29_out, F3);
  not not_30 (not_30_out, F2);
  not not_31 (not_31_out, F1);
  not not_32 (not_32_out, OP5);
  not not_33 (not_33_out, OP4);
  not not_34 (not_34_out, OP3);
  not not_35 (not_35_out, OP2);
  not not_36 (not_36_out, OP1);
  not not_37 (not_37_out, OP0);
  not not_38 (not_38_out, F4);
  not not_39 (not_39_out, F3);
  not not_40 (not_40_out, F1);
  not not_41 (not_41_out, F0);
  not not_42 (not_42_out, OP5);
  not not_43 (not_43_out, OP4);
  not not_44 (not_44_out, OP3);
  not not_45 (not_45_out, OP2);
  not not_46 (not_46_out, OP1);
  not not_47 (not_47_out, OP0);
  not not_48 (not_48_out, F4);
  not not_49 (not_49_out, F2);
  not not_50 (not_50_out, F0);
  not not_51 (not_51_out, OP5);
  not not_52 (not_52_out, OP4);
  not not_53 (not_53_out, OP2);
  not not_54 (not_54_out, OP1);
  not not_55 (not_55_out, OP0);
  not not_56 (not_56_out, OP5);
  not not_57 (not_57_out, OP4);
  not not_58 (not_58_out, OP1);
  not not_59 (not_59_out, OP0);
  not not_60 (not_60_out, OP5);
  not not_61 (not_61_out, OP4);
  not not_62 (not_62_out, OP2);
  not not_63 (not_63_out, OP1);
  not not_64 (not_64_out, OP5);
  not not_65 (not_65_out, OP4);
  not not_66 (not_66_out, OP2);
  not not_67 (not_67_out, OP0);
  not not_68 (not_68_out, OP4);
  not not_69 (not_69_out, OP3);
  not not_70 (not_70_out, OP2);
  not not_71 (not_71_out, OP4);
  not not_72 (not_72_out, OP2);
  not not_73 (not_73_out, OP5);
  not not_74 (not_74_out, OP4);
  not not_75 (not_75_out, OP3);
  not not_76 (not_76_out, OP2);
  not not_77 (not_77_out, OP1);
  not not_78 (not_78_out, OP0);
  not not_79 (not_79_out, F5);
  not not_80 (not_80_out, F4);
  not not_81 (not_81_out, F3);
  not not_82 (not_82_out, F2);
  not not_83 (not_83_out, F0);
  not not_84 (not_84_out, OP5);
  not not_85 (not_85_out, OP4);
  not not_86 (not_86_out, OP3);
  not not_87 (not_87_out, OP2);
  not not_88 (not_88_out, OP1);
  not not_89 (not_89_out, OP0);
  not not_90 (not_90_out, F4);
  not not_91 (not_91_out, F3);
  not not_92 (not_92_out, F2);
  not not_93 (not_93_out, F0);
  not not_94 (not_94_out, OP5);
  not not_95 (not_95_out, OP4);
  not not_96 (not_96_out, OP3);
  not not_97 (not_97_out, OP2);
  not not_98 (not_98_out, OP1);
  not not_99 (not_99_out, OP0);
  not not_100 (not_100_out, F4);
  not not_101 (not_101_out, F3);
  not not_102 (not_102_out, F1);
  not not_103 (not_103_out, F0);
  not not_104 (not_104_out, OP5);
  not not_105 (not_105_out, OP4);
  not not_106 (not_106_out, OP3);
  not not_107 (not_107_out, OP2);
  not not_108 (not_108_out, OP1);
  not not_109 (not_109_out, OP0);
  not not_110 (not_110_out, F4);
  not not_111 (not_111_out, F3);
  not not_112 (not_112_out, OP5);
  not not_113 (not_113_out, OP4);
  not not_114 (not_114_out, OP3);
  not not_115 (not_115_out, OP2);
  not not_116 (not_116_out, OP1);
  not not_117 (not_117_out, OP0);
  not not_118 (not_118_out, F4);
  not not_119 (not_119_out, F2);
  not not_120 (not_120_out, F0);
  not not_121 (not_121_out, OP5);
  not not_122 (not_122_out, OP4);
  not not_123 (not_123_out, OP1);
  not not_124 (not_124_out, OP0);
  not not_125 (not_125_out, OP5);
  not not_126 (not_126_out, OP4);
  not not_127 (not_127_out, OP2);
  not not_128 (not_128_out, OP0);
  not not_129 (not_129_out, OP5);
  not not_130 (not_130_out, OP4);
  not not_131 (not_131_out, OP3);
  not not_132 (not_132_out, OP2);
  not not_133 (not_133_out, OP1);
  not not_134 (not_134_out, OP0);
  not not_135 (not_135_out, F4);
  not not_136 (not_136_out, F3);
  not not_137 (not_137_out, F2);
  not not_138 (not_138_out, F1);
  not not_139 (not_139_out, F0);
  not not_140 (not_140_out, OP5);
  not not_141 (not_141_out, OP4);
  not not_142 (not_142_out, OP3);
  not not_143 (not_143_out, OP2);
  not not_144 (not_144_out, OP1);
  not not_145 (not_145_out, OP0);
  not not_146 (not_146_out, F4);
  not not_147 (not_147_out, F3);
  not not_148 (not_148_out, F2);
  not not_149 (not_149_out, F1);
  not not_150 (not_150_out, OP5);
  not not_151 (not_151_out, OP4);
  not not_152 (not_152_out, OP3);
  not not_153 (not_153_out, OP2);
  not not_154 (not_154_out, OP1);
  not not_155 (not_155_out, OP0);
  not not_156 (not_156_out, F4);
  not not_157 (not_157_out, F3);
  not not_158 (not_158_out, F2);
  not not_159 (not_159_out, F0);
  not not_160 (not_160_out, OP5);
  not not_161 (not_161_out, OP4);
  not not_162 (not_162_out, OP3);
  not not_163 (not_163_out, OP2);
  not not_164 (not_164_out, OP1);
  not not_165 (not_165_out, OP0);
  not not_166 (not_166_out, F4);
  not not_167 (not_167_out, F3);
  not not_168 (not_168_out, F1);
  not not_169 (not_169_out, F0);
  not not_170 (not_170_out, OP5);
  not not_171 (not_171_out, OP4);
  not not_172 (not_172_out, OP3);
  not not_173 (not_173_out, OP2);
  not not_174 (not_174_out, OP1);
  not not_175 (not_175_out, OP0);
  not not_176 (not_176_out, F4);
  not not_177 (not_177_out, F2);
  not not_178 (not_178_out, OP5);
  not not_179 (not_179_out, OP4);
  not not_180 (not_180_out, OP2);
  not not_181 (not_181_out, OP1);
  not not_182 (not_182_out, OP0);
  not not_183 (not_183_out, OP5);
  not not_184 (not_184_out, OP4);
  not not_185 (not_185_out, OP1);
  not not_186 (not_186_out, OP0);
  not not_187 (not_187_out, OP5);
  not not_188 (not_188_out, OP4);
  not not_189 (not_189_out, OP2);
  not not_190 (not_190_out, OP1);
  not not_191 (not_191_out, OP4);
  not not_192 (not_192_out, OP3);
  not not_193 (not_193_out, OP2);
  not not_194 (not_194_out, OP4);
  not not_195 (not_195_out, OP2);
  not not_196 (not_196_out, OP5);
  not not_197 (not_197_out, OP4);
  not not_198 (not_198_out, OP3);
  not not_199 (not_199_out, OP2);
  not not_200 (not_200_out, OP1);
  not not_201 (not_201_out, OP0);
  not not_202 (not_202_out, F4);
  not not_203 (not_203_out, F3);
  not not_204 (not_204_out, F1);
  not not_205 (not_205_out, OP5);
  not not_206 (not_206_out, OP4);
  not not_207 (not_207_out, OP3);
  not not_208 (not_208_out, OP2);
  not not_209 (not_209_out, OP1);
  not not_210 (not_210_out, OP0);
  not not_211 (not_211_out, F4);
  not not_212 (not_212_out, F3);
  not not_213 (not_213_out, OP5);
  not not_214 (not_214_out, OP4);
  not not_215 (not_215_out, OP3);
  not not_216 (not_216_out, OP2);
  not not_217 (not_217_out, OP1);
  not not_218 (not_218_out, OP0);
  not not_219 (not_219_out, F4);
  not not_220 (not_220_out, F2);
  not not_221 (not_221_out, F0);
  not not_222 (not_222_out, OP5);
  not not_223 (not_223_out, OP4);
  not not_224 (not_224_out, OP3);
  not not_225 (not_225_out, OP2);
  not not_226 (not_226_out, OP1);
  not not_227 (not_227_out, OP0);
  not not_228 (not_228_out, F4);
  not not_229 (not_229_out, F2);
  not not_230 (not_230_out, OP5);
  not not_231 (not_231_out, OP4);
  not not_232 (not_232_out, OP2);
  not not_233 (not_233_out, OP0);
  not not_234 (not_234_out, OP5);
  not not_235 (not_235_out, OP4);
  not not_236 (not_236_out, OP1);
  and and_1 (and_1_out, not_1_out, not_2_out, not_3_out, not_4_out, not_5_out, not_6_out, not_7_out, not_8_out, not_9_out, not_10_out, F1, F0);
  and and_2 (and_2_out, not_11_out, not_12_out, not_13_out, not_14_out, not_15_out, not_16_out, F5, not_17_out, not_18_out, not_19_out, not_20_out, not_21_out);
  and and_3 (and_3_out, not_22_out, not_23_out, not_24_out, not_25_out, not_26_out, not_27_out, F5, not_28_out, not_29_out, not_30_out, not_31_out, F0);
  and and_4 (and_4_out, not_32_out, not_33_out, not_34_out, not_35_out, not_36_out, not_37_out, F5, not_38_out, not_39_out, F2, not_40_out, not_41_out);
  and and_5 (and_5_out, not_42_out, not_43_out, not_44_out, not_45_out, not_46_out, not_47_out, F5, not_48_out, F3, not_49_out, F1, not_50_out);
  and and_6 (and_6_out, not_51_out, not_52_out, OP3, not_53_out, not_54_out, not_55_out);
  and and_7 (and_7_out, not_56_out, not_57_out, OP3, OP2, not_58_out, not_59_out);
  and and_8 (and_8_out, not_60_out, not_61_out, OP3, not_62_out, not_63_out, OP0);
  and and_9 (and_9_out, not_64_out, not_65_out, OP3, not_66_out, OP1, not_67_out);
  and and_10 (and_10_out, OP5, not_68_out, not_69_out, not_70_out, OP1, OP0);
  and and_11 (and_11_out, OP5, not_71_out, OP3, not_72_out, OP1, OP0);
  and and_12 (and_12_out, not_73_out, not_74_out, not_75_out, not_76_out, not_77_out, not_78_out, not_79_out, not_80_out, not_81_out, not_82_out, F1, not_83_out);
  and and_13 (and_13_out, not_84_out, not_85_out, not_86_out, not_87_out, not_88_out, not_89_out, F5, not_90_out, not_91_out, not_92_out, F1, not_93_out);
  and and_14 (and_14_out, not_94_out, not_95_out, not_96_out, not_97_out, not_98_out, not_99_out, F5, not_100_out, not_101_out, F2, not_102_out, not_103_out);
  and and_15 (and_15_out, not_104_out, not_105_out, not_106_out, not_107_out, not_108_out, not_109_out, F5, not_110_out, not_111_out, F2, F1, F0);
  and and_16 (and_16_out, not_112_out, not_113_out, not_114_out, not_115_out, not_116_out, not_117_out, F5, not_118_out, F3, not_119_out, F1, not_120_out);
  and and_17 (and_17_out, not_121_out, not_122_out, OP3, OP2, not_123_out, not_124_out);
  and and_18 (and_18_out, not_125_out, not_126_out, OP3, not_127_out, OP1, not_128_out);
  and and_19 (and_19_out, not_129_out, not_130_out, not_131_out, not_132_out, not_133_out, not_134_out, F5, not_135_out, not_136_out, not_137_out, not_138_out, not_139_out);
  and and_20 (and_20_out, not_140_out, not_141_out, not_142_out, not_143_out, not_144_out, not_145_out, F5, not_146_out, not_147_out, not_148_out, not_149_out, F0);
  and and_21 (and_21_out, not_150_out, not_151_out, not_152_out, not_153_out, not_154_out, not_155_out, F5, not_156_out, not_157_out, not_158_out, F1, not_159_out);
  and and_22 (and_22_out, not_160_out, not_161_out, not_162_out, not_163_out, not_164_out, not_165_out, F5, not_166_out, not_167_out, F2, not_168_out, not_169_out);
  and and_23 (and_23_out, not_170_out, not_171_out, not_172_out, not_173_out, not_174_out, not_175_out, F5, not_176_out, F3, not_177_out, F1, F0);
  and and_24 (and_24_out, not_178_out, not_179_out, OP3, not_180_out, not_181_out, not_182_out);
  and and_25 (and_25_out, not_183_out, not_184_out, OP3, OP2, not_185_out, not_186_out);
  and and_26 (and_26_out, not_187_out, not_188_out, OP3, not_189_out, not_190_out, OP0);
  and and_27 (and_27_out, OP5, not_191_out, not_192_out, not_193_out, OP1, OP0);
  and and_28 (and_28_out, OP5, not_194_out, OP3, not_195_out, OP1, OP0);
  and and_29 (and_29_out, not_196_out, not_197_out, not_198_out, not_199_out, not_200_out, not_201_out, F5, not_202_out, not_203_out, F2, not_204_out, F0);
  and and_30 (and_30_out, not_205_out, not_206_out, not_207_out, not_208_out, not_209_out, not_210_out, F5, not_211_out, not_212_out, F2, F1, F0);
  and and_31 (and_31_out, not_213_out, not_214_out, not_215_out, not_216_out, not_217_out, not_218_out, F5, not_219_out, F3, not_220_out, F1, not_221_out);
  and and_32 (and_32_out, not_222_out, not_223_out, not_224_out, not_225_out, not_226_out, not_227_out, F5, not_228_out, F3, not_229_out, F1, F0);
  and and_33 (and_33_out, not_230_out, not_231_out, OP3, not_232_out, OP1, not_233_out);
  and and_34 (and_34_out, not_234_out, not_235_out, OP3, OP2, not_236_out, OP0);
  or or_1 (S0, and_1_out, and_2_out, and_3_out, and_4_out, and_5_out, and_6_out, and_7_out, and_8_out, and_9_out, and_10_out, and_11_out);
  or or_2 (S1, and_12_out, and_13_out, and_14_out, and_15_out, and_16_out, and_17_out, and_18_out);
  or or_3 (S2, and_19_out, and_20_out, and_21_out, and_22_out, and_23_out, and_24_out, and_25_out, and_26_out, and_27_out, and_28_out);
  or or_4 (S3, and_29_out, and_30_out, and_31_out, and_32_out, and_33_out, and_34_out);
endmodule

// 控制信号生成
module \控制信号自动生成  (
  input  OP0,
  input  OP1,
  input  OP2,
  input  OP3,
  input  OP4,
  input  OP5,
  input  F0,
  input  F1,
  input  F2,
  input  F3,
  input  F4,
  input  F5,
  output MemToReg,
  output MemWrite,
  output ALU_SRC,
  output RegWrite,
  output SysCALL,
  output SignedExt,
  output RegDst,
  output BEQ,
  output BNE,
  output JR,
  output JUMP,
  output JAL
);

  wire and_3_out, and_4_out, and_5_out, and_6_out, and_7_out, and_8_out, and_9_out, and_10_out, and_11_out,
       and_12_out, and_13_out, and_14_out, and_15_out, and_16_out, and_17_out, and_18_out, and_19_out,
       and_20_out, and_21_out, and_22_out, and_23_out, and_24_out, and_25_out, and_26_out, and_27_out,
       and_29_out, and_30_out, and_31_out, and_32_out, and_33_out, and_34_out, and_35_out, and_36_out,
       and_37_out, and_38_out, and_39_out, and_40_out, and_41_out, and_42_out, and_43_out, and_44_out,
       and_45_out, and_46_out, and_50_out, and_51_out, and_52_out, not_1_out, not_2_out, not_3_out,
       not_4_out, not_5_out, not_6_out, not_7_out, not_8_out, not_9_out, not_10_out, not_11_out, not_12_out,
       not_13_out, not_14_out, not_15_out, not_16_out, not_17_out, not_18_out, not_19_out, not_20_out,
       not_21_out, not_22_out, not_23_out, not_24_out, not_25_out, not_26_out, not_27_out, not_28_out,
       not_29_out, not_30_out, not_31_out, not_32_out, not_33_out, not_34_out, not_35_out, not_36_out,
       not_37_out, not_38_out, not_39_out, not_40_out, not_41_out, not_42_out, not_43_out, not_44_out,
       not_45_out, not_46_out, not_47_out, not_48_out, not_49_out, not_50_out, not_51_out, not_52_out,
       not_53_out, not_54_out, not_55_out, not_56_out, not_57_out, not_58_out, not_59_out, not_60_out,
       not_61_out, not_62_out, not_63_out, not_64_out, not_65_out, not_66_out, not_67_out, not_68_out,
       not_69_out, not_70_out, not_71_out, not_72_out, not_73_out, not_74_out, not_75_out, not_76_out,
       not_77_out, not_78_out, not_79_out, not_80_out, not_81_out, not_82_out, not_83_out, not_84_out,
       not_85_out, not_86_out, not_87_out, not_88_out, not_89_out, not_90_out, not_91_out, not_92_out,
       not_93_out, not_94_out, not_95_out, not_96_out, not_97_out, not_98_out, not_99_out, not_100_out,
       not_101_out, not_102_out, not_103_out, not_104_out, not_105_out, not_106_out, not_107_out,
       not_108_out, not_109_out, not_110_out, not_111_out, not_112_out, not_113_out, not_114_out,
       not_115_out, not_116_out, not_117_out, not_118_out, not_119_out, not_120_out, not_121_out,
       not_122_out, not_123_out, not_124_out, not_125_out, not_126_out, not_127_out, not_128_out,
       not_129_out, not_130_out, not_131_out, not_132_out, not_133_out, not_134_out, not_135_out,
       not_136_out, not_137_out, not_138_out, not_139_out, not_140_out, not_141_out, not_142_out,
       not_143_out, not_144_out, not_145_out, not_146_out, not_147_out, not_148_out, not_149_out,
       not_150_out, not_151_out, not_152_out, not_153_out, not_154_out, not_155_out, not_156_out,
       not_157_out, not_158_out, not_159_out, not_160_out, not_161_out, not_162_out, not_163_out,
       not_164_out, not_165_out, not_166_out, not_167_out, not_168_out, not_169_out, not_170_out,
       not_171_out, not_172_out, not_173_out, not_174_out, not_175_out, not_176_out, not_177_out,
       not_178_out, not_179_out, not_180_out, not_181_out, not_182_out, not_183_out, not_184_out,
       not_185_out, not_186_out, not_187_out, not_188_out, not_189_out, not_190_out, not_191_out,
       not_192_out, not_193_out, not_194_out, not_195_out, not_196_out, not_197_out, not_198_out,
       not_199_out, not_200_out, not_201_out, not_202_out, not_203_out, not_204_out, not_205_out,
       not_206_out, not_207_out, not_208_out, not_209_out, not_210_out, not_211_out, not_212_out,
       not_213_out, not_214_out, not_215_out, not_216_out, not_217_out, not_218_out, not_219_out,
       not_220_out, not_221_out, not_222_out, not_223_out, not_224_out, not_225_out, not_226_out,
       not_227_out, not_228_out, not_229_out, not_230_out, not_231_out, not_232_out, not_233_out,
       not_234_out, not_235_out, not_236_out, not_237_out, not_238_out, not_239_out, not_240_out,
       not_241_out, not_242_out, not_243_out, not_244_out, not_245_out, not_246_out, not_247_out,
       not_248_out, not_249_out, not_250_out, not_251_out, not_252_out, not_253_out, not_254_out,
       not_255_out, not_256_out, not_257_out, not_258_out, not_259_out, not_260_out, not_261_out,
       not_262_out, not_263_out, not_264_out, not_265_out, not_266_out, not_267_out, not_268_out,
       not_269_out, not_270_out, not_271_out, not_272_out, not_273_out, not_274_out, not_275_out,
       not_276_out, not_277_out, not_278_out, not_279_out, not_280_out, not_281_out, not_282_out,
       not_283_out, not_284_out, not_285_out, not_286_out, not_287_out, not_288_out, not_289_out,
       not_290_out, not_291_out, not_292_out, not_293_out, not_294_out, not_295_out, not_296_out,
       not_297_out, not_298_out, not_299_out, not_300_out, not_301_out, not_302_out, not_303_out,
       not_304_out, not_305_out, not_306_out, not_307_out, not_308_out, not_309_out, not_310_out,
       not_311_out, not_312_out, not_313_out, not_314_out, not_315_out, not_316_out, not_317_out,
       not_318_out, not_319_out, not_320_out, not_321_out, not_322_out, not_323_out, not_324_out,
       not_325_out, not_326_out, not_327_out, not_328_out, not_329_out, not_330_out, not_331_out,
       not_332_out, not_333_out, not_334_out, not_335_out, not_336_out, not_337_out, not_338_out,
       not_339_out, not_340_out, not_341_out, not_342_out, not_343_out, not_344_out, not_345_out,
       not_346_out, not_347_out, not_348_out, not_349_out, not_350_out, not_351_out, not_352_out,
       not_353_out, not_354_out;

  not not_1 (not_1_out, OP4);
  not not_2 (not_2_out, OP3);
  not not_3 (not_3_out, OP2);
  not not_4 (not_4_out, OP4);
  not not_5 (not_5_out, OP2);
  not not_6 (not_6_out, OP5);
  not not_7 (not_7_out, OP4);
  not not_8 (not_8_out, OP2);
  not not_9 (not_9_out, OP1);
  not not_10 (not_10_out, OP0);
  not not_11 (not_11_out, OP5);
  not not_12 (not_12_out, OP4);
  not not_13 (not_13_out, OP1);
  not not_14 (not_14_out, OP0);
  not not_15 (not_15_out, OP5);
  not not_16 (not_16_out, OP4);
  not not_17 (not_17_out, OP2);
  not not_18 (not_18_out, OP1);
  not not_19 (not_19_out, OP5);
  not not_20 (not_20_out, OP4);
  not not_21 (not_21_out, OP2);
  not not_22 (not_22_out, OP0);
  not not_23 (not_23_out, OP5);
  not not_24 (not_24_out, OP4);
  not not_25 (not_25_out, OP1);
  not not_26 (not_26_out, OP4);
  not not_27 (not_27_out, OP3);
  not not_28 (not_28_out, OP2);
  not not_29 (not_29_out, OP4);
  not not_30 (not_30_out, OP2);
  not not_31 (not_31_out, OP5);
  not not_32 (not_32_out, OP4);
  not not_33 (not_33_out, OP3);
  not not_34 (not_34_out, OP2);
  not not_35 (not_35_out, OP1);
  not not_36 (not_36_out, OP0);
  not not_37 (not_37_out, F5);
  not not_38 (not_38_out, F4);
  not not_39 (not_39_out, F3);
  not not_40 (not_40_out, F2);
  not not_41 (not_41_out, F1);
  not not_42 (not_42_out, F0);
  not not_43 (not_43_out, OP5);
  not not_44 (not_44_out, OP4);
  not not_45 (not_45_out, OP3);
  not not_46 (not_46_out, OP2);
  not not_47 (not_47_out, OP1);
  not not_48 (not_48_out, OP0);
  not not_49 (not_49_out, F5);
  not not_50 (not_50_out, F4);
  not not_51 (not_51_out, F3);
  not not_52 (not_52_out, F2);
  not not_53 (not_53_out, OP5);
  not not_54 (not_54_out, OP4);
  not not_55 (not_55_out, OP3);
  not not_56 (not_56_out, OP2);
  not not_57 (not_57_out, OP1);
  not not_58 (not_58_out, OP0);
  not not_59 (not_59_out, F5);
  not not_60 (not_60_out, F4);
  not not_61 (not_61_out, F3);
  not not_62 (not_62_out, F2);
  not not_63 (not_63_out, F0);
  not not_64 (not_64_out, OP5);
  not not_65 (not_65_out, OP4);
  not not_66 (not_66_out, OP3);
  not not_67 (not_67_out, OP2);
  not not_68 (not_68_out, OP1);
  not not_69 (not_69_out, OP0);
  not not_70 (not_70_out, F4);
  not not_71 (not_71_out, F3);
  not not_72 (not_72_out, F2);
  not not_73 (not_73_out, F1);
  not not_74 (not_74_out, F0);
  not not_75 (not_75_out, OP5);
  not not_76 (not_76_out, OP4);
  not not_77 (not_77_out, OP3);
  not not_78 (not_78_out, OP2);
  not not_79 (not_79_out, OP1);
  not not_80 (not_80_out, OP0);
  not not_81 (not_81_out, F4);
  not not_82 (not_82_out, F3);
  not not_83 (not_83_out, F2);
  not not_84 (not_84_out, F1);
  not not_85 (not_85_out, OP5);
  not not_86 (not_86_out, OP4);
  not not_87 (not_87_out, OP3);
  not not_88 (not_88_out, OP2);
  not not_89 (not_89_out, OP1);
  not not_90 (not_90_out, OP0);
  not not_91 (not_91_out, F4);
  not not_92 (not_92_out, F3);
  not not_93 (not_93_out, F2);
  not not_94 (not_94_out, F0);
  not not_95 (not_95_out, OP5);
  not not_96 (not_96_out, OP4);
  not not_97 (not_97_out, OP3);
  not not_98 (not_98_out, OP2);
  not not_99 (not_99_out, OP1);
  not not_100 (not_100_out, OP0);
  not not_101 (not_101_out, F4);
  not not_102 (not_102_out, F3);
  not not_103 (not_103_out, F1);
  not not_104 (not_104_out, F0);
  not not_105 (not_105_out, OP5);
  not not_106 (not_106_out, OP4);
  not not_107 (not_107_out, OP3);
  not not_108 (not_108_out, OP2);
  not not_109 (not_109_out, OP1);
  not not_110 (not_110_out, OP0);
  not not_111 (not_111_out, F4);
  not not_112 (not_112_out, F3);
  not not_113 (not_113_out, F1);
  not not_114 (not_114_out, OP5);
  not not_115 (not_115_out, OP4);
  not not_116 (not_116_out, OP3);
  not not_117 (not_117_out, OP2);
  not not_118 (not_118_out, OP1);
  not not_119 (not_119_out, OP0);
  not not_120 (not_120_out, F4);
  not not_121 (not_121_out, F3);
  not not_122 (not_122_out, OP5);
  not not_123 (not_123_out, OP4);
  not not_124 (not_124_out, OP3);
  not not_125 (not_125_out, OP2);
  not not_126 (not_126_out, OP1);
  not not_127 (not_127_out, OP0);
  not not_128 (not_128_out, F4);
  not not_129 (not_129_out, F2);
  not not_130 (not_130_out, F0);
  not not_131 (not_131_out, OP5);
  not not_132 (not_132_out, OP4);
  not not_133 (not_133_out, OP3);
  not not_134 (not_134_out, OP2);
  not not_135 (not_135_out, OP1);
  not not_136 (not_136_out, OP0);
  not not_137 (not_137_out, F4);
  not not_138 (not_138_out, F2);
  not not_139 (not_139_out, OP5);
  not not_140 (not_140_out, OP4);
  not not_141 (not_141_out, OP3);
  not not_142 (not_142_out, OP2);
  not not_143 (not_143_out, OP5);
  not not_144 (not_144_out, OP4);
  not not_145 (not_145_out, OP2);
  not not_146 (not_146_out, OP1);
  not not_147 (not_147_out, OP0);
  not not_148 (not_148_out, OP5);
  not not_149 (not_149_out, OP4);
  not not_150 (not_150_out, OP1);
  not not_151 (not_151_out, OP0);
  not not_152 (not_152_out, OP5);
  not not_153 (not_153_out, OP4);
  not not_154 (not_154_out, OP2);
  not not_155 (not_155_out, OP1);
  not not_156 (not_156_out, OP5);
  not not_157 (not_157_out, OP4);
  not not_158 (not_158_out, OP2);
  not not_159 (not_159_out, OP0);
  not not_160 (not_160_out, OP5);
  not not_161 (not_161_out, OP4);
  not not_162 (not_162_out, OP1);
  not not_163 (not_163_out, OP4);
  not not_164 (not_164_out, OP3);
  not not_165 (not_165_out, OP2);
  not not_166 (not_166_out, OP5);
  not not_167 (not_167_out, OP4);
  not not_168 (not_168_out, OP3);
  not not_169 (not_169_out, OP2);
  not not_170 (not_170_out, OP1);
  not not_171 (not_171_out, OP0);
  not not_172 (not_172_out, F5);
  not not_173 (not_173_out, F4);
  not not_174 (not_174_out, F1);
  not not_175 (not_175_out, F0);
  not not_176 (not_176_out, OP5);
  not not_177 (not_177_out, OP4);
  not not_178 (not_178_out, OP3);
  not not_179 (not_179_out, OP1);
  not not_180 (not_180_out, OP0);
  not not_181 (not_181_out, OP5);
  not not_182 (not_182_out, OP4);
  not not_183 (not_183_out, OP3);
  not not_184 (not_184_out, OP1);
  not not_185 (not_185_out, OP5);
  not not_186 (not_186_out, OP4);
  not not_187 (not_187_out, OP2);
  not not_188 (not_188_out, OP1);
  not not_189 (not_189_out, OP0);
  not not_190 (not_190_out, OP5);
  not not_191 (not_191_out, OP4);
  not not_192 (not_192_out, OP2);
  not not_193 (not_193_out, OP1);
  not not_194 (not_194_out, OP5);
  not not_195 (not_195_out, OP4);
  not not_196 (not_196_out, OP2);
  not not_197 (not_197_out, OP0);
  not not_198 (not_198_out, OP4);
  not not_199 (not_199_out, OP3);
  not not_200 (not_200_out, OP2);
  not not_201 (not_201_out, OP4);
  not not_202 (not_202_out, OP2);
  not not_203 (not_203_out, OP5);
  not not_204 (not_204_out, OP4);
  not not_205 (not_205_out, OP3);
  not not_206 (not_206_out, OP2);
  not not_207 (not_207_out, OP1);
  not not_208 (not_208_out, OP0);
  not not_209 (not_209_out, F5);
  not not_210 (not_210_out, F4);
  not not_211 (not_211_out, F3);
  not not_212 (not_212_out, F2);
  not not_213 (not_213_out, F1);
  not not_214 (not_214_out, F0);
  not not_215 (not_215_out, OP5);
  not not_216 (not_216_out, OP4);
  not not_217 (not_217_out, OP3);
  not not_218 (not_218_out, OP2);
  not not_219 (not_219_out, OP1);
  not not_220 (not_220_out, OP0);
  not not_221 (not_221_out, F5);
  not not_222 (not_222_out, F4);
  not not_223 (not_223_out, F3);
  not not_224 (not_224_out, F2);
  not not_225 (not_225_out, OP5);
  not not_226 (not_226_out, OP4);
  not not_227 (not_227_out, OP3);
  not not_228 (not_228_out, OP2);
  not not_229 (not_229_out, OP1);
  not not_230 (not_230_out, OP0);
  not not_231 (not_231_out, F5);
  not not_232 (not_232_out, F4);
  not not_233 (not_233_out, F3);
  not not_234 (not_234_out, F2);
  not not_235 (not_235_out, F0);
  not not_236 (not_236_out, OP5);
  not not_237 (not_237_out, OP4);
  not not_238 (not_238_out, OP3);
  not not_239 (not_239_out, OP2);
  not not_240 (not_240_out, OP1);
  not not_241 (not_241_out, OP0);
  not not_242 (not_242_out, F4);
  not not_243 (not_243_out, F3);
  not not_244 (not_244_out, F2);
  not not_245 (not_245_out, F1);
  not not_246 (not_246_out, F0);
  not not_247 (not_247_out, OP5);
  not not_248 (not_248_out, OP4);
  not not_249 (not_249_out, OP3);
  not not_250 (not_250_out, OP2);
  not not_251 (not_251_out, OP1);
  not not_252 (not_252_out, OP0);
  not not_253 (not_253_out, F4);
  not not_254 (not_254_out, F3);
  not not_255 (not_255_out, F2);
  not not_256 (not_256_out, F1);
  not not_257 (not_257_out, OP5);
  not not_258 (not_258_out, OP4);
  not not_259 (not_259_out, OP3);
  not not_260 (not_260_out, OP2);
  not not_261 (not_261_out, OP1);
  not not_262 (not_262_out, OP0);
  not not_263 (not_263_out, F4);
  not not_264 (not_264_out, F3);
  not not_265 (not_265_out, F2);
  not not_266 (not_266_out, F0);
  not not_267 (not_267_out, OP5);
  not not_268 (not_268_out, OP4);
  not not_269 (not_269_out, OP3);
  not not_270 (not_270_out, OP2);
  not not_271 (not_271_out, OP1);
  not not_272 (not_272_out, OP0);
  not not_273 (not_273_out, F4);
  not not_274 (not_274_out, F3);
  not not_275 (not_275_out, F1);
  not not_276 (not_276_out, F0);
  not not_277 (not_277_out, OP5);
  not not_278 (not_278_out, OP4);
  not not_279 (not_279_out, OP3);
  not not_280 (not_280_out, OP2);
  not not_281 (not_281_out, OP1);
  not not_282 (not_282_out, OP0);
  not not_283 (not_283_out, F4);
  not not_284 (not_284_out, F3);
  not not_285 (not_285_out, F1);
  not not_286 (not_286_out, OP5);
  not not_287 (not_287_out, OP4);
  not not_288 (not_288_out, OP3);
  not not_289 (not_289_out, OP2);
  not not_290 (not_290_out, OP1);
  not not_291 (not_291_out, OP0);
  not not_292 (not_292_out, F4);
  not not_293 (not_293_out, F3);
  not not_294 (not_294_out, OP5);
  not not_295 (not_295_out, OP4);
  not not_296 (not_296_out, OP3);
  not not_297 (not_297_out, OP2);
  not not_298 (not_298_out, OP1);
  not not_299 (not_299_out, OP0);
  not not_300 (not_300_out, F4);
  not not_301 (not_301_out, F2);
  not not_302 (not_302_out, F0);
  not not_303 (not_303_out, OP5);
  not not_304 (not_304_out, OP4);
  not not_305 (not_305_out, OP3);
  not not_306 (not_306_out, OP2);
  not not_307 (not_307_out, OP1);
  not not_308 (not_308_out, OP0);
  not not_309 (not_309_out, F4);
  not not_310 (not_310_out, F2);
  not not_311 (not_311_out, OP5);
  not not_312 (not_312_out, OP4);
  not not_313 (not_313_out, OP3);
  not not_314 (not_314_out, OP1);
  not not_315 (not_315_out, OP0);
  not not_316 (not_316_out, OP5);
  not not_317 (not_317_out, OP4);
  not not_318 (not_318_out, OP3);
  not not_319 (not_319_out, OP1);
  not not_320 (not_320_out, OP5);
  not not_321 (not_321_out, OP4);
  not not_322 (not_322_out, OP3);
  not not_323 (not_323_out, OP2);
  not not_324 (not_324_out, OP1);
  not not_325 (not_325_out, OP0);
  not not_326 (not_326_out, F5);
  not not_327 (not_327_out, F4);
  not not_328 (not_328_out, F2);
  not not_329 (not_329_out, F1);
  not not_330 (not_330_out, F0);
  not not_331 (not_331_out, OP5);
  not not_332 (not_332_out, OP4);
  not not_333 (not_333_out, OP3);
  not not_334 (not_334_out, OP2);
  not not_335 (not_335_out, OP1);
  not not_336 (not_336_out, OP0);
  not not_337 (not_337_out, F5);
  not not_338 (not_338_out, F4);
  not not_339 (not_339_out, F2);
  not not_340 (not_340_out, F1);
  not not_341 (not_341_out, F0);
  not not_342 (not_342_out, OP5);
  not not_343 (not_343_out, OP4);
  not not_344 (not_344_out, OP3);
  not not_345 (not_345_out, OP2);
  not not_346 (not_346_out, OP0);
  not not_347 (not_347_out, OP5);
  not not_348 (not_348_out, OP4);
  not not_349 (not_349_out, OP3);
  not not_350 (not_350_out, OP2);
  not not_351 (not_351_out, OP5);
  not not_352 (not_352_out, OP4);
  not not_353 (not_353_out, OP3);
  not not_354 (not_354_out, OP2);
  and and_1 (MemToReg, OP5, not_1_out, not_2_out, not_3_out, OP1, OP0);
  and and_2 (MemWrite, OP5, not_4_out, OP3, not_5_out, OP1, OP0);
  and and_3 (and_3_out, not_6_out, not_7_out, OP3, not_8_out, not_9_out, not_10_out);
  and and_4 (and_4_out, not_11_out, not_12_out, OP3, OP2, not_13_out, not_14_out);
  and and_5 (and_5_out, not_15_out, not_16_out, OP3, not_17_out, not_18_out, OP0);
  and and_6 (and_6_out, not_19_out, not_20_out, OP3, not_21_out, OP1, not_22_out);
  and and_7 (and_7_out, not_23_out, not_24_out, OP3, OP2, not_25_out, OP0);
  and and_8 (and_8_out, OP5, not_26_out, not_27_out, not_28_out, OP1, OP0);
  and and_9 (and_9_out, OP5, not_29_out, OP3, not_30_out, OP1, OP0);
  and and_10 (and_10_out, not_31_out, not_32_out, not_33_out, not_34_out, not_35_out, not_36_out, not_37_out, not_38_out, not_39_out, not_40_out, not_41_out, not_42_out);
  and and_11 (and_11_out, not_43_out, not_44_out, not_45_out, not_46_out, not_47_out, not_48_out, not_49_out, not_50_out, not_51_out, not_52_out, F1, F0);
  and and_12 (and_12_out, not_53_out, not_54_out, not_55_out, not_56_out, not_57_out, not_58_out, not_59_out, not_60_out, not_61_out, not_62_out, F1, not_63_out);
  and and_13 (and_13_out, not_64_out, not_65_out, not_66_out, not_67_out, not_68_out, not_69_out, F5, not_70_out, not_71_out, not_72_out, not_73_out, not_74_out);
  and and_14 (and_14_out, not_75_out, not_76_out, not_77_out, not_78_out, not_79_out, not_80_out, F5, not_81_out, not_82_out, not_83_out, not_84_out, F0);
  and and_15 (and_15_out, not_85_out, not_86_out, not_87_out, not_88_out, not_89_out, not_90_out, F5, not_91_out, not_92_out, not_93_out, F1, not_94_out);
  and and_16 (and_16_out, not_95_out, not_96_out, not_97_out, not_98_out, not_99_out, not_100_out, F5, not_101_out, not_102_out, F2, not_103_out, not_104_out);
  and and_17 (and_17_out, not_105_out, not_106_out, not_107_out, not_108_out, not_109_out, not_110_out, F5, not_111_out, not_112_out, F2, not_113_out, F0);
  and and_18 (and_18_out, not_114_out, not_115_out, not_116_out, not_117_out, not_118_out, not_119_out, F5, not_120_out, not_121_out, F2, F1, F0);
  and and_19 (and_19_out, not_122_out, not_123_out, not_124_out, not_125_out, not_126_out, not_127_out, F5, not_128_out, F3, not_129_out, F1, not_130_out);
  and and_20 (and_20_out, not_131_out, not_132_out, not_133_out, not_134_out, not_135_out, not_136_out, F5, not_137_out, F3, not_138_out, F1, F0);
  and and_21 (and_21_out, not_139_out, not_140_out, not_141_out, not_142_out, OP1, OP0);
  and and_22 (and_22_out, not_143_out, not_144_out, OP3, not_145_out, not_146_out, not_147_out);
  and and_23 (and_23_out, not_148_out, not_149_out, OP3, OP2, not_150_out, not_151_out);
  and and_24 (and_24_out, not_152_out, not_153_out, OP3, not_154_out, not_155_out, OP0);
  and and_25 (and_25_out, not_156_out, not_157_out, OP3, not_158_out, OP1, not_159_out);
  and and_26 (and_26_out, not_160_out, not_161_out, OP3, OP2, not_162_out, OP0);
  and and_27 (and_27_out, OP5, not_163_out, not_164_out, not_165_out, OP1, OP0);
  and and_28 (SysCALL, not_166_out, not_167_out, not_168_out, not_169_out, not_170_out, not_171_out, not_172_out, not_173_out, F3, F2, not_174_out, not_175_out);
  and and_29 (and_29_out, not_176_out, not_177_out, not_178_out, OP2, not_179_out, not_180_out);
  and and_30 (and_30_out, not_181_out, not_182_out, not_183_out, OP2, not_184_out, OP0);
  and and_31 (and_31_out, not_185_out, not_186_out, OP3, not_187_out, not_188_out, not_189_out);
  and and_32 (and_32_out, not_190_out, not_191_out, OP3, not_192_out, not_193_out, OP0);
  and and_33 (and_33_out, not_194_out, not_195_out, OP3, not_196_out, OP1, not_197_out);
  and and_34 (and_34_out, OP5, not_198_out, not_199_out, not_200_out, OP1, OP0);
  and and_35 (and_35_out, OP5, not_201_out, OP3, not_202_out, OP1, OP0);
  and and_36 (and_36_out, not_203_out, not_204_out, not_205_out, not_206_out, not_207_out, not_208_out, not_209_out, not_210_out, not_211_out, not_212_out, not_213_out, not_214_out);
  and and_37 (and_37_out, not_215_out, not_216_out, not_217_out, not_218_out, not_219_out, not_220_out, not_221_out, not_222_out, not_223_out, not_224_out, F1, F0);
  and and_38 (and_38_out, not_225_out, not_226_out, not_227_out, not_228_out, not_229_out, not_230_out, not_231_out, not_232_out, not_233_out, not_234_out, F1, not_235_out);
  and and_39 (and_39_out, not_236_out, not_237_out, not_238_out, not_239_out, not_240_out, not_241_out, F5, not_242_out, not_243_out, not_244_out, not_245_out, not_246_out);
  and and_40 (and_40_out, not_247_out, not_248_out, not_249_out, not_250_out, not_251_out, not_252_out, F5, not_253_out, not_254_out, not_255_out, not_256_out, F0);
  and and_41 (and_41_out, not_257_out, not_258_out, not_259_out, not_260_out, not_261_out, not_262_out, F5, not_263_out, not_264_out, not_265_out, F1, not_266_out);
  and and_42 (and_42_out, not_267_out, not_268_out, not_269_out, not_270_out, not_271_out, not_272_out, F5, not_273_out, not_274_out, F2, not_275_out, not_276_out);
  and and_43 (and_43_out, not_277_out, not_278_out, not_279_out, not_280_out, not_281_out, not_282_out, F5, not_283_out, not_284_out, F2, not_285_out, F0);
  and and_44 (and_44_out, not_286_out, not_287_out, not_288_out, not_289_out, not_290_out, not_291_out, F5, not_292_out, not_293_out, F2, F1, F0);
  and and_45 (and_45_out, not_294_out, not_295_out, not_296_out, not_297_out, not_298_out, not_299_out, F5, not_300_out, F3, not_301_out, F1, not_302_out);
  and and_46 (and_46_out, not_303_out, not_304_out, not_305_out, not_306_out, not_307_out, not_308_out, F5, not_309_out, F3, not_310_out, F1, F0);
  and and_47 (BEQ, not_311_out, not_312_out, not_313_out, OP2, not_314_out, not_315_out);
  and and_48 (BNE, not_316_out, not_317_out, not_318_out, OP2, not_319_out, OP0);
  and and_49 (JR, not_320_out, not_321_out, not_322_out, not_323_out, not_324_out, not_325_out, not_326_out, not_327_out, F3, not_328_out, not_329_out, not_330_out);
  and and_50 (and_50_out, not_331_out, not_332_out, not_333_out, not_334_out, not_335_out, not_336_out, not_337_out, not_338_out, F3, not_339_out, not_340_out, not_341_out);
  and and_51 (and_51_out, not_342_out, not_343_out, not_344_out, not_345_out, OP1, not_346_out);
  and and_52 (and_52_out, not_347_out, not_348_out, not_349_out, not_350_out, OP1, OP0);
  and and_53 (JAL, not_351_out, not_352_out, not_353_out, not_354_out, OP1, OP0);
  or or_1 (ALU_SRC, and_3_out, and_4_out, and_5_out, and_6_out, and_7_out, and_8_out, and_9_out);
  or or_2 (SignedExt, and_29_out, and_30_out, and_31_out, and_32_out, and_33_out, and_34_out, and_35_out);
  or or_3 (RegDst, and_36_out, and_37_out, and_38_out, and_39_out, and_40_out, and_41_out, and_42_out, and_43_out, and_44_out, and_45_out, and_46_out);
  or or_4 (JUMP, and_50_out, and_51_out, and_52_out);
  or or_5 (RegWrite, and_10_out, and_11_out, and_12_out, and_13_out, and_14_out, and_15_out, and_16_out, and_17_out, and_18_out, and_19_out, and_20_out, and_21_out, and_22_out, and_23_out, and_24_out, and_25_out, and_26_out, and_27_out);
endmodule

module MIPS_Regifile (
  input  [31:0] Din,
  input  Clk,
  input  WE,
  input  [4:0] R1_num,
  input  [4:0] W_num,
  input  [4:0] R2_num,
  output [31:0] R1,
  output [31:0] R2
);

  // RegisterFile registerfile_1: pin names not known; wires that end beside it: Din, Clk, WE, W_num, R1_num, R2_num, R1, R2
endmodule

// ALU
module MIPS_ALU (
  input  [4:0] shamt,
  input  [31:0] X,
  input  [31:0] Y,
  input  [3:0] AluOP,
  output Equal,
  output [31:0] Result,
  output [31:0] Result_2
);

  wire [0:0] comparator_1_lt, comparator_2_lt;
  wire [31:0] adder_1_out, AND_out, divider_1_out, divider_1_rem, multiplier_1_cout, multiplier_1_out,
       NOR_out, OR_out, shifter_1_out, shifter_2_out, shifter_3_out, subtractor_1_out, XOR_out;

  assign AND_out = X & Y;  // AND_Gate AND, 32 bits wide
  assign OR_out = X | Y;  // OR_Gate OR, 32 bits wide
  Shifter #(.width(32), .shift("ll")) shifter_1 (.in(Y), .\dist (shamt), .out(shifter_1_out));
  Shifter #(.width(32), .shift("ar")) shifter_2 (.in(Y), .\dist (shamt), .out(shifter_2_out));
  Shifter #(.width(32), .shift("lr")) shifter_3 (.in(Y), .\dist (shamt), .out(shifter_3_out));
  Multiplier #(.width(32)) multiplier_1 (.a(X), .b(Y), .out(multiplier_1_out), .cout(multiplier_1_cout));  // open: cin
  Divider #(.width(32)) divider_1 (.a(X), .b(Y), .out(divider_1_out), .rem(divider_1_rem));  // open: upper
  Adder #(.width(32)) adder_1 (.a(X), .b(Y), .out(adder_1_out));  // open: cin, cout
  Subtractor #(.width(32)) subtractor_1 (.a(X), .b(Y), .out(subtractor_1_out));  // open: bin, bout
  assign XOR_out = X ^ Y;  // XOR_Gate XOR, 32 bits wide
  assign NOR_out = ~(X | Y);  // NOR_Gate NOR, 32 bits wide
  Comparator #(.width(32), .mode("twosComplement")) comparator_1 (
    .a(X), .b(Y), .eq(Equal), .lt(comparator_1_lt[0]));  // open: gt
  Comparator #(.width(32), .mode("unsigned")) comparator_2 (.a(X), .b(Y), .lt(comparator_2_lt[0]));  // open: gt, eq
  Multiplexer #(.select(4), .width(32), .disabled("Z"), .enable("false")) multiplexer_1 (
    .in0(shifter_1_out), .in1(shifter_2_out), .in2(shifter_3_out), .in3(multiplier_1_out),
    .in4(divider_1_out), .in5(adder_1_out), .in6(subtractor_1_out), .in7(AND_out), .in8(OR_out),
    .in9(XOR_out), .in10(NOR_out), .in11({{31{1'b0}}, comparator_1_lt[0]}),
    .in12({{31{1'b0}}, comparator_2_lt[0]}), .in13({32{1'b0}}), .in14({32{1'b0}}), .in15({32{1'b0}}),
    .out(Result), .sel(AluOP));
  Multiplexer #(.select(4), .width(32), .disabled("Z"), .enable("false")) multiplexer_2 (
    .in0({32{1'b0}}), .in1({32{1'b0}}), .in2({32{1'b0}}), .in3(multiplier_1_cout), .in4(divider_1_rem),
    .in5({32{1'b0}}), .in6({32{1'b0}}), .in7({32{1'b0}}), .in8({32{1'b0}}), .in9({32{1'b0}}),
    .in10({32{1'b0}}), .in11({32{1'b0}}), .in12({32{1'b0}}), .in13({32{1'b0}}), .in14({32{1'b0}}),
    .in15({32{1'b0}}), .out(Result_2), .sel(AluOP));

  // Other names for the same wires on the sheet: Result2[31:0] = Result_2; S[3:0] = AluOP

  // Notes on the sheet:
  //   不要改变此引脚区域内容，也不要改变ALU封装形式
  //   输入引脚
  //   输出引脚
endmodule

module \中断按键参考电路  (
  input  \同步清零信号 ,
  output \与中断屏蔽位与 
);

  wire \_1号中断_out , and_1_out, clock_1_out, d_ff_1_q, or_1_out, or_2_out;

  Clock #(.highDuration(1), .lowDuration(1)) clock_1 (.out(clock_1_out));
  Button \_1号中断  (.out(\_1号中断_out ));
  LED #(.active("true")) \_1号中断等待指示灯  (.in(or_1_out));
  or or_1 (or_1_out, \与中断屏蔽位与 , d_ff_1_q);
  D_Flip_Flop #(.trigger("rising"), .Pre_Clr_Positions("LEGACY"), .NegatePresetClear("false"), .enable("true"), .NewFFLayout("false")) d_ff_1 (
    .clk(\_1号中断_out ), .D(1'b1), .Q(d_ff_1_q), .reset(\与中断屏蔽位与 ));  // open: Qn, preset, en
  or or_2 (or_2_out, d_ff_1_q, \与中断屏蔽位与 );
  and and_1 (and_1_out, or_2_out, ~\同步清零信号 );  // AND_Gate
  D_Flip_Flop #(.trigger("rising"), .Pre_Clr_Positions("LEGACY"), .NegatePresetClear("false"), .enable("true"), .NewFFLayout("false")) IR1 (
    .clk(clock_1_out), .D(and_1_out), .Q(\与中断屏蔽位与 ));  // open: Qn, preset, en, reset
  \单周期硬布线控制器_2  \u_单周期硬布线控制器_1  ();  // open: Func, OP, ALU_OP, MemToReg, MemWrite, ALU_SRC, RegWrite, SysCALL, SignedExt, RegDst, JR, JMP, Beq, JAL, Bne

  // Notes on the sheet:
  //   Reset 
endmodule
