// Logisim project cpu31.circ as structural Verilog: 27 circuits, main circuit ◇单周期MIPS
// 单周期硬布线控制器
module \单周期硬布线控制器  (
  input  [5:0] OP,
  input  [5:0] Func,
  output [3:0] ALU_OP,
  output MemToReg,
  output MemWrite,
  output ALU_SRC,
  output RegWrite,
  output SysCALL,
  output SignedExt,
  output RegDst,
  output Beq,
  output Bne,
  output JR,
  output JMP,
  output JAL,
  output LUI,
  output LB,
  output BLEZ
);

  \运算控制器自动生成  \u_运算控制器自动生成_1  (
    .OP0(OP[0]), .OP1(OP[1]), .OP2(OP[2]), .OP3(OP[3]), .OP4(OP[4]), .OP5(OP[5]), .F0(Func[0]), .F1(Func[1]),
    .F2(Func[2]), .F3(Func[3]), .F4(Func[4]), .F5(Func[5]), .S0(ALU_OP[0]), .S1(ALU_OP[1]), .S2(ALU_OP[2]),
    .S3(ALU_OP[3]));
  \控制信号自动生成  \u_控制信号自动生成_1  (
    .OP0(OP[0]), .OP1(OP[1]), .OP2(OP[2]), .MemToReg(MemToReg), .OP3(OP[3]), .OP4(OP[4]), .OP5(OP[5]),
    .F0(Func[0]), .MemWrite(MemWrite), .F1(Func[1]), .F2(Func[2]), .F3(Func[3]), .F4(Func[4]), .F5(Func[5]),
    .ALU_SRC(ALU_SRC), .RegWrite(RegWrite), .SysCALL(SysCALL), .SignedExt(SignedExt), .RegDst(RegDst),
    .BEQ(Beq), .BNE(Bne), .JR(JR), .JUMP(JMP), .JAL(JAL), .LUI(LUI), .LB(LB), .BLEZ(BLEZ));

  // Other names for the same wires on the sheet: OP_CODE[5:0] = OP

  // Notes on the sheet:
  //   运算器控制器，根据指令生成运算器功能选择信号
  //   控制信号生成，产生数据通路需要的其他控制信号
endmodule

module \单周期MIPS  (
  output RegWrite,
  output MemWrite,
  output [31:0] PC,
  output [31:0] IR,
  output [31:0] RDin,
  output [31:0] MDin,
  output [31:0] LedData
);

  wire and_1_out, and_2_out, B___De, BLEZ, BLEZ_DE, CLK, comparator_1_gt, comparator_2_eq, Go, IR1, IR2, IR3,
       LB, LUI, mips_alu_1_equal, multiplexer_12_out, not_1_out, not_2_out, SignedExt, Syscall, W1, W2, W3,
       \单周期硬布线控制器_1_alu_src , \单周期硬布线控制器_1_beq , \单周期硬布线控制器_1_bne , \单周期硬布线控制器_1_jr , \单周期硬布线控制器_1_memtoreg ,
       \运行 ;
  wire [1:0] or_1_out, \单周期硬布线控制器_1_regdst ;
  wire [3:0] \单周期硬布线控制器_1_alu_op ;
  wire [4:0] multiplexer_2_out, multiplexer_3_out, multiplexer_4_out;
  wire [7:0] multiplexer_10_out, multiplexer_11_out, multiplexer_11_out_2, multiplexer_11_out_3,
       multiplexer_11_out_4;
  wire [15:0] \总周期数 ;
  wire [27:0] Next_PC;
  wire [31:0] B___PC, bit_extender_1_out, bit_extender_2_out, bit_extender_3_out, JR_PC, mips_alu_1_result,
       multiplexer_1_out, multiplexer_5_out, multiplexer_7_out, multiplexer_8_out, multiplexer_9_out,
       ram_1_data, shifter_1_out;
  wire [31:28] J_JAL_PC;

  Clock #(.highDuration(1), .lowDuration(1)) clock_1 (.out(CLK));
  Button _1 (.out(IR1));
  Button _2 (.out(IR2));
  Button _3 (.out(IR3));
  or or_1 (or_1_out[0], \单周期硬布线控制器_1_jr , BLEZ_DE, B___De);
  Multiplexer #(.select(2), .width(32), .disabled("Z"), .enable("false")) multiplexer_1 (
    .in0({J_JAL_PC, Next_PC}), .in1(B___PC), .in2({J_JAL_PC, IR[25:0], 2'b00}), .in3(JR_PC),
    .out(multiplexer_1_out), .sel(or_1_out));
  Button \u_继续运行  (.out(Go));
  LED #(.active("true")) led_1 (.in(W1));
  LED #(.active("true")) led_2 (.in(W2));
  LED #(.active("true")) led_3 (.in(W3));
  Register #(.width(32), .trigger("rising"), .Select("low")) u_PC (
    .D(multiplexer_1_out), .en(\运行 ), .Q(PC), .clk(CLK));  // open: clr
  Hex_Digit_Display hex_digit_display_1 (.value(LedData[31:28]));  // open: dp
  Hex_Digit_Display hex_digit_display_2 (.value(LedData[27:24]));  // open: dp
  Hex_Digit_Display hex_digit_display_3 (.value(LedData[23:20]));  // open: dp
  Hex_Digit_Display hex_digit_display_4 (.value(LedData[19:16]));  // open: dp
  Adder #(.width(32)) adder_1 (.a(PC), .b(32'h4), .out({J_JAL_PC, Next_PC}));  // open: cin, cout
  Hex_Digit_Display hex_digit_display_5 (.value(LedData[15:12]));  // open: dp
  Hex_Digit_Display hex_digit_display_6 (.value(LedData[11:8]));  // open: dp
  ROM #(.addrWidth(10), .dataWidth(32), .Select("high")) rom_1 (.addr(PC[11:2]), .data(IR));
  Hex_Digit_Display hex_digit_display_7 (.value(LedData[7:4]));  // open: dp
  Hex_Digit_Display hex_digit_display_8 (.value(LedData[3:0]));  // open: dp
  // Probe on \总周期数 
  \单周期硬布线控制器  \u_单周期硬布线控制器_1  (
    .Func(IR[5:0]), .OP(IR[31:26]), .ALU_OP(\单周期硬布线控制器_1_alu_op ), .MemToReg(\单周期硬布线控制器_1_memtoreg ),
    .MemWrite(MemWrite), .ALU_SRC(\单周期硬布线控制器_1_alu_src ), .RegWrite(RegWrite), .SysCALL(Syscall),
    .SignedExt(SignedExt), .RegDst(\单周期硬布线控制器_1_regdst [0]), .JR(\单周期硬布线控制器_1_jr ), .JMP(or_1_out[1]),
    .Beq(\单周期硬布线控制器_1_beq ), .JAL(\单周期硬布线控制器_1_regdst [1]), .Bne(\单周期硬布线控制器_1_bne ), .LUI(LUI), .LB(LB),
    .BLEZ(BLEZ));
  Multiplexer #(.select(1), .width(5), .disabled("Z"), .enable("false")) multiplexer_2 (
    .in0(IR[25:21]), .in1(5'b00010), .out(multiplexer_2_out), .sel(Syscall));
  Multiplexer #(.select(1), .width(5), .disabled("Z"), .enable("false")) multiplexer_3 (
    .in0(IR[20:16]), .in1(5'b00100), .out(multiplexer_3_out), .sel(Syscall));
  assign bit_extender_1_out = {{16{1'b0}}, IR[15:0]};  // Bit_Extender bit_extender_1
  assign bit_extender_2_out = {{16{IR[15]}}, IR[15:0]};  // Bit_Extender bit_extender_2
  Multiplexer #(.select(2), .width(5), .disabled("Z"), .enable("false")) multiplexer_4 (
    .in0(IR[20:16]), .in1(IR[15:11]), .in2({5{1'b1}}), .out(multiplexer_4_out), .sel(\单周期硬布线控制器_1_regdst ));  // open: in3
  Multiplexer #(.select(1), .width(32), .disabled("Z"), .enable("false")) multiplexer_5 (
    .in0(bit_extender_1_out), .in1(bit_extender_2_out), .out(multiplexer_5_out), .sel(SignedExt));
  Multiplexer #(.select(1), .width(32), .disabled("Z"), .enable("false")) multiplexer_6 (
    .in0(multiplexer_7_out), .in1({J_JAL_PC, Next_PC}), .out(RDin), .sel(\单周期硬布线控制器_1_regdst [1]));
  Multiplexer #(.select(1), .width(32), .disabled("Z"), .enable("false")) multiplexer_7 (
    .in0(multiplexer_9_out), .in1({IR[15:0], {16{1'b0}}}), .out(multiplexer_7_out), .sel(LUI));
  MIPS_Regifile mips_regifile_1 (
    .Din(RDin), .Clk(CLK), .R1(JR_PC), .R2(MDin), .WE(RegWrite), .W_num(multiplexer_4_out),
    .R1_num(multiplexer_2_out), .R2_num(multiplexer_3_out));
  Comparator #(.width(32), .mode("twosComplement")) comparator_1 (
    .a(JR_PC), .b({32{1'b0}}), .gt(comparator_1_gt));  // open: eq, lt
  Multiplexer #(.select(1), .width(32), .disabled("Z"), .enable("false")) multiplexer_8 (
    .in0(MDin), .in1(multiplexer_5_out), .out(multiplexer_8_out), .sel(\单周期硬布线控制器_1_alu_src ));
  Shifter #(.width(32), .shift("ll")) shifter_1 (.in(multiplexer_5_out), .\dist (5'b00010), .out(shifter_1_out));
  not not_1 (not_1_out, mips_alu_1_equal);
  not not_2 (not_2_out, comparator_1_gt);
  MIPS_ALU mips_alu_1 (
    .X(JR_PC), .Y(multiplexer_8_out), .AluOP(\单周期硬布线控制器_1_alu_op ), .Equal(mips_alu_1_equal),
    .Result(mips_alu_1_result), .shamt(IR[10:6]));  // open: Result_2
  Adder #(.width(32)) adder_2 (.a(shifter_1_out), .b({J_JAL_PC, Next_PC}), .out(B___PC));  // open: cin, cout
  and and_1 (and_1_out, mips_alu_1_equal, \单周期硬布线控制器_1_beq );
  and and_2 (and_2_out, not_1_out, \单周期硬布线控制器_1_bne );
  Multiplexer #(.select(1), .width(32), .disabled("Z"), .enable("false")) multiplexer_9 (
    .in0({multiplexer_11_out_4, multiplexer_11_out_3, multiplexer_11_out_2, multiplexer_11_out}),
    .in1(bit_extender_3_out), .out(multiplexer_9_out), .sel(LB));
  or or_2 (B___De, and_1_out, and_2_out);
  and and_3 (BLEZ_DE, BLEZ, not_2_out);
  Comparator #(.width(32), .mode("twosComplement")) comparator_2 (
    .a(JR_PC), .b(32'h22), .eq(comparator_2_eq));  // open: gt, lt
  RAM #(.addrWidth(10), .dataWidth(32), .bus("separate"), .Select("high")) ram_1 (
    .addr(mips_alu_1_result[11:2]), .din(MDin), .data(ram_1_data), .str(MemWrite), .clk(CLK));  // open: sel, ld, clr
  Multiplexer #(.select(2), .width(8), .disabled("Z"), .enable("false")) multiplexer_10 (
    .in0(multiplexer_11_out), .in1(multiplexer_11_out_2), .in2(multiplexer_11_out_3),
    .in3(multiplexer_11_out_4), .out(multiplexer_10_out), .sel(mips_alu_1_result[1:0]));
  assign bit_extender_3_out = {{24{multiplexer_10_out[7]}}, multiplexer_10_out};  // Bit_Extender bit_extender_3
  Counter #(.width(16), .max('hffff), .ongoal("wrap"), .trigger("rising"), .behavior("old")) counter_1 (
    .count(\运行 ), .Q(\总周期数 ), .clk(CLK));  // open: load, D, carry, clr, preset
  Multiplexer #(.select(1), .width(32), .disabled("Z"), .enable("false")) multiplexer_11 (
    .in0(mips_alu_1_result), .in1(ram_1_data),
    .out({multiplexer_11_out_4, multiplexer_11_out_3, multiplexer_11_out_2, multiplexer_11_out}),
    .sel(\单周期硬布线控制器_1_memtoreg ));
  Multiplexer #(.select(1), .width(1), .disabled("Z"), .enable("false")) multiplexer_12 (
    .in0(1'b0), .in1(comparator_2_eq), .out(multiplexer_12_out), .sel(Syscall));
  or or_3 (\运行 , Go, multiplexer_12_out, ~Syscall);  // OR_Gate
  Register #(.width(32), .trigger("rising"), .Select("low")) register_1 (
    .D(MDin), .en(multiplexer_12_out), .Q(LedData), .clk(CLK));  // open: clr

  // Other names for the same wires on the sheet: a0[31:0] = MDin; J_JAL_PC[27:2] = IR[25:0];
  //   Next_PC[31:28] = J_JAL_PC

  // Notes on the sheet:
  //   中断源
  //   中断等待指示
  //   总复位信号应将除ROM以外所有存储组件全部清零
  //   指令存储器
  //   数码管输出
  //   指令字
  //   contents of rom_1 (hex, n*v repeats v):
  //   20110001 8000c05 20110001 20120002 20130003 8000c09 20110001 20120002 20130003 8000c0d 20110001
  //   20120002 20130003 8000c11 20110001 20120002 20130003 c000cb8 20100001 20110001 118fc0 112020
  //   20020022 c 118882 12200001 8000c15 112020 20020022 c 20110001 118880 112020 20020022 c 12200001
  //   8000c1f 20110001 118fc0 112020 20020022 c 1188c3 112020 20020022 c 118903 112020 20020022 c 118903
  //   112020 20020022 c 118903 112020 20020022 c 118903 112020 20020022 c 118903 112020 20020022 c 118903
  //   112020 20020022 c 118903 112020 20020022 c 20100001 109fc0 139fc3 8021 2012000c 24160003 26100001
  //   3210000f 20080008 20090001 139900 2709825 132020 20020022 c 1094022 1500fff9 22100001 2018000f
  //   2188024 108700 20080008 20090001 139902 2709825 132021 20020022 c 1094022 1500fff9 108702 2c9b022
  //   12c00001 8000c50 4020 1084027 84400 3508ffff 82021 20020022 c 2010ffff 20110000 ae300000 22100001
  //   22310004 ae300000 22100001 22310004 ae300000 22100001 22310004 ae300000 22100001 22310004 ae300000
  //   22100001 22310004 ae300000 22100001 22310004 ae300000 22100001 22310004 ae300000 22100001 22310004
  //   ae300000 22100001 22310004 ae300000 22100001 22310004 ae300000 22100001 22310004 ae300000 22100001
  //   22310004 ae300000 22100001 22310004 ae300000 22100001 22310004 ae300000 22100001 22310004 ae300000
  //   22100001 22310004 22100001 8020 2011003c 8e130000 8e340000 274402a 11000002 ae330000 ae140000
  //   2231fffc 1611fff8 102020 20020022 c 22100004 2011003c 1611fff2 20020032 c 20100000 22100001 102020
  //   20020022 c 22100002 102020 20020022 c 22100003 102020 20020022 c 22100004 102020 20020022 c 22100005
  //   102020 20020022 c 22100006 102020 20020022 c 22100007 102020 20020022 c 22100008 102020 20020022
  //   20020022 c 3e00008
  //   数码管输出应该用寄存器锁存，否则显示数据只能一闪而过
  //   OP
  //   Func
  //   rs
  //   rt
  //   rd
  //   JMP
  //   JR
  //   LUI
  //   LB
  //   BLEZ
  //   OP
  //   Func
  //   Beq
  //   Bne
  //   AluOP
  //   AluSrcB
  //   RegWrite
  //   JAL
  //   RegDst
  //   Syscall
  //   MemToReg
  //   MemWrite
  //   为方便自动评测，需要输出PC，IR，寄存器文件写入端口RDin，内存写入端口MDin等信号
endmodule

// 运算器控制器
module \运算控制器自动生成  (
  input  OP0,
  input  OP1,
  input  OP2,
  input  OP3,
  input  OP4,
  input  OP5,
  input  F0,
  input  F1,
  input  F2,
  input  F3,
  input  F4,
  input  F5,
  output S0,
  output S1,
  output S2,
  output S3
);

  wire and_1_out, and_2_out, and_3_out, and_4_out, and_5_out, and_6_out, and_7_out, and_8_out, and_9_out,
       and_10_out, and_11_out, and_12_out, and_13_out, and_14_out, and_15_out, and_16_out, and_17_out,
       and_18_out, and_19_out, and_20_out, and_21_out, and_22_out, and_23_out, and_24_out, and_25_out,
       and_26_out, and_27_out, and_28_out, and_29_out, and_30_out, and_31_out, and_32_out, and_33_out,
       and_34_out, and_35_out, and_36_out, and_37_out, and_38_out, and_39_out, and_40_out, not_1_out,
       not_2_out, not_3_out, not_4_out, not_5_out, not_6_out, not_7_out, not_8_out, not_9_out, not_10_out,
       not_11_out, not_12_out, not_13_out, not_14_out, not_15_out, not_16_out, not_17_out, not_18_out,
       not_19_out, not_20_out, not_21_out, not_22_out, not_23_out, not_24_out, not_25_out, not_26_out,
       not_27_out, not_28_out, not_29_out, not_30_out, not_31_out, not_32_out, not_33_out, not_34_out,
       not_35_out, not_36_out, not_37_out, not_38_out, not_39_out, not_40_out, not_41_out, not_42_out,
       not_43_out, not_44_out, not_45_out, not_46_out, not_47_out, not_48_out, not_49_out, not_50_out,
       not_51_out, not_52_out, not_53_out, not_54_out, not_55_out, not_56_out, not_57_out, not_58_out,
       not_59_out, not_60_out, not_61_out, not_62_out, not_63_out, not_64_out, not_65_out, not_66_out,
       not_67_out, not_68_out, not_69_out, not_70_out, not_71_out, not_72_out, not_73_out, not_74_out,
       not_75_out, not_76_out, not_77_out, not_78_out, not_79_out, not_80_out, not_81_out, not_82_out,
       not_83_out, not_84_out, not_85_out, not_86_out, not_87_out, not_88_out, not_89_out, not_90_out,
       not_91_out, not_92_out, not_93_out, not_94_out, not_95_out, not_96_out, not_97_out, not_98_out,
       not_99_out, not_100_out, not_101_out, not_102_out, not_103_out, not_104_out, not_105_out, not_106_out,
       not_107_out, not_108_out, not_109_out, not_110_out, not_111_out, not_112_out, not_113_out,
       not_114_out, not_115_out, not_116_out, not_117_out, not_118_out, not_119_out, not_120_out,
       not_121_out, not_122_out, not_123_out, not_124_out, not_125_out, not_126_out, not_127_out,
       not_128_out, not_129_out, not_130_out, not_131_out, not_132_out, not_133_out, not_134_out,
       not_135_out, not_136_out, not_137_out, not_138_out, not_139_out, not_140_out, not_141_out,
       not_142_out, not_143_out, not_144_out, not_145_out, not_146_out, not_147_out, not_148_out,
       not_149_out, not_150_out, not_151_out, not_152_out, not_153_out, not_154_out, not_155_out,
       not_156_out, not_157_out, not_158_out, not_159_out, not_160_out, not_161_out, not_162_out,
       not_163_out, not_164_out, not_165_out, not_166_out, not_167_out, not_168_out, not_169_out,
       not_170_out, not_171_out, not_172_out, not_173_out, not_174_out, not_175_out, not_176_out,
       not_177_out, not_178_out, not_179_out, not_180_out, not_181_out, not_182_out, not_183_out,
       not_184_out, not_185_out, not_186_out, not_187_out, not_188_out, not_189_out, not_190_out,
       not_191_out, not_192_out, not_193_out, not_194_out, not_195_out, not_196_out, not_197_out,
       not_198_out, not_199_out, not_200_out, not_201_out, not_202_out, not_203_out, not_204_out,
       not_205_out, not_206_out, not_207_out, not_208_out, not_209_out, not_210_out, not_211_out,
       not_212_out, not_213_out, not_214_out, not_215_out, not_216_out, not_217_out, not_218_out,
       not_219_out, not_220_out, not_221_out, not_222_out, not_223_out, not_224_out, not_225_out,
       not_226_out, not_227_out, not_228_out, not_229_out, not_230_out, not_231_out, not_232_out,
       not_233_out, not_234_out, not_235_out, not_236_out, not_237_out, not_238_out, not_239_out,
       not_240_out, not_241_out, not_242_out, not_243_out, not_244_out, not_245_out, not_246_out,
       not_247_out, not_248_out, not_249_out, not_250_out, not_251_out, not_252_out, not_253_out,
       not_254_out, not_255_out, not_256_out, not_257_out, not_258_out, not_259_out, not_260_out,
       not_261_out, not_262_out, not_263_out, not_264_out, not_265_out, not_266_out, not_267_out,
       not_268_out, not_269_out, not_270_out, not_271_out, not_272_out, not_273_out, not_274_out,
       not_275_out, not_276_out, not_277_out, not_278_out, not_279_out, not_280_out, not_281_out;

  not not_1 (not_1_out, OP5);
  not not_2 (not_2_out, OP4);
  not not_3 (not_3_out, OP3);
  not not_4 (not_4_out, OP2);
  not not_5 (not_5_out, OP1);
  not not_6 (not_6_out, OP0);
  not not_7 (not_7_out, F5);
  not not_8 (not_8_out, F4);
  not not_9 (not_9_out, F3);
  not not_10 (not_10_out, F2);
  not not_11 (not_11_out, OP5);
  not not_12 (not_12_out, OP4);
  not not_13 (not_13_out, OP3);
  not not_14 (not_14_out, OP2);
  not not_15 (not_15_out, OP1);
  not not_16 (not_16_out, OP0);
  not not_17 (not_17_out, F4);
  not not_18 (not_18_out, F3);
  not not_19 (not_19_out, F2);
  not not_20 (not_20_out, F1);
  not not_21 (not_21_out, F0);
  not not_22 (not_22_out, OP5);
  not not_23 (not_23_out, OP4);
  not not_24 (not_24_out, OP3);
  not not_25 (not_25_out, OP2);
  not not_26 (not_26_out, OP1);
  not not_27 (not_27_out, OP0);
  not not_28 (not_28_out, F4);
  not not_29 (not_29_out, F3);
  not not_30 (not_30_out, F2);
  not not_31 (not_31_out, F1);
  not not_32 (not_32_out, OP5);
  not not_33 (not_33_out, OP4);
  not not_34 (not_34_out, OP3);
  not not_35 (not_35_out, OP2);
  not not_36 (not_36_out, OP1);
  not not_37 (not_37_out, OP0);
  not not_38 (not_38_out, F4);
  not not_39 (not_39_out, F3);
  not not_40 (not_40_out, F1);
  not not_41 (not_41_out, F0);
  not not_42 (not_42_out, OP5);
  not not_43 (not_43_out, OP4);
  not not_44 (not_44_out, OP3);
  not not_45 (not_45_out, OP2);
  not not_46 (not_46_out, OP1);
  not not_47 (not_47_out, OP0);
  not not_48 (not_48_out, F4);
  not not_49 (not_49_out, F2);
  not not_50 (not_50_out, F0);
  not not_51 (not_51_out, OP5);
  not not_52 (not_52_out, OP4);
  not not_53 (not_53_out, OP2);
  not not_54 (not_54_out, OP1);
  not not_55 (not_55_out, OP0);
  not not_56 (not_56_out, OP5);
  not not_57 (not_57_out, OP4);
  not not_58 (not_58_out, OP1);
  not not_59 (not_59_out, OP0);
  not not_60 (not_60_out, OP5);
  not not_61 (not_61_out, OP4);
  not not_62 (not_62_out, OP2);
  not not_63 (not_63_out, OP1);
  not not_64 (not_64_out, OP5);
  not not_65 (not_65_out, OP4);
  not not_66 (not_66_out, OP2);
  not not_67 (not_67_out, OP0);
  not not_68 (not_68_out, OP4);
  not not_69 (not_69_out, OP3);
  not not_70 (not_70_out, OP2);
  not not_71 (not_71_out, OP4);
  not not_72 (not_72_out, OP2);
  not not_73 (not_73_out, OP5);
  not not_74 (not_74_out, OP4);
  not not_75 (not_75_out, OP3);
  not not_76 (not_76_out, OP2);
  not not_77 (not_77_out, OP1);
  not not_78 (not_78_out, OP0);
  not not_79 (not_79_out, F4);
  not not_80 (not_80_out, F3);
  not not_81 (not_81_out, F0);
  not not_82 (not_82_out, OP4);
  not not_83 (not_83_out, OP3);
  not not_84 (not_84_out, OP2);
  not not_85 (not_85_out, OP1);
  not not_86 (not_86_out, OP0);
  not not_87 (not_87_out, OP5);
  not not_88 (not_88_out, OP4);
  not not_89 (not_89_out, OP3);
  not not_90 (not_90_out, OP2);
  not not_91 (not_91_out, OP1);
  not not_92 (not_92_out, OP0);
  not not_93 (not_93_out, F5);
  not not_94 (not_94_out, F4);
  not not_95 (not_95_out, F3);
  not not_96 (not_96_out, F2);
  not not_97 (not_97_out, F0);
  not not_98 (not_98_out, OP5);
  not not_99 (not_99_out, OP4);
  not not_100 (not_100_out, OP3);
  not not_101 (not_101_out, OP2);
  not not_102 (not_102_out, OP1);
  not not_103 (not_103_out, OP0);
  not not_104 (not_104_out, F4);
  not not_105 (not_105_out, F3);
  not not_106 (not_106_out, F2);
  not not_107 (not_107_out, F0);
  not not_108 (not_108_out, OP5);
  not not_109 (not_109_out, OP4);
  not not_110 (not_110_out, OP3);
  not not_111 (not_111_out, OP2);
  not not_112 (not_112_out, OP1);
  not not_113 (not_113_out, OP0);
  not not_114 (not_114_out, F4);
  not not_115 (not_115_out, F3);
  not not_116 (not_116_out, F1);
  not not_117 (not_117_out, F0);
  not not_118 (not_118_out, OP5);
  not not_119 (not_119_out, OP4);
  not not_120 (not_120_out, OP3);
  not not_121 (not_121_out, OP2);
  not not_122 (not_122_out, OP1);
  not not_123 (not_123_out, OP0);
  not not_124 (not_124_out, F4);
  not not_125 (not_125_out, F3);
  not not_126 (not_126_out, OP5);
  not not_127 (not_127_out, OP4);
  not not_128 (not_128_out, OP3);
  not not_129 (not_129_out, OP2);
  not not_130 (not_130_out, OP1);
  not not_131 (not_131_out, OP0);
  not not_132 (not_132_out, F4);
  not not_133 (not_133_out, F2);
  not not_134 (not_134_out, F0);
  not not_135 (not_135_out, OP5);
  not not_136 (not_136_out, OP4);
  not not_137 (not_137_out, OP1);
  not not_138 (not_138_out, OP0);
  not not_139 (not_139_out, OP5);
  not not_140 (not_140_out, OP4);
  not not_141 (not_141_out, OP2);
  not not_142 (not_142_out, OP0);
  not not_143 (not_143_out, OP5);
  not not_144 (not_144_out, OP4);
  not not_145 (not_145_out, OP3);
  not not_146 (not_146_out, OP2);
  not not_147 (not_147_out, OP1);
  not not_148 (not_148_out, OP0);
  not not_149 (not_149_out, F4);
  not not_150 (not_150_out, F3);
  not not_151 (not_151_out, F2);
  not not_152 (not_152_out, F1);
  not not_153 (not_153_out, F0);
  not not_154 (not_154_out, OP5);
  not not_155 (not_155_out, OP4);
  not not_156 (not_156_out, OP3);
  not not_157 (not_157_out, OP2);
  not not_158 (not_158_out, OP1);
  not not_159 (not_159_out, OP0);
  not not_160 (not_160_out, F4);
  not not_161 (not_161_out, F3);
  not not_162 (not_162_out, F2);
  not not_163 (not_163_out, F1);
  not not_164 (not_164_out, OP5);
  not not_165 (not_165_out, OP4);
  not not_166 (not_166_out, OP3);
  not not_167 (not_167_out, OP2);
  not not_168 (not_168_out, OP1);
  not not_169 (not_169_out, OP0);
  not not_170 (not_170_out, F4);
  not not_171 (not_171_out, F3);
  not not_172 (not_172_out, F2);
  not not_173 (not_173_out, F0);
  not not_174 (not_174_out, OP5);
  not not_175 (not_175_out, OP4);
  not not_176 (not_176_out, OP3);
  not not_177 (not_177_out, OP2);
  not not_178 (not_178_out, OP1);
  not not_179 (not_179_out, OP0);
  not not_180 (not_180_out, F4);
  not not_181 (not_181_out, F3);
  not not_182 (not_182_out, F1);
  not not_183 (not_183_out, F0);
  not not_184 (not_184_out, OP5);
  not not_185 (not_185_out, OP4);
  not not_186 (not_186_out, OP3);
  not not_187 (not_187_out, OP2);
  not not_188 (not_188_out, OP1);
  not not_189 (not_189_out, OP0);
  not not_190 (not_190_out, F4);
  not not_191 (not_191_out, F2);
  not not_192 (not_192_out, OP5);
  not not_193 (not_193_out, OP4);
  not not_194 (not_194_out, OP2);
  not not_195 (not_195_out, OP1);
  not not_196 (not_196_out, OP0);
  not not_197 (not_197_out, OP5);
  not not_198 (not_198_out, OP4);
  not not_199 (not_199_out, OP1);
  not not_200 (not_200_out, OP0);
  not not_201 (not_201_out, OP5);
  not not_202 (not_202_out, OP4);
  not not_203 (not_203_out, OP2);
  not not_204 (not_204_out, OP1);
  not not_205 (not_205_out, OP4);
  not not_206 (not_206_out, OP3);
  not not_207 (not_207_out, OP2);
  not not_208 (not_208_out, OP4);
  not not_209 (not_209_out, OP2);
  not not_210 (not_210_out, OP4);
  not not_211 (not_211_out, OP3);
  not not_212 (not_212_out, OP2);
  not not_213 (not_213_out, OP1);
  not not_214 (not_214_out, OP0);
  not not_215 (not_215_out, OP5);
  not not_216 (not_216_out, OP4);
  not not_217 (not_217_out, OP3);
  not not_218 (not_218_out, OP2);
  not not_219 (not_219_out, OP1);
  not not_220 (not_220_out, OP0);
  not not_221 (not_221_out, F4);
  not not_222 (not_222_out, F3);
  not not_223 (not_223_out, F1);
  not not_224 (not_224_out, OP5);
  not not_225 (not_225_out, OP4);
  not not_226 (not_226_out, OP3);
  not not_227 (not_227_out, OP2);
  not not_228 (not_228_out, OP1);
  not not_229 (not_229_out, OP0);
  not not_230 (not_230_out, F4);
  not not_231 (not_231_out, F3);
  not not_232 (not_232_out, OP5);
  not not_233 (not_233_out, OP4);
  not not_234 (not_234_out, OP3);
  not not_235 (not_235_out, OP2);
  not not_236 (not_236_out, OP1);
  not not_237 (not_237_out, OP0);
  not not_238 (not_238_out, F4);
  not not_239 (not_239_out, F3);
  not not_240 (not_240_out, F1);
  not not_241 (not_241_out, OP5);
  not not_242 (not_242_out, OP4);
  not not_243 (not_243_out, OP3);
  not not_244 (not_244_out, OP2);
  not not_245 (not_245_out, OP1);
  not not_246 (not_246_out, OP0);
  not not_247 (not_247_out, F4);
  not not_248 (not_248_out, F3);
  not not_249 (not_249_out, OP5);
  not not_250 (not_250_out, OP4);
  not not_251 (not_251_out, OP3);
  not not_252 (not_252_out, OP2);
  not not_253 (not_253_out, OP1);
  not not_254 (not_254_out, OP0);
  not not_255 (not_255_out, F4);
  not not_256 (not_256_out, F2);
  not not_257 (not_257_out, F0);
  not not_258 (not_258_out, OP5);
  not not_259 (not_259_out, OP4);
  not not_260 (not_260_out, OP3);
  not not_261 (not_261_out, OP2);
  not not_262 (not_262_out, OP1);
  not not_263 (not_263_out, OP0);
  not not_264 (not_264_out, F4);
  not not_265 (not_265_out, F2);
  not not_266 (not_266_out, OP5);
  not not_267 (not_267_out, OP4);
  not not_268 (not_268_out, OP2);
  not not_269 (not_269_out, OP0);
  not not_270 (not_270_out, OP5);
  not not_271 (not_271_out, OP4);
  not not_272 (not_272_out, OP1);
  not not_273 (not_273_out, OP5);
  not not_274 (not_274_out, OP4);
  not not_275 (not_275_out, OP3);
  not not_276 (not_276_out, OP2);
  not not_277 (not_277_out, OP1);
  not not_278 (not_278_out, OP0);
  not not_279 (not_279_out, F4);
  not not_280 (not_280_out, F3);
  not not_281 (not_281_out, F0);
  and and_1 (and_1_out, not_1_out, not_2_out, not_3_out, not_4_out, not_5_out, not_6_out, not_7_out, not_8_out, not_9_out, not_10_out, F1, F0);
  and and_2 (and_2_out, not_11_out, not_12_out, not_13_out, not_14_out, not_15_out, not_16_out, F5, not_17_out, not_18_out, not_19_out, not_20_out, not_21_out);
  and and_3 (and_3_out, not_22_out, not_23_out, not_24_out, not_25_out, not_26_out, not_27_out, F5, not_28_out, not_29_out, not_30_out, not_31_out, F0);
  and and_4 (and_4_out, not_32_out, not_33_out, not_34_out, not_35_out, not_36_out, not_37_out, F5, not_38_out, not_39_out, F2, not_40_out, not_41_out);
  and and_5 (and_5_out, not_42_out, not_43_out, not_44_out, not_45_out, not_46_out, not_47_out, F5, not_48_out, F3, not_49_out, F1, not_50_out);
  and and_6 (and_6_out, not_51_out, not_52_out, OP3, not_53_out, not_54_out, not_55_out);
  and and_7 (and_7_out, not_56_out, not_57_out, OP3, OP2, not_58_out, not_59_out);
  and and_8 (and_8_out, not_60_out, not_61_out, OP3, not_62_out, not_63_out, OP0);
  and and_9 (and_9_out, not_64_out, not_65_out, OP3, not_66_out, OP1, not_67_out);
  and and_10 (and_10_out, OP5, not_68_out, not_69_out, not_70_out, OP1, OP0);
  and and_11 (and_11_out, OP5, not_71_out, OP3, not_72_out, OP1, OP0);
  and and_12 (and_12_out, not_73_out, not_74_out, not_75_out, not_76_out, not_77_out, not_78_out, F5, not_79_out, not_80_out, F2, F1, not_81_out);
  and and_13 (and_13_out, OP5, not_82_out, not_83_out, not_84_out, not_85_out, not_86_out);
  and and_14 (and_14_out, not_87_out, not_88_out, not_89_out, not_90_out, not_91_out, not_92_out, not_93_out, not_94_out, not_95_out, not_96_out, F1, not_97_out);
  and and_15 (and_15_out, not_98_out, not_99_out, not_100_out, not_101_out, not_102_out, not_103_out, F5, not_104_out, not_105_out, not_106_out, F1, not_107_out);
  and and_16 (and_16_out, not_108_out, not_109_out, not_110_out, not_111_out, not_112_out, not_113_out, F5, not_114_out, not_115_out, F2, not_116_out, not_117_out);
  and and_17 (and_17_out, not_118_out, not_119_out, not_120_out, not_121_out, not_122_out, not_123_out, F5, not_124_out, not_125_out, F2, F1, F0);
  and and_18 (and_18_out, not_126_out, not_127_out, not_128_out, not_129_out, not_130_out, not_131_out, F5, not_132_out, F3, not_133_out, F1, not_134_out);
  and and_19 (and_19_out, not_135_out, not_136_out, OP3, OP2, not_137_out, not_138_out);
  and and_20 (and_20_out, not_139_out, not_140_out, OP3, not_141_out, OP1, not_142_out);
  and and_21 (and_21_out, not_143_out, not_144_out, not_145_out, not_146_out, not_147_out, not_148_out, F5, not_149_out, not_150_out, not_151_out, not_152_out, not_153_out);
  and and_22 (and_22_out, not_154_out, not_155_out, not_156_out, not_157_out, not_158_out, not_159_out, F5, not_160_out, not_161_out, not_162_out, not_163_out, F0);
  and and_23 (and_23_out, not_164_out, not_165_out, not_166_out, not_167_out, not_168_out, not_169_out, F5, not_170_out, not_171_out, not_172_out, F1, not_173_out);
  and and_24 (and_24_out, not_174_out, not_175_out, not_176_out, not_177_out, not_178_out, not_179_out, F5, not_180_out, not_181_out, F2, not_182_out, not_183_out);
  and and_25 (and_25_out, not_184_out, not_185_out, not_186_out, not_187_out, not_188_out, not_189_out, F5, not_190_out, F3, not_191_out, F1, F0);
  and and_26 (and_26_out, not_192_out, not_193_out, OP3, not_194_out, not_195_out, not_196_out);
  and and_27 (and_27_out, not_197_out, not_198_out, OP3, OP2, not_199_out, not_200_out);
  and and_28 (and_28_out, not_201_out, not_202_out, OP3, not_203_out, not_204_out, OP0);
  and and_29 (and_29_out, OP5, not_205_out, not_206_out, not_207_out, OP1, OP0);
  and and_30 (and_30_out, OP5, not_208_out, OP3, not_209_out, OP1, OP0);
  and and_31 (and_31_out, OP5, not_210_out, not_211_out, not_212_out, not_213_out, not_214_out);
  and and_32 (and_32_out, not_215_out, not_216_out, not_217_out, not_218_out, not_219_out, not_220_out, F5, not_221_out, not_222_out, F2, not_223_out, F0);
  and and_33 (and_33_out, not_224_out, not_225_out, not_226_out, not_227_out, not_228_out, not_229_out, F5, not_230_out, not_231_out, F2, F1, F0);
  and and_34 (and_34_out, not_232_out, not_233_out, not_234_out, not_235_out, not_236_out, not_237_out, F5, not_238_out, not_239_out, F2, not_240_out, F0);
  and and_35 (and_35_out, not_241_out, not_242_out, not_243_out, not_244_out, not_245_out, not_246_out, F5, not_247_out, not_248_out, F2, F1, F0);
  and and_36 (and_36_out, not_249_out, not_250_out, not_251_out, not_252_out, not_253_out, not_254_out, F5, not_255_out, F3, not_256_out, F1, not_257_out);
  and and_37 (and_37_out, not_258_out, not_259_out, not_260_out, not_261_out, not_262_out, not_263_out, F5, not_264_out, F3, not_265_out, F1, F0);
  and and_38 (and_38_out, not_266_out, not_267_out, OP3, not_268_out, OP1, not_269_out);
  and and_39 (and_39_out, not_270_out, not_271_out, OP3, OP2, not_272_out, OP0);
  and and_40 (and_40_out, not_273_out, not_274_out, not_275_out, not_276_out, not_277_out, not_278_out, F5, not_279_out, not_280_out, F2, F1, not_281_out);
  or or_1 (S1, and_14_out, and_15_out, and_16_out, and_17_out, and_18_out, and_19_out, and_20_out);
  or or_2 (S2, and_21_out, and_22_out, and_23_out, and_24_out, and_25_out, and_26_out, and_27_out, and_28_out, and_29_out, and_30_out, and_31_out);
  or or_3 (S3, and_32_out, and_33_out, and_34_out, and_35_out, and_36_out, and_37_out, and_38_out, and_39_out, and_40_out);
  or or_4 (S0, and_1_out, and_2_out, and_3_out, and_4_out, and_5_out, and_6_out, and_7_out, and_8_out, and_9_out, and_10_out, and_11_out, and_12_out, and_13_out);
endmodule

// 控制信号生成
module \控制信号自动生成  (
  input  OP0,
  input  OP1,
  input  OP2,
  input  OP3,
  input  OP4,
  input  OP5,
  input  F0,
  input  F1,
  input  F2,
  input  F3,
  input  F4,
  input  F5,
  output MemToReg,
  output MemWrite,
  output ALU_SRC,
  output RegWrite,
  output SysCALL,
  output SignedExt,
  output RegDst,
  output BEQ,
  output BNE,
  output JR,
  output JUMP,
  output JAL,
  output LUI,
  output LB,
  output BLEZ
);

  wire and_1_out, and_2_out, and_4_out, and_5_out, and_6_out, and_7_out, and_8_out, and_9_out, and_10_out,
       and_11_out, and_12_out, and_13_out, and_14_out, and_15_out, and_16_out, and_17_out, and_18_out,
       and_19_out, and_20_out, and_21_out, and_22_out, and_23_out, and_24_out, and_25_out, and_26_out,
       and_27_out, and_28_out, and_29_out, and_30_out, and_31_out, and_32_out, and_33_out, and_34_out,
       and_35_out, and_36_out, and_38_out, and_39_out, and_40_out, and_41_out, and_42_out, and_43_out,
       and_44_out, and_45_out, and_46_out, and_47_out, and_48_out, and_49_out, and_50_out, and_51_out,
       and_52_out, and_53_out, and_54_out, and_55_out, and_56_out, and_57_out, and_58_out, and_62_out,
       and_63_out, and_64_out, not_1_out, not_2_out, not_3_out, not_4_out, not_5_out, not_6_out, not_7_out,
       not_8_out, not_9_out, not_10_out, not_11_out, not_12_out, not_13_out, not_14_out, not_15_out,
       not_16_out, not_17_out, not_18_out, not_19_out, not_20_out, not_21_out, not_22_out, not_23_out,
       not_24_out, not_25_out, not_26_out, not_27_out, not_28_out, not_29_out, not_30_out, not_31_out,
       not_32_out, not_33_out, not_34_out, not_35_out, not_36_out, not_37_out, not_38_out, not_39_out,
       not_40_out, not_41_out, not_42_out, not_43_out, not_44_out, not_45_out, not_46_out, not_47_out,
       not_48_out, not_49_out, not_50_out, not_51_out, not_52_out, not_53_out, not_54_out, not_55_out,
       not_56_out, not_57_out, not_58_out, not_59_out, not_60_out, not_61_out, not_62_out, not_63_out,
       not_64_out, not_65_out, not_66_out, not_67_out, not_68_out, not_69_out, not_70_out, not_71_out,
       not_72_out, not_73_out, not_74_out, not_75_out, not_76_out, not_77_out, not_78_out, not_79_out,
       not_80_out, not_81_out, not_82_out, not_83_out, not_84_out, not_85_out, not_86_out, not_87_out,
       not_88_out, not_89_out, not_90_out, not_91_out, not_92_out, not_93_out, not_94_out, not_95_out,
       not_96_out, not_97_out, not_98_out, not_99_out, not_100_out, not_101_out, not_102_out, not_103_out,
       not_104_out, not_105_out, not_106_out, not_107_out, not_108_out, not_109_out, not_110_out,
       not_111_out, not_112_out, not_113_out, not_114_out, not_115_out, not_116_out, not_117_out,
       not_118_out, not_119_out, not_120_out, not_121_out, not_122_out, not_123_out, not_124_out,
       not_125_out, not_126_out, not_127_out, not_128_out, not_129_out, not_130_out, not_131_out,
       not_132_out, not_133_out, not_134_out, not_135_out, not_136_out, not_137_out, not_138_out,
       not_139_out, not_140_out, not_141_out, not_142_out, not_143_out, not_144_out, not_145_out,
       not_146_out, not_147_out, not_148_out, not_149_out, not_150_out, not_151_out, not_152_out,
       not_153_out, not_154_out, not_155_out, not_156_out, not_157_out, not_158_out, not_159_out,
       not_160_out, not_161_out, not_162_out, not_163_out, not_164_out, not_165_out, not_166_out,
       not_167_out, not_168_out, not_169_out, not_170_out, not_171_out, not_172_out, not_173_out,
       not_174_out, not_175_out, not_176_out, not_177_out, not_178_out, not_179_out, not_180_out,
       not_181_out, not_182_out, not_183_out, not_184_out, not_185_out, not_186_out, not_187_out,
       not_188_out, not_189_out, not_190_out, not_191_out, not_192_out, not_193_out, not_194_out,
       not_195_out, not_196_out, not_197_out, not_198_out, not_199_out, not_200_out, not_201_out,
       not_202_out, not_203_out, not_204_out, not_205_out, not_206_out, not_207_out, not_208_out,
       not_209_out, not_210_out, not_211_out, not_212_out, not_213_out, not_214_out, not_215_out,
       not_216_out, not_217_out, not_218_out, not_219_out, not_220_out, not_221_out, not_222_out,
       not_223_out, not_224_out, not_225_out, not_226_out, not_227_out, not_228_out, not_229_out,
       not_230_out, not_231_out, not_232_out, not_233_out, not_234_out, not_235_out, not_236_out,
       not_237_out, not_238_out, not_239_out, not_240_out, not_241_out, not_242_out, not_243_out,
       not_244_out, not_245_out, not_246_out, not_247_out, not_248_out, not_249_out, not_250_out,
       not_251_out, not_252_out, not_253_out, not_254_out, not_255_out, not_256_out, not_257_out,
       not_258_out, not_259_out, not_260_out, not_261_out, not_262_out, not_263_out, not_264_out,
       not_265_out, not_266_out, not_267_out, not_268_out, not_269_out, not_270_out, not_271_out,
       not_272_out, not_273_out, not_274_out, not_275_out, not_276_out, not_277_out, not_278_out,
       not_279_out, not_280_out, not_281_out, not_282_out, not_283_out, not_284_out, not_285_out,
       not_286_out, not_287_out, not_288_out, not_289_out, not_290_out, not_291_out, not_292_out,
       not_293_out, not_294_out, not_295_out, not_296_out, not_297_out, not_298_out, not_299_out,
       not_300_out, not_301_out, not_302_out, not_303_out, not_304_out, not_305_out, not_306_out,
       not_307_out, not_308_out, not_309_out, not_310_out, not_311_out, not_312_out, not_313_out,
       not_314_out, not_315_out, not_316_out, not_317_out, not_318_out, not_319_out, not_320_out,
       not_321_out, not_322_out, not_323_out, not_324_out, not_325_out, not_326_out, not_327_out,
       not_328_out, not_329_out, not_330_out, not_331_out, not_332_out, not_333_out, not_334_out,
       not_335_out, not_336_out, not_337_out, not_338_out, not_339_out, not_340_out, not_341_out,
       not_342_out, not_343_out, not_344_out, not_345_out, not_346_out, not_347_out, not_348_out,
       not_349_out, not_350_out, not_351_out, not_352_out, not_353_out, not_354_out, not_355_out,
       not_356_out, not_357_out, not_358_out, not_359_out, not_360_out, not_361_out, not_362_out,
       not_363_out, not_364_out, not_365_out, not_366_out, not_367_out, not_368_out, not_369_out,
       not_370_out, not_371_out, not_372_out, not_373_out, not_374_out, not_375_out, not_376_out,
       not_377_out, not_378_out, not_379_out, not_380_out, not_381_out, not_382_out, not_383_out,
       not_384_out, not_385_out, not_386_out, not_387_out, not_388_out, not_389_out, not_390_out,
       not_391_out, not_392_out, not_393_out, not_394_out, not_395_out, not_396_out, not_397_out,
       not_398_out, not_399_out, not_400_out, not_401_out, not_402_out, not_403_out, not_404_out,
       not_405_out, not_406_out, not_407_out, not_408_out, not_409_out, not_410_out, not_411_out,
       not_412_out, not_413_out, not_414_out, not_415_out, not_416_out, not_417_out, not_418_out,
       not_419_out, not_420_out, not_421_out, not_422_out, not_423_out, not_424_out, not_425_out,
       not_426_out, not_427_out, not_428_out;

  not not_1 (not_1_out, OP4);
  not not_2 (not_2_out, OP3);
  not not_3 (not_3_out, OP2);
  not not_4 (not_4_out, OP4);
  not not_5 (not_5_out, OP3);
  not not_6 (not_6_out, OP2);
  not not_7 (not_7_out, OP1);
  not not_8 (not_8_out, OP0);
  not not_9 (not_9_out, OP4);
  not not_10 (not_10_out, OP2);
  not not_11 (not_11_out, OP5);
  not not_12 (not_12_out, OP4);
  not not_13 (not_13_out, OP2);
  not not_14 (not_14_out, OP1);
  not not_15 (not_15_out, OP0);
  not not_16 (not_16_out, OP5);
  not not_17 (not_17_out, OP4);
  not not_18 (not_18_out, OP1);
  not not_19 (not_19_out, OP0);
  not not_20 (not_20_out, OP5);
  not not_21 (not_21_out, OP4);
  not not_22 (not_22_out, OP2);
  not not_23 (not_23_out, OP1);
  not not_24 (not_24_out, OP5);
  not not_25 (not_25_out, OP4);
  not not_26 (not_26_out, OP2);
  not not_27 (not_27_out, OP0);
  not not_28 (not_28_out, OP5);
  not not_29 (not_29_out, OP4);
  not not_30 (not_30_out, OP5);
  not not_31 (not_31_out, OP4);
  not not_32 (not_32_out, OP2);
  not not_33 (not_33_out, OP1);
  not not_34 (not_34_out, OP0);
  not not_35 (not_35_out, OP5);
  not not_36 (not_36_out, OP4);
  not not_37 (not_37_out, OP1);
  not not_38 (not_38_out, OP0);
  not not_39 (not_39_out, OP5);
  not not_40 (not_40_out, OP4);
  not not_41 (not_41_out, OP2);
  not not_42 (not_42_out, OP1);
  not not_43 (not_43_out, OP5);
  not not_44 (not_44_out, OP4);
  not not_45 (not_45_out, OP2);
  not not_46 (not_46_out, OP0);
  not not_47 (not_47_out, OP5);
  not not_48 (not_48_out, OP4);
  not not_49 (not_49_out, OP1);
  not not_50 (not_50_out, OP4);
  not not_51 (not_51_out, OP3);
  not not_52 (not_52_out, OP2);
  not not_53 (not_53_out, OP4);
  not not_54 (not_54_out, OP2);
  not not_55 (not_55_out, OP4);
  not not_56 (not_56_out, OP3);
  not not_57 (not_57_out, OP2);
  not not_58 (not_58_out, OP1);
  not not_59 (not_59_out, OP0);
  not not_60 (not_60_out, OP5);
  not not_61 (not_61_out, OP4);
  not not_62 (not_62_out, OP3);
  not not_63 (not_63_out, OP2);
  not not_64 (not_64_out, OP1);
  not not_65 (not_65_out, OP0);
  not not_66 (not_66_out, F5);
  not not_67 (not_67_out, F4);
  not not_68 (not_68_out, F3);
  not not_69 (not_69_out, F2);
  not not_70 (not_70_out, F1);
  not not_71 (not_71_out, F0);
  not not_72 (not_72_out, OP5);
  not not_73 (not_73_out, OP4);
  not not_74 (not_74_out, OP3);
  not not_75 (not_75_out, OP2);
  not not_76 (not_76_out, OP1);
  not not_77 (not_77_out, OP0);
  not not_78 (not_78_out, F5);
  not not_79 (not_79_out, F4);
  not not_80 (not_80_out, F3);
  not not_81 (not_81_out, F2);
  not not_82 (not_82_out, OP5);
  not not_83 (not_83_out, OP4);
  not not_84 (not_84_out, OP3);
  not not_85 (not_85_out, OP2);
  not not_86 (not_86_out, OP1);
  not not_87 (not_87_out, OP0);
  not not_88 (not_88_out, F5);
  not not_89 (not_89_out, F4);
  not not_90 (not_90_out, F3);
  not not_91 (not_91_out, F2);
  not not_92 (not_92_out, F0);
  not not_93 (not_93_out, OP5);
  not not_94 (not_94_out, OP4);
  not not_95 (not_95_out, OP3);
  not not_96 (not_96_out, OP2);
  not not_97 (not_97_out, OP1);
  not not_98 (not_98_out, OP0);
  not not_99 (not_99_out, F4);
  not not_100 (not_100_out, F3);
  not not_101 (not_101_out, F2);
  not not_102 (not_102_out, F1);
  not not_103 (not_103_out, F0);
  not not_104 (not_104_out, OP5);
  not not_105 (not_105_out, OP4);
  not not_106 (not_106_out, OP3);
  not not_107 (not_107_out, OP2);
  not not_108 (not_108_out, OP1);
  not not_109 (not_109_out, OP0);
  not not_110 (not_110_out, F4);
  not not_111 (not_111_out, F3);
  not not_112 (not_112_out, F2);
  not not_113 (not_113_out, F1);
  not not_114 (not_114_out, OP5);
  not not_115 (not_115_out, OP4);
  not not_116 (not_116_out, OP3);
  not not_117 (not_117_out, OP2);
  not not_118 (not_118_out, OP1);
  not not_119 (not_119_out, OP0);
  not not_120 (not_120_out, F4);
  not not_121 (not_121_out, F3);
  not not_122 (not_122_out, F2);
  not not_123 (not_123_out, F0);
  not not_124 (not_124_out, OP5);
  not not_125 (not_125_out, OP4);
  not not_126 (not_126_out, OP3);
  not not_127 (not_127_out, OP2);
  not not_128 (not_128_out, OP1);
  not not_129 (not_129_out, OP0);
  not not_130 (not_130_out, F4);
  not not_131 (not_131_out, F3);
  not not_132 (not_132_out, F1);
  not not_133 (not_133_out, F0);
  not not_134 (not_134_out, OP5);
  not not_135 (not_135_out, OP4);
  not not_136 (not_136_out, OP3);
  not not_137 (not_137_out, OP2);
  not not_138 (not_138_out, OP1);
  not not_139 (not_139_out, OP0);
  not not_140 (not_140_out, F4);
  not not_141 (not_141_out, F3);
  not not_142 (not_142_out, F1);
  not not_143 (not_143_out, OP5);
  not not_144 (not_144_out, OP4);
  not not_145 (not_145_out, OP3);
  not not_146 (not_146_out, OP2);
  not not_147 (not_147_out, OP1);
  not not_148 (not_148_out, OP0);
  not not_149 (not_149_out, F4);
  not not_150 (not_150_out, F3);
  not not_151 (not_151_out, OP5);
  not not_152 (not_152_out, OP4);
  not not_153 (not_153_out, OP3);
  not not_154 (not_154_out, OP2);
  not not_155 (not_155_out, OP1);
  not not_156 (not_156_out, OP0);
  not not_157 (not_157_out, F4);
  not not_158 (not_158_out, F2);
  not not_159 (not_159_out, F0);
  not not_160 (not_160_out, OP5);
  not not_161 (not_161_out, OP4);
  not not_162 (not_162_out, OP3);
  not not_163 (not_163_out, OP2);
  not not_164 (not_164_out, OP1);
  not not_165 (not_165_out, OP0);
  not not_166 (not_166_out, F4);
  not not_167 (not_167_out, F2);
  not not_168 (not_168_out, OP5);
  not not_169 (not_169_out, OP4);
  not not_170 (not_170_out, OP3);
  not not_171 (not_171_out, OP2);
  not not_172 (not_172_out, OP5);
  not not_173 (not_173_out, OP4);
  not not_174 (not_174_out, OP2);
  not not_175 (not_175_out, OP1);
  not not_176 (not_176_out, OP0);
  not not_177 (not_177_out, OP5);
  not not_178 (not_178_out, OP4);
  not not_179 (not_179_out, OP1);
  not not_180 (not_180_out, OP0);
  not not_181 (not_181_out, OP5);
  not not_182 (not_182_out, OP4);
  not not_183 (not_183_out, OP2);
  not not_184 (not_184_out, OP1);
  not not_185 (not_185_out, OP5);
  not not_186 (not_186_out, OP4);
  not not_187 (not_187_out, OP2);
  not not_188 (not_188_out, OP0);
  not not_189 (not_189_out, OP5);
  not not_190 (not_190_out, OP4);
  not not_191 (not_191_out, OP1);
  not not_192 (not_192_out, OP4);
  not not_193 (not_193_out, OP3);
  not not_194 (not_194_out, OP2);
  not not_195 (not_195_out, OP5);
  not not_196 (not_196_out, OP4);
  not not_197 (not_197_out, OP3);
  not not_198 (not_198_out, OP2);
  not not_199 (not_199_out, OP1);
  not not_200 (not_200_out, OP0);
  not not_201 (not_201_out, F4);
  not not_202 (not_202_out, F3);
  not not_203 (not_203_out, F0);
  not not_204 (not_204_out, OP5);
  not not_205 (not_205_out, OP4);
  not not_206 (not_206_out, OP4);
  not not_207 (not_207_out, OP3);
  not not_208 (not_208_out, OP2);
  not not_209 (not_209_out, OP1);
  not not_210 (not_210_out, OP0);
  not not_211 (not_211_out, OP5);
  not not_212 (not_212_out, OP4);
  not not_213 (not_213_out, OP3);
  not not_214 (not_214_out, OP2);
  not not_215 (not_215_out, OP1);
  not not_216 (not_216_out, OP0);
  not not_217 (not_217_out, F5);
  not not_218 (not_218_out, F4);
  not not_219 (not_219_out, F1);
  not not_220 (not_220_out, F0);
  not not_221 (not_221_out, OP5);
  not not_222 (not_222_out, OP4);
  not not_223 (not_223_out, OP3);
  not not_224 (not_224_out, OP1);
  not not_225 (not_225_out, OP0);
  not not_226 (not_226_out, OP5);
  not not_227 (not_227_out, OP4);
  not not_228 (not_228_out, OP3);
  not not_229 (not_229_out, OP1);
  not not_230 (not_230_out, OP5);
  not not_231 (not_231_out, OP4);
  not not_232 (not_232_out, OP2);
  not not_233 (not_233_out, OP1);
  not not_234 (not_234_out, OP0);
  not not_235 (not_235_out, OP5);
  not not_236 (not_236_out, OP4);
  not not_237 (not_237_out, OP2);
  not not_238 (not_238_out, OP1);
  not not_239 (not_239_out, OP5);
  not not_240 (not_240_out, OP4);
  not not_241 (not_241_out, OP2);
  not not_242 (not_242_out, OP0);
  not not_243 (not_243_out, OP4);
  not not_244 (not_244_out, OP3);
  not not_245 (not_245_out, OP2);
  not not_246 (not_246_out, OP4);
  not not_247 (not_247_out, OP2);
  not not_248 (not_248_out, OP4);
  not not_249 (not_249_out, OP3);
  not not_250 (not_250_out, OP2);
  not not_251 (not_251_out, OP1);
  not not_252 (not_252_out, OP0);
  not not_253 (not_253_out, OP5);
  not not_254 (not_254_out, OP4);
  not not_255 (not_255_out, OP3);
  not not_256 (not_256_out, OP0);
  not not_257 (not_257_out, OP5);
  not not_258 (not_258_out, OP4);
  not not_259 (not_259_out, OP3);
  not not_260 (not_260_out, OP2);
  not not_261 (not_261_out, OP1);
  not not_262 (not_262_out, OP0);
  not not_263 (not_263_out, F5);
  not not_264 (not_264_out, F4);
  not not_265 (not_265_out, F3);
  not not_266 (not_266_out, F2);
  not not_267 (not_267_out, F1);
  not not_268 (not_268_out, F0);
  not not_269 (not_269_out, OP5);
  not not_270 (not_270_out, OP4);
  not not_271 (not_271_out, OP3);
  not not_272 (not_272_out, OP2);
  not not_273 (not_273_out, OP1);
  not not_274 (not_274_out, OP0);
  not not_275 (not_275_out, F5);
  not not_276 (not_276_out, F4);
  not not_277 (not_277_out, F3);
  not not_278 (not_278_out, F2);
  not not_279 (not_279_out, OP5);
  not not_280 (not_280_out, OP4);
  not not_281 (not_281_out, OP3);
  not not_282 (not_282_out, OP2);
  not not_283 (not_283_out, OP1);
  not not_284 (not_284_out, OP0);
  not not_285 (not_285_out, F5);
  not not_286 (not_286_out, F4);
  not not_287 (not_287_out, F3);
  not not_288 (not_288_out, F2);
  not not_289 (not_289_out, F0);
  not not_290 (not_290_out, OP5);
  not not_291 (not_291_out, OP4);
  not not_292 (not_292_out, OP3);
  not not_293 (not_293_out, OP2);
  not not_294 (not_294_out, OP1);
  not not_295 (not_295_out, OP0);
  not not_296 (not_296_out, F4);
  not not_297 (not_297_out, F3);
  not not_298 (not_298_out, F2);
  not not_299 (not_299_out, F1);
  not not_300 (not_300_out, F0);
  not not_301 (not_301_out, OP5);
  not not_302 (not_302_out, OP4);
  not not_303 (not_303_out, OP3);
  not not_304 (not_304_out, OP2);
  not not_305 (not_305_out, OP1);
  not not_306 (not_306_out, OP0);
  not not_307 (not_307_out, F4);
  not not_308 (not_308_out, F3);
  not not_309 (not_309_out, F2);
  not not_310 (not_310_out, F1);
  not not_311 (not_311_out, OP5);
  not not_312 (not_312_out, OP4);
  not not_313 (not_313_out, OP3);
  not not_314 (not_314_out, OP2);
  not not_315 (not_315_out, OP1);
  not not_316 (not_316_out, OP0);
  not not_317 (not_317_out, F4);
  not not_318 (not_318_out, F3);
  not not_319 (not_319_out, F2);
  not not_320 (not_320_out, F0);
  not not_321 (not_321_out, OP5);
  not not_322 (not_322_out, OP4);
  not not_323 (not_323_out, OP3);
  not not_324 (not_324_out, OP2);
  not not_325 (not_325_out, OP1);
  not not_326 (not_326_out, OP0);
  not not_327 (not_327_out, F4);
  not not_328 (not_328_out, F3);
  not not_329 (not_329_out, F1);
  not not_330 (not_330_out, F0);
  not not_331 (not_331_out, OP5);
  not not_332 (not_332_out, OP4);
  not not_333 (not_333_out, OP3);
  not not_334 (not_334_out, OP2);
  not not_335 (not_335_out, OP1);
  not not_336 (not_336_out, OP0);
  not not_337 (not_337_out, F4);
  not not_338 (not_338_out, F3);
  not not_339 (not_339_out, F1);
  not not_340 (not_340_out, OP5);
  not not_341 (not_341_out, OP4);
  not not_342 (not_342_out, OP3);
  not not_343 (not_343_out, OP2);
  not not_344 (not_344_out, OP1);
  not not_345 (not_345_out, OP0);
  not not_346 (not_346_out, F4);
  not not_347 (not_347_out, F3);
  not not_348 (not_348_out, OP5);
  not not_349 (not_349_out, OP4);
  not not_350 (not_350_out, OP3);
  not not_351 (not_351_out, OP2);
  not not_352 (not_352_out, OP1);
  not not_353 (not_353_out, OP0);
  not not_354 (not_354_out, F4);
  not not_355 (not_355_out, F2);
  not not_356 (not_356_out, F0);
  not not_357 (not_357_out, OP5);
  not not_358 (not_358_out, OP4);
  not not_359 (not_359_out, OP3);
  not not_360 (not_360_out, OP2);
  not not_361 (not_361_out, OP1);
  not not_362 (not_362_out, OP0);
  not not_363 (not_363_out, F4);
  not not_364 (not_364_out, F2);
  not not_365 (not_365_out, OP5);
  not not_366 (not_366_out, OP4);
  not not_367 (not_367_out, OP3);
  not not_368 (not_368_out, OP2);
  not not_369 (not_369_out, OP1);
  not not_370 (not_370_out, OP0);
  not not_371 (not_371_out, F4);
  not not_372 (not_372_out, F3);
  not not_373 (not_373_out, F0);
  not not_374 (not_374_out, OP5);
  not not_375 (not_375_out, OP4);
  not not_376 (not_376_out, OP3);
  not not_377 (not_377_out, OP1);
  not not_378 (not_378_out, OP0);
  not not_379 (not_379_out, OP5);
  not not_380 (not_380_out, OP4);
  not not_381 (not_381_out, OP3);
  not not_382 (not_382_out, OP1);
  not not_383 (not_383_out, OP5);
  not not_384 (not_384_out, OP4);
  not not_385 (not_385_out, OP3);
  not not_386 (not_386_out, OP2);
  not not_387 (not_387_out, OP1);
  not not_388 (not_388_out, OP0);
  not not_389 (not_389_out, F5);
  not not_390 (not_390_out, F4);
  not not_391 (not_391_out, F2);
  not not_392 (not_392_out, F1);
  not not_393 (not_393_out, F0);
  not not_394 (not_394_out, OP5);
  not not_395 (not_395_out, OP4);
  not not_396 (not_396_out, OP3);
  not not_397 (not_397_out, OP2);
  not not_398 (not_398_out, OP1);
  not not_399 (not_399_out, OP0);
  not not_400 (not_400_out, F5);
  not not_401 (not_401_out, F4);
  not not_402 (not_402_out, F2);
  not not_403 (not_403_out, F1);
  not not_404 (not_404_out, F0);
  not not_405 (not_405_out, OP5);
  not not_406 (not_406_out, OP4);
  not not_407 (not_407_out, OP3);
  not not_408 (not_408_out, OP2);
  not not_409 (not_409_out, OP0);
  not not_410 (not_410_out, OP5);
  not not_411 (not_411_out, OP4);
  not not_412 (not_412_out, OP3);
  not not_413 (not_413_out, OP2);
  not not_414 (not_414_out, OP5);
  not not_415 (not_415_out, OP4);
  not not_416 (not_416_out, OP3);
  not not_417 (not_417_out, OP2);
  not not_418 (not_418_out, OP5);
  not not_419 (not_419_out, OP4);
  not not_420 (not_420_out, OP4);
  not not_421 (not_421_out, OP3);
  not not_422 (not_422_out, OP2);
  not not_423 (not_423_out, OP1);
  not not_424 (not_424_out, OP0);
  not not_425 (not_425_out, OP5);
  not not_426 (not_426_out, OP4);
  not not_427 (not_427_out, OP3);
  not not_428 (not_428_out, OP0);
  and and_1 (and_1_out, OP5, not_1_out, not_2_out, not_3_out, OP1, OP0);
  and and_2 (and_2_out, OP5, not_4_out, not_5_out, not_6_out, not_7_out, not_8_out);
  and and_3 (MemWrite, OP5, not_9_out, OP3, not_10_out, OP1, OP0);
  and and_4 (and_4_out, not_11_out, not_12_out, OP3, not_13_out, not_14_out, not_15_out);
  and and_5 (and_5_out, not_16_out, not_17_out, OP3, OP2, not_18_out, not_19_out);
  and and_6 (and_6_out, not_20_out, not_21_out, OP3, not_22_out, not_23_out, OP0);
  and and_7 (and_7_out, not_24_out, not_25_out, OP3, not_26_out, OP1, not_27_out);
  and and_8 (and_8_out, not_28_out, not_29_out, not_30_out, not_31_out, OP3, not_32_out, not_33_out, not_34_out);
  and and_9 (and_9_out, not_35_out, not_36_out, OP3, OP2, not_37_out, not_38_out);
  and and_10 (and_10_out, not_39_out, not_40_out, OP3, not_41_out, not_42_out, OP0);
  and and_11 (and_11_out, not_43_out, not_44_out, OP3, not_45_out, OP1, not_46_out);
  and and_12 (and_12_out, not_47_out, not_48_out, OP3, OP2, not_49_out, OP0);
  and and_13 (and_13_out, OP5, not_50_out, not_51_out, not_52_out, OP1, OP0);
  and and_14 (and_14_out, OP5, not_53_out, OP3, not_54_out, OP1, OP0);
  and and_15 (and_15_out, OP5, not_55_out, not_56_out, not_57_out, not_58_out, not_59_out);
  and and_16 (and_16_out, not_60_out, not_61_out, not_62_out, not_63_out, not_64_out, not_65_out, not_66_out, not_67_out, not_68_out, not_69_out, not_70_out, not_71_out);
  and and_17 (and_17_out, not_72_out, not_73_out, not_74_out, not_75_out, not_76_out, not_77_out, not_78_out, not_79_out, not_80_out, not_81_out, F1, F0);
  and and_18 (and_18_out, not_82_out, not_83_out, not_84_out, not_85_out, not_86_out, not_87_out, not_88_out, not_89_out, not_90_out, not_91_out, F1, not_92_out);
  and and_19 (and_19_out, not_93_out, not_94_out, not_95_out, not_96_out, not_97_out, not_98_out, F5, not_99_out, not_100_out, not_101_out, not_102_out, not_103_out);
  and and_20 (and_20_out, not_104_out, not_105_out, not_106_out, not_107_out, not_108_out, not_109_out, F5, not_110_out, not_111_out, not_112_out, not_113_out, F0);
  and and_21 (and_21_out, not_114_out, not_115_out, not_116_out, not_117_out, not_118_out, not_119_out, F5, not_120_out, not_121_out, not_122_out, F1, not_123_out);
  and and_22 (and_22_out, not_124_out, not_125_out, not_126_out, not_127_out, not_128_out, not_129_out, F5, not_130_out, not_131_out, F2, not_132_out, not_133_out);
  and and_23 (and_23_out, not_134_out, not_135_out, not_136_out, not_137_out, not_138_out, not_139_out, F5, not_140_out, not_141_out, F2, not_142_out, F0);
  and and_24 (and_24_out, not_143_out, not_144_out, not_145_out, not_146_out, not_147_out, not_148_out, F5, not_149_out, not_150_out, F2, F1, F0);
  and and_25 (and_25_out, not_151_out, not_152_out, not_153_out, not_154_out, not_155_out, not_156_out, F5, not_157_out, F3, not_158_out, F1, not_159_out);
  and and_26 (and_26_out, not_160_out, not_161_out, not_162_out, not_163_out, not_164_out, not_165_out, F5, not_166_out, F3, not_167_out, F1, F0);
  and and_27 (and_27_out, not_168_out, not_169_out, not_170_out, not_171_out, OP1, OP0);
  and and_28 (and_28_out, not_172_out, not_173_out, OP3, not_174_out, not_175_out, not_176_out);
  and and_29 (and_29_out, not_177_out, not_178_out, OP3, OP2, not_179_out, not_180_out);
  and and_30 (and_30_out, not_181_out, not_182_out, OP3, not_183_out, not_184_out, OP0);
  and and_31 (and_31_out, not_185_out, not_186_out, OP3, not_187_out, OP1, not_188_out);
  and and_32 (and_32_out, not_189_out, not_190_out, OP3, OP2, not_191_out, OP0);
  and and_33 (and_33_out, OP5, not_192_out, not_193_out, not_194_out, OP1, OP0);
  and and_34 (and_34_out, not_195_out, not_196_out, not_197_out, not_198_out, not_199_out, not_200_out, F5, not_201_out, not_202_out, F2, F1, not_203_out);
  and and_35 (and_35_out, not_204_out, not_205_out, OP3, OP2, OP1, OP0);
  and and_36 (and_36_out, OP5, not_206_out, not_207_out, not_208_out, not_209_out, not_210_out);
  and and_37 (SysCALL, not_211_out, not_212_out, not_213_out, not_214_out, not_215_out, not_216_out, not_217_out, not_218_out, F3, F2, not_219_out, not_220_out);
  and and_38 (and_38_out, not_221_out, not_222_out, not_223_out, OP2, not_224_out, not_225_out);
  and and_39 (and_39_out, not_226_out, not_227_out, not_228_out, OP2, not_229_out, OP0);
  and and_40 (and_40_out, not_230_out, not_231_out, OP3, not_232_out, not_233_out, not_234_out);
  and and_41 (and_41_out, not_235_out, not_236_out, OP3, not_237_out, not_238_out, OP0);
  and and_42 (and_42_out, not_239_out, not_240_out, OP3, not_241_out, OP1, not_242_out);
  and and_43 (and_43_out, OP5, not_243_out, not_244_out, not_245_out, OP1, OP0);
  and and_44 (and_44_out, OP5, not_246_out, OP3, not_247_out, OP1, OP0);
  and and_45 (and_45_out, OP5, not_248_out, not_249_out, not_250_out, not_251_out, not_252_out);
  and and_46 (and_46_out, not_253_out, not_254_out, not_255_out, OP2, OP1, not_256_out);
  and and_47 (and_47_out, not_257_out, not_258_out, not_259_out, not_260_out, not_261_out, not_262_out, not_263_out, not_264_out, not_265_out, not_266_out, not_267_out, not_268_out);
  and and_48 (and_48_out, not_269_out, not_270_out, not_271_out, not_272_out, not_273_out, not_274_out, not_275_out, not_276_out, not_277_out, not_278_out, F1, F0);
  and and_49 (and_49_out, not_279_out, not_280_out, not_281_out, not_282_out, not_283_out, not_284_out, not_285_out, not_286_out, not_287_out, not_288_out, F1, not_289_out);
  and and_50 (and_50_out, not_290_out, not_291_out, not_292_out, not_293_out, not_294_out, not_295_out, F5, not_296_out, not_297_out, not_298_out, not_299_out, not_300_out);
  and and_51 (and_51_out, not_301_out, not_302_out, not_303_out, not_304_out, not_305_out, not_306_out, F5, not_307_out, not_308_out, not_309_out, not_310_out, F0);
  and and_52 (and_52_out, not_311_out, not_312_out, not_313_out, not_314_out, not_315_out, not_316_out, F5, not_317_out, not_318_out, not_319_out, F1, not_320_out);
  and and_53 (and_53_out, not_321_out, not_322_out, not_323_out, not_324_out, not_325_out, not_326_out, F5, not_327_out, not_328_out, F2, not_329_out, not_330_out);
  and and_54 (and_54_out, not_331_out, not_332_out, not_333_out, not_334_out, not_335_out, not_336_out, F5, not_337_out, not_338_out, F2, not_339_out, F0);
  and and_55 (and_55_out, not_340_out, not_341_out, not_342_out, not_343_out, not_344_out, not_345_out, F5, not_346_out, not_347_out, F2, F1, F0);
  and and_56 (and_56_out, not_348_out, not_349_out, not_350_out, not_351_out, not_352_out, not_353_out, F5, not_354_out, F3, not_355_out, F1, not_356_out);
  and and_57 (and_57_out, not_357_out, not_358_out, not_359_out, not_360_out, not_361_out, not_362_out, F5, not_363_out, F3, not_364_out, F1, F0);
  and and_58 (and_58_out, not_365_out, not_366_out, not_367_out, not_368_out, not_369_out, not_370_out, F5, not_371_out, not_372_out, F2, F1, not_373_out);
  and and_59 (BEQ, not_374_out, not_375_out, not_376_out, OP2, not_377_out, not_378_out);
  and and_60 (BNE, not_379_out, not_380_out, not_381_out, OP2, not_382_out, OP0);
  and and_61 (JR, not_383_out, not_384_out, not_385_out, not_386_out, not_387_out, not_388_out, not_389_out, not_390_out, F3, not_391_out, not_392_out, not_393_out);
  and and_62 (and_62_out, not_394_out, not_395_out, not_396_out, not_397_out, not_398_out, not_399_out, not_400_out, not_401_out, F3, not_402_out, not_403_out, not_404_out);
  and and_63 (and_63_out, not_405_out, not_406_out, not_407_out, not_408_out, OP1, not_409_out);
  and and_64 (and_64_out, not_410_out, not_411_out, not_412_out, not_413_out, OP1, OP0);
  and and_65 (JAL, not_414_out, not_415_out, not_416_out, not_417_out, OP1, OP0);
  and and_66 (LUI, not_418_out, not_419_out, OP3, OP2, OP1, OP0);
  and and_67 (LB, OP5, not_420_out, not_421_out, not_422_out, not_423_out, not_424_out);
  and and_68 (BLEZ, not_425_out, not_426_out, not_427_out, OP2, OP1, not_428_out);
  or or_1 (MemToReg, and_1_out, and_2_out);
  or or_2 (ALU_SRC, and_4_out, and_5_out, and_6_out, and_7_out, and_8_out, and_9_out, and_10_out, and_11_out, and_12_out, and_13_out, and_14_out, and_15_out);
  or or_3 (SignedExt, and_38_out, and_39_out, and_40_out, and_41_out, and_42_out, and_43_out, and_44_out, and_45_out, and_46_out);
  or or_4 (JUMP, and_62_out, and_63_out, and_64_out);
  or or_5 (RegWrite, and_16_out, and_17_out, and_18_out, and_19_out, and_20_out, and_21_out, and_22_out, and_23_out, and_24_out, and_25_out, and_26_out, and_27_out, and_28_out, and_29_out, and_30_out, and_31_out, and_32_out, and_33_out, and_34_out, and_35_out, and_36_out);
  or or_6 (RegDst, and_47_out, and_48_out, and_49_out, and_50_out, and_51_out, and_52_out, and_53_out, and_54_out, and_55_out, and_56_out, and_57_out, and_58_out);
endmodule

// ALU
module MIPS_ALU (
  input  [4:0] shamt,
  input  [31:0] X,
  input  [31:0] Y,
  input  [3:0] AluOP,
  output Equal,
  output [31:0] Result,
  output [31:0] Result_2
);

  wire [0:0] comparator_1_lt, comparator_2_lt;
  wire [31:0] adder_1_out, AND_out, divider_1_out, divider_1_rem, multiplier_1_cout, multiplier_1_out,
       NOR_out, OR_out, shifter_1_out, shifter_2_out, shifter_3_out, subtractor_1_out, XOR_out;

  assign AND_out = X & Y;  // AND_Gate AND, 32 bits wide
  assign OR_out = X | Y;  // OR_Gate OR, 32 bits wide
  Shifter #(.width(32), .shift("ll")) shifter_1 (.in(Y), .\dist (shamt), .out(shifter_1_out));
  Shifter #(.width(32), .shift("ar")) shifter_2 (.in(Y), .\dist (shamt), .out(shifter_2_out));
  Shifter #(.width(32), .shift("lr")) shifter_3 (.in(Y), .\dist (shamt), .out(shifter_3_out));
  Multiplier #(.width(32)) multiplier_1 (.a(X), .b(Y), .out(multiplier_1_out), .cout(multiplier_1_cout));  // open: cin
  Divider #(.width(32)) divider_1 (.a(X), .b(Y), .out(divider_1_out), .rem(divider_1_rem));  // open: upper
  Adder #(.width(32)) adder_1 (.a(X), .b(Y), .out(adder_1_out));  // open: cin, cout
  Subtractor #(.width(32)) subtractor_1 (.a(X), .b(Y), .out(subtractor_1_out));  // open: bin, bout
  assign XOR_out = X ^ Y;  // XOR_Gate XOR, 32 bits wide
  assign NOR_out = ~(X | Y);  // NOR_Gate NOR, 32 bits wide
  Comparator #(.width(32), .mode("twosComplement")) comparator_1 (
    .a(X), .b(Y), .eq(Equal), .lt(comparator_1_lt[0]));  // open: gt
  Comparator #(.width(32), .mode("unsigned")) comparator_2 (.a(X), .b(Y), .lt(comparator_2_lt[0]));  // open: gt, eq
  Multiplexer #(.select(4), .width(32), .disabled("Z"), .enable("false")) multiplexer_1 (
    .in0(shifter_1_out), .in1(shifter_2_out), .in2(shifter_3_out), .in3(multiplier_1_out),
    .in4(divider_1_out), .in5(adder_1_out), .in6(subtractor_1_out), .in7(AND_out), .in8(OR_out),
    .in9(XOR_out), .in10(NOR_out), .in11({{31{1'b0}}, comparator_1_lt[0]}),
    .in12({{31{1'b0}}, comparator_2_lt[0]}), .in13({32{1'b0}}), .in14({32{1'b0}}), .in15({32{1'b0}}),
    .out(Result), .sel(AluOP));
  Multiplexer #(.select(4), .width(32), .disabled("Z"), .enable("false")) multiplexer_2 (
    .in0({32{1'b0}}), .in1({32{1'b0}}), .in2({32{1'b0}}), .in3(multiplier_1_cout), .in4(divider_1_rem),
    .in5({32{1'b0}}), .in6({32{1'b0}}), .in7({32{1'b0}}), .in8({32{1'b0}}), .in9({32{1'b0}}),
    .in10({32{1'b0}}), .in11({32{1'b0}}), .in12({32{1'b0}}), .in13({32{1'b0}}), .in14({32{1'b0}}),
    .in15({32{1'b0}}), .out(Result_2), .sel(AluOP));

  // Other names for the same wires on the sheet: Result2[31:0] = Result_2; S[3:0] = AluOP

  // Notes on the sheet:
  //   不要改变此引脚区域内容，也不要改变ALU封装形式
  //   输入引脚
  //   输出引脚
endmodule

module MIPS_Regifile (
  input  [31:0] Din,
  input  Clk,
  input  WE,
  input  [4:0] R1_num,
  input  [4:0] W_num,
  input  [4:0] R2_num,
  output [31:0] R1,
  output [31:0] R2
);

  // RegisterFile registerfile_1: pin names not known; wires that end beside it: Din, Clk, WE, W_num, R1_num, R2_num, R1, R2
endmodule

module \理想流水线  (
  output RegWrite,
  output MemWrite,
  output [31:0] IF_PC,
  output [31:0] ID_PC,
  output [31:0] EX_PC,
  output [31:0] M_PC,
  output [31:0] WB_PC,
  output [31:0] RDin,
  output [31:0] MDin,
  output [31:0] LedData
);

  wire and_1_out, and_2_out, and_3_out, and_4_out, and_5_out, and_6_out, and_8_out, and_9_out, B___De, BLEZ,
       BLEZ_DE, BracnhConflict, branch, CLK, comparator_1_gt, comparator_2_eq, DataConflict, ex_mem_1_out_18,
       ex_mem_1_out_19, ex_mem_1_out_20, ex_mem_1_out_24, EX_RegWrite, Go, id_ex_1_out_31, id_ex_1_out_33,
       id_ex_1_out_34, id_ex_1_out_35, id_ex_1_out_36, id_ex_1_out_37, id_ex_1_out_39, id_ex_1_out_41, IR1,
       IR2, IR3, JAL_1, JAL_2, JAL_3, JAL_4, JMP, JR, LUI, MEM_RegWrite, mem_wb_1_out_19, mem_wb_1_out_20,
       mips_alu_1_equal, multiplexer_12_out, not_1_out, not_2_out, or_3_out, or_4_out, or_5_out, or_6_out,
       or_10_out, R1_U, R2_U, RST, SignedExt, STALL, Syscall, W1, W2, W3, \拓展单周期硬布线控制器_31_1_alu_src ,
       \拓展单周期硬布线控制器_31_1_beq , \拓展单周期硬布线控制器_31_1_blez , \拓展单周期硬布线控制器_31_1_bne , \拓展单周期硬布线控制器_31_1_jmp ,
       \拓展单周期硬布线控制器_31_1_jr , \拓展单周期硬布线控制器_31_1_lb , \拓展单周期硬布线控制器_31_1_lui , \拓展单周期硬布线控制器_31_1_memtoreg ,
       \拓展单周期硬布线控制器_31_1_memwrite , \拓展单周期硬布线控制器_31_1_regwrite , \拓展单周期硬布线控制器_31_1_syscall ,
       \数据相关检测_24_3_2_1_ex相关 , \数据相关检测_24_3_2_1_mem相关 , \运行 ;
  wire [0:0] or_1_out, \拓展单周期硬布线控制器_31_1_regdst ;
  wire [3:0] id_ex_1_out_38, \拓展单周期硬布线控制器_31_1_alu_op ;
  wire [4:0] EX_WriteReg_num, id_ex_1_out_47, MEM_WriteReg_num, multiplexer_4_out, R1_num, R2_num, W_num;
  wire [7:0] multiplexer_11_out;
  wire [15:0] \LoadUse次数 , \总周期数 , \插入气泡数 , \无条件分支数 , \条件分支成功数 ;
  wire [27:0] adder_2_out;
  wire [31:0] a0, adder_4_out, B___PC, bit_extender_1_out, bit_extender_2_out, bit_extender_3_out,
       ex_mem_1_out_23, ex_mem_1_out_27, ex_mem_1_out_30, id_ex_1_out_45, id_ex_1_out_46, id_ex_1_out_49,
       IR_1, IR_2, IR_3, IR_4, JR_PC, mem_wb_1_out_22, mem_wb_1_out_26, mem_wb_1_out_27, mem_wb_1_out_30,
       mips_alu_1_result, mips_regifile_1_r1, mips_regifile_1_r2, multiplexer_1_out, multiplexer_5_out,
       multiplexer_6_out, multiplexer_8_out, multiplexer_9_out, multiplexer_10_out, Next_PC, ram_1_data,
       register_1_q, rom_1_data, shifter_1_out;
  wire [31:28] J_JAL_PC;

  Clock #(.highDuration(1), .lowDuration(1)) clock_1 (.out(CLK));
  Button _1 (.out(IR1));
  Button _2 (.out(IR2));
  Button _3 (.out(IR3));
  Button \u_清零  (.out(RST));
  Button \u_继续运行  (.out(Go));
  LED #(.active("true")) led_1 (.in(W1));
  LED #(.active("true")) led_2 (.in(W2));
  LED #(.active("true")) led_3 (.in(W3));
  Hex_Digit_Display hex_digit_display_1 (.value(LedData[31:28]));  // open: dp
  or or_1 (or_1_out[0], JR, BLEZ_DE, B___De);
  and and_1 (and_1_out, ~DataConflict, \运行 );  // AND_Gate
  Hex_Digit_Display hex_digit_display_2 (.value(LedData[27:24]));  // open: dp
  Hex_Digit_Display hex_digit_display_3 (.value(LedData[23:20]));  // open: dp
  or or_2 (branch, BLEZ_DE, B___De);
  Multiplexer #(.select(2), .width(32), .disabled("Z"), .enable("false")) multiplexer_1 (
    .in0(Next_PC), .in1(B___PC), .in2({J_JAL_PC, IR_2[25:0], 2'b00}), .in3(JR_PC), .out(multiplexer_1_out),
    .sel({JMP, or_1_out[0]}));
  Register #(.width(32), .trigger("rising"), .Select("low")) PC (
    .D(multiplexer_1_out), .en(and_1_out), .Q(IF_PC), .clk(CLK));  // open: clr
  Hex_Digit_Display hex_digit_display_4 (.value(LedData[15:12]));  // open: dp
  Hex_Digit_Display hex_digit_display_5 (.value(LedData[19:16]));  // open: dp
  Hex_Digit_Display hex_digit_display_6 (.value(LedData[11:8]));  // open: dp
  Hex_Digit_Display hex_digit_display_7 (.value(LedData[7:4]));  // open: dp
  Hex_Digit_Display hex_digit_display_8 (.value(LedData[3:0]));  // open: dp
  // Probe on \总周期数 
  Adder #(.width(32)) adder_1 (.a(IF_PC), .b(32'h4), .out(Next_PC));  // open: cin, cout
  ROM #(.addrWidth(10), .dataWidth(32), .Select("high")) rom_1 (.addr(IF_PC[11:2]), .data(rom_1_data));
  and and_2 (and_2_out, JMP, ~STALL);  // AND_Gate
  or or_3 (or_3_out, RST, BracnhConflict);
  IF_ID if_id_1 (
    .in_5(CLK), .in_2(rom_1_data), .in_1(IF_PC), .out_8(ID_PC), .out_9(IR_1), .in_7(or_3_out), .in_6(or_4_out));  // open: in_3, out_10, in_4, out_11
  or or_4 (or_4_out, STALL, DataConflict);
  // Probe on \总周期数 
  // Probe on \无条件分支数 
  // Probe on \条件分支成功数 
  // Probe on \插入气泡数 
  // Probe on \LoadUse次数 
  Counter #(.width(16), .max('hffff), .ongoal("wrap"), .trigger("rising"), .behavior("new")) counter_1 (
    .count(and_2_out), .Q(\无条件分支数 ), .clk(CLK), .clr(RST));  // open: load, D, carry, preset, down
  and and_3 (and_3_out, branch, ~STALL);  // AND_Gate
  // Probe on ID_PC[11:0]
  // Probe on IF_PC[11:0]
  Counter #(.width(16), .max('hffff), .ongoal("wrap"), .trigger("rising"), .behavior("new")) counter_2 (
    .count(and_3_out), .Q(\条件分支成功数 ), .clk(CLK), .clr(RST));  // open: load, D, carry, preset, down
  // Probe on M_PC[11:0]
  // Probe on EX_PC[11:0]
  Counter #(.width(16), .max('hffff), .ongoal("wrap"), .trigger("rising"), .behavior("new")) counter_3 (
    .count(and_4_out), .Q(\插入气泡数 ), .clk(CLK), .clr(RST));  // open: load, D, carry, preset, down
  and and_4 (and_4_out, or_5_out, \运行 );
  or or_5 (or_5_out, STALL, DataConflict);
  \拓展单周期硬布线控制器_31  \u_拓展单周期硬布线控制器_31_1  (
    .OP(IR_1[31:26]), .Func(IR_1[5:0]), .ALU_OP(\拓展单周期硬布线控制器_31_1_alu_op ),
    .MemToReg(\拓展单周期硬布线控制器_31_1_memtoreg ), .MemWrite(\拓展单周期硬布线控制器_31_1_memwrite ),
    .ALU_SRC(\拓展单周期硬布线控制器_31_1_alu_src ), .RegWrite(\拓展单周期硬布线控制器_31_1_regwrite ),
    .SysCALL(\拓展单周期硬布线控制器_31_1_syscall ), .SignedExt(SignedExt), .RegDst(\拓展单周期硬布线控制器_31_1_regdst [0]),
    .Beq(\拓展单周期硬布线控制器_31_1_beq ), .Bne(\拓展单周期硬布线控制器_31_1_bne ), .JR(\拓展单周期硬布线控制器_31_1_jr ),
    .JMP(\拓展单周期硬布线控制器_31_1_jmp ), .JAL(JAL_1), .LUI(\拓展单周期硬布线控制器_31_1_lui ), .LB(\拓展单周期硬布线控制器_31_1_lb ),
    .BLEZ(\拓展单周期硬布线控制器_31_1_blez ), .R1_Used(R1_U), .R2_Used(R2_U));  // open: MFC0, MTC0, ERET, M
  // Probe on WB_PC[11:0]
  Counter #(.width(16), .max('hffff), .ongoal("wrap"), .trigger("rising"), .behavior("new")) counter_4 (
    .count(and_4_out), .Q(\LoadUse次数 ), .clr(RST));  // open: load, D, carry, clk, preset, down
  Multiplexer #(.select(1), .width(5), .disabled("Z"), .enable("false")) multiplexer_2 (
    .in0(IR_1[25:21]), .in1(5'b00010), .out(R1_num), .sel(\拓展单周期硬布线控制器_31_1_syscall ));
  Multiplexer #(.select(1), .width(5), .disabled("Z"), .enable("false")) multiplexer_3 (
    .in0(IR_1[20:16]), .in1(5'b00100), .out(R2_num), .sel(\拓展单周期硬布线控制器_31_1_syscall ));
  assign bit_extender_1_out = {{16{1'b0}}, IR_1[15:0]};  // Bit_Extender bit_extender_1
  assign bit_extender_2_out = {{16{IR_1[15]}}, IR_1[15:0]};  // Bit_Extender bit_extender_2
  Multiplexer #(.select(2), .width(5), .disabled("Z"), .enable("false")) multiplexer_4 (
    .in0(IR_1[20:16]), .in1(IR_1[15:11]), .in2({5{1'b1}}), .out(multiplexer_4_out),
    .sel({JAL_1, \拓展单周期硬布线控制器_31_1_regdst [0]}));  // open: in3
  Multiplexer #(.select(1), .width(32), .disabled("Z"), .enable("false")) multiplexer_5 (
    .in0(bit_extender_1_out), .in1(bit_extender_2_out), .out(multiplexer_5_out), .sel(SignedExt));
  MIPS_Regifile mips_regifile_1 (
    .Din(RDin), .Clk(CLK), .R1(mips_regifile_1_r1), .R2(mips_regifile_1_r2), .WE(RegWrite), .W_num(W_num),
    .R1_num(R1_num), .R2_num(R2_num));
  or or_6 (or_6_out, RST, BracnhConflict, DataConflict);
  ID_EX id_ex_1 (
    .in_1(\拓展单周期硬布线控制器_31_1_jr ), .in_4(\拓展单周期硬布线控制器_31_1_blez ), .in_5(\拓展单周期硬布线控制器_31_1_lb ),
    .in_6(\拓展单周期硬布线控制器_31_1_beq ), .in_7(\拓展单周期硬布线控制器_31_1_bne ), .in_8(\拓展单周期硬布线控制器_31_1_memtoreg ),
    .in_9(\拓展单周期硬布线控制器_31_1_memwrite ), .in_10(\拓展单周期硬布线控制器_31_1_alu_op ),
    .in_11(\拓展单周期硬布线控制器_31_1_alu_src ), .in_12(\拓展单周期硬布线控制器_31_1_regwrite ),
    .in_13(\拓展单周期硬布线控制器_31_1_syscall ), .in_14(ID_PC), .in_15(IR_1), .in_16(mips_regifile_1_r1),
    .in_17(mips_regifile_1_r2), .in_18(multiplexer_5_out), .in_19(IR_1[10:6]), .in_20(multiplexer_4_out),
    .in_21({IR_1[15:0], {16{1'b0}}}), .out_29(JR), .out_30(JMP), .out_31(id_ex_1_out_31), .out_32(BLEZ),
    .out_33(id_ex_1_out_33), .out_34(id_ex_1_out_34), .out_35(id_ex_1_out_35), .out_36(id_ex_1_out_36),
    .out_37(id_ex_1_out_37), .out_40(EX_RegWrite), .out_41(id_ex_1_out_41), .out_42(EX_PC),
    .out_38(id_ex_1_out_38), .out_39(id_ex_1_out_39), .out_43(IR_2), .out_44(JR_PC), .out_45(id_ex_1_out_45),
    .out_46(id_ex_1_out_46), .out_47(id_ex_1_out_47), .out_48(EX_WriteReg_num), .out_49(id_ex_1_out_49),
    .in_26(CLK), .in_3(\拓展单周期硬布线控制器_31_1_lui ), .in_2(\拓展单周期硬布线控制器_31_1_jmp ), .in_27(STALL),
    .in_28(or_6_out), .out_51(JAL_2), .in_23(JAL_1));  // open: in_22, out_50, in_24, out_52, in_25, out_53
  or or_7 (BracnhConflict, JMP, JR, B___De, BLEZ_DE);
  Multiplexer #(.select(1), .width(32), .disabled("Z"), .enable("false")) multiplexer_6 (
    .in0(id_ex_1_out_45), .in1(id_ex_1_out_46), .out(multiplexer_6_out), .sel(id_ex_1_out_39));
  Shifter #(.width(32), .shift("ll")) shifter_1 (.in(id_ex_1_out_46), .\dist (5'b00010), .out(shifter_1_out));
  Adder #(.width(32)) adder_2 (.a(EX_PC), .b(32'h4), .out({J_JAL_PC, adder_2_out}));  // open: cin, cout
  Comparator #(.width(32), .mode("twosComplement")) comparator_1 (
    .a(JR_PC), .b({32{1'b0}}), .gt(comparator_1_gt));  // open: eq, lt
  Adder #(.width(32)) adder_3 (.a(shifter_1_out), .b({J_JAL_PC, adder_2_out}), .out(B___PC));  // open: cin, cout
  and and_5 (and_5_out, mips_alu_1_equal, id_ex_1_out_34);
  not not_1 (not_1_out, mips_alu_1_equal);
  and and_6 (and_6_out, not_1_out, id_ex_1_out_35);
  not not_2 (not_2_out, comparator_1_gt);
  MIPS_ALU mips_alu_1 (
    .X(JR_PC), .Y(multiplexer_6_out), .AluOP(id_ex_1_out_38), .Equal(mips_alu_1_equal),
    .Result(mips_alu_1_result), .shamt(id_ex_1_out_47));  // open: Result_2
  \数据相关检测_24_3_2  \u_数据相关检测_24_3_2_1  (
    .EX_RegWrite(EX_RegWrite), .R1_num(R1_num), .EX_WriteReg_num(EX_WriteReg_num),
    .MEM_RegWrite(MEM_RegWrite), .R2_num(R2_num), .MEM_WriteReg_num(MEM_WriteReg_num), .R1_Used(R1_U),
    .R2_Used(R2_U), .\MEM相关 (\数据相关检测_24_3_2_1_mem相关 ), .\EX相关 (\数据相关检测_24_3_2_1_ex相关 ));  // open: R1_MEM
  or or_8 (B___De, and_5_out, and_6_out);
  and and_7 (BLEZ_DE, BLEZ, not_2_out);
  or or_9 (DataConflict, \数据相关检测_24_3_2_1_ex相关 , \数据相关检测_24_3_2_1_mem相关 );
  Counter #(.width(16), .max('hffff), .ongoal("wrap"), .trigger("rising"), .behavior("old")) counter_5 (
    .count(\运行 ), .Q(\总周期数 ), .clk(CLK));  // open: load, D, carry, clr, preset
  EX_MEM ex_mem_1 (
    .in_1(id_ex_1_out_31), .out_18(ex_mem_1_out_18), .in_2(id_ex_1_out_33), .out_19(ex_mem_1_out_19),
    .in_3(id_ex_1_out_36), .out_20(ex_mem_1_out_20), .in_4(id_ex_1_out_37), .out_21(MemWrite), .in_8(EX_PC),
    .out_25(M_PC), .in_9(IR_2), .out_26(IR_3), .in_10(mips_alu_1_result), .out_27(ex_mem_1_out_27),
    .in_11(id_ex_1_out_45), .out_28(MDin), .in_12(EX_WriteReg_num), .out_29(MEM_WriteReg_num),
    .in_13(id_ex_1_out_49), .out_30(ex_mem_1_out_30), .in_15(CLK), .in_5(EX_RegWrite), .out_22(MEM_RegWrite),
    .in_16(STALL), .in_17(RST), .in_6(JR_PC), .out_23(ex_mem_1_out_23), .in_7(id_ex_1_out_41),
    .out_24(ex_mem_1_out_24), .in_14(JAL_2), .out_31(JAL_3));
  RAM #(.addrWidth(10), .dataWidth(32), .bus("separate"), .Select("high")) ram_1 (
    .addr(ex_mem_1_out_27[11:2]), .din(MDin), .data(ram_1_data), .str(MemWrite), .clk(CLK));  // open: sel, ld, clr
  Multiplexer #(.select(1), .width(32), .disabled("Z"), .enable("false")) multiplexer_7 (
    .in0(multiplexer_8_out), .in1(adder_4_out), .out(RDin), .sel(JAL_4));
  Adder #(.width(32)) adder_4 (.a(WB_PC), .b(32'h4), .out(adder_4_out));  // open: cin, cout
  MEM_WB mem_wb_1 (
    .in_1(ex_mem_1_out_18), .out_18(LUI), .in_2(ex_mem_1_out_19), .out_19(mem_wb_1_out_19),
    .in_3(ex_mem_1_out_20), .out_20(mem_wb_1_out_20), .in_4(MEM_RegWrite), .out_21(RegWrite), .in_7(M_PC),
    .out_24(WB_PC), .in_8(IR_3), .out_25(IR_4), .in_9(ex_mem_1_out_27), .out_26(mem_wb_1_out_26),
    .in_10(ram_1_data), .out_27(mem_wb_1_out_27), .in_12(MEM_WriteReg_num), .out_29(W_num),
    .in_13(ex_mem_1_out_30), .out_30(mem_wb_1_out_30), .in_15(CLK), .in_16(STALL), .in_5(ex_mem_1_out_23),
    .out_22(mem_wb_1_out_22), .in_6(ex_mem_1_out_24), .out_23(Syscall), .in_11(MDin), .out_28(a0),
    .in_17(RST), .in_14(JAL_3), .out_31(JAL_4));
  Multiplexer #(.select(1), .width(32), .disabled("Z"), .enable("false")) multiplexer_8 (
    .in0(multiplexer_9_out), .in1(mem_wb_1_out_30), .out(multiplexer_8_out), .sel(LUI));
  Multiplexer #(.select(1), .width(32), .disabled("Z"), .enable("false")) multiplexer_9 (
    .in0(multiplexer_10_out), .in1(bit_extender_3_out), .out(multiplexer_9_out), .sel(mem_wb_1_out_19));
  Multiplexer #(.select(1), .width(32), .disabled("Z"), .enable("false")) multiplexer_10 (
    .in0(mem_wb_1_out_26), .in1(mem_wb_1_out_27), .out(multiplexer_10_out), .sel(mem_wb_1_out_20));
  Multiplexer #(.select(2), .width(8), .disabled("Z"), .enable("false")) multiplexer_11 (
    .in0(multiplexer_10_out[7:0]), .in1(multiplexer_10_out[15:8]), .in2(multiplexer_10_out[23:16]),
    .in3(multiplexer_10_out[31:24]), .out(multiplexer_11_out), .sel(mem_wb_1_out_26[1:0]));
  assign bit_extender_3_out = {{24{multiplexer_11_out[7]}}, multiplexer_11_out};  // Bit_Extender bit_extender_3
  Comparator #(.width(32), .mode("twosComplement")) comparator_2 (
    .a(mem_wb_1_out_22), .b(32'h22), .eq(comparator_2_eq));  // open: gt, lt
  Multiplexer #(.select(1), .width(1), .disabled("Z"), .enable("false")) multiplexer_12 (
    .in0(1'b0), .in1(comparator_2_eq), .out(multiplexer_12_out), .sel(Syscall));
  or or_10 (or_10_out, Go, multiplexer_12_out, ~Syscall);  // OR_Gate
  Register #(.width(32), .trigger("rising"), .Select("low")) register_1 (
    .D(a0), .en(multiplexer_12_out), .Q(register_1_q), .clk(CLK));  // open: clr
  and and_8 (and_8_out, Syscall, comparator_2_eq);
  // NOT_Gate not_3 has open pins: in=or_10_out, out=open
  Register #(.width(32), .trigger("rising"), .Select("low")) register_2 (
    .D(a0), .Q(LedData), .clk(and_8_out));  // open: en, clr
  and and_9 (and_9_out, Syscall, ~comparator_2_eq);  // AND_Gate
  D_Flip_Flop #(.trigger("falling"), .Pre_Clr_Positions("LEGACY"), .NegatePresetClear("false"), .enable("true"), .NewFFLayout("false")) d_ff_1 (
    .clk(CLK), .D(and_9_out), .Q(STALL), .reset(Go));  // open: Qn, preset, en
  not not_4 (\运行 , STALL);

  // Other names for the same wires on the sheet: Din[31:0] = RDin; J_JAL_PC[27:2] = IR_2[25:0];
  //   Next_PC_1[31:0] = ID_PC; Next_PC_2[31:0] = EX_PC; MEM_PC[31:0] = M_PC; Next_PC_3[31:0] = M_PC;
  //   Next_PC_4[31:0] = WB_PC; RegWrite_1 = RegWrite

  // Notes on the sheet:
  //   中断源
  //   中断等待指示
  //   总复位信号应将除ROM以外所有存储组件全部清零
  //   数码管输出
  //   数码管输出应该用寄存器锁存，否则显示数据只能一闪而过
  //   指令存储器
  //   指令字
  //   contents of rom_1 (hex, n*v repeats v):
  //   20110001 8000c05 20110001 20120002 20130003 8000c09 20110001 20120002 20130003 8000c0d 20110001
  //   20120002 20130003 8000c11 20110001 20120002 20130003 c000cb8 20100001 20110001 118fc0 112020
  //   20020022 c 118882 12200001 8000c15 112020 20020022 c 20110001 118880 112020 20020022 c 12200001
  //   8000c1f 20110001 118fc0 112020 20020022 c 1188c3 112020 20020022 c 118903 112020 20020022 c 118903
  //   112020 20020022 c 118903 112020 20020022 c 118903 112020 20020022 c 118903 112020 20020022 c 118903
  //   112020 20020022 c 118903 112020 20020022 c 20100001 109fc0 139fc3 8021 2012000c 24160003 26100001
  //   3210000f 20080008 20090001 139900 2709825 132020 20020022 c 1094022 1500fff9 22100001 2018000f
  //   2188024 108700 20080008 20090001 139902 2709825 132021 20020022 c 1094022 1500fff9 108702 2c9b022
  //   12c00001 8000c50 4020 1084027 84400 3508ffff 82021 20020022 c 2010ffff 20110000 ae300000 22100001
  //   22310004 ae300000 22100001 22310004 ae300000 22100001 22310004 ae300000 22100001 22310004 ae300000
  //   22100001 22310004 ae300000 22100001 22310004 ae300000 22100001 22310004 ae300000 22100001 22310004
  //   ae300000 22100001 22310004 ae300000 22100001 22310004 ae300000 22100001 22310004 ae300000 22100001
  //   22310004 ae300000 22100001 22310004 ae300000 22100001 22310004 ae300000 22100001 22310004 ae300000
  //   22100001 22310004 22100001 8020 2011003c 8e130000 8e340000 274402a 11000002 ae330000 ae140000
  //   2231fffc 1611fff8 102020 20020022 c 22100004 2011003c 1611fff2 20020032 c 20100000 22100001 102020
  //   20020022 c 22100002 102020 20020022 c 22100003 102020 20020022 c 22100004 102020 20020022 c 22100005
  //   102020 20020022 c 22100006 102020 20020022 c 22100007 102020 20020022 c 22100008 102020 20020022
  //   20020022 c 3e00008
  //   指令字
  //   OP
  //   Func
  //   rs
  //   rt
  //   rd
  //   流水调试日志用
  //   Syscall
  //   JAL
  //   RegDst
  //   MemToReg
  //   MemWrite
  //   AluOP
  //   AluSrcB
  //   RegWrite
  //   W#
  //   JR
  //   JMP
  //   LUI
  //   LUI
  //   BLEZ
  //   BLEZ
  //   LB
  //   LB
  //   Beq
  //   Beq
  //   Bne
  //   Bne
  //   AluOP
  //   W#
  //   为方便自动评测，需要输出流水线各段保存的PC值，注意是PC不是PC+4，另外ID段寄存器写入信息，Mem段内存写入信息也要输出
  //   MemToReg
  //   MemWrite
  //   AluSrcB
  //   RegWrite
  //   LUI
  //   LB
  //   MemToReg
  //   MemWrite
  //   RegWrite
  //   W#
  //   LUI
  //   LB
  //   W#
  //   MemToReg
  //   LUI
  //   LB
  //   RegWrite
  //   W#
endmodule

module \气泡流水线  (
  output RegWrite,
  output MemWrite,
  output [31:0] IF_PC,
  output [31:0] ID_PC,
  output [31:0] EX_PC,
  output [31:0] M_PC,
  output [31:0] WB_PC,
  output [31:0] RDin,
  output [31:0] MDin,
  output [31:0] LedData
);

  wire and_1_out, and_2_out, and_3_out, and_4_out, and_5_out, and_6_out, and_8_out, and_9_out, B___De, BLEZ,
       BLEZ_DE, BracnhConflict, branch, CLK, comparator_1_gt, comparator_2_eq, DataConflict, ex_mem_1_out_18,
       ex_mem_1_out_19, ex_mem_1_out_20, ex_mem_1_out_24, EX_RegWrite, Go, id_ex_1_out_31, id_ex_1_out_33,
       id_ex_1_out_34, id_ex_1_out_35, id_ex_1_out_36, id_ex_1_out_37, id_ex_1_out_39, id_ex_1_out_41, IR1,
       IR2, IR3, JAL_1, JAL_2, JAL_3, JAL_4, JMP, JR, LUI, MEM_RegWrite, mem_wb_1_out_19, mem_wb_1_out_20,
       mips_alu_1_equal, multiplexer_12_out, not_1_out, not_2_out, or_3_out, or_4_out, or_5_out, or_6_out,
       or_10_out, R1_U, R2_U, RST, SignedExt, STALL, Syscall, W1, W2, W3, \拓展单周期硬布线控制器_31_1_alu_src ,
       \拓展单周期硬布线控制器_31_1_beq , \拓展单周期硬布线控制器_31_1_blez , \拓展单周期硬布线控制器_31_1_bne , \拓展单周期硬布线控制器_31_1_jmp ,
       \拓展单周期硬布线控制器_31_1_jr , \拓展单周期硬布线控制器_31_1_lb , \拓展单周期硬布线控制器_31_1_lui , \拓展单周期硬布线控制器_31_1_memtoreg ,
       \拓展单周期硬布线控制器_31_1_memwrite , \拓展单周期硬布线控制器_31_1_regwrite , \拓展单周期硬布线控制器_31_1_syscall ,
       \数据相关检测_24_3_2_1_ex相关 , \数据相关检测_24_3_2_1_mem相关 , \运行 ;
  wire [0:0] or_1_out, \拓展单周期硬布线控制器_31_1_regdst ;
  wire [3:0] id_ex_1_out_38, \拓展单周期硬布线控制器_31_1_alu_op ;
  wire [4:0] EX_WriteReg_num, id_ex_1_out_47, MEM_WriteReg_num, multiplexer_4_out, R1_num, R2_num, W_num;
  wire [7:0] multiplexer_10_out, multiplexer_10_out_2, multiplexer_10_out_3, multiplexer_10_out_4,
       multiplexer_11_out;
  wire [15:0] \LoadUse次数 , \总周期数 , \插入气泡数 , \无条件分支数 , \条件分支成功数 ;
  wire [27:0] adder_2_out;
  wire [31:0] a0, adder_4_out, B___PC, bit_extender_1_out, bit_extender_2_out, bit_extender_3_out,
       ex_mem_1_out_23, ex_mem_1_out_27, ex_mem_1_out_30, id_ex_1_out_45, id_ex_1_out_46, id_ex_1_out_49,
       IR_1, IR_2, IR_3, IR_4, JR_PC, mem_wb_1_out_22, mem_wb_1_out_26, mem_wb_1_out_27, mem_wb_1_out_30,
       mips_alu_1_result, mips_regifile_1_r1, mips_regifile_1_r2, multiplexer_1_out, multiplexer_5_out,
       multiplexer_6_out, multiplexer_8_out, multiplexer_9_out, Next_PC, ram_1_data, register_1_q,
       rom_1_data, shifter_1_out;
  wire [31:28] J_JAL_PC;

  Clock #(.highDuration(1), .lowDuration(1)) clock_1 (.out(CLK));
  Button _1 (.out(IR1));
  Button _2 (.out(IR2));
  Button _3 (.out(IR3));
  Button \u_清零  (.out(RST));
  Button \u_继续运行  (.out(Go));
  LED #(.active("true")) led_1 (.in(W1));
  LED #(.active("true")) led_2 (.in(W2));
  LED #(.active("true")) led_3 (.in(W3));
  Hex_Digit_Display hex_digit_display_1 (.value(LedData[31:28]));  // open: dp
  or or_1 (or_1_out[0], JR, BLEZ_DE, B___De);
  and and_1 (and_1_out, ~DataConflict, \运行 );  // AND_Gate
  Hex_Digit_Display hex_digit_display_2 (.value(LedData[23:20]));  // open: dp
  Hex_Digit_Display hex_digit_display_3 (.value(LedData[27:24]));  // open: dp
  or or_2 (branch, BLEZ_DE, B___De);
  Multiplexer #(.select(2), .width(32), .disabled("Z"), .enable("false")) multiplexer_1 (
    .in0(Next_PC), .in1(B___PC), .in2({J_JAL_PC, IR_2[25:0], 2'b00}), .in3(JR_PC), .out(multiplexer_1_out),
    .sel({JMP, or_1_out[0]}));
  Register #(.width(32), .trigger("rising"), .Select("low")) PC (
    .D(multiplexer_1_out), .en(and_1_out), .Q(IF_PC), .clk(CLK));  // open: clr
  Hex_Digit_Display hex_digit_display_4 (.value(LedData[19:16]));  // open: dp
  Hex_Digit_Display hex_digit_display_5 (.value(LedData[15:12]));  // open: dp
  Hex_Digit_Display hex_digit_display_6 (.value(LedData[7:4]));  // open: dp
  Hex_Digit_Display hex_digit_display_7 (.value(LedData[11:8]));  // open: dp
  Hex_Digit_Display hex_digit_display_8 (.value(LedData[3:0]));  // open: dp
  // Probe on \总周期数 
  Adder #(.width(32)) adder_1 (.a(IF_PC), .b(32'h4), .out(Next_PC));  // open: cin, cout
  ROM #(.addrWidth(10), .dataWidth(32), .Select("high")) rom_1 (.addr(IF_PC[11:2]), .data(rom_1_data));
  and and_2 (and_2_out, JMP, ~STALL);  // AND_Gate
  or or_3 (or_3_out, RST, BracnhConflict);
  IF_ID if_id_1 (
    .in_5(CLK), .in_2(rom_1_data), .in_1(IF_PC), .out_8(ID_PC), .out_9(IR_1), .in_7(or_3_out), .in_6(or_4_out));  // open: in_3, out_10, in_4, out_11
  or or_4 (or_4_out, STALL, DataConflict);
  // Probe on \总周期数 
  // Probe on \无条件分支数 
  // Probe on \条件分支成功数 
  // Probe on \插入气泡数 
  // Probe on \LoadUse次数 
  Counter #(.width(16), .max('hffff), .ongoal("wrap"), .trigger("rising"), .behavior("new")) counter_1 (
    .count(and_2_out), .Q(\无条件分支数 ), .clk(CLK), .clr(RST));  // open: load, D, carry, preset, down
  and and_3 (and_3_out, branch, ~STALL);  // AND_Gate
  // Probe on IF_PC[11:0]
  // Probe on ID_PC[11:0]
  Counter #(.width(16), .max('hffff), .ongoal("wrap"), .trigger("rising"), .behavior("new")) counter_2 (
    .count(and_3_out), .Q(\条件分支成功数 ), .clk(CLK), .clr(RST));  // open: load, D, carry, preset, down
  // Probe on EX_PC[11:0]
  // Probe on M_PC[11:0]
  Counter #(.width(16), .max('hffff), .ongoal("wrap"), .trigger("rising"), .behavior("new")) counter_3 (
    .count(and_4_out), .Q(\插入气泡数 ), .clk(CLK), .clr(RST));  // open: load, D, carry, preset, down
  and and_4 (and_4_out, or_5_out, \运行 );
  or or_5 (or_5_out, STALL, DataConflict);
  \拓展单周期硬布线控制器_31  \u_拓展单周期硬布线控制器_31_1  (
    .OP(IR_1[31:26]), .Func(IR_1[5:0]), .ALU_OP(\拓展单周期硬布线控制器_31_1_alu_op ),
    .MemToReg(\拓展单周期硬布线控制器_31_1_memtoreg ), .MemWrite(\拓展单周期硬布线控制器_31_1_memwrite ),
    .ALU_SRC(\拓展单周期硬布线控制器_31_1_alu_src ), .RegWrite(\拓展单周期硬布线控制器_31_1_regwrite ),
    .SysCALL(\拓展单周期硬布线控制器_31_1_syscall ), .SignedExt(SignedExt), .RegDst(\拓展单周期硬布线控制器_31_1_regdst [0]),
    .Beq(\拓展单周期硬布线控制器_31_1_beq ), .Bne(\拓展单周期硬布线控制器_31_1_bne ), .JR(\拓展单周期硬布线控制器_31_1_jr ),
    .JMP(\拓展单周期硬布线控制器_31_1_jmp ), .JAL(JAL_1), .LUI(\拓展单周期硬布线控制器_31_1_lui ), .LB(\拓展单周期硬布线控制器_31_1_lb ),
    .BLEZ(\拓展单周期硬布线控制器_31_1_blez ), .R1_Used(R1_U), .R2_Used(R2_U));  // open: MFC0, MTC0, ERET, M
  // Probe on WB_PC[11:0]
  Counter #(.width(16), .max('hffff), .ongoal("wrap"), .trigger("rising"), .behavior("new")) counter_4 (
    .count(and_4_out), .Q(\LoadUse次数 ), .clr(RST));  // open: load, D, carry, clk, preset, down
  Multiplexer #(.select(1), .width(5), .disabled("Z"), .enable("false")) multiplexer_2 (
    .in0(IR_1[25:21]), .in1(5'b00010), .out(R1_num), .sel(\拓展单周期硬布线控制器_31_1_syscall ));
  Multiplexer #(.select(1), .width(5), .disabled("Z"), .enable("false")) multiplexer_3 (
    .in0(IR_1[20:16]), .in1(5'b00100), .out(R2_num), .sel(\拓展单周期硬布线控制器_31_1_syscall ));
  assign bit_extender_1_out = {{16{1'b0}}, IR_1[15:0]};  // Bit_Extender bit_extender_1
  assign bit_extender_2_out = {{16{IR_1[15]}}, IR_1[15:0]};  // Bit_Extender bit_extender_2
  Multiplexer #(.select(2), .width(5), .disabled("Z"), .enable("false")) multiplexer_4 (
    .in0(IR_1[20:16]), .in1(IR_1[15:11]), .in2({5{1'b1}}), .out(multiplexer_4_out),
    .sel({JAL_1, \拓展单周期硬布线控制器_31_1_regdst [0]}));  // open: in3
  Multiplexer #(.select(1), .width(32), .disabled("Z"), .enable("false")) multiplexer_5 (
    .in0(bit_extender_1_out), .in1(bit_extender_2_out), .out(multiplexer_5_out), .sel(SignedExt));
  MIPS_Regifile mips_regifile_1 (
    .Din(RDin), .Clk(CLK), .R1(mips_regifile_1_r1), .R2(mips_regifile_1_r2), .WE(RegWrite), .W_num(W_num),
    .R1_num(R1_num), .R2_num(R2_num));
  or or_6 (or_6_out, RST, BracnhConflict, DataConflict);
  ID_EX id_ex_1 (
    .in_1(\拓展单周期硬布线控制器_31_1_jr ), .in_4(\拓展单周期硬布线控制器_31_1_blez ), .in_5(\拓展单周期硬布线控制器_31_1_lb ),
    .in_6(\拓展单周期硬布线控制器_31_1_beq ), .in_7(\拓展单周期硬布线控制器_31_1_bne ), .in_8(\拓展单周期硬布线控制器_31_1_memtoreg ),
    .in_9(\拓展单周期硬布线控制器_31_1_memwrite ), .in_10(\拓展单周期硬布线控制器_31_1_alu_op ),
    .in_11(\拓展单周期硬布线控制器_31_1_alu_src ), .in_12(\拓展单周期硬布线控制器_31_1_regwrite ),
    .in_13(\拓展单周期硬布线控制器_31_1_syscall ), .in_14(ID_PC), .in_15(IR_1), .in_16(mips_regifile_1_r1),
    .in_17(mips_regifile_1_r2), .in_18(multiplexer_5_out), .in_19(IR_1[10:6]), .in_20(multiplexer_4_out),
    .in_21({IR_1[15:0], {16{1'b0}}}), .out_29(JR), .out_30(JMP), .out_31(id_ex_1_out_31), .out_32(BLEZ),
    .out_33(id_ex_1_out_33), .out_34(id_ex_1_out_34), .out_35(id_ex_1_out_35), .out_36(id_ex_1_out_36),
    .out_37(id_ex_1_out_37), .out_40(EX_RegWrite), .out_41(id_ex_1_out_41), .out_42(EX_PC),
    .out_38(id_ex_1_out_38), .out_39(id_ex_1_out_39), .out_43(IR_2), .out_44(JR_PC), .out_45(id_ex_1_out_45),
    .out_46(id_ex_1_out_46), .out_47(id_ex_1_out_47), .out_48(EX_WriteReg_num), .out_49(id_ex_1_out_49),
    .in_26(CLK), .in_3(\拓展单周期硬布线控制器_31_1_lui ), .in_2(\拓展单周期硬布线控制器_31_1_jmp ), .in_27(STALL),
    .in_28(or_6_out), .out_51(JAL_2), .in_23(JAL_1));  // open: in_22, out_50, in_24, out_52, in_25, out_53
  or or_7 (BracnhConflict, JMP, JR, B___De, BLEZ_DE);
  Multiplexer #(.select(1), .width(32), .disabled("Z"), .enable("false")) multiplexer_6 (
    .in0(id_ex_1_out_45), .in1(id_ex_1_out_46), .out(multiplexer_6_out), .sel(id_ex_1_out_39));
  Shifter #(.width(32), .shift("ll")) shifter_1 (.in(id_ex_1_out_46), .\dist (5'b00010), .out(shifter_1_out));
  Adder #(.width(32)) adder_2 (.a(EX_PC), .b(32'h4), .out({J_JAL_PC, adder_2_out}));  // open: cin, cout
  Comparator #(.width(32), .mode("twosComplement")) comparator_1 (
    .a(JR_PC), .b({32{1'b0}}), .gt(comparator_1_gt));  // open: eq, lt
  Adder #(.width(32)) adder_3 (.a(shifter_1_out), .b({J_JAL_PC, adder_2_out}), .out(B___PC));  // open: cin, cout
  and and_5 (and_5_out, mips_alu_1_equal, id_ex_1_out_34);
  not not_1 (not_1_out, mips_alu_1_equal);
  and and_6 (and_6_out, not_1_out, id_ex_1_out_35);
  not not_2 (not_2_out, comparator_1_gt);
  MIPS_ALU mips_alu_1 (
    .X(JR_PC), .Y(multiplexer_6_out), .AluOP(id_ex_1_out_38), .Equal(mips_alu_1_equal),
    .Result(mips_alu_1_result), .shamt(id_ex_1_out_47));  // open: Result_2
  \数据相关检测_24_3_2  \u_数据相关检测_24_3_2_1  (
    .EX_RegWrite(EX_RegWrite), .R1_num(R1_num), .EX_WriteReg_num(EX_WriteReg_num),
    .MEM_RegWrite(MEM_RegWrite), .R2_num(R2_num), .MEM_WriteReg_num(MEM_WriteReg_num), .R1_Used(R1_U),
    .R2_Used(R2_U), .\MEM相关 (\数据相关检测_24_3_2_1_mem相关 ), .\EX相关 (\数据相关检测_24_3_2_1_ex相关 ));  // open: R1_MEM
  or or_8 (B___De, and_5_out, and_6_out);
  and and_7 (BLEZ_DE, BLEZ, not_2_out);
  or or_9 (DataConflict, \数据相关检测_24_3_2_1_ex相关 , \数据相关检测_24_3_2_1_mem相关 );
  Counter #(.width(16), .max('hffff), .ongoal("wrap"), .trigger("rising"), .behavior("old")) counter_5 (
    .count(\运行 ), .Q(\总周期数 ), .clk(CLK));  // open: load, D, carry, clr, preset
  EX_MEM ex_mem_1 (
    .in_1(id_ex_1_out_31), .out_18(ex_mem_1_out_18), .in_2(id_ex_1_out_33), .out_19(ex_mem_1_out_19),
    .in_3(id_ex_1_out_36), .out_20(ex_mem_1_out_20), .in_4(id_ex_1_out_37), .out_21(MemWrite), .in_8(EX_PC),
    .out_25(M_PC), .in_9(IR_2), .out_26(IR_3), .in_10(mips_alu_1_result), .out_27(ex_mem_1_out_27),
    .in_11(id_ex_1_out_45), .out_28(MDin), .in_12(EX_WriteReg_num), .out_29(MEM_WriteReg_num),
    .in_13(id_ex_1_out_49), .out_30(ex_mem_1_out_30), .in_15(CLK), .in_5(EX_RegWrite), .out_22(MEM_RegWrite),
    .in_16(STALL), .in_17(RST), .in_6(JR_PC), .out_23(ex_mem_1_out_23), .in_7(id_ex_1_out_41),
    .out_24(ex_mem_1_out_24), .in_14(JAL_2), .out_31(JAL_3));
  RAM #(.addrWidth(10), .dataWidth(32), .bus("separate"), .Select("high")) ram_1 (
    .addr(ex_mem_1_out_27[11:2]), .din(MDin), .data(ram_1_data), .str(MemWrite), .clk(CLK));  // open: sel, ld, clr
  Multiplexer #(.select(1), .width(32), .disabled("Z"), .enable("false")) multiplexer_7 (
    .in0(multiplexer_8_out), .in1(adder_4_out), .out(RDin), .sel(JAL_4));
  Adder #(.width(32)) adder_4 (.a(WB_PC), .b(32'h4), .out(adder_4_out));  // open: cin, cout
  MEM_WB mem_wb_1 (
    .in_1(ex_mem_1_out_18), .out_18(LUI), .in_2(ex_mem_1_out_19), .out_19(mem_wb_1_out_19),
    .in_3(ex_mem_1_out_20), .out_20(mem_wb_1_out_20), .in_4(MEM_RegWrite), .out_21(RegWrite), .in_7(M_PC),
    .out_24(WB_PC), .in_8(IR_3), .out_25(IR_4), .in_9(ex_mem_1_out_27), .out_26(mem_wb_1_out_26),
    .in_10(ram_1_data), .out_27(mem_wb_1_out_27), .in_12(MEM_WriteReg_num), .out_29(W_num),
    .in_13(ex_mem_1_out_30), .out_30(mem_wb_1_out_30), .in_15(CLK), .in_16(STALL), .in_5(ex_mem_1_out_23),
    .out_22(mem_wb_1_out_22), .in_6(ex_mem_1_out_24), .out_23(Syscall), .in_11(MDin), .out_28(a0),
    .in_17(RST), .in_14(JAL_3), .out_31(JAL_4));
  Multiplexer #(.select(1), .width(32), .disabled("Z"), .enable("false")) multiplexer_8 (
    .in0(multiplexer_9_out), .in1(mem_wb_1_out_30), .out(multiplexer_8_out), .sel(LUI));
  Multiplexer #(.select(1), .width(32), .disabled("Z"), .enable("false")) multiplexer_9 (
    .in0({multiplexer_10_out_4, multiplexer_10_out_3, multiplexer_10_out_2, multiplexer_10_out}),
    .in1(bit_extender_3_out), .out(multiplexer_9_out), .sel(mem_wb_1_out_19));
  Multiplexer #(.select(1), .width(32), .disabled("Z"), .enable("false")) multiplexer_10 (
    .in0(mem_wb_1_out_26), .in1(mem_wb_1_out_27),
    .out({multiplexer_10_out_4, multiplexer_10_out_3, multiplexer_10_out_2, multiplexer_10_out}),
    .sel(mem_wb_1_out_20));
  Multiplexer #(.select(2), .width(8), .disabled("Z"), .enable("false")) multiplexer_11 (
    .in0(multiplexer_10_out), .in1(multiplexer_10_out_2), .in2(multiplexer_10_out_3),
    .in3(multiplexer_10_out_4), .out(multiplexer_11_out), .sel(mem_wb_1_out_26[1:0]));
  assign bit_extender_3_out = {{24{multiplexer_11_out[7]}}, multiplexer_11_out};  // Bit_Extender bit_extender_3
  Comparator #(.width(32), .mode("twosComplement")) comparator_2 (
    .a(mem_wb_1_out_22), .b(32'h22), .eq(comparator_2_eq));  // open: gt, lt
  Multiplexer #(.select(1), .width(1), .disabled("Z"), .enable("false")) multiplexer_12 (
    .in0(1'b0), .in1(comparator_2_eq), .out(multiplexer_12_out), .sel(Syscall));
  or or_10 (or_10_out, Go, multiplexer_12_out, ~Syscall);  // OR_Gate
  Register #(.width(32), .trigger("rising"), .Select("low")) register_1 (
    .D(a0), .en(multiplexer_12_out), .Q(register_1_q), .clk(CLK));  // open: clr
  and and_8 (and_8_out, Syscall, comparator_2_eq);
  // NOT_Gate not_3 has open pins: in=or_10_out, out=open
  Register #(.width(32), .trigger("rising"), .Select("low")) register_2 (
    .D(a0), .Q(LedData), .clk(and_8_out));  // open: en, clr
  and and_9 (and_9_out, Syscall, ~comparator_2_eq);  // AND_Gate
  D_Flip_Flop #(.trigger("falling"), .Pre_Clr_Positions("LEGACY"), .NegatePresetClear("false"), .enable("true"), .NewFFLayout("false")) d_ff_1 (
    .clk(CLK), .D(and_9_out), .Q(STALL), .reset(Go));  // open: Qn, preset, en
  not not_4 (\运行 , STALL);

  // Other names for the same wires on the sheet: Din[31:0] = RDin; J_JAL_PC[27:2] = IR_2[25:0];
  //   Next_PC_1[31:0] = ID_PC; Next_PC_2[31:0] = EX_PC; MEM_PC[31:0] = M_PC; Next_PC_3[31:0] = M_PC;
  //   Next_PC_4[31:0] = WB_PC; RegWrite_1 = RegWrite

  // Notes on the sheet:
  //   中断源
  //   中断等待指示
  //   总复位信号应将除ROM以外所有存储组件全部清零
  //   数码管输出
  //   数码管输出应该用寄存器锁存，否则显示数据只能一闪而过
  //   指令存储器
  //   指令字
  //   contents of rom_1 (hex, n*v repeats v):
  //   20110001 8000c05 20110001 20120002 20130003 8000c09 20110001 20120002 20130003 8000c0d 20110001
  //   20120002 20130003 8000c11 20110001 20120002 20130003 c000cb8 20100001 20110001 118fc0 112020
  //   20020022 c 118882 12200001 8000c15 112020 20020022 c 20110001 118880 112020 20020022 c 12200001
  //   8000c1f 20110001 118fc0 112020 20020022 c 1188c3 112020 20020022 c 118903 112020 20020022 c 118903
  //   112020 20020022 c 118903 112020 20020022 c 118903 112020 20020022 c 118903 112020 20020022 c 118903
  //   112020 20020022 c 118903 112020 20020022 c 20100001 109fc0 139fc3 8021 2012000c 24160003 26100001
  //   3210000f 20080008 20090001 139900 2709825 132020 20020022 c 1094022 1500fff9 22100001 2018000f
  //   2188024 108700 20080008 20090001 139902 2709825 132021 20020022 c 1094022 1500fff9 108702 2c9b022
  //   12c00001 8000c50 4020 1084027 84400 3508ffff 82021 20020022 c 2010ffff 20110000 ae300000 22100001
  //   22310004 ae300000 22100001 22310004 ae300000 22100001 22310004 ae300000 22100001 22310004 ae300000
  //   22100001 22310004 ae300000 22100001 22310004 ae300000 22100001 22310004 ae300000 22100001 22310004
  //   ae300000 22100001 22310004 ae300000 22100001 22310004 ae300000 22100001 22310004 ae300000 22100001
  //   22310004 ae300000 22100001 22310004 ae300000 22100001 22310004 ae300000 22100001 22310004 ae300000
  //   22100001 22310004 22100001 8020 2011003c 8e130000 8e340000 274402a 11000002 ae330000 ae140000
  //   2231fffc 1611fff8 102020 20020022 c 22100004 2011003c 1611fff2 20020032 c 20100000 22100001 102020
  //   20020022 c 22100002 102020 20020022 c 22100003 102020 20020022 c 22100004 102020 20020022 c 22100005
  //   102020 20020022 c 22100006 102020 20020022 c 22100007 102020 20020022 c 22100008 102020 20020022
  //   20020022 c 3e00008
  //   指令字
  //   OP
  //   Func
  //   rs
  //   rt
  //   rd
  //   流水调试日志用
  //   Syscall
  //   JAL
  //   RegDst
  //   MemToReg
  //   MemWrite
  //   AluOP
  //   AluSrcB
  //   RegWrite
  //   W#
  //   JR
  //   JMP
  //   LUI
  //   LUI
  //   BLEZ
  //   BLEZ
  //   LB
  //   LB
  //   Beq
  //   Beq
  //   Bne
  //   Bne
  //   AluOP
  //   W#
  //   为方便自动评测，需要输出流水线各段保存的PC值，注意是PC不是PC+4，另外ID段寄存器写入信息，Mem段内存写入信息也要输出
  //   MemToReg
  //   MemWrite
  //   AluSrcB
  //   RegWrite
  //   LUI
  //   LB
  //   MemToReg
  //   MemWrite
  //   RegWrite
  //   W#
  //   LUI
  //   LB
  //   W#
  //   MemToReg
  //   LUI
  //   LB
  //   RegWrite
  //   W#
endmodule
module \重定向流水线  (
  output RegWrite,
  output MemWrite,
  output [31:0] IF_PC,
  output [31:0] ID_PC,
  output [31:0] EX_PC,
  output [31:0] M_PC,
  output [31:0] WB_PC,
  output [31:0] RDin,
  output [31:0] MDin,
  output [31:0] LedData
);

  wire and_1_out, and_2_out, and_3_out, and_4_out, and_5_out, and_7_out, B___De, BLEZ, BLEZ_DE,
       BracnhConflict, branch, CLK, comparator_1_gt, comparator_2_eq, DataConflict, EX_Con, ex_mem_1_out_18,
       ex_mem_1_out_19, ex_mem_1_out_20, ex_mem_1_out_24, EX_RegWrite, Go, id_ex_1_out_31, id_ex_1_out_33,
       id_ex_1_out_34, id_ex_1_out_35, id_ex_1_out_36, id_ex_1_out_37, id_ex_1_out_39, id_ex_1_out_41, IR1,
       IR2, IR3, JAL_1, JAL_2, JAL_3, JAL_4, JMP, JR, LoadUse, LUI, MEM_RegWrite, mem_wb_1_out_19,
       mem_wb_1_out_20, mem_wb_1_out_23, mips_alu_1_equal, multiplexer_15_out, not_1_out, not_2_out,
       or_3_out, or_4_out, or_6_out, or_9_out, R1_U, R2_U, RST, SignedExt, STALL, W1, W2, W3,
       \拓展单周期硬布线控制器_31_1_alu_src , \拓展单周期硬布线控制器_31_1_beq , \拓展单周期硬布线控制器_31_1_blez , \拓展单周期硬布线控制器_31_1_bne ,
       \拓展单周期硬布线控制器_31_1_jmp , \拓展单周期硬布线控制器_31_1_jr , \拓展单周期硬布线控制器_31_1_lb , \拓展单周期硬布线控制器_31_1_lui ,
       \拓展单周期硬布线控制器_31_1_memtoreg , \拓展单周期硬布线控制器_31_1_memwrite , \拓展单周期硬布线控制器_31_1_regwrite ,
       \拓展单周期硬布线控制器_31_1_syscall , \数据相关检测_24_3_2_1_mem相关 , \运行 ;
  wire [0:0] or_1_out, \拓展单周期硬布线控制器_31_1_regdst ;
  wire [3:0] id_ex_1_out_38, relation, relation_1, \拓展单周期硬布线控制器_31_1_alu_op ;
  wire [4:0] EX_WriteReg_num, id_ex_1_out_47, MEM_WriteReg_num, multiplexer_4_out, R1_num, R2_num, W_num;
  wire [7:0] multiplexer_14_out;
  wire [15:0] \LoadUse次数 , \总周期数 , \插入气泡数 , \无条件分支数 , \条件分支成功数 ;
  wire [27:0] adder_2_out;
  wire [31:0] a0, adder_4_out, B___PC, bit_extender_1_out, bit_extender_2_out, bit_extender_3_out,
       ex_mem_1_out_23, ex_mem_1_out_30, id_ex_1_out_44, id_ex_1_out_45, id_ex_1_out_46, id_ex_1_out_49,
       IR_1, IR_2, IR_3, IR_4, JR_PC, MEM_AluR, mem_wb_1_out_22, mem_wb_1_out_30, mips_alu_1_result,
       mips_regifile_1_r1, mips_regifile_1_r2, multiplexer_1_out, multiplexer_5_out, multiplexer_8_out,
       multiplexer_9_out, multiplexer_11_out, multiplexer_12_out, Next_PC, ram_1_data, rom_1_data,
       shifter_1_out, W, WB_AluR, WB_Read;
  wire [31:28] J_JAL_PC;

  Clock #(.highDuration(1), .lowDuration(1)) clock_1 (.out(CLK));
  Button _1 (.out(IR1));
  Button _2 (.out(IR2));
  Button _3 (.out(IR3));
  Button \u_继续运行  (.out(Go));
  LED #(.active("true")) led_1 (.in(W1));
  LED #(.active("true")) led_2 (.in(W2));
  LED #(.active("true")) led_3 (.in(W3));
  Hex_Digit_Display hex_digit_display_1 (.value(LedData[31:28]));  // open: dp
  Button \u_清零  (.out(RST));
  Hex_Digit_Display hex_digit_display_2 (.value(LedData[23:20]));  // open: dp
  Hex_Digit_Display hex_digit_display_3 (.value(LedData[27:24]));  // open: dp
  Hex_Digit_Display hex_digit_display_4 (.value(LedData[19:16]));  // open: dp
  Hex_Digit_Display hex_digit_display_5 (.value(LedData[15:12]));  // open: dp
  or or_1 (or_1_out[0], JR, BLEZ_DE, B___De);
  Multiplexer #(.select(2), .width(32), .disabled("Z"), .enable("false")) multiplexer_1 (
    .in0(Next_PC), .in1(B___PC), .in2({J_JAL_PC, IR_2[25:0], 2'b00}), .in3(JR_PC), .out(multiplexer_1_out),
    .sel({JMP, or_1_out[0]}));
  and and_1 (and_1_out, ~LoadUse, \运行 );  // AND_Gate
  Hex_Digit_Display hex_digit_display_6 (.value(LedData[11:8]));  // open: dp
  Hex_Digit_Display hex_digit_display_7 (.value(LedData[7:4]));  // open: dp
  or or_2 (branch, BLEZ_DE, B___De);
  Register #(.width(32), .trigger("rising"), .Select("low")) PC (
    .D(multiplexer_1_out), .en(and_1_out), .Q(IF_PC), .clk(CLK));  // open: clr
  Hex_Digit_Display hex_digit_display_8 (.value(LedData[3:0]));  // open: dp
  // Probe on \总周期数 
  Adder #(.width(32)) adder_1 (.a(IF_PC), .b(32'h4), .out(Next_PC));  // open: cin, cout
  // Probe on \总周期数 
  // Probe on \无条件分支数 
  // Probe on \条件分支成功数 
  // Probe on \插入气泡数 
  // Probe on \LoadUse次数 
  Counter #(.width(16), .max('hffff), .ongoal("wrap"), .trigger("rising"), .behavior("old")) counter_1 (
    .count(\运行 ), .Q(\总周期数 ), .clk(CLK));  // open: load, D, carry, clr, preset
  ROM #(.addrWidth(10), .dataWidth(32), .Select("high")) rom_1 (.addr(IF_PC[11:2]), .data(rom_1_data));
  or or_3 (or_3_out, RST, BracnhConflict);
  IF_ID if_id_1 (
    .in_5(CLK), .in_2(rom_1_data), .in_1(IF_PC), .out_8(ID_PC), .out_9(IR_1), .in_7(or_3_out), .in_6(or_4_out));  // open: in_3, out_10, in_4, out_11
  or or_4 (or_4_out, STALL, LoadUse);
  // Probe on ID_PC[11:0]
  // Probe on IF_PC[11:0]
  // Probe on EX_PC[11:0]
  // Probe on M_PC[11:0]
  // Probe on WB_PC[11:0]
  \拓展单周期硬布线控制器_31  \u_拓展单周期硬布线控制器_31_1  (
    .OP(IR_1[31:26]), .Func(IR_1[5:0]), .ALU_OP(\拓展单周期硬布线控制器_31_1_alu_op ),
    .MemToReg(\拓展单周期硬布线控制器_31_1_memtoreg ), .MemWrite(\拓展单周期硬布线控制器_31_1_memwrite ),
    .ALU_SRC(\拓展单周期硬布线控制器_31_1_alu_src ), .RegWrite(\拓展单周期硬布线控制器_31_1_regwrite ),
    .SysCALL(\拓展单周期硬布线控制器_31_1_syscall ), .SignedExt(SignedExt), .RegDst(\拓展单周期硬布线控制器_31_1_regdst [0]),
    .Beq(\拓展单周期硬布线控制器_31_1_beq ), .Bne(\拓展单周期硬布线控制器_31_1_bne ), .JR(\拓展单周期硬布线控制器_31_1_jr ),
    .JMP(\拓展单周期硬布线控制器_31_1_jmp ), .JAL(JAL_1), .LUI(\拓展单周期硬布线控制器_31_1_lui ), .LB(\拓展单周期硬布线控制器_31_1_lb ),
    .BLEZ(\拓展单周期硬布线控制器_31_1_blez ), .R1_Used(R1_U), .R2_Used(R2_U));  // open: MFC0, MTC0, ERET, M
  or or_5 (DataConflict, EX_Con, \数据相关检测_24_3_2_1_mem相关 );
  \数据相关检测_24_3_2  \u_数据相关检测_24_3_2_1  (
    .EX_RegWrite(EX_RegWrite), .R1_num(R1_num), .EX_WriteReg_num(EX_WriteReg_num),
    .MEM_RegWrite(MEM_RegWrite), .R2_num(R2_num), .MEM_WriteReg_num(MEM_WriteReg_num), .R1_Used(R1_U),
    .R2_Used(R2_U), .\MEM相关 (\数据相关检测_24_3_2_1_mem相关 ), .\EX相关 (EX_Con), .R1_MEM(relation));
  Multiplexer #(.select(1), .width(5), .disabled("Z"), .enable("false")) multiplexer_2 (
    .in0(IR_1[25:21]), .in1(5'b00010), .out(R1_num), .sel(\拓展单周期硬布线控制器_31_1_syscall ));
  Multiplexer #(.select(1), .width(5), .disabled("Z"), .enable("false")) multiplexer_3 (
    .in0(IR_1[20:16]), .in1(5'b00100), .out(R2_num), .sel(\拓展单周期硬布线控制器_31_1_syscall ));
  assign bit_extender_1_out = {{16{1'b0}}, IR_1[15:0]};  // Bit_Extender bit_extender_1
  assign bit_extender_2_out = {{16{IR_1[15]}}, IR_1[15:0]};  // Bit_Extender bit_extender_2
  Multiplexer #(.select(2), .width(5), .disabled("Z"), .enable("false")) multiplexer_4 (
    .in0(IR_1[20:16]), .in1(IR_1[15:11]), .in2({5{1'b1}}), .out(multiplexer_4_out),
    .sel({JAL_1, \拓展单周期硬布线控制器_31_1_regdst [0]}));  // open: in3
  Multiplexer #(.select(1), .width(32), .disabled("Z"), .enable("false")) multiplexer_5 (
    .in0(bit_extender_1_out), .in1(bit_extender_2_out), .out(multiplexer_5_out), .sel(SignedExt));
  MIPS_Regifile mips_regifile_1 (
    .Din(RDin), .Clk(CLK), .R1(mips_regifile_1_r1), .R2(mips_regifile_1_r2), .WE(RegWrite), .W_num(W_num),
    .R1_num(R1_num), .R2_num(R2_num));
  ID_EX id_ex_1 (
    .in_1(\拓展单周期硬布线控制器_31_1_jr ), .in_4(\拓展单周期硬布线控制器_31_1_blez ), .in_5(\拓展单周期硬布线控制器_31_1_lb ),
    .in_6(\拓展单周期硬布线控制器_31_1_beq ), .in_7(\拓展单周期硬布线控制器_31_1_bne ), .in_8(\拓展单周期硬布线控制器_31_1_memtoreg ),
    .in_9(\拓展单周期硬布线控制器_31_1_memwrite ), .in_10(\拓展单周期硬布线控制器_31_1_alu_op ),
    .in_11(\拓展单周期硬布线控制器_31_1_alu_src ), .in_12(\拓展单周期硬布线控制器_31_1_regwrite ),
    .in_13(\拓展单周期硬布线控制器_31_1_syscall ), .in_14(ID_PC), .in_15(IR_1), .in_16(mips_regifile_1_r1),
    .in_17(mips_regifile_1_r2), .in_18(multiplexer_5_out), .in_19(IR_1[10:6]), .in_20(multiplexer_4_out),
    .in_21({IR_1[15:0], {16{1'b0}}}), .out_29(JR), .out_30(JMP), .out_31(id_ex_1_out_31), .out_32(BLEZ),
    .out_33(id_ex_1_out_33), .out_34(id_ex_1_out_34), .out_35(id_ex_1_out_35), .out_36(id_ex_1_out_36),
    .out_37(id_ex_1_out_37), .out_40(EX_RegWrite), .out_41(id_ex_1_out_41), .out_42(EX_PC),
    .out_38(id_ex_1_out_38), .out_39(id_ex_1_out_39), .out_43(IR_2), .out_44(id_ex_1_out_44),
    .out_45(id_ex_1_out_45), .out_46(id_ex_1_out_46), .out_47(id_ex_1_out_47), .out_48(EX_WriteReg_num),
    .out_49(id_ex_1_out_49), .in_26(CLK), .in_3(\拓展单周期硬布线控制器_31_1_lui ), .in_2(\拓展单周期硬布线控制器_31_1_jmp ),
    .in_27(STALL), .in_28(or_6_out), .out_51(JAL_2), .in_23(JAL_1), .in_22(relation), .out_50(relation_1));  // open: in_24, out_52, in_25, out_53
  or or_6 (or_6_out, RST, BracnhConflict, LoadUse);
  Multiplexer #(.select(1), .width(1), .disabled("Z"), .enable("false")) multiplexer_6 (
    .in0(1'b0), .in1(id_ex_1_out_36), .out(LoadUse), .sel(EX_Con));
  Adder #(.width(32)) adder_2 (.a(EX_PC), .b(32'h4), .out({J_JAL_PC, adder_2_out}));  // open: cin, cout
  Multiplexer #(.select(2), .width(32), .disabled("Z"), .enable("false")) multiplexer_7 (
    .in0(id_ex_1_out_44), .in1(MEM_AluR), .in2(W), .in3(MEM_AluR), .out(JR_PC), .sel(relation_1[1:0]));
  Multiplexer #(.select(2), .width(32), .disabled("Z"), .enable("false")) multiplexer_8 (
    .in0(id_ex_1_out_45), .in1(MEM_AluR), .in2(W), .in3(MEM_AluR), .out(multiplexer_8_out),
    .sel(relation_1[3:2]));
  Multiplexer #(.select(1), .width(32), .disabled("Z"), .enable("false")) multiplexer_9 (
    .in0(multiplexer_8_out), .in1(id_ex_1_out_46), .out(multiplexer_9_out), .sel(id_ex_1_out_39));
  Shifter #(.width(32), .shift("ll")) shifter_1 (.in(id_ex_1_out_46), .\dist (5'b00010), .out(shifter_1_out));
  or or_7 (BracnhConflict, JMP, JR, B___De, BLEZ_DE);
  MIPS_ALU mips_alu_1 (
    .X(JR_PC), .Y(multiplexer_9_out), .AluOP(id_ex_1_out_38), .Equal(mips_alu_1_equal),
    .Result(mips_alu_1_result), .shamt(id_ex_1_out_47));  // open: Result_2
  Adder #(.width(32)) adder_3 (.a(shifter_1_out), .b({J_JAL_PC, adder_2_out}), .out(B___PC));  // open: cin, cout
  not not_1 (not_1_out, mips_alu_1_equal);
  and and_2 (and_2_out, JMP, ~STALL);  // AND_Gate
  and and_3 (and_3_out, mips_alu_1_equal, id_ex_1_out_34);
  or or_8 (B___De, and_3_out, and_4_out);
  and and_4 (and_4_out, not_1_out, id_ex_1_out_35);
  Comparator #(.width(32), .mode("twosComplement")) comparator_1 (
    .a(JR_PC), .b({32{1'b0}}), .gt(comparator_1_gt));  // open: eq, lt
  Counter #(.width(16), .max('hffff), .ongoal("wrap"), .trigger("rising"), .behavior("new")) counter_2 (
    .count(and_2_out), .Q(\无条件分支数 ), .clk(CLK), .clr(RST));  // open: load, D, carry, preset, down
  and and_5 (and_5_out, branch, ~STALL);  // AND_Gate
  and and_6 (BLEZ_DE, BLEZ, not_2_out);
  not not_2 (not_2_out, comparator_1_gt);
  Counter #(.width(16), .max('hffff), .ongoal("wrap"), .trigger("rising"), .behavior("new")) counter_3 (
    .count(and_5_out), .Q(\条件分支成功数 ), .clk(CLK), .clr(RST));  // open: load, D, carry, preset, down
  // Probe on mips_alu_1_result
  Counter #(.width(16), .max('hffff), .ongoal("wrap"), .trigger("rising"), .behavior("new")) counter_4 (
    .count(and_7_out), .Q(\插入气泡数 ), .clk(CLK), .clr(RST));  // open: load, D, carry, preset, down
  and and_7 (and_7_out, or_9_out, \运行 );
  or or_9 (or_9_out, STALL, LoadUse);
  Counter #(.width(16), .max('hffff), .ongoal("wrap"), .trigger("rising"), .behavior("new")) counter_5 (
    .count(and_7_out), .Q(\LoadUse次数 ), .clr(RST));  // open: load, D, carry, clk, preset, down
  EX_MEM ex_mem_1 (
    .in_1(id_ex_1_out_31), .out_18(ex_mem_1_out_18), .in_2(id_ex_1_out_33), .out_19(ex_mem_1_out_19),
    .in_3(id_ex_1_out_36), .out_20(ex_mem_1_out_20), .in_4(id_ex_1_out_37), .out_21(MemWrite), .in_8(EX_PC),
    .out_25(M_PC), .in_9(IR_2), .out_26(IR_3), .in_10(mips_alu_1_result), .out_27(MEM_AluR),
    .in_11(multiplexer_8_out), .out_28(MDin), .in_12(EX_WriteReg_num), .out_29(MEM_WriteReg_num),
    .in_13(id_ex_1_out_49), .out_30(ex_mem_1_out_30), .in_15(CLK), .in_5(EX_RegWrite), .out_22(MEM_RegWrite),
    .in_16(STALL), .in_17(RST), .in_6(JR_PC), .out_23(ex_mem_1_out_23), .in_7(id_ex_1_out_41),
    .out_24(ex_mem_1_out_24), .in_14(JAL_2), .out_31(JAL_3));
  RAM #(.addrWidth(10), .dataWidth(32), .bus("separate"), .Select("high")) ram_1 (
    .addr(MEM_AluR[11:2]), .din(MDin), .data(ram_1_data), .str(MemWrite), .clk(CLK));  // open: sel, ld, clr
  Multiplexer #(.select(1), .width(32), .disabled("Z"), .enable("false")) multiplexer_10 (
    .in0(multiplexer_11_out), .in1(adder_4_out), .out(RDin), .sel(JAL_4));
  Multiplexer #(.select(1), .width(32), .disabled("Z"), .enable("false")) multiplexer_11 (
    .in0(multiplexer_12_out), .in1(mem_wb_1_out_30), .out(multiplexer_11_out), .sel(LUI));
  Adder #(.width(32)) adder_4 (.a(WB_PC), .b(32'h4), .out(adder_4_out));  // open: cin, cout
  MEM_WB mem_wb_1 (
    .in_1(ex_mem_1_out_18), .out_18(LUI), .in_2(ex_mem_1_out_19), .out_19(mem_wb_1_out_19),
    .in_3(ex_mem_1_out_20), .out_20(mem_wb_1_out_20), .in_4(MEM_RegWrite), .out_21(RegWrite), .in_7(M_PC),
    .out_24(WB_PC), .in_8(IR_3), .out_25(IR_4), .in_9(MEM_AluR), .out_26(WB_AluR), .in_10(ram_1_data),
    .out_27(WB_Read), .in_12(MEM_WriteReg_num), .out_29(W_num), .in_13(ex_mem_1_out_30),
    .out_30(mem_wb_1_out_30), .in_15(CLK), .in_16(STALL), .in_5(ex_mem_1_out_23), .out_22(mem_wb_1_out_22),
    .in_6(ex_mem_1_out_24), .out_23(mem_wb_1_out_23), .in_11(MDin), .out_28(a0), .in_17(RST), .in_14(JAL_3),
    .out_31(JAL_4));
  Multiplexer #(.select(1), .width(32), .disabled("Z"), .enable("false")) multiplexer_12 (
    .in0(W), .in1(bit_extender_3_out), .out(multiplexer_12_out), .sel(mem_wb_1_out_19));
  Multiplexer #(.select(1), .width(32), .disabled("Z"), .enable("false")) multiplexer_13 (
    .in0(WB_AluR), .in1(WB_Read), .out(W), .sel(mem_wb_1_out_20));
  assign bit_extender_3_out = {{24{multiplexer_14_out[7]}}, multiplexer_14_out};  // Bit_Extender bit_extender_3
  Multiplexer #(.select(2), .width(8), .disabled("Z"), .enable("false")) multiplexer_14 (
    .in0(W[7:0]), .in1(W[15:8]), .in2(W[23:16]), .in3(W[31:24]), .out(multiplexer_14_out), .sel(WB_AluR[1:0]));
  Comparator #(.width(32), .mode("twosComplement")) comparator_2 (
    .a(mem_wb_1_out_22), .b(32'h22), .eq(comparator_2_eq));  // open: gt, lt
  Multiplexer #(.select(1), .width(1), .disabled("Z"), .enable("false")) multiplexer_15 (
    .in0(1'b0), .in1(comparator_2_eq), .out(multiplexer_15_out), .sel(mem_wb_1_out_23));
  or or_10 (\运行 , Go, multiplexer_15_out, ~mem_wb_1_out_23);  // OR_Gate
  Register #(.width(32), .trigger("rising"), .Select("low")) register_1 (
    .D(a0), .en(multiplexer_15_out), .Q(LedData), .clk(CLK));  // open: clr
  not not_3 (STALL, \运行 );

  // Other names for the same wires on the sheet: Din[31:0] = RDin; J_JAL_PC[27:2] = IR_2[25:0];
  //   Next_PC_1[31:0] = ID_PC; Next_PC_2[31:0] = EX_PC; MEM_PC[31:0] = M_PC; Next_PC_3[31:0] = M_PC;
  //   Next_PC_4[31:0] = WB_PC; RegWrite_1 = RegWrite

  // Notes on the sheet:
  //   中断源
  //   中断等待指示
  //   总复位信号应将除ROM以外所有存储组件全部清零
  //   数码管输出
  //   数码管输出应该用寄存器锁存，否则显示数据只能一闪而过
  //   指令存储器
  //   指令字
  //   contents of rom_1 (hex, n*v repeats v):
  //   20110001 8000c05 20110001 20120002 20130003 8000c09 20110001 20120002 20130003 8000c0d 20110001
  //   20120002 20130003 8000c11 20110001 20120002 20130003 c000cb8 20100001 20110001 118fc0 112020
  //   20020022 c 118882 12200001 8000c15 112020 20020022 c 20110001 118880 112020 20020022 c 12200001
  //   8000c1f 20110001 118fc0 112020 20020022 c 1188c3 112020 20020022 c 118903 112020 20020022 c 118903
  //   112020 20020022 c 118903 112020 20020022 c 118903 112020 20020022 c 118903 112020 20020022 c 118903
  //   112020 20020022 c 118903 112020 20020022 c 20100001 109fc0 139fc3 8021 2012000c 24160003 26100001
  //   3210000f 20080008 20090001 139900 2709825 132020 20020022 c 1094022 1500fff9 22100001 2018000f
  //   2188024 108700 20080008 20090001 139902 2709825 132021 20020022 c 1094022 1500fff9 108702 2c9b022
  //   12c00001 8000c50 4020 1084027 84400 3508ffff 82021 20020022 c 2010ffff 20110000 ae300000 22100001
  //   22310004 ae300000 22100001 22310004 ae300000 22100001 22310004 ae300000 22100001 22310004 ae300000
  //   22100001 22310004 ae300000 22100001 22310004 ae300000 22100001 22310004 ae300000 22100001 22310004
  //   ae300000 22100001 22310004 ae300000 22100001 22310004 ae300000 22100001 22310004 ae300000 22100001
  //   22310004 ae300000 22100001 22310004 ae300000 22100001 22310004 ae300000 22100001 22310004 ae300000
  //   22100001 22310004 22100001 8020 2011003c 8e130000 8e340000 274402a 11000002 ae330000 ae140000
  //   2231fffc 1611fff8 102020 20020022 c 22100004 2011003c 1611fff2 20020032 c 20100000 22100001 102020
  //   20020022 c 22100002 102020 20020022 c 22100003 102020 20020022 c 22100004 102020 20020022 c 22100005
  //   102020 20020022 c 22100006 102020 20020022 c 22100007 102020 20020022 c 22100008 102020 20020022
  //   20020022 c 3e00008
  //   OP
  //   Func
  //   rs
  //   指令字
  //   rt
  //   rd
  //   流水调试日志用
  //   JAL
  //   RegDst
  //   Syscall
  //   为方便自动评测，需要输出流水线各段保存的PC值，注意是PC不是PC+4，另外ID段寄存器写入信息，Mem段内存写入信息也要输出
  //   JR
  //   JMP
  //   LUI
  //   BLEZ
  //   LB
  //   Beq
  //   Bne
  //   MemToReg
  //   MemWrite
  //   AluOP
  //   AluSrcB
  //   RegWrite
  //   W#
  //   LUI
  //   BLEZ
  //   LB
  //   Beq
  //   Bne
  //   MemToReg
  //   MemWrite
  //   AluOP
  //   AluSrcB
  //   RegWrite
  //   W#
  //   LUI
  //   LB
  //   MemToReg
  //   MemWrite
  //   RegWrite
  //   W#
  //   LUI
  //   LB
  //   W#
  //   LUI
  //   LB
  //   MemToReg
  //   RegWrite
  //   W#
endmodule

module \中断按键参考电路  (
  input  \中断输入 ,
  input  \同步清零信号 ,
  output \与中断屏蔽位与 ,
  output out_4
);

  wire and_1_out, clock_1_out, d_ff_1_q, or_2_out;

  Clock #(.highDuration(1), .lowDuration(1)) clock_1 (.out(clock_1_out));
  or or_1 (out_4, \与中断屏蔽位与 , d_ff_1_q);
  D_Flip_Flop #(.trigger("rising"), .Pre_Clr_Positions("LEGACY"), .NegatePresetClear("false"), .enable("true"), .NewFFLayout("false")) d_ff_1 (
    .clk(\中断输入 ), .D(1'b1), .Q(d_ff_1_q), .reset(\与中断屏蔽位与 ));  // open: Qn, preset, en
  or or_2 (or_2_out, d_ff_1_q, \与中断屏蔽位与 );
  and and_1 (and_1_out, or_2_out, ~\同步清零信号 );  // AND_Gate
  D_Flip_Flop #(.trigger("rising"), .Pre_Clr_Positions("LEGACY"), .NegatePresetClear("false"), .enable("true"), .NewFFLayout("false")) IR1 (
    .clk(clock_1_out), .D(and_1_out), .Q(\与中断屏蔽位与 ));  // open: Qn, preset, en, reset
  Pull_Resistor #(.pull(0)) pull_resistor_1 (.node(\同步清零信号 ));

  // Notes on the sheet:
  //   中断信号采样参考电路
  //   Reset 
endmodule

module IF_ID (
  input  [31:0] in_1,
  input  [31:0] in_2,
  input  [31:0] in_3,
  input  [2:0] in_4,
  input  in_5,
  input  in_6,
  input  in_7,
  output [31:0] out_8,
  output [31:0] out_9,
  output [31:0] out_10,
  output [2:0] out_11
);

  wire not_1_out;
  wire [2:0] multiplexer_4_out;
  wire [31:0] multiplexer_1_out, multiplexer_2_out, multiplexer_3_out;

  not not_1 (not_1_out, in_6);
  Multiplexer #(.select(1), .width(32), .disabled("Z"), .enable("false")) multiplexer_1 (
    .in0(in_1), .in1({32{1'b0}}), .out(multiplexer_1_out), .sel(in_7));
  Multiplexer #(.select(1), .width(32), .disabled("Z"), .enable("false")) multiplexer_2 (
    .in0(in_2), .in1({32{1'b0}}), .out(multiplexer_2_out), .sel(in_7));
  Multiplexer #(.select(1), .width(32), .disabled("Z"), .enable("false")) multiplexer_3 (
    .in0(in_3), .in1({32{1'b0}}), .out(multiplexer_3_out), .sel(in_7));
  Multiplexer #(.select(1), .width(3), .disabled("Z"), .enable("false")) multiplexer_4 (
    .in0(in_4), .in1(3'b000), .out(multiplexer_4_out), .sel(in_7));
  Register #(.width(32), .trigger("rising"), .Select("low")) register_1 (
    .D(multiplexer_1_out), .en(not_1_out), .Q(out_8), .clk(in_5));  // open: clr
  Register #(.width(32), .trigger("rising"), .Select("low")) register_2 (
    .D(multiplexer_2_out), .en(not_1_out), .Q(out_9), .clk(in_5));  // open: clr
  Register #(.width(32), .trigger("rising"), .Select("low")) register_3 (
    .D(multiplexer_3_out), .en(not_1_out), .Q(out_10), .clk(in_5));  // open: clr
  Register #(.width(3), .trigger("rising"), .Select("low")) register_4 (
    .D(multiplexer_4_out), .en(not_1_out), .Q(out_11), .clk(in_5));  // open: clr
endmodule

module ID_EX (
  input  in_1,
  input  in_2,
  input  in_3,
  input  in_4,
  input  in_5,
  input  in_6,
  input  in_7,
  input  in_8,
  input  in_9,
  input  [3:0] in_10,
  input  in_11,
  input  in_12,
  input  in_13,
  input  [31:0] in_14,
  input  [31:0] in_15,
  input  [31:0] in_16,
  input  [31:0] in_17,
  input  [31:0] in_18,
  input  [4:0] in_19,
  input  [4:0] in_20,
  input  [31:0] in_21,
  input  [3:0] in_22,
  input  in_23,
  input  [31:0] in_24,
  input  [2:0] in_25,
  input  in_26,
  input  in_27,
  input  in_28,
  output out_29,
  output out_30,
  output out_31,
  output out_32,
  output out_33,
  output out_34,
  output out_35,
  output out_36,
  output out_37,
  output [3:0] out_38,
  output out_39,
  output out_40,
  output out_41,
  output [31:0] out_42,
  output [31:0] out_43,
  output [31:0] out_44,
  output [31:0] out_45,
  output [31:0] out_46,
  output [4:0] out_47,
  output [4:0] out_48,
  output [31:0] out_49,
  output [3:0] out_50,
  output out_51,
  output [31:0] out_52,
  output [2:0] out_53
);

  wire multiplexer_1_out, multiplexer_2_out, multiplexer_3_out, multiplexer_4_out, multiplexer_5_out,
       multiplexer_6_out, multiplexer_7_out, multiplexer_8_out, multiplexer_9_out, multiplexer_11_out,
       multiplexer_12_out, multiplexer_13_out, multiplexer_23_out, not_1_out;
  wire [2:0] multiplexer_25_out;
  wire [3:0] multiplexer_10_out, multiplexer_22_out;
  wire [4:0] multiplexer_19_out, multiplexer_20_out;
  wire [31:0] multiplexer_14_out, multiplexer_15_out, multiplexer_16_out, multiplexer_17_out,
       multiplexer_18_out, multiplexer_21_out, multiplexer_24_out;

  not not_1 (not_1_out, in_27);
  Multiplexer #(.select(1), .width(1), .disabled("Z"), .enable("false")) multiplexer_1 (
    .in0(in_1), .in1(1'b0), .out(multiplexer_1_out), .sel(in_28));
  Multiplexer #(.select(1), .width(1), .disabled("Z"), .enable("false")) multiplexer_2 (
    .in0(in_2), .in1(1'b0), .out(multiplexer_2_out), .sel(in_28));
  Multiplexer #(.select(1), .width(1), .disabled("Z"), .enable("false")) multiplexer_3 (
    .in0(in_3), .in1(1'b0), .out(multiplexer_3_out), .sel(in_28));
  Multiplexer #(.select(1), .width(1), .disabled("Z"), .enable("false")) multiplexer_4 (
    .in0(in_4), .in1(1'b0), .out(multiplexer_4_out), .sel(in_28));
  Multiplexer #(.select(1), .width(1), .disabled("Z"), .enable("false")) multiplexer_5 (
    .in0(in_5), .in1(1'b0), .out(multiplexer_5_out), .sel(in_28));
  Multiplexer #(.select(1), .width(1), .disabled("Z"), .enable("false")) multiplexer_6 (
    .in0(in_6), .in1(1'b0), .out(multiplexer_6_out), .sel(in_28));
  Multiplexer #(.select(1), .width(1), .disabled("Z"), .enable("false")) multiplexer_7 (
    .in0(in_7), .in1(1'b0), .out(multiplexer_7_out), .sel(in_28));
  Multiplexer #(.select(1), .width(1), .disabled("Z"), .enable("false")) multiplexer_8 (
    .in0(in_8), .in1(1'b0), .out(multiplexer_8_out), .sel(in_28));
  Multiplexer #(.select(1), .width(1), .disabled("Z"), .enable("false")) multiplexer_9 (
    .in0(in_9), .in1(1'b0), .out(multiplexer_9_out), .sel(in_28));
  Multiplexer #(.select(1), .width(4), .disabled("Z"), .enable("false")) multiplexer_10 (
    .in0(in_10), .in1(4'b0000), .out(multiplexer_10_out), .sel(in_28));
  Multiplexer #(.select(1), .width(1), .disabled("Z"), .enable("false")) multiplexer_11 (
    .in0(in_11), .in1(1'b0), .out(multiplexer_11_out), .sel(in_28));
  Multiplexer #(.select(1), .width(1), .disabled("Z"), .enable("false")) multiplexer_12 (
    .in0(in_12), .in1(1'b0), .out(multiplexer_12_out), .sel(in_28));
  Multiplexer #(.select(1), .width(1), .disabled("Z"), .enable("false")) multiplexer_13 (
    .in0(in_13), .in1(1'b0), .out(multiplexer_13_out), .sel(in_28));
  Multiplexer #(.select(1), .width(32), .disabled("Z"), .enable("false")) multiplexer_14 (
    .in0(in_14), .in1({32{1'b0}}), .out(multiplexer_14_out), .sel(in_28));
  Multiplexer #(.select(1), .width(32), .disabled("Z"), .enable("false")) multiplexer_15 (
    .in0(in_15), .in1({32{1'b0}}), .out(multiplexer_15_out), .sel(in_28));
  Multiplexer #(.select(1), .width(32), .disabled("Z"), .enable("false")) multiplexer_16 (
    .in0(in_16), .in1({32{1'b0}}), .out(multiplexer_16_out), .sel(in_28));
  Multiplexer #(.select(1), .width(32), .disabled("Z"), .enable("false")) multiplexer_17 (
    .in0(in_17), .in1({32{1'b0}}), .out(multiplexer_17_out), .sel(in_28));
  Multiplexer #(.select(1), .width(32), .disabled("Z"), .enable("false")) multiplexer_18 (
    .in0(in_18), .in1({32{1'b0}}), .out(multiplexer_18_out), .sel(in_28));
  Multiplexer #(.select(1), .width(5), .disabled("Z"), .enable("false")) multiplexer_19 (
    .in0(in_19), .in1({5{1'b0}}), .out(multiplexer_19_out), .sel(in_28));
  Multiplexer #(.select(1), .width(5), .disabled("Z"), .enable("false")) multiplexer_20 (
    .in0(in_20), .in1({5{1'b0}}), .out(multiplexer_20_out), .sel(in_28));
  Multiplexer #(.select(1), .width(32), .disabled("Z"), .enable("false")) multiplexer_21 (
    .in0(in_21), .in1({32{1'b0}}), .out(multiplexer_21_out), .sel(in_28));
  Multiplexer #(.select(1), .width(4), .disabled("Z"), .enable("false")) multiplexer_22 (
    .in0(in_22), .in1(4'b0000), .out(multiplexer_22_out), .sel(in_28));
  Multiplexer #(.select(1), .width(1), .disabled("Z"), .enable("false")) multiplexer_23 (
    .in0(in_23), .in1(1'b0), .out(multiplexer_23_out), .sel(in_28));
  Multiplexer #(.select(1), .width(32), .disabled("Z"), .enable("false")) multiplexer_24 (
    .in0(in_24), .in1({32{1'b0}}), .out(multiplexer_24_out), .sel(in_28));
  Multiplexer #(.select(1), .width(3), .disabled("Z"), .enable("false")) multiplexer_25 (
    .in0(in_25), .in1(3'b000), .out(multiplexer_25_out), .sel(in_28));
  Register #(.width(1), .trigger("rising"), .Select("low")) register_1 (
    .D(multiplexer_1_out), .en(not_1_out), .Q(out_29), .clk(in_26));  // open: clr
  Register #(.width(1), .trigger("rising"), .Select("low")) register_2 (
    .D(multiplexer_2_out), .en(not_1_out), .Q(out_30), .clk(in_26));  // open: clr
  Register #(.width(1), .trigger("rising"), .Select("low")) register_3 (
    .D(multiplexer_3_out), .en(not_1_out), .Q(out_31), .clk(in_26));  // open: clr
  Register #(.width(1), .trigger("rising"), .Select("low")) register_4 (
    .D(multiplexer_4_out), .en(not_1_out), .Q(out_32), .clk(in_26));  // open: clr
  Register #(.width(1), .trigger("rising"), .Select("low")) register_5 (
    .D(multiplexer_5_out), .en(not_1_out), .Q(out_33), .clk(in_26));  // open: clr
  Register #(.width(1), .trigger("rising"), .Select("low")) register_6 (
    .D(multiplexer_6_out), .en(not_1_out), .Q(out_34), .clk(in_26));  // open: clr
  Register #(.width(1), .trigger("rising"), .Select("low")) register_7 (
    .D(multiplexer_7_out), .en(not_1_out), .Q(out_35), .clk(in_26));  // open: clr
  Register #(.width(1), .trigger("rising"), .Select("low")) register_8 (
    .D(multiplexer_8_out), .en(not_1_out), .Q(out_36), .clk(in_26));  // open: clr
  Register #(.width(1), .trigger("rising"), .Select("low")) register_9 (
    .D(multiplexer_9_out), .en(not_1_out), .Q(out_37), .clk(in_26));  // open: clr
  Register #(.width(4), .trigger("rising"), .Select("low")) register_10 (
    .D(multiplexer_10_out), .en(not_1_out), .Q(out_38), .clk(in_26));  // open: clr
  Register #(.width(1), .trigger("rising"), .Select("low")) register_11 (
    .D(multiplexer_11_out), .en(not_1_out), .Q(out_39), .clk(in_26));  // open: clr
  Register #(.width(1), .trigger("rising"), .Select("low")) register_12 (
    .D(multiplexer_12_out), .en(not_1_out), .Q(out_40), .clk(in_26));  // open: clr
  Register #(.width(1), .trigger("rising"), .Select("low")) register_13 (
    .D(multiplexer_13_out), .en(not_1_out), .Q(out_41), .clk(in_26));  // open: clr
  Register #(.width(32), .trigger("rising"), .Select("low")) register_14 (
    .D(multiplexer_14_out), .en(not_1_out), .Q(out_42), .clk(in_26));  // open: clr
  Register #(.width(32), .trigger("rising"), .Select("low")) register_15 (
    .D(multiplexer_15_out), .en(not_1_out), .Q(out_43), .clk(in_26));  // open: clr
  Register #(.width(32), .trigger("rising"), .Select("low")) register_16 (
    .D(multiplexer_16_out), .en(not_1_out), .Q(out_44), .clk(in_26));  // open: clr
  Register #(.width(32), .trigger("rising"), .Select("low")) register_17 (
    .D(multiplexer_17_out), .en(not_1_out), .Q(out_45), .clk(in_26));  // open: clr
  Register #(.width(32), .trigger("rising"), .Select("low")) register_18 (
    .D(multiplexer_18_out), .en(not_1_out), .Q(out_46), .clk(in_26));  // open: clr
  Register #(.width(5), .trigger("rising"), .Select("low")) register_19 (
    .D(multiplexer_19_out), .en(not_1_out), .Q(out_47), .clk(in_26));  // open: clr
  Register #(.width(5), .trigger("rising"), .Select("low")) register_20 (
    .D(multiplexer_20_out), .en(not_1_out), .Q(out_48), .clk(in_26));  // open: clr
  Register #(.width(32), .trigger("rising"), .Select("low")) register_21 (
    .D(multiplexer_21_out), .en(not_1_out), .Q(out_49), .clk(in_26));  // open: clr
  Register #(.width(4), .trigger("rising"), .Select("low")) register_22 (
    .D(multiplexer_22_out), .en(not_1_out), .Q(out_50), .clk(in_26));  // open: clr
  Register #(.width(1), .trigger("rising"), .Select("low")) register_23 (
    .D(multiplexer_23_out), .en(not_1_out), .Q(out_51), .clk(in_26));  // open: clr
  Register #(.width(32), .trigger("rising"), .Select("low")) register_24 (
    .D(multiplexer_24_out), .en(not_1_out), .Q(out_52), .clk(in_26));  // open: clr
  Register #(.width(3), .trigger("rising"), .Select("low")) register_25 (
    .D(multiplexer_25_out), .en(not_1_out), .Q(out_53), .clk(in_26));  // open: clr
endmodule

module EX_MEM (
  input  in_1,
  input  in_2,
  input  in_3,
  input  in_4,
  input  in_5,
  input  [31:0] in_6,
  input  in_7,
  input  [31:0] in_8,
  input  [31:0] in_9,
  input  [31:0] in_10,
  input  [31:0] in_11,
  input  [4:0] in_12,
  input  [31:0] in_13,
  input  in_14,
  input  in_15,
  input  in_16,
  input  in_17,
  output out_18,
  output out_19,
  output out_20,
  output out_21,
  output out_22,
  output [31:0] out_23,
  output out_24,
  output [31:0] out_25,
  output [31:0] out_26,
  output [31:0] out_27,
  output [31:0] out_28,
  output [4:0] out_29,
  output [31:0] out_30,
  output out_31
);

  wire multiplexer_1_out, multiplexer_2_out, multiplexer_3_out, multiplexer_4_out, multiplexer_5_out,
       multiplexer_7_out, multiplexer_14_out, not_1_out;
  wire [4:0] multiplexer_12_out;
  wire [31:0] multiplexer_6_out, multiplexer_8_out, multiplexer_9_out, multiplexer_10_out,
       multiplexer_11_out, multiplexer_13_out;

  not not_1 (not_1_out, in_16);
  Multiplexer #(.select(1), .width(1), .disabled("Z"), .enable("false")) multiplexer_1 (
    .in0(in_1), .in1(1'b0), .out(multiplexer_1_out), .sel(in_17));
  Multiplexer #(.select(1), .width(1), .disabled("Z"), .enable("false")) multiplexer_2 (
    .in0(in_2), .in1(1'b0), .out(multiplexer_2_out), .sel(in_17));
  Multiplexer #(.select(1), .width(1), .disabled("Z"), .enable("false")) multiplexer_3 (
    .in0(in_3), .in1(1'b0), .out(multiplexer_3_out), .sel(in_17));
  Multiplexer #(.select(1), .width(1), .disabled("Z"), .enable("false")) multiplexer_4 (
    .in0(in_4), .in1(1'b0), .out(multiplexer_4_out), .sel(in_17));
  Multiplexer #(.select(1), .width(1), .disabled("Z"), .enable("false")) multiplexer_5 (
    .in0(in_5), .in1(1'b0), .out(multiplexer_5_out), .sel(in_17));
  Multiplexer #(.select(1), .width(32), .disabled("Z"), .enable("false")) multiplexer_6 (
    .in0(in_6), .in1({32{1'b0}}), .out(multiplexer_6_out), .sel(in_17));
  Multiplexer #(.select(1), .width(1), .disabled("Z"), .enable("false")) multiplexer_7 (
    .in0(in_7), .in1(1'b0), .out(multiplexer_7_out), .sel(in_17));
  Multiplexer #(.select(1), .width(32), .disabled("Z"), .enable("false")) multiplexer_8 (
    .in0(in_8), .in1({32{1'b0}}), .out(multiplexer_8_out), .sel(in_17));
  Multiplexer #(.select(1), .width(32), .disabled("Z"), .enable("false")) multiplexer_9 (
    .in0(in_9), .in1({32{1'b0}}), .out(multiplexer_9_out), .sel(in_17));
  Multiplexer #(.select(1), .width(32), .disabled("Z"), .enable("false")) multiplexer_10 (
    .in0(in_10), .in1({32{1'b0}}), .out(multiplexer_10_out), .sel(in_17));
  Multiplexer #(.select(1), .width(32), .disabled("Z"), .enable("false")) multiplexer_11 (
    .in0(in_11), .in1({32{1'b0}}), .out(multiplexer_11_out), .sel(in_17));
  Multiplexer #(.select(1), .width(5), .disabled("Z"), .enable("false")) multiplexer_12 (
    .in0(in_12), .in1({5{1'b0}}), .out(multiplexer_12_out), .sel(in_17));
  Multiplexer #(.select(1), .width(32), .disabled("Z"), .enable("false")) multiplexer_13 (
    .in0(in_13), .in1({32{1'b0}}), .out(multiplexer_13_out), .sel(in_17));
  Multiplexer #(.select(1), .width(1), .disabled("Z"), .enable("false")) multiplexer_14 (
    .in0(in_14), .in1(1'b0), .out(multiplexer_14_out), .sel(in_17));
  Register #(.width(1), .trigger("rising"), .Select("low")) register_1 (
    .D(multiplexer_1_out), .en(not_1_out), .Q(out_18), .clk(in_15));  // open: clr
  Register #(.width(1), .trigger("rising"), .Select("low")) register_2 (
    .D(multiplexer_2_out), .en(not_1_out), .Q(out_19), .clk(in_15));  // open: clr
  Register #(.width(1), .trigger("rising"), .Select("low")) register_3 (
    .D(multiplexer_3_out), .en(not_1_out), .Q(out_20), .clk(in_15));  // open: clr
  Register #(.width(1), .trigger("rising"), .Select("low")) register_4 (
    .D(multiplexer_4_out), .en(not_1_out), .Q(out_21), .clk(in_15));  // open: clr
  Register #(.width(1), .trigger("rising"), .Select("low")) register_5 (
    .D(multiplexer_5_out), .en(not_1_out), .Q(out_22), .clk(in_15));  // open: clr
  Register #(.width(32), .trigger("rising"), .Select("low")) register_6 (
    .D(multiplexer_6_out), .en(not_1_out), .Q(out_23), .clk(in_15));  // open: clr
  Register #(.width(1), .trigger("rising"), .Select("low")) register_7 (
    .D(multiplexer_7_out), .en(not_1_out), .Q(out_24), .clk(in_15));  // open: clr
  Register #(.width(32), .trigger("rising"), .Select("low")) register_8 (
    .D(multiplexer_8_out), .en(not_1_out), .Q(out_25), .clk(in_15));  // open: clr
  Register #(.width(32), .trigger("rising"), .Select("low")) register_9 (
    .D(multiplexer_9_out), .en(not_1_out), .Q(out_26), .clk(in_15));  // open: clr
  Register #(.width(32), .trigger("rising"), .Select("low")) register_10 (
    .D(multiplexer_10_out), .en(not_1_out), .Q(out_27), .clk(in_15));  // open: clr
  Register #(.width(32), .trigger("rising"), .Select("low")) register_11 (
    .D(multiplexer_11_out), .en(not_1_out), .Q(out_28), .clk(in_15));  // open: clr
  Register #(.width(5), .trigger("rising"), .Select("low")) register_12 (
    .D(multiplexer_12_out), .en(not_1_out), .Q(out_29), .clk(in_15));  // open: clr
  Register #(.width(32), .trigger("rising"), .Select("low")) register_13 (
    .D(multiplexer_13_out), .en(not_1_out), .Q(out_30), .clk(in_15));  // open: clr
  Register #(.width(1), .trigger("rising"), .Select("low")) register_14 (
    .D(multiplexer_14_out), .en(not_1_out), .Q(out_31), .clk(in_15));  // open: clr
endmodule

module MEM_WB (
  input  in_1,
  input  in_2,
  input  in_3,
  input  in_4,
  input  [31:0] in_5,
  input  in_6,
  input  [31:0] in_7,
  input  [31:0] in_8,
  input  [31:0] in_9,
  input  [31:0] in_10,
  input  [31:0] in_11,
  input  [4:0] in_12,
  input  [31:0] in_13,
  input  in_14,
  input  in_15,
  input  in_16,
  input  in_17,
  output out_18,
  output out_19,
  output out_20,
  output out_21,
  output [31:0] out_22,
  output out_23,
  output [31:0] out_24,
  output [31:0] out_25,
  output [31:0] out_26,
  output [31:0] out_27,
  output [31:0] out_28,
  output [4:0] out_29,
  output [31:0] out_30,
  output out_31
);

  wire multiplexer_1_out, multiplexer_2_out, multiplexer_3_out, multiplexer_4_out, multiplexer_6_out,
       multiplexer_14_out, not_1_out;
  wire [4:0] multiplexer_12_out;
  wire [31:0] multiplexer_5_out, multiplexer_7_out, multiplexer_8_out, multiplexer_9_out, multiplexer_10_out,
       multiplexer_11_out, multiplexer_13_out;

  not not_1 (not_1_out, in_16);
  Multiplexer #(.select(1), .width(1), .disabled("Z"), .enable("false")) multiplexer_1 (
    .in0(in_1), .in1(1'b0), .out(multiplexer_1_out), .sel(in_17));
  Multiplexer #(.select(1), .width(1), .disabled("Z"), .enable("false")) multiplexer_2 (
    .in0(in_2), .in1(1'b0), .out(multiplexer_2_out), .sel(in_17));
  Multiplexer #(.select(1), .width(1), .disabled("Z"), .enable("false")) multiplexer_3 (
    .in0(in_3), .in1(1'b0), .out(multiplexer_3_out), .sel(in_17));
  Multiplexer #(.select(1), .width(1), .disabled("Z"), .enable("false")) multiplexer_4 (
    .in0(in_4), .in1(1'b0), .out(multiplexer_4_out), .sel(in_17));
  Multiplexer #(.select(1), .width(32), .disabled("Z"), .enable("false")) multiplexer_5 (
    .in0(in_5), .in1({32{1'b0}}), .out(multiplexer_5_out), .sel(in_17));
  Multiplexer #(.select(1), .width(1), .disabled("Z"), .enable("false")) multiplexer_6 (
    .in0(in_6), .in1(1'b0), .out(multiplexer_6_out), .sel(in_17));
  Multiplexer #(.select(1), .width(32), .disabled("Z"), .enable("false")) multiplexer_7 (
    .in0(in_7), .in1({32{1'b0}}), .out(multiplexer_7_out), .sel(in_17));
  Multiplexer #(.select(1), .width(32), .disabled("Z"), .enable("false")) multiplexer_8 (
    .in0(in_8), .in1({32{1'b0}}), .out(multiplexer_8_out), .sel(in_17));
  Multiplexer #(.select(1), .width(32), .disabled("Z"), .enable("false")) multiplexer_9 (
    .in0(in_9), .in1({32{1'b0}}), .out(multiplexer_9_out), .sel(in_17));
  Multiplexer #(.select(1), .width(32), .disabled("Z"), .enable("false")) multiplexer_10 (
    .in0(in_10), .in1({32{1'b0}}), .out(multiplexer_10_out), .sel(in_17));
  Multiplexer #(.select(1), .width(32), .disabled("Z"), .enable("false")) multiplexer_11 (
    .in0(in_11), .in1({32{1'b0}}), .out(multiplexer_11_out), .sel(in_17));
  Multiplexer #(.select(1), .width(5), .disabled("Z"), .enable("false")) multiplexer_12 (
    .in0(in_12), .in1({5{1'b0}}), .out(multiplexer_12_out), .sel(in_17));
  Multiplexer #(.select(1), .width(32), .disabled("Z"), .enable("false")) multiplexer_13 (
    .in0(in_13), .in1({32{1'b0}}), .out(multiplexer_13_out), .sel(in_17));
  Multiplexer #(.select(1), .width(1), .disabled("Z"), .enable("false")) multiplexer_14 (
    .in0(in_14), .in1(1'b0), .out(multiplexer_14_out), .sel(in_17));
  Register #(.width(1), .trigger("rising"), .Select("low")) register_1 (
    .D(multiplexer_1_out), .en(not_1_out), .Q(out_18), .clk(in_15));  // open: clr
  Register #(.width(1), .trigger("rising"), .Select("low")) register_2 (
    .D(multiplexer_2_out), .en(not_1_out), .Q(out_19), .clk(in_15));  // open: clr
  Register #(.width(1), .trigger("rising"), .Select("low")) register_3 (
    .D(multiplexer_3_out), .en(not_1_out), .Q(out_20), .clk(in_15));  // open: clr
  Register #(.width(1), .trigger("rising"), .Select("low")) register_4 (
    .D(multiplexer_4_out), .en(not_1_out), .Q(out_21), .clk(in_15));  // open: clr
  Register #(.width(32), .trigger("rising"), .Select("low")) register_5 (
    .D(multiplexer_5_out), .en(not_1_out), .Q(out_22), .clk(in_15));  // open: clr
  Register #(.width(1), .trigger("rising"), .Select("low")) register_6 (
    .D(multiplexer_6_out), .en(not_1_out), .Q(out_23), .clk(in_15));  // open: clr
  Register #(.width(32), .trigger("rising"), .Select("low")) register_7 (
    .D(multiplexer_7_out), .en(not_1_out), .Q(out_24), .clk(in_15));  // open: clr
  Register #(.width(32), .trigger("rising"), .Select("low")) register_8 (
    .D(multiplexer_8_out), .en(not_1_out), .Q(out_25), .clk(in_15));  // open: clr
  Register #(.width(32), .trigger("rising"), .Select("low")) register_9 (
    .D(multiplexer_9_out), .en(not_1_out), .Q(out_26), .clk(in_15));  // open: clr
  Register #(.width(32), .trigger("rising"), .Select("low")) register_10 (
    .D(multiplexer_10_out), .en(not_1_out), .Q(out_27), .clk(in_15));  // open: clr
  Register #(.width(32), .trigger("rising"), .Select("low")) register_11 (
    .D(multiplexer_11_out), .en(not_1_out), .Q(out_28), .clk(in_15));  // open: clr
  Register #(.width(5), .trigger("rising"), .Select("low")) register_12 (
    .D(multiplexer_12_out), .en(not_1_out), .Q(out_29), .clk(in_15));  // open: clr
  Register #(.width(32), .trigger("rising"), .Select("low")) register_13 (
    .D(multiplexer_13_out), .en(not_1_out), .Q(out_30), .clk(in_15));  // open: clr
  Register #(.width(1), .trigger("rising"), .Select("low")) register_14 (
    .D(multiplexer_14_out), .en(not_1_out), .Q(out_31), .clk(in_15));  // open: clr
endmodule

module \拓展单周期硬布线控制器_31  (
  input  [5:0] OP,
  input  [5:0] Func,
  input  [4:0] M,
  output [3:0] ALU_OP,
  output MemToReg,
  output MemWrite,
  output ALU_SRC,
  output RegWrite,
  output SysCALL,
  output SignedExt,
  output RegDst,
  output Beq,
  output Bne,
  output JR,
  output JMP,
  output JAL,
  output LUI,
  output LB,
  output BLEZ,
  output MFC0,
  output MTC0,
  output ERET,
  output R1_Used,
  output R2_Used
);

  \拓展运算器控制器自动生成_31  \u_拓展运算器控制器自动生成_31_1  (
    .OP0(OP[0]), .OP1(OP[1]), .OP2(OP[2]), .OP3(OP[3]), .OP4(OP[4]), .OP5(OP[5]), .F0(Func[0]), .F1(Func[1]),
    .F2(Func[2]), .F3(Func[3]), .F4(Func[4]), .F5(Func[5]), .S0(ALU_OP[0]), .S1(ALU_OP[1]), .S2(ALU_OP[2]),
    .S3(ALU_OP[3]));
  \拓展控制信号自动生成_31  \u_拓展控制信号自动生成_31_1  (
    .OP0(OP[0]), .OP1(OP[1]), .OP2(OP[2]), .MemToReg(MemToReg), .OP3(OP[3]), .OP4(OP[4]), .OP5(OP[5]),
    .MemWrite(MemWrite), .F0(Func[0]), .F1(Func[1]), .F2(Func[2]), .F3(Func[3]), .F4(Func[4]), .F5(Func[5]),
    .ALU_SRC(ALU_SRC), .M0(M[0]), .M1(M[1]), .M2(M[2]), .M3(M[3]), .M4(M[4]), .RegWrite(RegWrite),
    .SysCALL(SysCALL), .SignedExt(SignedExt), .RegDst(RegDst), .BEQ(Beq), .BNE(Bne), .JR(JR), .JUMP(JMP),
    .JAL(JAL), .LUI(LUI), .LB(LB), .BLEZ(BLEZ), .MFC0(MFC0), .MTC0(MTC0), .ERET(ERET));
  \寄存器使用情况_24_3_2  \u_寄存器使用情况_24_3_2_1  (
    .OP0(OP[0]), .OP1(OP[1]), .OP2(OP[2]), .OP3(OP[3]), .OP4(OP[4]), .OP5(OP[5]), .F0(Func[0]), .F1(Func[1]),
    .F2(Func[2]), .F3(Func[3]), .F4(Func[4]), .F5(Func[5]), .R1_used(R1_Used), .R2_used(R2_Used));

  // Other names for the same wires on the sheet: OP_CODE[5:0] = OP

  // Notes on the sheet:
  //   运算器控制器，根据指令生成运算器功能选择信号
  //   控制信号生成，产生数据通路需要的其他控制信号
endmodule

// 拓展运算器控制器
module \拓展运算器控制器自动生成_31  (
  input  OP0,
  input  OP1,
  input  OP2,
  input  OP3,
  input  OP4,
  input  OP5,
  input  F0,
  input  F1,
  input  F2,
  input  F3,
  input  F4,
  input  F5,
  output S0,
  output S1,
  output S2,
  output S3
);

  wire and_1_out, and_2_out, and_3_out, and_4_out, and_5_out, and_6_out, and_7_out, and_8_out, and_9_out,
       and_10_out, and_11_out, and_12_out, and_13_out, and_14_out, and_15_out, and_16_out, and_17_out,
       and_18_out, and_19_out, and_20_out, and_21_out, and_22_out, and_23_out, and_24_out, and_25_out,
       and_26_out, and_27_out, and_28_out, and_29_out, and_30_out, and_31_out, and_32_out, and_33_out,
       and_34_out, and_35_out, and_36_out, and_37_out, and_38_out, not_1_out, not_2_out, not_3_out,
       not_4_out, not_5_out, not_6_out, not_7_out, not_8_out, not_9_out, not_10_out, not_11_out, not_12_out,
       not_13_out, not_14_out, not_15_out, not_16_out, not_17_out, not_18_out, not_19_out, not_20_out,
       not_21_out, not_22_out, not_23_out, not_24_out, not_25_out, not_26_out, not_27_out, not_28_out,
       not_29_out, not_30_out, not_31_out, not_32_out, not_33_out, not_34_out, not_35_out, not_36_out,
       not_37_out, not_38_out, not_39_out, not_40_out, not_41_out, not_42_out, not_43_out, not_44_out,
       not_45_out, not_46_out, not_47_out, not_48_out, not_49_out, not_50_out, not_51_out, not_52_out,
       not_53_out, not_54_out, not_55_out, not_56_out, not_57_out, not_58_out, not_59_out, not_60_out,
       not_61_out, not_62_out, not_63_out, not_64_out, not_65_out, not_66_out, not_67_out, not_68_out,
       not_69_out, not_70_out, not_71_out, not_72_out, not_73_out, not_74_out, not_75_out, not_76_out,
       not_77_out, not_78_out, not_79_out, not_80_out, not_81_out, not_82_out, not_83_out, not_84_out,
       not_85_out, not_86_out, not_87_out, not_88_out, not_89_out, not_90_out, not_91_out, not_92_out,
       not_93_out, not_94_out, not_95_out, not_96_out, not_97_out, not_98_out, not_99_out, not_100_out,
       not_101_out, not_102_out, not_103_out, not_104_out, not_105_out, not_106_out, not_107_out,
       not_108_out, not_109_out, not_110_out, not_111_out, not_112_out, not_113_out, not_114_out,
       not_115_out, not_116_out, not_117_out, not_118_out, not_119_out, not_120_out, not_121_out,
       not_122_out, not_123_out, not_124_out, not_125_out, not_126_out, not_127_out, not_128_out,
       not_129_out, not_130_out, not_131_out, not_132_out, not_133_out, not_134_out, not_135_out,
       not_136_out, not_137_out, not_138_out, not_139_out, not_140_out, not_141_out, not_142_out,
       not_143_out, not_144_out, not_145_out, not_146_out, not_147_out, not_148_out, not_149_out,
       not_150_out, not_151_out, not_152_out, not_153_out, not_154_out, not_155_out, not_156_out,
       not_157_out, not_158_out, not_159_out, not_160_out, not_161_out, not_162_out, not_163_out,
       not_164_out, not_165_out, not_166_out, not_167_out, not_168_out, not_169_out, not_170_out,
       not_171_out, not_172_out, not_173_out, not_174_out, not_175_out, not_176_out, not_177_out,
       not_178_out, not_179_out, not_180_out, not_181_out, not_182_out, not_183_out, not_184_out,
       not_185_out, not_186_out, not_187_out, not_188_out, not_189_out, not_190_out, not_191_out,
       not_192_out, not_193_out, not_194_out, not_195_out, not_196_out, not_197_out, not_198_out,
       not_199_out, not_200_out, not_201_out, not_202_out, not_203_out, not_204_out, not_205_out,
       not_206_out, not_207_out, not_208_out, not_209_out, not_210_out, not_211_out, not_212_out,
       not_213_out, not_214_out, not_215_out, not_216_out, not_217_out, not_218_out, not_219_out,
       not_220_out, not_221_out, not_222_out, not_223_out, not_224_out, not_225_out, not_226_out,
       not_227_out, not_228_out, not_229_out, not_230_out, not_231_out, not_232_out, not_233_out,
       not_234_out, not_235_out, not_236_out, not_237_out, not_238_out, not_239_out, not_240_out,
       not_241_out, not_242_out, not_243_out, not_244_out, not_245_out, not_246_out, not_247_out,
       not_248_out, not_249_out, not_250_out, not_251_out, not_252_out, not_253_out, not_254_out,
       not_255_out, not_256_out, not_257_out, not_258_out, not_259_out, not_260_out, not_261_out,
       not_262_out, not_263_out, not_264_out;

  not not_1 (not_1_out, OP5);
  not not_2 (not_2_out, OP4);
  not not_3 (not_3_out, OP3);
  not not_4 (not_4_out, OP2);
  not not_5 (not_5_out, OP1);
  not not_6 (not_6_out, OP0);
  not not_7 (not_7_out, F5);
  not not_8 (not_8_out, F4);
  not not_9 (not_9_out, F3);
  not not_10 (not_10_out, F2);
  not not_11 (not_11_out, OP5);
  not not_12 (not_12_out, OP4);
  not not_13 (not_13_out, OP3);
  not not_14 (not_14_out, OP2);
  not not_15 (not_15_out, OP1);
  not not_16 (not_16_out, OP0);
  not not_17 (not_17_out, F4);
  not not_18 (not_18_out, F3);
  not not_19 (not_19_out, F2);
  not not_20 (not_20_out, F1);
  not not_21 (not_21_out, F0);
  not not_22 (not_22_out, OP5);
  not not_23 (not_23_out, OP4);
  not not_24 (not_24_out, OP3);
  not not_25 (not_25_out, OP2);
  not not_26 (not_26_out, OP1);
  not not_27 (not_27_out, OP0);
  not not_28 (not_28_out, F4);
  not not_29 (not_29_out, F3);
  not not_30 (not_30_out, F2);
  not not_31 (not_31_out, F1);
  not not_32 (not_32_out, OP5);
  not not_33 (not_33_out, OP4);
  not not_34 (not_34_out, OP3);
  not not_35 (not_35_out, OP2);
  not not_36 (not_36_out, OP1);
  not not_37 (not_37_out, OP0);
  not not_38 (not_38_out, F4);
  not not_39 (not_39_out, F3);
  not not_40 (not_40_out, F1);
  not not_41 (not_41_out, F0);
  not not_42 (not_42_out, OP5);
  not not_43 (not_43_out, OP4);
  not not_44 (not_44_out, OP3);
  not not_45 (not_45_out, OP2);
  not not_46 (not_46_out, OP1);
  not not_47 (not_47_out, OP0);
  not not_48 (not_48_out, F4);
  not not_49 (not_49_out, F2);
  not not_50 (not_50_out, F0);
  not not_51 (not_51_out, OP5);
  not not_52 (not_52_out, OP4);
  not not_53 (not_53_out, OP2);
  not not_54 (not_54_out, OP1);
  not not_55 (not_55_out, OP0);
  not not_56 (not_56_out, OP5);
  not not_57 (not_57_out, OP4);
  not not_58 (not_58_out, OP1);
  not not_59 (not_59_out, OP0);
  not not_60 (not_60_out, OP5);
  not not_61 (not_61_out, OP4);
  not not_62 (not_62_out, OP2);
  not not_63 (not_63_out, OP1);
  not not_64 (not_64_out, OP5);
  not not_65 (not_65_out, OP4);
  not not_66 (not_66_out, OP2);
  not not_67 (not_67_out, OP0);
  not not_68 (not_68_out, OP4);
  not not_69 (not_69_out, OP3);
  not not_70 (not_70_out, OP2);
  not not_71 (not_71_out, OP4);
  not not_72 (not_72_out, OP2);
  not not_73 (not_73_out, OP5);
  not not_74 (not_74_out, OP4);
  not not_75 (not_75_out, OP3);
  not not_76 (not_76_out, OP2);
  not not_77 (not_77_out, OP1);
  not not_78 (not_78_out, OP0);
  not not_79 (not_79_out, F4);
  not not_80 (not_80_out, F3);
  not not_81 (not_81_out, F0);
  not not_82 (not_82_out, OP4);
  not not_83 (not_83_out, OP3);
  not not_84 (not_84_out, OP2);
  not not_85 (not_85_out, OP1);
  not not_86 (not_86_out, OP0);
  not not_87 (not_87_out, OP5);
  not not_88 (not_88_out, OP4);
  not not_89 (not_89_out, OP3);
  not not_90 (not_90_out, OP2);
  not not_91 (not_91_out, OP1);
  not not_92 (not_92_out, OP0);
  not not_93 (not_93_out, F5);
  not not_94 (not_94_out, F4);
  not not_95 (not_95_out, F3);
  not not_96 (not_96_out, F2);
  not not_97 (not_97_out, F0);
  not not_98 (not_98_out, OP5);
  not not_99 (not_99_out, OP4);
  not not_100 (not_100_out, OP3);
  not not_101 (not_101_out, OP2);
  not not_102 (not_102_out, OP1);
  not not_103 (not_103_out, OP0);
  not not_104 (not_104_out, F4);
  not not_105 (not_105_out, F3);
  not not_106 (not_106_out, F2);
  not not_107 (not_107_out, F0);
  not not_108 (not_108_out, OP5);
  not not_109 (not_109_out, OP4);
  not not_110 (not_110_out, OP3);
  not not_111 (not_111_out, OP2);
  not not_112 (not_112_out, OP1);
  not not_113 (not_113_out, OP0);
  not not_114 (not_114_out, F4);
  not not_115 (not_115_out, F3);
  not not_116 (not_116_out, F1);
  not not_117 (not_117_out, F0);
  not not_118 (not_118_out, OP5);
  not not_119 (not_119_out, OP4);
  not not_120 (not_120_out, OP3);
  not not_121 (not_121_out, OP2);
  not not_122 (not_122_out, OP1);
  not not_123 (not_123_out, OP0);
  not not_124 (not_124_out, F4);
  not not_125 (not_125_out, F3);
  not not_126 (not_126_out, OP5);
  not not_127 (not_127_out, OP4);
  not not_128 (not_128_out, OP3);
  not not_129 (not_129_out, OP2);
  not not_130 (not_130_out, OP1);
  not not_131 (not_131_out, OP0);
  not not_132 (not_132_out, F4);
  not not_133 (not_133_out, F2);
  not not_134 (not_134_out, F0);
  not not_135 (not_135_out, OP5);
  not not_136 (not_136_out, OP4);
  not not_137 (not_137_out, OP1);
  not not_138 (not_138_out, OP0);
  not not_139 (not_139_out, OP5);
  not not_140 (not_140_out, OP4);
  not not_141 (not_141_out, OP2);
  not not_142 (not_142_out, OP0);
  not not_143 (not_143_out, OP5);
  not not_144 (not_144_out, OP4);
  not not_145 (not_145_out, OP3);
  not not_146 (not_146_out, OP2);
  not not_147 (not_147_out, OP1);
  not not_148 (not_148_out, OP0);
  not not_149 (not_149_out, F4);
  not not_150 (not_150_out, F3);
  not not_151 (not_151_out, F2);
  not not_152 (not_152_out, F1);
  not not_153 (not_153_out, F0);
  not not_154 (not_154_out, OP5);
  not not_155 (not_155_out, OP4);
  not not_156 (not_156_out, OP3);
  not not_157 (not_157_out, OP2);
  not not_158 (not_158_out, OP1);
  not not_159 (not_159_out, OP0);
  not not_160 (not_160_out, F4);
  not not_161 (not_161_out, F3);
  not not_162 (not_162_out, F2);
  not not_163 (not_163_out, F1);
  not not_164 (not_164_out, OP5);
  not not_165 (not_165_out, OP4);
  not not_166 (not_166_out, OP3);
  not not_167 (not_167_out, OP2);
  not not_168 (not_168_out, OP1);
  not not_169 (not_169_out, OP0);
  not not_170 (not_170_out, F4);
  not not_171 (not_171_out, F3);
  not not_172 (not_172_out, F2);
  not not_173 (not_173_out, F0);
  not not_174 (not_174_out, OP5);
  not not_175 (not_175_out, OP4);
  not not_176 (not_176_out, OP3);
  not not_177 (not_177_out, OP2);
  not not_178 (not_178_out, OP1);
  not not_179 (not_179_out, OP0);
  not not_180 (not_180_out, F4);
  not not_181 (not_181_out, F3);
  not not_182 (not_182_out, F1);
  not not_183 (not_183_out, F0);
  not not_184 (not_184_out, OP5);
  not not_185 (not_185_out, OP4);
  not not_186 (not_186_out, OP3);
  not not_187 (not_187_out, OP2);
  not not_188 (not_188_out, OP1);
  not not_189 (not_189_out, OP0);
  not not_190 (not_190_out, F4);
  not not_191 (not_191_out, F2);
  not not_192 (not_192_out, OP5);
  not not_193 (not_193_out, OP4);
  not not_194 (not_194_out, OP2);
  not not_195 (not_195_out, OP1);
  not not_196 (not_196_out, OP0);
  not not_197 (not_197_out, OP5);
  not not_198 (not_198_out, OP4);
  not not_199 (not_199_out, OP1);
  not not_200 (not_200_out, OP0);
  not not_201 (not_201_out, OP5);
  not not_202 (not_202_out, OP4);
  not not_203 (not_203_out, OP2);
  not not_204 (not_204_out, OP1);
  not not_205 (not_205_out, OP4);
  not not_206 (not_206_out, OP3);
  not not_207 (not_207_out, OP2);
  not not_208 (not_208_out, OP4);
  not not_209 (not_209_out, OP2);
  not not_210 (not_210_out, OP4);
  not not_211 (not_211_out, OP3);
  not not_212 (not_212_out, OP2);
  not not_213 (not_213_out, OP1);
  not not_214 (not_214_out, OP0);
  not not_215 (not_215_out, OP5);
  not not_216 (not_216_out, OP4);
  not not_217 (not_217_out, OP3);
  not not_218 (not_218_out, OP2);
  not not_219 (not_219_out, OP1);
  not not_220 (not_220_out, OP0);
  not not_221 (not_221_out, F4);
  not not_222 (not_222_out, F3);
  not not_223 (not_223_out, F1);
  not not_224 (not_224_out, OP5);
  not not_225 (not_225_out, OP4);
  not not_226 (not_226_out, OP3);
  not not_227 (not_227_out, OP2);
  not not_228 (not_228_out, OP1);
  not not_229 (not_229_out, OP0);
  not not_230 (not_230_out, F4);
  not not_231 (not_231_out, F3);
  not not_232 (not_232_out, OP5);
  not not_233 (not_233_out, OP4);
  not not_234 (not_234_out, OP3);
  not not_235 (not_235_out, OP2);
  not not_236 (not_236_out, OP1);
  not not_237 (not_237_out, OP0);
  not not_238 (not_238_out, F4);
  not not_239 (not_239_out, F2);
  not not_240 (not_240_out, F0);
  not not_241 (not_241_out, OP5);
  not not_242 (not_242_out, OP4);
  not not_243 (not_243_out, OP3);
  not not_244 (not_244_out, OP2);
  not not_245 (not_245_out, OP1);
  not not_246 (not_246_out, OP0);
  not not_247 (not_247_out, F4);
  not not_248 (not_248_out, F2);
  not not_249 (not_249_out, OP5);
  not not_250 (not_250_out, OP4);
  not not_251 (not_251_out, OP2);
  not not_252 (not_252_out, OP0);
  not not_253 (not_253_out, OP5);
  not not_254 (not_254_out, OP4);
  not not_255 (not_255_out, OP1);
  not not_256 (not_256_out, OP5);
  not not_257 (not_257_out, OP4);
  not not_258 (not_258_out, OP3);
  not not_259 (not_259_out, OP2);
  not not_260 (not_260_out, OP1);
  not not_261 (not_261_out, OP0);
  not not_262 (not_262_out, F4);
  not not_263 (not_263_out, F3);
  not not_264 (not_264_out, F0);
  and and_1 (and_1_out, not_1_out, not_2_out, not_3_out, not_4_out, not_5_out, not_6_out, not_7_out, not_8_out, not_9_out, not_10_out, F1, F0);
  and and_2 (and_2_out, not_11_out, not_12_out, not_13_out, not_14_out, not_15_out, not_16_out, F5, not_17_out, not_18_out, not_19_out, not_20_out, not_21_out);
  and and_3 (and_3_out, not_22_out, not_23_out, not_24_out, not_25_out, not_26_out, not_27_out, F5, not_28_out, not_29_out, not_30_out, not_31_out, F0);
  and and_4 (and_4_out, not_32_out, not_33_out, not_34_out, not_35_out, not_36_out, not_37_out, F5, not_38_out, not_39_out, F2, not_40_out, not_41_out);
  and and_5 (and_5_out, not_42_out, not_43_out, not_44_out, not_45_out, not_46_out, not_47_out, F5, not_48_out, F3, not_49_out, F1, not_50_out);
  and and_6 (and_6_out, not_51_out, not_52_out, OP3, not_53_out, not_54_out, not_55_out);
  and and_7 (and_7_out, not_56_out, not_57_out, OP3, OP2, not_58_out, not_59_out);
  and and_8 (and_8_out, not_60_out, not_61_out, OP3, not_62_out, not_63_out, OP0);
  and and_9 (and_9_out, not_64_out, not_65_out, OP3, not_66_out, OP1, not_67_out);
  and and_10 (and_10_out, OP5, not_68_out, not_69_out, not_70_out, OP1, OP0);
  and and_11 (and_11_out, OP5, not_71_out, OP3, not_72_out, OP1, OP0);
  and and_12 (and_12_out, not_73_out, not_74_out, not_75_out, not_76_out, not_77_out, not_78_out, F5, not_79_out, not_80_out, F2, F1, not_81_out);
  and and_13 (and_13_out, OP5, not_82_out, not_83_out, not_84_out, not_85_out, not_86_out);
  and and_14 (and_14_out, not_87_out, not_88_out, not_89_out, not_90_out, not_91_out, not_92_out, not_93_out, not_94_out, not_95_out, not_96_out, F1, not_97_out);
  and and_15 (and_15_out, not_98_out, not_99_out, not_100_out, not_101_out, not_102_out, not_103_out, F5, not_104_out, not_105_out, not_106_out, F1, not_107_out);
  and and_16 (and_16_out, not_108_out, not_109_out, not_110_out, not_111_out, not_112_out, not_113_out, F5, not_114_out, not_115_out, F2, not_116_out, not_117_out);
  and and_17 (and_17_out, not_118_out, not_119_out, not_120_out, not_121_out, not_122_out, not_123_out, F5, not_124_out, not_125_out, F2, F1, F0);
  and and_18 (and_18_out, not_126_out, not_127_out, not_128_out, not_129_out, not_130_out, not_131_out, F5, not_132_out, F3, not_133_out, F1, not_134_out);
  and and_19 (and_19_out, not_135_out, not_136_out, OP3, OP2, not_137_out, not_138_out);
  and and_20 (and_20_out, not_139_out, not_140_out, OP3, not_141_out, OP1, not_142_out);
  and and_21 (and_21_out, not_143_out, not_144_out, not_145_out, not_146_out, not_147_out, not_148_out, F5, not_149_out, not_150_out, not_151_out, not_152_out, not_153_out);
  and and_22 (and_22_out, not_154_out, not_155_out, not_156_out, not_157_out, not_158_out, not_159_out, F5, not_160_out, not_161_out, not_162_out, not_163_out, F0);
  and and_23 (and_23_out, not_164_out, not_165_out, not_166_out, not_167_out, not_168_out, not_169_out, F5, not_170_out, not_171_out, not_172_out, F1, not_173_out);
  and and_24 (and_24_out, not_174_out, not_175_out, not_176_out, not_177_out, not_178_out, not_179_out, F5, not_180_out, not_181_out, F2, not_182_out, not_183_out);
  and and_25 (and_25_out, not_184_out, not_185_out, not_186_out, not_187_out, not_188_out, not_189_out, F5, not_190_out, F3, not_191_out, F1, F0);
  and and_26 (and_26_out, not_192_out, not_193_out, OP3, not_194_out, not_195_out, not_196_out);
  and and_27 (and_27_out, not_197_out, not_198_out, OP3, OP2, not_199_out, not_200_out);
  and and_28 (and_28_out, not_201_out, not_202_out, OP3, not_203_out, not_204_out, OP0);
  and and_29 (and_29_out, OP5, not_205_out, not_206_out, not_207_out, OP1, OP0);
  and and_30 (and_30_out, OP5, not_208_out, OP3, not_209_out, OP1, OP0);
  and and_31 (and_31_out, OP5, not_210_out, not_211_out, not_212_out, not_213_out, not_214_out);
  and and_32 (and_32_out, not_215_out, not_216_out, not_217_out, not_218_out, not_219_out, not_220_out, F5, not_221_out, not_222_out, F2, not_223_out, F0);
  and and_33 (and_33_out, not_224_out, not_225_out, not_226_out, not_227_out, not_228_out, not_229_out, F5, not_230_out, not_231_out, F2, F1, F0);
  and and_34 (and_34_out, not_232_out, not_233_out, not_234_out, not_235_out, not_236_out, not_237_out, F5, not_238_out, F3, not_239_out, F1, not_240_out);
  and and_35 (and_35_out, not_241_out, not_242_out, not_243_out, not_244_out, not_245_out, not_246_out, F5, not_247_out, F3, not_248_out, F1, F0);
  and and_36 (and_36_out, not_249_out, not_250_out, OP3, not_251_out, OP1, not_252_out);
  and and_37 (and_37_out, not_253_out, not_254_out, OP3, OP2, not_255_out, OP0);
  and and_38 (and_38_out, not_256_out, not_257_out, not_258_out, not_259_out, not_260_out, not_261_out, F5, not_262_out, not_263_out, F2, F1, not_264_out);
  or or_1 (S1, and_14_out, and_15_out, and_16_out, and_17_out, and_18_out, and_19_out, and_20_out);
  or or_2 (S2, and_21_out, and_22_out, and_23_out, and_24_out, and_25_out, and_26_out, and_27_out, and_28_out, and_29_out, and_30_out, and_31_out);
  or or_3 (S3, and_32_out, and_33_out, and_34_out, and_35_out, and_36_out, and_37_out, and_38_out);
  or or_4 (S0, and_1_out, and_2_out, and_3_out, and_4_out, and_5_out, and_6_out, and_7_out, and_8_out, and_9_out, and_10_out, and_11_out, and_12_out, and_13_out);
endmodule

// 拓展控制信号
module \拓展控制信号自动生成_31  (
  input  OP0,
  input  OP1,
  input  OP2,
  input  OP3,
  input  OP4,
  input  OP5,
  input  F0,
  input  F1,
  input  F2,
  input  F3,
  input  F4,
  input  F5,
  input  M0,
  input  M1,
  input  M2,
  input  M3,
  input  M4,
  output MemToReg,
  output MemWrite,
  output ALU_SRC,
  output RegWrite,
  output SysCALL,
  output SignedExt,
  output RegDst,
  output BEQ,
  output BNE,
  output JR,
  output JUMP,
  output JAL,
  output LUI,
  output LB,
  output BLEZ,
  output MFC0,
  output MTC0,
  output ERET
);

  wire and_1_out, and_2_out, and_4_out, and_5_out, and_6_out, and_7_out, and_8_out, and_9_out, and_10_out,
       and_11_out, and_12_out, and_13_out, and_14_out, and_15_out, and_16_out, and_17_out, and_19_out,
       and_20_out, and_21_out, and_22_out, and_23_out, and_24_out, and_25_out, and_26_out, and_27_out,
       and_28_out, and_29_out, and_33_out, and_34_out, not_1_out, not_2_out, not_3_out, not_4_out, not_5_out,
       not_6_out, not_7_out, not_8_out, not_9_out, not_10_out, not_11_out, not_12_out, not_13_out,
       not_14_out, not_15_out, not_16_out, not_17_out, not_18_out, not_19_out, not_20_out, not_21_out,
       not_22_out, not_23_out, not_24_out, not_25_out, not_26_out, not_27_out, not_28_out, not_29_out,
       not_30_out, not_31_out, not_32_out, not_33_out, not_34_out, not_35_out, not_36_out, not_37_out,
       not_38_out, not_39_out, not_40_out, not_41_out, not_42_out, not_43_out, not_44_out, not_45_out,
       not_46_out, not_47_out, not_48_out, not_49_out, not_50_out, not_51_out, not_52_out, not_53_out,
       not_54_out, not_55_out, not_56_out, not_57_out, not_58_out, not_59_out, not_60_out, not_61_out,
       not_62_out, not_63_out, not_64_out, not_65_out, not_66_out, not_67_out, not_68_out, not_69_out,
       not_70_out, not_71_out, not_72_out, not_73_out, not_74_out, not_75_out, not_76_out, not_77_out,
       not_78_out, not_79_out, not_80_out, not_81_out, not_82_out, not_83_out, not_84_out, not_85_out,
       not_86_out, not_87_out, not_88_out, not_89_out, not_90_out, not_91_out, not_92_out, not_93_out,
       not_94_out, not_95_out, not_96_out, not_97_out, not_98_out, not_99_out, not_100_out, not_101_out,
       not_102_out, not_103_out, not_104_out, not_105_out, not_106_out, not_107_out, not_108_out,
       not_109_out, not_110_out, not_111_out, not_112_out, not_113_out, not_114_out, not_115_out,
       not_116_out, not_117_out, not_118_out, not_119_out, not_120_out, not_121_out, not_122_out,
       not_123_out, not_124_out, not_125_out, not_126_out, not_127_out, not_128_out, not_129_out,
       not_130_out, not_131_out, not_132_out, not_133_out, not_134_out, not_135_out, not_136_out,
       not_137_out, not_138_out, not_139_out, not_140_out, not_141_out, not_142_out, not_143_out,
       not_144_out, not_145_out, not_146_out, not_147_out, not_148_out, not_149_out, not_150_out,
       not_151_out, not_152_out, not_153_out, not_154_out, not_155_out, not_156_out, not_157_out,
       not_158_out, not_159_out, not_160_out, not_161_out, not_162_out, not_163_out, not_164_out,
       not_165_out, not_166_out, not_167_out, not_168_out, not_169_out, not_170_out, not_171_out,
       not_172_out, not_173_out, not_174_out, not_175_out, not_176_out, not_177_out, not_178_out,
       not_179_out, not_180_out, not_181_out, not_182_out, not_183_out, not_184_out, not_185_out,
       not_186_out, not_187_out, not_188_out, not_189_out, not_190_out, not_191_out, not_192_out,
       not_193_out, not_194_out, not_195_out, not_196_out, not_197_out, not_198_out, not_199_out,
       not_200_out, not_201_out, not_202_out, not_203_out, not_204_out, not_205_out, not_206_out,
       not_207_out, not_208_out, not_209_out, not_210_out, not_211_out, not_212_out, not_213_out,
       not_214_out, not_215_out, not_216_out, not_217_out, not_218_out, not_219_out, not_220_out,
       not_221_out, not_222_out, not_223_out, not_224_out, not_225_out, not_226_out, not_227_out,
       not_228_out, not_229_out, not_230_out, not_231_out, not_232_out, not_233_out, not_234_out,
       not_235_out, not_236_out;

  not not_1 (not_1_out, OP0);
  not not_2 (not_2_out, OP1);
  not not_3 (not_3_out, OP2);
  not not_4 (not_4_out, OP3);
  not not_5 (not_5_out, OP4);
  not not_6 (not_6_out, OP2);
  not not_7 (not_7_out, OP3);
  not not_8 (not_8_out, OP4);
  not not_9 (not_9_out, OP2);
  not not_10 (not_10_out, OP4);
  not not_11 (not_11_out, OP0);
  not not_12 (not_12_out, OP1);
  not not_13 (not_13_out, OP2);
  not not_14 (not_14_out, OP3);
  not not_15 (not_15_out, OP4);
  not not_16 (not_16_out, OP0);
  not not_17 (not_17_out, OP2);
  not not_18 (not_18_out, OP4);
  not not_19 (not_19_out, OP5);
  not not_20 (not_20_out, OP1);
  not not_21 (not_21_out, OP4);
  not not_22 (not_22_out, OP5);
  not not_23 (not_23_out, OP2);
  not not_24 (not_24_out, OP4);
  not not_25 (not_25_out, OP0);
  not not_26 (not_26_out, OP1);
  not not_27 (not_27_out, OP2);
  not not_28 (not_28_out, OP3);
  not not_29 (not_29_out, OP4);
  not not_30 (not_30_out, F0);
  not not_31 (not_31_out, F2);
  not not_32 (not_32_out, F3);
  not not_33 (not_33_out, F4);
  not not_34 (not_34_out, OP0);
  not not_35 (not_35_out, OP1);
  not not_36 (not_36_out, OP2);
  not not_37 (not_37_out, OP4);
  not not_38 (not_38_out, OP5);
  not not_39 (not_39_out, F1);
  not not_40 (not_40_out, F3);
  not not_41 (not_41_out, F4);
  not not_42 (not_42_out, OP0);
  not not_43 (not_43_out, OP1);
  not not_44 (not_44_out, OP2);
  not not_45 (not_45_out, OP4);
  not not_46 (not_46_out, OP5);
  not not_47 (not_47_out, F3);
  not not_48 (not_48_out, F4);
  not not_49 (not_49_out, OP0);
  not not_50 (not_50_out, OP1);
  not not_51 (not_51_out, OP2);
  not not_52 (not_52_out, OP3);
  not not_53 (not_53_out, OP4);
  not not_54 (not_54_out, F2);
  not not_55 (not_55_out, F3);
  not not_56 (not_56_out, F4);
  not not_57 (not_57_out, F5);
  not not_58 (not_58_out, OP0);
  not not_59 (not_59_out, OP1);
  not not_60 (not_60_out, OP2);
  not not_61 (not_61_out, OP3);
  not not_62 (not_62_out, OP4);
  not not_63 (not_63_out, F2);
  not not_64 (not_64_out, F4);
  not not_65 (not_65_out, OP0);
  not not_66 (not_66_out, OP1);
  not not_67 (not_67_out, OP2);
  not not_68 (not_68_out, OP3);
  not not_69 (not_69_out, OP4);
  not not_70 (not_70_out, OP0);
  not not_71 (not_71_out, OP2);
  not not_72 (not_72_out, OP4);
  not not_73 (not_73_out, OP5);
  not not_74 (not_74_out, OP1);
  not not_75 (not_75_out, OP4);
  not not_76 (not_76_out, OP5);
  not not_77 (not_77_out, OP4);
  not not_78 (not_78_out, OP5);
  not not_79 (not_79_out, OP2);
  not not_80 (not_80_out, OP3);
  not not_81 (not_81_out, OP4);
  not not_82 (not_82_out, OP0);
  not not_83 (not_83_out, OP1);
  not not_84 (not_84_out, OP2);
  not not_85 (not_85_out, OP3);
  not not_86 (not_86_out, OP4);
  not not_87 (not_87_out, OP5);
  not not_88 (not_88_out, F0);
  not not_89 (not_89_out, F1);
  not not_90 (not_90_out, F4);
  not not_91 (not_91_out, F5);
  not not_92 (not_92_out, OP0);
  not not_93 (not_93_out, OP1);
  not not_94 (not_94_out, OP2);
  not not_95 (not_95_out, OP3);
  not not_96 (not_96_out, OP4);
  not not_97 (not_97_out, OP0);
  not not_98 (not_98_out, OP2);
  not not_99 (not_99_out, OP4);
  not not_100 (not_100_out, OP5);
  not not_101 (not_101_out, OP1);
  not not_102 (not_102_out, OP2);
  not not_103 (not_103_out, OP4);
  not not_104 (not_104_out, OP5);
  not not_105 (not_105_out, OP0);
  not not_106 (not_106_out, OP3);
  not not_107 (not_107_out, OP4);
  not not_108 (not_108_out, OP5);
  not not_109 (not_109_out, OP1);
  not not_110 (not_110_out, OP3);
  not not_111 (not_111_out, OP4);
  not not_112 (not_112_out, OP5);
  not not_113 (not_113_out, OP2);
  not not_114 (not_114_out, OP4);
  not not_115 (not_115_out, OP0);
  not not_116 (not_116_out, OP1);
  not not_117 (not_117_out, OP2);
  not not_118 (not_118_out, OP3);
  not not_119 (not_119_out, OP4);
  not not_120 (not_120_out, OP5);
  not not_121 (not_121_out, F0);
  not not_122 (not_122_out, F2);
  not not_123 (not_123_out, F3);
  not not_124 (not_124_out, F4);
  not not_125 (not_125_out, OP0);
  not not_126 (not_126_out, OP1);
  not not_127 (not_127_out, OP2);
  not not_128 (not_128_out, OP3);
  not not_129 (not_129_out, OP4);
  not not_130 (not_130_out, OP5);
  not not_131 (not_131_out, F1);
  not not_132 (not_132_out, F3);
  not not_133 (not_133_out, F4);
  not not_134 (not_134_out, OP0);
  not not_135 (not_135_out, OP1);
  not not_136 (not_136_out, OP2);
  not not_137 (not_137_out, OP3);
  not not_138 (not_138_out, OP4);
  not not_139 (not_139_out, OP5);
  not not_140 (not_140_out, F3);
  not not_141 (not_141_out, F4);
  not not_142 (not_142_out, OP0);
  not not_143 (not_143_out, OP1);
  not not_144 (not_144_out, OP2);
  not not_145 (not_145_out, OP3);
  not not_146 (not_146_out, OP4);
  not not_147 (not_147_out, OP5);
  not not_148 (not_148_out, F2);
  not not_149 (not_149_out, F3);
  not not_150 (not_150_out, F4);
  not not_151 (not_151_out, F5);
  not not_152 (not_152_out, OP0);
  not not_153 (not_153_out, OP1);
  not not_154 (not_154_out, OP2);
  not not_155 (not_155_out, OP3);
  not not_156 (not_156_out, OP4);
  not not_157 (not_157_out, OP5);
  not not_158 (not_158_out, F2);
  not not_159 (not_159_out, F4);
  not not_160 (not_160_out, OP0);
  not not_161 (not_161_out, OP1);
  not not_162 (not_162_out, OP3);
  not not_163 (not_163_out, OP4);
  not not_164 (not_164_out, OP5);
  not not_165 (not_165_out, OP1);
  not not_166 (not_166_out, OP3);
  not not_167 (not_167_out, OP4);
  not not_168 (not_168_out, OP5);
  not not_169 (not_169_out, OP0);
  not not_170 (not_170_out, OP1);
  not not_171 (not_171_out, OP2);
  not not_172 (not_172_out, OP3);
  not not_173 (not_173_out, OP4);
  not not_174 (not_174_out, OP5);
  not not_175 (not_175_out, F0);
  not not_176 (not_176_out, F1);
  not not_177 (not_177_out, F2);
  not not_178 (not_178_out, F4);
  not not_179 (not_179_out, F5);
  not not_180 (not_180_out, OP0);
  not not_181 (not_181_out, OP2);
  not not_182 (not_182_out, OP3);
  not not_183 (not_183_out, OP4);
  not not_184 (not_184_out, OP5);
  not not_185 (not_185_out, F0);
  not not_186 (not_186_out, F1);
  not not_187 (not_187_out, F2);
  not not_188 (not_188_out, F4);
  not not_189 (not_189_out, F5);
  not not_190 (not_190_out, OP2);
  not not_191 (not_191_out, OP3);
  not not_192 (not_192_out, OP4);
  not not_193 (not_193_out, OP5);
  not not_194 (not_194_out, OP2);
  not not_195 (not_195_out, OP3);
  not not_196 (not_196_out, OP4);
  not not_197 (not_197_out, OP5);
  not not_198 (not_198_out, OP4);
  not not_199 (not_199_out, OP5);
  not not_200 (not_200_out, OP0);
  not not_201 (not_201_out, OP1);
  not not_202 (not_202_out, OP2);
  not not_203 (not_203_out, OP3);
  not not_204 (not_204_out, OP4);
  not not_205 (not_205_out, OP0);
  not not_206 (not_206_out, OP3);
  not not_207 (not_207_out, OP4);
  not not_208 (not_208_out, OP5);
  not not_209 (not_209_out, OP0);
  not not_210 (not_210_out, OP1);
  not not_211 (not_211_out, OP2);
  not not_212 (not_212_out, OP3);
  not not_213 (not_213_out, OP5);
  not not_214 (not_214_out, M0);
  not not_215 (not_215_out, M1);
  not not_216 (not_216_out, M2);
  not not_217 (not_217_out, M3);
  not not_218 (not_218_out, M4);
  not not_219 (not_219_out, OP0);
  not not_220 (not_220_out, OP1);
  not not_221 (not_221_out, OP2);
  not not_222 (not_222_out, OP3);
  not not_223 (not_223_out, OP5);
  not not_224 (not_224_out, M0);
  not not_225 (not_225_out, M1);
  not not_226 (not_226_out, M3);
  not not_227 (not_227_out, M4);
  not not_228 (not_228_out, OP0);
  not not_229 (not_229_out, OP1);
  not not_230 (not_230_out, OP2);
  not not_231 (not_231_out, OP3);
  not not_232 (not_232_out, OP5);
  not not_233 (not_233_out, F0);
  not not_234 (not_234_out, F1);
  not not_235 (not_235_out, F2);
  not not_236 (not_236_out, F5);
  and and_1 (and_1_out, not_1_out, not_2_out, not_3_out, not_4_out, not_5_out, OP5);
  and and_2 (and_2_out, OP0, OP1, not_6_out, not_7_out, not_8_out, OP5);
  and and_3 (MemWrite, OP0, OP1, not_9_out, OP3, not_10_out, OP5);
  and and_4 (and_4_out, not_11_out, not_12_out, not_13_out, not_14_out, not_15_out, OP5);
  and and_5 (and_5_out, not_16_out, not_17_out, OP3, not_18_out, not_19_out);
  and and_6 (and_6_out, not_20_out, OP3, not_21_out, not_22_out);
  and and_7 (and_7_out, OP0, OP1, not_23_out, not_24_out, OP5);
  and and_8 (and_8_out, not_25_out, not_26_out, not_27_out, not_28_out, not_29_out, not_30_out, not_31_out, not_32_out, not_33_out);
  and and_9 (and_9_out, not_34_out, not_35_out, not_36_out, not_37_out, not_38_out, not_39_out, not_40_out, not_41_out, F5);
  and and_10 (and_10_out, not_42_out, not_43_out, not_44_out, not_45_out, not_46_out, F2, not_47_out, not_48_out, F5);
  and and_11 (and_11_out, not_49_out, not_50_out, not_51_out, not_52_out, not_53_out, F1, not_54_out, not_55_out, not_56_out, not_57_out);
  and and_12 (and_12_out, not_58_out, not_59_out, not_60_out, not_61_out, not_62_out, F1, not_63_out, F3, not_64_out, F5);
  and and_13 (and_13_out, not_65_out, not_66_out, not_67_out, not_68_out, not_69_out, OP5);
  and and_14 (and_14_out, not_70_out, not_71_out, OP3, not_72_out, not_73_out);
  and and_15 (and_15_out, not_74_out, OP3, not_75_out, not_76_out);
  and and_16 (and_16_out, OP0, OP2, OP3, not_77_out, not_78_out);
  and and_17 (and_17_out, OP0, OP1, not_79_out, not_80_out, not_81_out);
  and and_18 (SysCALL, not_82_out, not_83_out, not_84_out, not_85_out, not_86_out, not_87_out, not_88_out, not_89_out, F2, F3, not_90_out, not_91_out);
  and and_19 (and_19_out, not_92_out, not_93_out, not_94_out, not_95_out, not_96_out, OP5);
  and and_20 (and_20_out, not_97_out, not_98_out, OP3, not_99_out, not_100_out);
  and and_21 (and_21_out, not_101_out, not_102_out, OP3, not_103_out, not_104_out);
  and and_22 (and_22_out, not_105_out, OP2, not_106_out, not_107_out, not_108_out);
  and and_23 (and_23_out, not_109_out, OP2, not_110_out, not_111_out, not_112_out);
  and and_24 (and_24_out, OP0, OP1, not_113_out, not_114_out, OP5);
  and and_25 (and_25_out, not_115_out, not_116_out, not_117_out, not_118_out, not_119_out, not_120_out, not_121_out, not_122_out, not_123_out, not_124_out);
  and and_26 (and_26_out, not_125_out, not_126_out, not_127_out, not_128_out, not_129_out, not_130_out, not_131_out, not_132_out, not_133_out, F5);
  and and_27 (and_27_out, not_134_out, not_135_out, not_136_out, not_137_out, not_138_out, not_139_out, F2, not_140_out, not_141_out, F5);
  and and_28 (and_28_out, not_142_out, not_143_out, not_144_out, not_145_out, not_146_out, not_147_out, F1, not_148_out, not_149_out, not_150_out, not_151_out);
  and and_29 (and_29_out, not_152_out, not_153_out, not_154_out, not_155_out, not_156_out, not_157_out, F1, not_158_out, F3, not_159_out, F5);
  and and_30 (BEQ, not_160_out, not_161_out, OP2, not_162_out, not_163_out, not_164_out);
  and and_31 (BNE, OP0, not_165_out, OP2, not_166_out, not_167_out, not_168_out);
  and and_32 (JR, not_169_out, not_170_out, not_171_out, not_172_out, not_173_out, not_174_out, not_175_out, not_176_out, not_177_out, F3, not_178_out, not_179_out);
  and and_33 (and_33_out, not_180_out, not_181_out, not_182_out, not_183_out, not_184_out, not_185_out, not_186_out, not_187_out, F3, not_188_out, not_189_out);
  and and_34 (and_34_out, OP1, not_190_out, not_191_out, not_192_out, not_193_out);
  and and_35 (JAL, OP0, OP1, not_194_out, not_195_out, not_196_out, not_197_out);
  and and_36 (LUI, OP0, OP1, OP2, OP3, not_198_out, not_199_out);
  and and_37 (LB, not_200_out, not_201_out, not_202_out, not_203_out, not_204_out, OP5);
  and and_38 (BLEZ, not_205_out, OP1, OP2, not_206_out, not_207_out, not_208_out);
  and and_39 (MFC0, not_209_out, not_210_out, not_211_out, not_212_out, OP4, not_213_out, not_214_out, not_215_out, not_216_out, not_217_out, not_218_out);
  and and_40 (MTC0, not_219_out, not_220_out, not_221_out, not_222_out, OP4, not_223_out, not_224_out, not_225_out, M2, not_226_out, not_227_out);
  and and_41 (ERET, not_228_out, not_229_out, not_230_out, not_231_out, OP4, not_232_out, not_233_out, not_234_out, not_235_out, F3, F4, not_236_out, M4);
  or or_1 (MemToReg, and_1_out, and_2_out);
  or or_2 (ALU_SRC, and_4_out, and_5_out, and_6_out, and_7_out);
  or or_3 (SignedExt, and_19_out, and_20_out, and_21_out, and_22_out, and_23_out, and_24_out);
  or or_4 (RegDst, and_25_out, and_26_out, and_27_out, and_28_out, and_29_out);
  or or_5 (JUMP, and_33_out, and_34_out);
  or or_6 (RegWrite, and_8_out, and_9_out, and_10_out, and_11_out, and_12_out, and_13_out, and_14_out, and_15_out, and_16_out, and_17_out);
endmodule

// 寄存器使用情况
module \寄存器使用情况_24_3_2  (
  input  OP0,
  input  OP1,
  input  OP2,
  input  OP3,
  input  OP4,
  input  OP5,
  input  F0,
  input  F1,
  input  F2,
  input  F3,
  input  F4,
  input  F5,
  output R1_used,
  output R2_used
);

  wire and_1_out, and_2_out, and_3_out, and_4_out, and_5_out, and_6_out, and_7_out, and_8_out, and_9_out,
       and_10_out, and_11_out, and_12_out, and_13_out, and_14_out, and_15_out, and_16_out, and_17_out,
       and_18_out, and_19_out, and_20_out, and_21_out, and_22_out, and_23_out, and_24_out, and_25_out,
       and_26_out, and_27_out, and_28_out, and_29_out, and_30_out, and_31_out, and_32_out, and_33_out,
       and_34_out, and_35_out, and_36_out, and_37_out, and_38_out, not_1_out, not_2_out, not_3_out,
       not_4_out, not_5_out, not_6_out, not_7_out, not_8_out, not_9_out, not_10_out, not_11_out, not_12_out,
       not_13_out, not_14_out, not_15_out, not_16_out, not_17_out, not_18_out, not_19_out, not_20_out,
       not_21_out, not_22_out, not_23_out, not_24_out, not_25_out, not_26_out, not_27_out, not_28_out,
       not_29_out, not_30_out, not_31_out, not_32_out, not_33_out, not_34_out, not_35_out, not_36_out,
       not_37_out, not_38_out, not_39_out, not_40_out, not_41_out, not_42_out, not_43_out, not_44_out,
       not_45_out, not_46_out, not_47_out, not_48_out, not_49_out, not_50_out, not_51_out, not_52_out,
       not_53_out, not_54_out, not_55_out, not_56_out, not_57_out, not_58_out, not_59_out, not_60_out,
       not_61_out, not_62_out, not_63_out, not_64_out, not_65_out, not_66_out, not_67_out, not_68_out,
       not_69_out, not_70_out, not_71_out, not_72_out, not_73_out, not_74_out, not_75_out, not_76_out,
       not_77_out, not_78_out, not_79_out, not_80_out, not_81_out, not_82_out, not_83_out, not_84_out,
       not_85_out, not_86_out, not_87_out, not_88_out, not_89_out, not_90_out, not_91_out, not_92_out,
       not_93_out, not_94_out, not_95_out, not_96_out, not_97_out, not_98_out, not_99_out, not_100_out,
       not_101_out, not_102_out, not_103_out, not_104_out, not_105_out, not_106_out, not_107_out,
       not_108_out, not_109_out, not_110_out, not_111_out, not_112_out, not_113_out, not_114_out,
       not_115_out, not_116_out, not_117_out, not_118_out, not_119_out, not_120_out, not_121_out,
       not_122_out, not_123_out, not_124_out, not_125_out, not_126_out, not_127_out, not_128_out,
       not_129_out, not_130_out, not_131_out, not_132_out, not_133_out, not_134_out, not_135_out,
       not_136_out, not_137_out, not_138_out, not_139_out, not_140_out, not_141_out, not_142_out,
       not_143_out, not_144_out, not_145_out, not_146_out, not_147_out, not_148_out, not_149_out,
       not_150_out, not_151_out, not_152_out, not_153_out, not_154_out, not_155_out, not_156_out,
       not_157_out, not_158_out, not_159_out, not_160_out, not_161_out, not_162_out, not_163_out,
       not_164_out, not_165_out, not_166_out, not_167_out, not_168_out, not_169_out, not_170_out,
       not_171_out, not_172_out, not_173_out, not_174_out, not_175_out, not_176_out, not_177_out,
       not_178_out, not_179_out, not_180_out, not_181_out, not_182_out, not_183_out, not_184_out,
       not_185_out, not_186_out, not_187_out, not_188_out, not_189_out, not_190_out, not_191_out,
       not_192_out, not_193_out, not_194_out, not_195_out, not_196_out, not_197_out, not_198_out,
       not_199_out, not_200_out, not_201_out, not_202_out, not_203_out, not_204_out, not_205_out,
       not_206_out, not_207_out, not_208_out, not_209_out, not_210_out, not_211_out, not_212_out,
       not_213_out, not_214_out, not_215_out, not_216_out, not_217_out, not_218_out, not_219_out,
       not_220_out, not_221_out, not_222_out, not_223_out, not_224_out, not_225_out, not_226_out,
       not_227_out, not_228_out, not_229_out, not_230_out, not_231_out, not_232_out, not_233_out,
       not_234_out, not_235_out, not_236_out, not_237_out, not_238_out, not_239_out, not_240_out,
       not_241_out, not_242_out, not_243_out, not_244_out, not_245_out, not_246_out, not_247_out,
       not_248_out, not_249_out, not_250_out, not_251_out, not_252_out, not_253_out, not_254_out,
       not_255_out, not_256_out, not_257_out, not_258_out, not_259_out, not_260_out, not_261_out,
       not_262_out, not_263_out, not_264_out, not_265_out, not_266_out, not_267_out, not_268_out,
       not_269_out, not_270_out, not_271_out, not_272_out, not_273_out, not_274_out, not_275_out,
       not_276_out, not_277_out, not_278_out, not_279_out, not_280_out, not_281_out, not_282_out,
       not_283_out, not_284_out, not_285_out, not_286_out;

  not not_1 (not_1_out, OP5);
  not not_2 (not_2_out, OP4);
  not not_3 (not_3_out, OP3);
  not not_4 (not_4_out, OP2);
  not not_5 (not_5_out, OP1);
  not not_6 (not_6_out, OP0);
  not not_7 (not_7_out, F4);
  not not_8 (not_8_out, F3);
  not not_9 (not_9_out, F2);
  not not_10 (not_10_out, F1);
  not not_11 (not_11_out, F0);
  not not_12 (not_12_out, OP5);
  not not_13 (not_13_out, OP4);
  not not_14 (not_14_out, OP3);
  not not_15 (not_15_out, OP2);
  not not_16 (not_16_out, OP1);
  not not_17 (not_17_out, OP0);
  not not_18 (not_18_out, F4);
  not not_19 (not_19_out, F3);
  not not_20 (not_20_out, F2);
  not not_21 (not_21_out, F1);
  not not_22 (not_22_out, OP5);
  not not_23 (not_23_out, OP4);
  not not_24 (not_24_out, OP3);
  not not_25 (not_25_out, OP2);
  not not_26 (not_26_out, OP1);
  not not_27 (not_27_out, OP0);
  not not_28 (not_28_out, F4);
  not not_29 (not_29_out, F3);
  not not_30 (not_30_out, F2);
  not not_31 (not_31_out, F0);
  not not_32 (not_32_out, OP5);
  not not_33 (not_33_out, OP4);
  not not_34 (not_34_out, OP3);
  not not_35 (not_35_out, OP2);
  not not_36 (not_36_out, OP1);
  not not_37 (not_37_out, OP0);
  not not_38 (not_38_out, F4);
  not not_39 (not_39_out, F3);
  not not_40 (not_40_out, F1);
  not not_41 (not_41_out, F0);
  not not_42 (not_42_out, OP5);
  not not_43 (not_43_out, OP4);
  not not_44 (not_44_out, OP3);
  not not_45 (not_45_out, OP2);
  not not_46 (not_46_out, OP1);
  not not_47 (not_47_out, OP0);
  not not_48 (not_48_out, F4);
  not not_49 (not_49_out, F3);
  not not_50 (not_50_out, F1);
  not not_51 (not_51_out, OP5);
  not not_52 (not_52_out, OP4);
  not not_53 (not_53_out, OP3);
  not not_54 (not_54_out, OP2);
  not not_55 (not_55_out, OP1);
  not not_56 (not_56_out, OP0);
  not not_57 (not_57_out, F4);
  not not_58 (not_58_out, F3);
  not not_59 (not_59_out, OP5);
  not not_60 (not_60_out, OP4);
  not not_61 (not_61_out, OP3);
  not not_62 (not_62_out, OP2);
  not not_63 (not_63_out, OP1);
  not not_64 (not_64_out, OP0);
  not not_65 (not_65_out, F4);
  not not_66 (not_66_out, F2);
  not not_67 (not_67_out, F0);
  not not_68 (not_68_out, OP5);
  not not_69 (not_69_out, OP4);
  not not_70 (not_70_out, OP3);
  not not_71 (not_71_out, OP2);
  not not_72 (not_72_out, OP1);
  not not_73 (not_73_out, OP0);
  not not_74 (not_74_out, F4);
  not not_75 (not_75_out, F2);
  not not_76 (not_76_out, OP5);
  not not_77 (not_77_out, OP4);
  not not_78 (not_78_out, OP3);
  not not_79 (not_79_out, OP2);
  not not_80 (not_80_out, OP1);
  not not_81 (not_81_out, OP0);
  not not_82 (not_82_out, F5);
  not not_83 (not_83_out, F4);
  not not_84 (not_84_out, F2);
  not not_85 (not_85_out, F1);
  not not_86 (not_86_out, F0);
  not not_87 (not_87_out, OP5);
  not not_88 (not_88_out, OP4);
  not not_89 (not_89_out, OP3);
  not not_90 (not_90_out, OP2);
  not not_91 (not_91_out, OP1);
  not not_92 (not_92_out, OP0);
  not not_93 (not_93_out, F5);
  not not_94 (not_94_out, F4);
  not not_95 (not_95_out, F1);
  not not_96 (not_96_out, F0);
  not not_97 (not_97_out, OP5);
  not not_98 (not_98_out, OP4);
  not not_99 (not_99_out, OP3);
  not not_100 (not_100_out, OP1);
  not not_101 (not_101_out, OP0);
  not not_102 (not_102_out, OP5);
  not not_103 (not_103_out, OP4);
  not not_104 (not_104_out, OP3);
  not not_105 (not_105_out, OP1);
  not not_106 (not_106_out, OP5);
  not not_107 (not_107_out, OP4);
  not not_108 (not_108_out, OP2);
  not not_109 (not_109_out, OP1);
  not not_110 (not_110_out, OP0);
  not not_111 (not_111_out, OP5);
  not not_112 (not_112_out, OP4);
  not not_113 (not_113_out, OP1);
  not not_114 (not_114_out, OP0);
  not not_115 (not_115_out, OP5);
  not not_116 (not_116_out, OP4);
  not not_117 (not_117_out, OP2);
  not not_118 (not_118_out, OP1);
  not not_119 (not_119_out, OP5);
  not not_120 (not_120_out, OP4);
  not not_121 (not_121_out, OP2);
  not not_122 (not_122_out, OP0);
  not not_123 (not_123_out, OP5);
  not not_124 (not_124_out, OP4);
  not not_125 (not_125_out, OP1);
  not not_126 (not_126_out, OP4);
  not not_127 (not_127_out, OP3);
  not not_128 (not_128_out, OP2);
  not not_129 (not_129_out, OP4);
  not not_130 (not_130_out, OP2);
  not not_131 (not_131_out, OP5);
  not not_132 (not_132_out, OP4);
  not not_133 (not_133_out, OP3);
  not not_134 (not_134_out, OP2);
  not not_135 (not_135_out, OP1);
  not not_136 (not_136_out, OP0);
  not not_137 (not_137_out, F4);
  not not_138 (not_138_out, F3);
  not not_139 (not_139_out, F0);
  not not_140 (not_140_out, OP4);
  not not_141 (not_141_out, OP3);
  not not_142 (not_142_out, OP2);
  not not_143 (not_143_out, OP1);
  not not_144 (not_144_out, OP0);
  not not_145 (not_145_out, OP5);
  not not_146 (not_146_out, OP4);
  not not_147 (not_147_out, OP3);
  not not_148 (not_148_out, OP0);
  not not_149 (not_149_out, OP5);
  not not_150 (not_150_out, OP4);
  not not_151 (not_151_out, OP3);
  not not_152 (not_152_out, OP2);
  not not_153 (not_153_out, OP1);
  not not_154 (not_154_out, OP0);
  not not_155 (not_155_out, F5);
  not not_156 (not_156_out, F4);
  not not_157 (not_157_out, F3);
  not not_158 (not_158_out, F2);
  not not_159 (not_159_out, F1);
  not not_160 (not_160_out, F0);
  not not_161 (not_161_out, OP5);
  not not_162 (not_162_out, OP4);
  not not_163 (not_163_out, OP3);
  not not_164 (not_164_out, OP2);
  not not_165 (not_165_out, OP1);
  not not_166 (not_166_out, OP0);
  not not_167 (not_167_out, F5);
  not not_168 (not_168_out, F4);
  not not_169 (not_169_out, F3);
  not not_170 (not_170_out, F2);
  not not_171 (not_171_out, OP5);
  not not_172 (not_172_out, OP4);
  not not_173 (not_173_out, OP3);
  not not_174 (not_174_out, OP2);
  not not_175 (not_175_out, OP1);
  not not_176 (not_176_out, OP0);
  not not_177 (not_177_out, F5);
  not not_178 (not_178_out, F4);
  not not_179 (not_179_out, F3);
  not not_180 (not_180_out, F2);
  not not_181 (not_181_out, F0);
  not not_182 (not_182_out, OP5);
  not not_183 (not_183_out, OP4);
  not not_184 (not_184_out, OP3);
  not not_185 (not_185_out, OP2);
  not not_186 (not_186_out, OP1);
  not not_187 (not_187_out, OP0);
  not not_188 (not_188_out, F4);
  not not_189 (not_189_out, F3);
  not not_190 (not_190_out, F2);
  not not_191 (not_191_out, F1);
  not not_192 (not_192_out, F0);
  not not_193 (not_193_out, OP5);
  not not_194 (not_194_out, OP4);
  not not_195 (not_195_out, OP3);
  not not_196 (not_196_out, OP2);
  not not_197 (not_197_out, OP1);
  not not_198 (not_198_out, OP0);
  not not_199 (not_199_out, F4);
  not not_200 (not_200_out, F3);
  not not_201 (not_201_out, F2);
  not not_202 (not_202_out, F1);
  not not_203 (not_203_out, OP5);
  not not_204 (not_204_out, OP4);
  not not_205 (not_205_out, OP3);
  not not_206 (not_206_out, OP2);
  not not_207 (not_207_out, OP1);
  not not_208 (not_208_out, OP0);
  not not_209 (not_209_out, F4);
  not not_210 (not_210_out, F3);
  not not_211 (not_211_out, F2);
  not not_212 (not_212_out, F0);
  not not_213 (not_213_out, OP5);
  not not_214 (not_214_out, OP4);
  not not_215 (not_215_out, OP3);
  not not_216 (not_216_out, OP2);
  not not_217 (not_217_out, OP1);
  not not_218 (not_218_out, OP0);
  not not_219 (not_219_out, F4);
  not not_220 (not_220_out, F3);
  not not_221 (not_221_out, F1);
  not not_222 (not_222_out, F0);
  not not_223 (not_223_out, OP5);
  not not_224 (not_224_out, OP4);
  not not_225 (not_225_out, OP3);
  not not_226 (not_226_out, OP2);
  not not_227 (not_227_out, OP1);
  not not_228 (not_228_out, OP0);
  not not_229 (not_229_out, F4);
  not not_230 (not_230_out, F3);
  not not_231 (not_231_out, F1);
  not not_232 (not_232_out, OP5);
  not not_233 (not_233_out, OP4);
  not not_234 (not_234_out, OP3);
  not not_235 (not_235_out, OP2);
  not not_236 (not_236_out, OP1);
  not not_237 (not_237_out, OP0);
  not not_238 (not_238_out, F4);
  not not_239 (not_239_out, F3);
  not not_240 (not_240_out, OP5);
  not not_241 (not_241_out, OP4);
  not not_242 (not_242_out, OP3);
  not not_243 (not_243_out, OP2);
  not not_244 (not_244_out, OP1);
  not not_245 (not_245_out, OP0);
  not not_246 (not_246_out, F4);
  not not_247 (not_247_out, F2);
  not not_248 (not_248_out, F0);
  not not_249 (not_249_out, OP5);
  not not_250 (not_250_out, OP4);
  not not_251 (not_251_out, OP3);
  not not_252 (not_252_out, OP2);
  not not_253 (not_253_out, OP1);
  not not_254 (not_254_out, OP0);
  not not_255 (not_255_out, F4);
  not not_256 (not_256_out, F2);
  not not_257 (not_257_out, OP5);
  not not_258 (not_258_out, OP4);
  not not_259 (not_259_out, OP3);
  not not_260 (not_260_out, OP2);
  not not_261 (not_261_out, OP1);
  not not_262 (not_262_out, OP0);
  not not_263 (not_263_out, F5);
  not not_264 (not_264_out, F4);
  not not_265 (not_265_out, F1);
  not not_266 (not_266_out, F0);
  not not_267 (not_267_out, OP5);
  not not_268 (not_268_out, OP4);
  not not_269 (not_269_out, OP3);
  not not_270 (not_270_out, OP1);
  not not_271 (not_271_out, OP0);
  not not_272 (not_272_out, OP5);
  not not_273 (not_273_out, OP4);
  not not_274 (not_274_out, OP3);
  not not_275 (not_275_out, OP1);
  not not_276 (not_276_out, OP4);
  not not_277 (not_277_out, OP2);
  not not_278 (not_278_out, OP5);
  not not_279 (not_279_out, OP4);
  not not_280 (not_280_out, OP3);
  not not_281 (not_281_out, OP2);
  not not_282 (not_282_out, OP1);
  not not_283 (not_283_out, OP0);
  not not_284 (not_284_out, F4);
  not not_285 (not_285_out, F3);
  not not_286 (not_286_out, F0);
  and and_1 (and_1_out, not_1_out, not_2_out, not_3_out, not_4_out, not_5_out, not_6_out, F5, not_7_out, not_8_out, not_9_out, not_10_out, not_11_out);
  and and_2 (and_2_out, not_12_out, not_13_out, not_14_out, not_15_out, not_16_out, not_17_out, F5, not_18_out, not_19_out, not_20_out, not_21_out, F0);
  and and_3 (and_3_out, not_22_out, not_23_out, not_24_out, not_25_out, not_26_out, not_27_out, F5, not_28_out, not_29_out, not_30_out, F1, not_31_out);
  and and_4 (and_4_out, not_32_out, not_33_out, not_34_out, not_35_out, not_36_out, not_37_out, F5, not_38_out, not_39_out, F2, not_40_out, not_41_out);
  and and_5 (and_5_out, not_42_out, not_43_out, not_44_out, not_45_out, not_46_out, not_47_out, F5, not_48_out, not_49_out, F2, not_50_out, F0);
  and and_6 (and_6_out, not_51_out, not_52_out, not_53_out, not_54_out, not_55_out, not_56_out, F5, not_57_out, not_58_out, F2, F1, F0);
  and and_7 (and_7_out, not_59_out, not_60_out, not_61_out, not_62_out, not_63_out, not_64_out, F5, not_65_out, F3, not_66_out, F1, not_67_out);
  and and_8 (and_8_out, not_68_out, not_69_out, not_70_out, not_71_out, not_72_out, not_73_out, F5, not_74_out, F3, not_75_out, F1, F0);
  and and_9 (and_9_out, not_76_out, not_77_out, not_78_out, not_79_out, not_80_out, not_81_out, not_82_out, not_83_out, F3, not_84_out, not_85_out, not_86_out);
  and and_10 (and_10_out, not_87_out, not_88_out, not_89_out, not_90_out, not_91_out, not_92_out, not_93_out, not_94_out, F3, F2, not_95_out, not_96_out);
  and and_11 (and_11_out, not_97_out, not_98_out, not_99_out, OP2, not_100_out, not_101_out);
  and and_12 (and_12_out, not_102_out, not_103_out, not_104_out, OP2, not_105_out, OP0);
  and and_13 (and_13_out, not_106_out, not_107_out, OP3, not_108_out, not_109_out, not_110_out);
  and and_14 (and_14_out, not_111_out, not_112_out, OP3, OP2, not_113_out, not_114_out);
  and and_15 (and_15_out, not_115_out, not_116_out, OP3, not_117_out, not_118_out, OP0);
  and and_16 (and_16_out, not_119_out, not_120_out, OP3, not_121_out, OP1, not_122_out);
  and and_17 (and_17_out, not_123_out, not_124_out, OP3, OP2, not_125_out, OP0);
  and and_18 (and_18_out, OP5, not_126_out, not_127_out, not_128_out, OP1, OP0);
  and and_19 (and_19_out, OP5, not_129_out, OP3, not_130_out, OP1, OP0);
  and and_20 (and_20_out, not_131_out, not_132_out, not_133_out, not_134_out, not_135_out, not_136_out, F5, not_137_out, not_138_out, F2, F1, not_139_out);
  and and_21 (and_21_out, OP5, not_140_out, not_141_out, not_142_out, not_143_out, not_144_out);
  and and_22 (and_22_out, not_145_out, not_146_out, not_147_out, OP2, OP1, not_148_out);
  and and_23 (and_23_out, not_149_out, not_150_out, not_151_out, not_152_out, not_153_out, not_154_out, not_155_out, not_156_out, not_157_out, not_158_out, not_159_out, not_160_out);
  and and_24 (and_24_out, not_161_out, not_162_out, not_163_out, not_164_out, not_165_out, not_166_out, not_167_out, not_168_out, not_169_out, not_170_out, F1, F0);
  and and_25 (and_25_out, not_171_out, not_172_out, not_173_out, not_174_out, not_175_out, not_176_out, not_177_out, not_178_out, not_179_out, not_180_out, F1, not_181_out);
  and and_26 (and_26_out, not_182_out, not_183_out, not_184_out, not_185_out, not_186_out, not_187_out, F5, not_188_out, not_189_out, not_190_out, not_191_out, not_192_out);
  and and_27 (and_27_out, not_193_out, not_194_out, not_195_out, not_196_out, not_197_out, not_198_out, F5, not_199_out, not_200_out, not_201_out, not_202_out, F0);
  and and_28 (and_28_out, not_203_out, not_204_out, not_205_out, not_206_out, not_207_out, not_208_out, F5, not_209_out, not_210_out, not_211_out, F1, not_212_out);
  and and_29 (and_29_out, not_213_out, not_214_out, not_215_out, not_216_out, not_217_out, not_218_out, F5, not_219_out, not_220_out, F2, not_221_out, not_222_out);
  and and_30 (and_30_out, not_223_out, not_224_out, not_225_out, not_226_out, not_227_out, not_228_out, F5, not_229_out, not_230_out, F2, not_231_out, F0);
  and and_31 (and_31_out, not_232_out, not_233_out, not_234_out, not_235_out, not_236_out, not_237_out, F5, not_238_out, not_239_out, F2, F1, F0);
  and and_32 (and_32_out, not_240_out, not_241_out, not_242_out, not_243_out, not_244_out, not_245_out, F5, not_246_out, F3, not_247_out, F1, not_248_out);
  and and_33 (and_33_out, not_249_out, not_250_out, not_251_out, not_252_out, not_253_out, not_254_out, F5, not_255_out, F3, not_256_out, F1, F0);
  and and_34 (and_34_out, not_257_out, not_258_out, not_259_out, not_260_out, not_261_out, not_262_out, not_263_out, not_264_out, F3, F2, not_265_out, not_266_out);
  and and_35 (and_35_out, not_267_out, not_268_out, not_269_out, OP2, not_270_out, not_271_out);
  and and_36 (and_36_out, not_272_out, not_273_out, not_274_out, OP2, not_275_out, OP0);
  and and_37 (and_37_out, OP5, not_276_out, OP3, not_277_out, OP1, OP0);
  and and_38 (and_38_out, not_278_out, not_279_out, not_280_out, not_281_out, not_282_out, not_283_out, F5, not_284_out, not_285_out, F2, F1, not_286_out);
  or or_1 (R1_used, and_1_out, and_2_out, and_3_out, and_4_out, and_5_out, and_6_out, and_7_out, and_8_out, and_9_out, and_10_out, and_11_out, and_12_out, and_13_out, and_14_out, and_15_out, and_16_out, and_17_out, and_18_out, and_19_out, and_20_out, and_21_out, and_22_out);
  or or_2 (R2_used, and_23_out, and_24_out, and_25_out, and_26_out, and_27_out, and_28_out, and_29_out, and_30_out, and_31_out, and_32_out, and_33_out, and_34_out, and_35_out, and_36_out, and_37_out, and_38_out);
endmodule

module \数据相关检测_24_3_2  (
  input  EX_RegWrite,
  input  R1_Used,
  input  [4:0] R1_num,
  input  [4:0] EX_WriteReg_num,
  input  MEM_RegWrite,
  input  R2_Used,
  input  [4:0] R2_num,
  input  [4:0] MEM_WriteReg_num,
  output \MEM相关 ,
  output [3:0] R1_MEM,
  output \EX相关 
);

  wire comparator_1_eq, comparator_2_eq, comparator_3_eq, comparator_4_eq, multiplexer_1_out,
       multiplexer_2_out, multiplexer_3_out, multiplexer_4_out, R1___0, R2___0;

  Comparator #(.width(5), .mode("twosComplement")) comparator_1 (
    .a(R1_num), .b(EX_WriteReg_num), .eq(comparator_1_eq));  // open: gt, lt
  Comparator #(.width(5), .mode("twosComplement")) comparator_2 (
    .a(R1_num), .b(MEM_WriteReg_num), .eq(comparator_2_eq));  // open: gt, lt
  Comparator #(.width(5), .mode("twosComplement")) comparator_3 (
    .a(R2_num), .b(MEM_WriteReg_num), .eq(comparator_3_eq));  // open: gt, lt
  Comparator #(.width(5), .mode("twosComplement")) comparator_4 (
    .a(R2_num), .b(EX_WriteReg_num), .eq(comparator_4_eq));  // open: gt, lt
  Comparator #(.width(5), .mode("twosComplement")) comparator_5 (
    .a(R1_num), .b({5{1'b0}}), .eq(R1___0));  // open: gt, lt
  Comparator #(.width(5), .mode("twosComplement")) comparator_6 (
    .a(R2_num), .b({5{1'b0}}), .eq(R2___0));  // open: gt, lt
  Multiplexer #(.select(1), .width(1), .disabled("Z"), .enable("false")) multiplexer_1 (
    .in0(1'b0), .in1(comparator_1_eq), .out(multiplexer_1_out), .sel(R1_Used));
  Multiplexer #(.select(1), .width(1), .disabled("Z"), .enable("false")) multiplexer_2 (
    .in0(1'b0), .in1(comparator_2_eq), .out(multiplexer_2_out), .sel(R1_Used));
  Multiplexer #(.select(1), .width(1), .disabled("Z"), .enable("false")) multiplexer_3 (
    .in0(1'b0), .in1(comparator_3_eq), .out(multiplexer_3_out), .sel(R2_Used));
  Multiplexer #(.select(1), .width(1), .disabled("Z"), .enable("false")) multiplexer_4 (
    .in0(1'b0), .in1(comparator_4_eq), .out(multiplexer_4_out), .sel(R2_Used));
  Multiplexer #(.select(2), .width(1), .disabled("Z"), .enable("false")) multiplexer_5 (
    .in0(1'b0), .in1(multiplexer_1_out), .in2(1'b0), .in3(1'b0), .out(R1_MEM[0]), .sel({R1___0, EX_RegWrite}));
  Multiplexer #(.select(2), .width(1), .disabled("Z"), .enable("false")) multiplexer_6 (
    .in0(1'b0), .in1(multiplexer_2_out), .in2(1'b0), .in3(1'b0), .out(R1_MEM[1]), .sel({R1___0, MEM_RegWrite}));
  Multiplexer #(.select(2), .width(1), .disabled("Z"), .enable("false")) multiplexer_7 (
    .in0(1'b0), .in1(multiplexer_3_out), .in2(1'b0), .in3(1'b0), .out(R1_MEM[3]), .sel({R2___0, MEM_RegWrite}));
  Multiplexer #(.select(2), .width(1), .disabled("Z"), .enable("false")) multiplexer_8 (
    .in0(1'b0), .in1(multiplexer_4_out), .in2(1'b0), .in3(1'b0), .out(R1_MEM[2]), .sel({R2___0, EX_RegWrite}));
  or or_1 (\MEM相关 , R1_MEM[1], R1_MEM[3]);
  or or_2 (\EX相关 , R1_MEM[0], R1_MEM[2]);

  // Notes on the sheet:
  //   R1/EX
  //   R2/EX
  //   R2/MEM
endmodule
module \单周期MIPS_单级中断  (
  input  IR1,
  input  IR2,
  input  IR3,
  output RegWrite,
  output MemWrite,
  output [31:0] PC,
  output [31:0] IR,
  output [31:0] RDin,
  output [31:0] MDin,
  output [31:0] LedData
);

  wire and_5_out, and_6_out, B___De, BLEZ, BLEZ_DE, C_IR1, C_IR2, C_IR3, CLK, comparator_1_gt,
       comparator_2_eq, comparator_3_eq, comparator_4_eq, comparator_5_eq, comparator_6_eq, d_ff_1_qn,
       decoder_1_out1, decoder_1_out2, decoder_1_out3, ERET, Go, IR1_t, IR2_t, IR3_t, IRA, IRB, IRC, JMP, JR,
       LB, LUI, mips_alu_1_equal, multiplexer_4_out, multiplexer_16_out, not_1_out, not_2_out, or_2_out,
       or_3_out, or_8_out, priority_encoder_1_gs, register_1_q, SignedExt, Syscall, W1, W2, W3, \中断发生信号 ,
       \中断按键参考电路_1_与中断屏蔽位与 , \中断按键参考电路_2_与中断屏蔽位与 , \中断按键参考电路_3_与中断屏蔽位与 , \拓展单周期硬布线控制器_31_1_alu_src ,
       \拓展单周期硬布线控制器_31_1_beq , \拓展单周期硬布线控制器_31_1_bne , \拓展单周期硬布线控制器_31_1_memtoreg , \运行 ;
  wire [0:0] or_1_out;
  wire [1:0] priority_encoder_1_out, register_2_q, \拓展单周期硬布线控制器_31_1_regdst ;
  wire [3:0] \拓展单周期硬布线控制器_31_1_alu_op ;
  wire [4:0] multiplexer_5_out, multiplexer_6_out, multiplexer_8_out;
  wire [7:0] multiplexer_14_out, multiplexer_15_out, multiplexer_15_out_2, multiplexer_15_out_3,
       multiplexer_15_out_4;
  wire [15:0] \总周期数 ;
  wire [27:0] Next_PC;
  wire [31:0] B___PC, bit_extender_1_out, bit_extender_2_out, bit_extender_3_out, EPC__PC, JR_PC,
       mips_alu_1_result, multiplexer_2_out, multiplexer_3_out, multiplexer_9_out, multiplexer_10_out,
       multiplexer_12_out, multiplexer_13_out, PC__EPC, ram_1_data, shifter_1_out, \服务地址 ;
  wire [31:28] J_JAL_PC;

  Clock #(.highDuration(1), .lowDuration(1)) clock_1 (.out(CLK));
  Button \u_继续运行  (.out(Go));
  LED #(.active("true")) led_1 (.in(W1));
  LED #(.active("true")) led_2 (.in(W2));
  LED #(.active("true")) led_3 (.in(W3));
  or or_1 (or_1_out[0], JR, BLEZ_DE, B___De);
  Multiplexer #(.select(2), .width(32), .disabled("Z"), .enable("false")) multiplexer_1 (
    .in0({J_JAL_PC, Next_PC}), .in1(B___PC), .in2({J_JAL_PC, IR[25:0], 2'b00}), .in3(JR_PC), .out(PC__EPC),
    .sel({JMP, or_1_out[0]}));
  Hex_Digit_Display hex_digit_display_1 (.value(LedData[31:28]));  // open: dp
  Multiplexer #(.select(1), .width(32), .disabled("Z"), .enable("false")) multiplexer_2 (
    .in0(PC__EPC), .in1(\服务地址 ), .out(multiplexer_2_out), .sel(\中断发生信号 ));
  \中断按键参考电路  \u_中断按键参考电路_1  (.\与中断屏蔽位与 (\中断按键参考电路_1_与中断屏蔽位与 ), .\同步清零信号 (C_IR1), .\中断输入 (IR1_t), .out_4(W1));
  \中断按键参考电路  \u_中断按键参考电路_2  (.\与中断屏蔽位与 (\中断按键参考电路_2_与中断屏蔽位与 ), .\同步清零信号 (C_IR2), .\中断输入 (IR2_t), .out_4(W2));
  \中断按键参考电路  \u_中断按键参考电路_3  (.\与中断屏蔽位与 (\中断按键参考电路_3_与中断屏蔽位与 ), .\同步清零信号 (C_IR3), .\中断输入 (IR3_t), .out_4(W3));
  Hex_Digit_Display hex_digit_display_2 (.value(LedData[23:20]));  // open: dp
  Hex_Digit_Display hex_digit_display_3 (.value(LedData[27:24]));  // open: dp
  Multiplexer #(.select(1), .width(32), .disabled("Z"), .enable("false")) multiplexer_3 (
    .in0(multiplexer_2_out), .in1(EPC__PC), .out(multiplexer_3_out), .sel(ERET));
  Register #(.width(32), .trigger("rising"), .Select("low")) EPC (
    .D(PC__EPC), .en(\中断发生信号 ), .Q(EPC__PC), .clk(CLK));  // open: clr
  Multiplexer #(.select(1), .width(1), .disabled("Z"), .enable("false")) multiplexer_4 (
    .in0(1'b0), .in1(1'b1), .out(multiplexer_4_out), .sel(or_2_out));
  or or_2 (or_2_out, d_ff_1_qn, ERET);
  D_Flip_Flop #(.trigger("rising"), .Pre_Clr_Positions("LEGACY"), .NegatePresetClear("false"), .enable("true"), .NewFFLayout("false")) d_ff_1 (
    .clk(CLK), .D(1'b1), .Qn(d_ff_1_qn));  // open: Q, preset, en, reset
  Hex_Digit_Display hex_digit_display_4 (.value(LedData[15:12]));  // open: dp
  Hex_Digit_Display hex_digit_display_5 (.value(LedData[19:16]));  // open: dp
  Register #(.width(32), .trigger("rising"), .Select("low")) u_PC (
    .D(multiplexer_3_out), .en(\运行 ), .Q(PC), .clk(CLK));  // open: clr
  Priority_Encoder #(.select(2), .disabled("Z")) priority_encoder_1 (
    .in0(1'b0), .in1(\中断按键参考电路_1_与中断屏蔽位与 ), .in2(\中断按键参考电路_2_与中断屏蔽位与 ), .in3(\中断按键参考电路_3_与中断屏蔽位与 ),
    .out(priority_encoder_1_out), .gs(priority_encoder_1_gs));  // open: en_out, en_in
  Register #(.width(1), .trigger("rising"), .Select("low")) register_1 (
    .D(multiplexer_4_out), .en(or_3_out), .Q(register_1_q), .clk(CLK));  // open: clr
  or or_3 (or_3_out, d_ff_1_qn, ERET, \中断发生信号 );
  Hex_Digit_Display hex_digit_display_6 (.value(LedData[7:4]));  // open: dp
  Hex_Digit_Display hex_digit_display_7 (.value(LedData[11:8]));  // open: dp
  Hex_Digit_Display hex_digit_display_8 (.value(LedData[3:0]));  // open: dp
  // Probe on \总周期数 
  Decoder #(.select(2), .tristate("false"), .disabled("Z"), .enable("false")) decoder_1 (
    .out1(decoder_1_out1), .out2(decoder_1_out2), .out3(decoder_1_out3), .sel(register_2_q));  // open: out0
  Register #(.width(2), .trigger("rising"), .Select("low")) register_2 (
    .D(priority_encoder_1_out), .en(\中断发生信号 ), .Q(register_2_q), .clk(CLK));  // open: clr
  and and_1 (\中断发生信号 , priority_encoder_1_gs, register_1_q);
  Counter #(.width(16), .max('hffff), .ongoal("wrap"), .trigger("rising"), .behavior("old")) counter_1 (
    .count(\运行 ), .Q(\总周期数 ), .clk(CLK));  // open: load, D, carry, clr, preset
  ROM #(.addrWidth(10), .dataWidth(32), .Select("high")) rom_1 (.addr(PC[11:2]), .data(IR));
  Adder #(.width(32)) adder_1 (.a(PC), .b(32'h4), .out({J_JAL_PC, Next_PC}));  // open: cin, cout
  or or_4 (IR1_t, IR1, IRA);
  and and_2 (C_IR1, decoder_1_out1, ERET);
  and and_3 (C_IR2, decoder_1_out2, ERET);
  and and_4 (C_IR3, decoder_1_out3, ERET);
  or or_5 (IR2_t, IR2, IRB);
  \拓展单周期硬布线控制器_31  \u_拓展单周期硬布线控制器_31_1  (
    .OP(IR[31:26]), .Func(IR[5:0]), .ALU_OP(\拓展单周期硬布线控制器_31_1_alu_op ),
    .MemToReg(\拓展单周期硬布线控制器_31_1_memtoreg ), .MemWrite(MemWrite), .ALU_SRC(\拓展单周期硬布线控制器_31_1_alu_src ),
    .RegWrite(RegWrite), .SysCALL(Syscall), .SignedExt(SignedExt), .RegDst(\拓展单周期硬布线控制器_31_1_regdst [0]),
    .Beq(\拓展单周期硬布线控制器_31_1_beq ), .Bne(\拓展单周期硬布线控制器_31_1_bne ), .JR(JR), .JMP(JMP),
    .JAL(\拓展单周期硬布线控制器_31_1_regdst [1]), .LUI(LUI), .LB(LB), .BLEZ(BLEZ), .ERET(ERET), .M(IR[25:21]));  // open: R1_Used, R2_Used, MFC0, MTC0
  Multiplexer #(.select(1), .width(5), .disabled("Z"), .enable("false")) multiplexer_5 (
    .in0(IR[25:21]), .in1(5'b00010), .out(multiplexer_5_out), .sel(Syscall));
  Multiplexer #(.select(1), .width(5), .disabled("Z"), .enable("false")) multiplexer_6 (
    .in0(IR[20:16]), .in1(5'b00100), .out(multiplexer_6_out), .sel(Syscall));
  assign bit_extender_1_out = {{16{1'b0}}, IR[15:0]};  // Bit_Extender bit_extender_1
  assign bit_extender_2_out = {{16{IR[15]}}, IR[15:0]};  // Bit_Extender bit_extender_2
  Multiplexer #(.select(2), .width(32), .disabled("Z"), .enable("false")) multiplexer_7 (
    .in1(32'h30ac), .in2(32'h3150), .in3(32'h31f4), .out(\服务地址 ), .sel(priority_encoder_1_out));  // open: in0
  or or_6 (IR3_t, IR3, IRC);
  Multiplexer #(.select(2), .width(5), .disabled("Z"), .enable("false")) multiplexer_8 (
    .in0(IR[20:16]), .in1(IR[15:11]), .in2({5{1'b1}}), .out(multiplexer_8_out),
    .sel(\拓展单周期硬布线控制器_31_1_regdst ));  // open: in3
  Multiplexer #(.select(1), .width(32), .disabled("Z"), .enable("false")) multiplexer_9 (
    .in0(bit_extender_1_out), .in1(bit_extender_2_out), .out(multiplexer_9_out), .sel(SignedExt));
  Multiplexer #(.select(1), .width(32), .disabled("Z"), .enable("false")) multiplexer_10 (
    .in0(multiplexer_13_out), .in1({IR[15:0], {16{1'b0}}}), .out(multiplexer_10_out), .sel(LUI));
  Multiplexer #(.select(1), .width(32), .disabled("Z"), .enable("false")) multiplexer_11 (
    .in0(multiplexer_10_out), .in1({J_JAL_PC, Next_PC}), .out(RDin), .sel(\拓展单周期硬布线控制器_31_1_regdst [1]));
  MIPS_Regifile mips_regifile_1 (
    .Din(RDin), .Clk(CLK), .R1(JR_PC), .R2(MDin), .WE(RegWrite), .W_num(multiplexer_8_out),
    .R1_num(multiplexer_5_out), .R2_num(multiplexer_6_out));
  Multiplexer #(.select(1), .width(32), .disabled("Z"), .enable("false")) multiplexer_12 (
    .in0(MDin), .in1(multiplexer_9_out), .out(multiplexer_12_out), .sel(\拓展单周期硬布线控制器_31_1_alu_src ));
  Shifter #(.width(32), .shift("ll")) shifter_1 (.in(multiplexer_9_out), .\dist (5'b00010), .out(shifter_1_out));
  Comparator #(.width(32), .mode("twosComplement")) comparator_1 (
    .a(JR_PC), .b({32{1'b0}}), .gt(comparator_1_gt));  // open: eq, lt
  and and_5 (and_5_out, mips_alu_1_equal, \拓展单周期硬布线控制器_31_1_beq );
  not not_1 (not_1_out, mips_alu_1_equal);
  and and_6 (and_6_out, not_1_out, \拓展单周期硬布线控制器_31_1_bne );
  not not_2 (not_2_out, comparator_1_gt);
  MIPS_ALU mips_alu_1 (
    .X(JR_PC), .Y(multiplexer_12_out), .AluOP(\拓展单周期硬布线控制器_31_1_alu_op ), .Equal(mips_alu_1_equal),
    .Result(mips_alu_1_result), .shamt(IR[10:6]));  // open: Result_2
  Adder #(.width(32)) adder_2 (.a(shifter_1_out), .b({J_JAL_PC, Next_PC}), .out(B___PC));  // open: cin, cout
  or or_7 (B___De, and_5_out, and_6_out);
  and and_7 (BLEZ_DE, BLEZ, not_2_out);
  Multiplexer #(.select(1), .width(32), .disabled("Z"), .enable("false")) multiplexer_13 (
    .in0({multiplexer_15_out_4, multiplexer_15_out_3, multiplexer_15_out_2, multiplexer_15_out}),
    .in1(bit_extender_3_out), .out(multiplexer_13_out), .sel(LB));
  Comparator #(.width(32), .mode("twosComplement")) comparator_2 (
    .a(JR_PC), .b(32'h22), .eq(comparator_2_eq));  // open: gt, lt
  assign bit_extender_3_out = {{24{multiplexer_14_out[7]}}, multiplexer_14_out};  // Bit_Extender bit_extender_3
  RAM #(.addrWidth(10), .dataWidth(32), .bus("separate"), .Select("high")) ram_1 (
    .addr(mips_alu_1_result[11:2]), .din(MDin), .data(ram_1_data), .str(MemWrite), .clk(CLK));  // open: sel, ld, clr
  Multiplexer #(.select(2), .width(8), .disabled("Z"), .enable("false")) multiplexer_14 (
    .in0(multiplexer_15_out), .in1(multiplexer_15_out_2), .in2(multiplexer_15_out_3),
    .in3(multiplexer_15_out_4), .out(multiplexer_14_out), .sel(mips_alu_1_result[1:0]));
  Multiplexer #(.select(1), .width(32), .disabled("Z"), .enable("false")) multiplexer_15 (
    .in0(mips_alu_1_result), .in1(ram_1_data),
    .out({multiplexer_15_out_4, multiplexer_15_out_3, multiplexer_15_out_2, multiplexer_15_out}),
    .sel(\拓展单周期硬布线控制器_31_1_memtoreg ));
  Comparator #(.width(16), .mode("twosComplement")) comparator_3 (
    .a(16'h258), .b(\总周期数 ), .eq(comparator_3_eq));  // open: gt, lt
  Comparator #(.width(16), .mode("twosComplement")) comparator_4 (
    .a(\总周期数 ), .b(16'h1), .eq(comparator_4_eq));  // open: gt, lt
  Comparator #(.width(16), .mode("twosComplement")) comparator_5 (
    .a(\总周期数 ), .b(16'h4), .eq(comparator_5_eq));  // open: gt, lt
  Comparator #(.width(16), .mode("twosComplement")) comparator_6 (
    .a(\总周期数 ), .b(16'h7), .eq(comparator_6_eq));  // open: gt, lt
  or or_8 (or_8_out, comparator_3_eq, comparator_4_eq);
  assign IRA = or_8_out ? ~CLK : 1'bz;  // Controlled_Inverter controlled_inverter_1
  assign IRB = comparator_5_eq ? ~CLK : 1'bz;  // Controlled_Inverter controlled_inverter_2
  assign IRC = comparator_6_eq ? ~CLK : 1'bz;  // Controlled_Inverter controlled_inverter_3
  Multiplexer #(.select(1), .width(1), .disabled("Z"), .enable("false")) multiplexer_16 (
    .in0(1'b0), .in1(comparator_2_eq), .out(multiplexer_16_out), .sel(Syscall));
  or or_9 (\运行 , Go, multiplexer_16_out, ~Syscall);  // OR_Gate
  Register #(.width(32), .trigger("rising"), .Select("low")) register_3 (
    .D(MDin), .en(multiplexer_16_out), .Q(LedData), .clk(CLK));  // open: clr

  // Other names for the same wires on the sheet: FUNC[5:0] = IR[5:0]; J_JAL_PC[27:2] = IR[25:0]; a0[31:0] = MDin;
  //   OP[5:0] = IR[31:26]; M[4:0] = IR[25:21]; Next_PC[31:28] = J_JAL_PC

  // Notes on the sheet:
  //   中断源
  //   中断等待指示
  //   总复位信号应将除ROM以外所有存储组件全部清零
  //   数码管输出
  //   发生中断时，中断源的序号便存储到寄存器中
  //   数码管输出应该用寄存器锁存，否则显示数据只能一闪而过
  //   指令存储器
  //   指令字
  //   contents of rom_1 (hex, n*v repeats v):
  //   201d07d0 20100001 109fc0 139fc3 8021 2012000c 24160008 26100001 3210000f 20080008 20090001 139900
  //   2709825 132020 20020022 c 1094022 1500fff9 22100001 2018000f 2188024 108700 20080008 20090001 139902
  //   2709825 132021 20020022 c 1094022 1500fff9 108702 2c9b022 12c00001 8000c07 4020 1084027 84400
  //   3508ffff 82021 20020022 c 8000c01 afa20000 23bd0004 afa40000 23bd0004 afb00000 23bd0004 afb30000
  //   23bd0004 afb40000 23bd0004 afb50000 23bd0004 afb60000 23bd0004 20160001 20140003 20150001 168020
  //   108100 2149825 132020 20020022 c 1600fffa 295a022 1680fff7 23bdfffc 8fb60000 23bdfffc 8fb50000
  //   23bdfffc 8fb40000 23bdfffc 8fb30000 23bdfffc 8fb00000 23bdfffc 8fa40000 23bdfffc 8fa20000 42000018
  //   afa20000 23bd0004 afa40000 23bd0004 afb00000 23bd0004 afb30000 23bd0004 afb40000 23bd0004 afb50000
  //   23bd0004 afb60000 23bd0004 20160002 20140003 20150001 168020 108100 2149825 132020 20020022 c
  //   1600fffa 295a022 1680fff7 23bdfffc 8fb60000 23bdfffc 8fb50000 23bdfffc 8fb40000 23bdfffc 8fb30000
  //   23bdfffc 8fb00000 23bdfffc 8fa40000 23bdfffc 8fa20000 42000018 afa20000 23bd0004 afa40000 23bd0004
  //   afb00000 23bd0004 afb30000 23bd0004 afb40000 23bd0004 afb50000 23bd0004 afb60000 23bd0004 20160003
  //   20140003 20150001 168020 108100 2149825 132020 20020022 c 1600fffa 295a022 1680fff7 23bdfffc
  //   8fb60000 23bdfffc 8fb50000 23bdfffc 8fb40000 23bdfffc 8fb30000 23bdfffc 8fb00000 23bdfffc 8fa40000
  //   23bdfffc 8fa20000 42000018
  //   OP
  //   Func
  //   rs
  //   rt
  //   rd
  //   OP
  //   Func
  //   JAL
  //   RegDst
  //   RegWrite
  //   为方便自动评测，需要输出PC，IR，寄存器堆写如数据RDin
  //   Beq
  //   Bne
  //   MemToReg
  //   MemWrite
  //   AluOP
  //   AluSrcB
  //   RAM写使能MemWrite、RAM写入数据MDin等信号
  //   先断开三个按钮和IRA~IRC的连接
  //   再加入这个电路
endmodule

module \单周期MIPS_多级中断  (
  input  IR1,
  input  IR2,
  input  IR3,
  output RegWrite,
  output MemWrite,
  output [31:0] PC,
  output [31:0] IR,
  output [31:0] RDin,
  output [31:0] MDin,
  output [31:0] LedData
);

  wire _1, _2, _3, and_2_out, and_3_out, and_7_out, and_8_out, and_9_out, and_10_out, and_11_out, and_13_out,
       and_14_out, and_15_out, B___De, BLEZ, BLEZ_DE, C_IR1, C_IR2, C_IR3, CLK, comparator_2_gt,
       comparator_3_gt, comparator_4_gt, comparator_5_gt, comparator_6_eq, comparator_7_eq, comparator_8_eq,
       comparator_9_eq, comparator_10_eq, comparator_11_eq, d_ff_1_qn, d_ff_2_q, d_ff_3_q, d_ff_4_q,
       decoder_1_out1, decoder_1_out2, decoder_1_out3, decoder_2_out1, decoder_2_out2, decoder_2_out3, ERET,
       Go, \IE信号 , IR1_t, IR2_t, IR3_t, IRA, IRB, IRC, JMP, JR, judge, LB, LUI, MFC0, mips_alu_1_equal, MTC0,
       multiplexer_4_out, multiplexer_6_out, multiplexer_20_out, multiplexer_21_out, multiplexer_22_out,
       multiplexer_24_out, multiplexer_25_out, multiplexer_26_out, multiplexer_29_out, multiplexer_30_out,
       not_1_out, not_2_out, not_3_out, not_4_out, not_5_out, or_2_out, or_3_out, or_4_out, or_5_out,
       or_6_out, or_8_out, or_10_out, or_12_out, or_14_out, or_15_out, or_16_out, or_17_out, or_18_out,
       SignedExt, Syscall, W1, W2, W3, \中断嵌套_中断 , \优先级高的中断出现 , \拓展单周期硬布线控制器_31_1_alu_src ,
       \拓展单周期硬布线控制器_31_1_beq , \拓展单周期硬布线控制器_31_1_bne , \拓展单周期硬布线控制器_31_1_memtoreg , \清零_2_out , \清零_3_out ,
       \清零_out , \运行 ;
  wire [0:0] or_1_out;
  wire [1:0] level, multiplexer_5_out, multiplexer_7_out, priority_encoder_2_out, register_2_q,
       \拓展单周期硬布线控制器_31_1_regdst ;
  wire [3:0] \拓展单周期硬布线控制器_31_1_alu_op ;
  wire [4:0] multiplexer_10_out, multiplexer_11_out, multiplexer_12_out;
  wire [7:0] multiplexer_27_out, multiplexer_28_out, multiplexer_28_out_2, multiplexer_28_out_3,
       multiplexer_28_out_4;
  wire [15:0] \总周期数 ;
  wire [27:0] Next_PC;
  wire [31:0] B___PC, bit_extender_1_out, bit_extender_2_out, bit_extender_3_out, EPC_2_q, EPC_3_q, EPC__PC,
       EPC_q, JR_PC, mips_alu_1_result, multiplexer_2_out, multiplexer_3_out, multiplexer_8_out,
       multiplexer_9_out, multiplexer_13_out, multiplexer_14_out, multiplexer_15_out, multiplexer_18_out,
       multiplexer_23_out, PC__EPC, ram_1_data, shifter_1_out, \服务地址 ;
  wire [31:28] J_JAL_PC;

  Clock #(.highDuration(1), .lowDuration(1)) clock_1 (.out(CLK));
  Button \u_继续运行  (.out(Go));
  LED #(.active("true")) led_1 (.in(W1));
  LED #(.active("true")) led_2 (.in(W2));
  LED #(.active("true")) led_3 (.in(W3));
  or or_1 (or_1_out[0], JR, BLEZ_DE, B___De);
  Multiplexer #(.select(2), .width(32), .disabled("Z"), .enable("false")) multiplexer_1 (
    .in0({J_JAL_PC, Next_PC}), .in1(B___PC), .in2({J_JAL_PC, IR[25:0], 2'b00}), .in3(JR_PC), .out(PC__EPC),
    .sel({JMP, or_1_out[0]}));
  Hex_Digit_Display hex_digit_display_1 (.value(LedData[31:28]));  // open: dp
  Multiplexer #(.select(1), .width(32), .disabled("Z"), .enable("false")) multiplexer_2 (
    .in0(PC__EPC), .in1(\服务地址 ), .out(multiplexer_2_out), .sel(\中断嵌套_中断 ));
  and and_1 (\中断嵌套_中断 , \优先级高的中断出现 , \IE信号 );
  and and_2 (and_2_out, judge, \IE信号 );
  \中断按键参考电路  \u_中断按键参考电路_1  (.\与中断屏蔽位与 (_1), .\同步清零信号 (C_IR1), .\中断输入 (IR1_t), .out_4(W1));
  \中断按键参考电路  \u_中断按键参考电路_2  (.\与中断屏蔽位与 (_2), .\同步清零信号 (C_IR2), .\中断输入 (IR2_t), .out_4(W2));
  \中断按键参考电路  \u_中断按键参考电路_3  (.\与中断屏蔽位与 (_3), .\同步清零信号 (C_IR3), .\中断输入 (IR3_t), .out_4(W3));
  Hex_Digit_Display hex_digit_display_2 (.value(LedData[23:20]));  // open: dp
  Hex_Digit_Display hex_digit_display_3 (.value(LedData[27:24]));  // open: dp
  Multiplexer #(.select(1), .width(32), .disabled("Z"), .enable("false")) multiplexer_3 (
    .in0(multiplexer_2_out), .in1(EPC__PC), .out(multiplexer_3_out), .sel(ERET));
  Multiplexer #(.select(1), .width(1), .disabled("Z"), .enable("false")) multiplexer_4 (
    .in0(1'b0), .in1(1'b1), .out(multiplexer_4_out), .sel(or_2_out));
  or or_2 (or_2_out, d_ff_1_qn, MFC0, ERET);
  D_Flip_Flop #(.trigger("rising"), .Pre_Clr_Positions("LEGACY"), .NegatePresetClear("false"), .enable("true"), .NewFFLayout("false")) d_ff_1 (
    .clk(CLK), .D(1'b1), .Qn(d_ff_1_qn));  // open: Q, preset, en, reset
  Hex_Digit_Display hex_digit_display_4 (.value(LedData[15:12]));  // open: dp
  Hex_Digit_Display hex_digit_display_5 (.value(LedData[19:16]));  // open: dp
  // Mips_Probe mips_probe_1: pin names not known; wires that end beside it: IR
  Register #(.width(32), .trigger("rising"), .Select("low")) u_PC (
    .D(multiplexer_3_out), .en(\运行 ), .Q(PC), .clk(CLK));  // open: clr
  Multiplexer #(.select(1), .width(2), .disabled("Z"), .enable("false")) multiplexer_5 (
    .in0(level), .in1(2'b00), .out(multiplexer_5_out), .sel(ERET));
  or or_3 (or_3_out, ERET, and_2_out);
  or or_4 (or_4_out, _1, _2, _3);
  Priority_Encoder #(.select(2), .disabled("Z")) priority_encoder_1 (
    .in0(1'b0), .in1(_1), .in2(_2), .in3(_3), .out(level));  // open: gs, en_out, en_in
  Register #(.width(1), .trigger("rising"), .Select("low")) register_1 (
    .D(multiplexer_4_out), .en(multiplexer_6_out), .Q(\IE信号 ), .clk(CLK));  // open: clr
  Multiplexer #(.select(1), .width(1), .disabled("Z"), .enable("false")) multiplexer_6 (
    .in0(or_6_out), .in1(1'b1), .out(multiplexer_6_out), .sel(or_5_out));
  or or_5 (or_5_out, MTC0, MFC0);
  or or_6 (or_6_out, d_ff_1_qn, ERET, \中断嵌套_中断 );
  Hex_Digit_Display hex_digit_display_6 (.value(LedData[7:4]));  // open: dp
  Hex_Digit_Display hex_digit_display_7 (.value(LedData[11:8]));  // open: dp
  // Probe on \总周期数 
  Hex_Digit_Display hex_digit_display_8 (.value(LedData[3:0]));  // open: dp
  Register #(.width(2), .trigger("rising"), .Select("low")) register_2 (
    .D(multiplexer_5_out), .en(or_3_out), .Q(register_2_q), .clk(CLK));  // open: clr
  Multiplexer #(.select(1), .width(2), .disabled("Z"), .enable("false")) multiplexer_7 (
    .in0(2'b00), .in1(level), .out(multiplexer_7_out), .sel(or_4_out));
  Counter #(.width(16), .max('hffff), .ongoal("wrap"), .trigger("rising"), .behavior("old")) counter_1 (
    .count(\运行 ), .Q(\总周期数 ), .clk(CLK));  // open: load, D, carry, clr, preset
  ROM #(.addrWidth(10), .dataWidth(32), .Select("high")) rom_1 (.addr(PC[11:2]), .data(IR));
  Adder #(.width(32)) adder_1 (.a(PC), .b(32'h4), .out({J_JAL_PC, Next_PC}));  // open: cin, cout
  Comparator #(.width(2), .mode("unsigned")) comparator_1 (
    .a(register_2_q), .b(multiplexer_7_out), .lt(judge));  // open: gt, eq
  and \u_清零  (\清零_out , ERET, decoder_2_out3);
  or or_7 (IR1_t, IR1, IRA);
  Multiplexer #(.select(1), .width(32), .disabled("Z"), .enable("false")) multiplexer_8 (
    .in0(PC__EPC), .in1({32{1'b0}}), .out(multiplexer_8_out), .sel(\清零_out ));
  Register #(.width(32), .trigger("rising"), .Select("low")) EPC (
    .D(multiplexer_8_out), .en(or_8_out), .Q(EPC_q), .clk(CLK));  // open: clr
  or or_8 (or_8_out, \清零_out , \中断嵌套_中断 );
  Comparator #(.width(32), .mode("unsigned")) comparator_2 (
    .a(EPC_q), .b({32{1'b0}}), .gt(comparator_2_gt));  // open: eq, lt
  or or_9 (IR2_t, IR2, IRB);
  Decoder #(.select(2), .tristate("false"), .disabled("Z"), .enable("false")) decoder_1 (
    .out1(decoder_1_out1), .out2(decoder_1_out2), .out3(decoder_1_out3), .sel(register_2_q));  // open: out0
  Multiplexer #(.select(1), .width(32), .disabled("Z"), .enable("false")) multiplexer_9 (
    .in0(EPC_q), .in1({32{1'b0}}), .out(multiplexer_9_out), .sel(\清零_2_out ));
  or or_10 (or_10_out, \清零_2_out , and_3_out);
  and and_3 (and_3_out, comparator_2_gt, \中断嵌套_中断 );
  and \u_清零_2  (\清零_2_out , ERET, decoder_2_out2);
  Comparator #(.width(32), .mode("unsigned")) comparator_3 (
    .a(EPC_2_q), .b({32{1'b0}}), .gt(comparator_3_gt));  // open: eq, lt
  Decoder #(.select(2), .tristate("false"), .disabled("Z"), .enable("false")) decoder_2 (
    .out1(decoder_2_out1), .out2(decoder_2_out2), .out3(decoder_2_out3), .sel(priority_encoder_2_out));  // open: out0
  \拓展单周期硬布线控制器_31  \u_拓展单周期硬布线控制器_31_1  (
    .OP(IR[31:26]), .Func(IR[5:0]), .ALU_OP(\拓展单周期硬布线控制器_31_1_alu_op ),
    .MemToReg(\拓展单周期硬布线控制器_31_1_memtoreg ), .MemWrite(MemWrite), .ALU_SRC(\拓展单周期硬布线控制器_31_1_alu_src ),
    .RegWrite(RegWrite), .SysCALL(Syscall), .SignedExt(SignedExt), .RegDst(\拓展单周期硬布线控制器_31_1_regdst [0]),
    .Beq(\拓展单周期硬布线控制器_31_1_beq ), .Bne(\拓展单周期硬布线控制器_31_1_bne ), .JR(JR), .JMP(JMP),
    .JAL(\拓展单周期硬布线控制器_31_1_regdst [1]), .LUI(LUI), .LB(LB), .BLEZ(BLEZ), .MFC0(MFC0), .MTC0(MTC0),
    .ERET(ERET), .M(IR[25:21]));  // open: R1_Used, R2_Used
  Multiplexer #(.select(1), .width(5), .disabled("Z"), .enable("false")) multiplexer_10 (
    .in0(IR[25:21]), .in1(5'b00010), .out(multiplexer_10_out), .sel(Syscall));
  Multiplexer #(.select(1), .width(5), .disabled("Z"), .enable("false")) multiplexer_11 (
    .in0(IR[20:16]), .in1(5'b00100), .out(multiplexer_11_out), .sel(Syscall));
  assign bit_extender_1_out = {{16{1'b0}}, IR[15:0]};  // Bit_Extender bit_extender_1
  assign bit_extender_2_out = {{16{IR[15]}}, IR[15:0]};  // Bit_Extender bit_extender_2
  Register #(.width(32), .trigger("rising"), .Select("low")) EPC_2 (
    .D(multiplexer_9_out), .en(or_10_out), .Q(EPC_2_q), .clk(CLK));  // open: clr
  and \u_清零_3  (\清零_3_out , ERET, decoder_2_out1);
  Comparator #(.width(32), .mode("unsigned")) comparator_4 (
    .a(EPC_3_q), .b({32{1'b0}}), .gt(comparator_4_gt));  // open: eq, lt
  Priority_Encoder #(.select(2), .disabled("Z")) priority_encoder_2 (
    .in0(1'b1), .in1(comparator_4_gt), .in2(comparator_3_gt), .in3(comparator_2_gt),
    .out(priority_encoder_2_out));  // open: gs, en_out, en_in
  or or_11 (IR3_t, IR3, IRC);
  Multiplexer #(.select(2), .width(5), .disabled("Z"), .enable("false")) multiplexer_12 (
    .in0(IR[20:16]), .in1(IR[15:11]), .in2({5{1'b1}}), .out(multiplexer_12_out),
    .sel(\拓展单周期硬布线控制器_31_1_regdst ));  // open: in3
  Multiplexer #(.select(1), .width(32), .disabled("Z"), .enable("false")) multiplexer_13 (
    .in0(bit_extender_1_out), .in1(bit_extender_2_out), .out(multiplexer_13_out), .sel(SignedExt));
  Multiplexer #(.select(1), .width(32), .disabled("Z"), .enable("false")) multiplexer_14 (
    .in0(multiplexer_23_out), .in1({IR[15:0], {16{1'b0}}}), .out(multiplexer_14_out), .sel(LUI));
  and and_4 (C_IR1, decoder_1_out1, ERET);
  and and_5 (C_IR2, decoder_1_out2, ERET);
  and and_6 (C_IR3, decoder_1_out3, ERET);
  Register #(.width(32), .trigger("rising"), .Select("low")) EPC_3 (
    .D(multiplexer_15_out), .en(or_12_out), .Q(EPC_3_q), .clk(CLK));  // open: clr
  Multiplexer #(.select(1), .width(32), .disabled("Z"), .enable("false")) multiplexer_15 (
    .in0(EPC_2_q), .in1({32{1'b0}}), .out(multiplexer_15_out), .sel(\清零_3_out ));
  or or_12 (or_12_out, \清零_3_out , and_7_out);
  and and_7 (and_7_out, comparator_3_gt, and_3_out, \中断嵌套_中断 );
  Multiplexer #(.select(2), .width(32), .disabled("Z"), .enable("false")) multiplexer_16 (
    .in0({32{1'b0}}), .in1(EPC_3_q), .in2(EPC_2_q), .in3(EPC_q), .out(EPC__PC), .sel(priority_encoder_2_out));
  Multiplexer #(.select(1), .width(32), .disabled("Z"), .enable("false")) multiplexer_17 (
    .in0(multiplexer_14_out), .in1({J_JAL_PC, Next_PC}), .out(RDin), .sel(\拓展单周期硬布线控制器_31_1_regdst [1]));
  MIPS_Regifile mips_regifile_1 (
    .Din(RDin), .Clk(CLK), .R1(JR_PC), .R2(MDin), .WE(RegWrite), .W_num(multiplexer_12_out),
    .R1_num(multiplexer_10_out), .R2_num(multiplexer_11_out));
  Multiplexer #(.select(1), .width(32), .disabled("Z"), .enable("false")) multiplexer_18 (
    .in0(MDin), .in1(multiplexer_13_out), .out(multiplexer_18_out), .sel(\拓展单周期硬布线控制器_31_1_alu_src ));
  Shifter #(.width(32), .shift("ll")) shifter_1 (.in(multiplexer_13_out), .\dist (5'b00010), .out(shifter_1_out));
  Comparator #(.width(32), .mode("twosComplement")) comparator_5 (
    .a(JR_PC), .b({32{1'b0}}), .gt(comparator_5_gt));  // open: eq, lt
  Multiplexer #(.select(2), .width(32), .disabled("Z"), .enable("false")) multiplexer_19 (
    .in1(32'h30ac), .in2(32'h3158), .in3(32'h3204), .out(\服务地址 ), .sel(level));  // open: in0
  and and_8 (and_8_out, mips_alu_1_equal, \拓展单周期硬布线控制器_31_1_beq );
  not not_1 (not_1_out, mips_alu_1_equal);
  and and_9 (and_9_out, not_1_out, \拓展单周期硬布线控制器_31_1_bne );
  not not_2 (not_2_out, comparator_5_gt);
  MIPS_ALU mips_alu_1 (
    .X(JR_PC), .Y(multiplexer_18_out), .AluOP(\拓展单周期硬布线控制器_31_1_alu_op ), .Equal(mips_alu_1_equal),
    .Result(mips_alu_1_result), .shamt(IR[10:6]));  // open: Result_2
  Adder #(.width(32)) adder_2 (.a(shifter_1_out), .b({J_JAL_PC, Next_PC}), .out(B___PC));  // open: cin, cout
  Multiplexer #(.select(1), .width(1), .disabled("Z"), .enable("false")) multiplexer_20 (
    .in0(1'b0), .in1(_1), .out(multiplexer_20_out), .sel(and_10_out));
  and and_10 (and_10_out, ~_2, \IE信号 , ~_3);  // AND_Gate
  Multiplexer #(.select(1), .width(1), .disabled("Z"), .enable("false")) multiplexer_21 (
    .in0(1'b0), .in1(_2), .out(multiplexer_21_out), .sel(and_11_out));
  and and_11 (and_11_out, ~_3, \IE信号 );  // AND_Gate
  Multiplexer #(.select(1), .width(1), .disabled("Z"), .enable("false")) multiplexer_22 (
    .in0(1'b0), .in1(_3), .out(multiplexer_22_out), .sel(\IE信号 ));
  or or_13 (B___De, and_8_out, and_9_out);
  and and_12 (BLEZ_DE, BLEZ, not_2_out);
  Multiplexer #(.select(1), .width(32), .disabled("Z"), .enable("false")) multiplexer_23 (
    .in0({multiplexer_28_out_4, multiplexer_28_out_3, multiplexer_28_out_2, multiplexer_28_out}),
    .in1(bit_extender_3_out), .out(multiplexer_23_out), .sel(LB));
  Multiplexer #(.select(1), .width(1), .disabled("Z"), .enable("false")) multiplexer_24 (
    .in0(multiplexer_20_out), .in1(1'b0), .out(multiplexer_24_out), .sel(C_IR1));
  Multiplexer #(.select(1), .width(1), .disabled("Z"), .enable("false")) multiplexer_25 (
    .in0(multiplexer_21_out), .in1(1'b0), .out(multiplexer_25_out), .sel(C_IR2));
  Multiplexer #(.select(1), .width(1), .disabled("Z"), .enable("false")) multiplexer_26 (
    .in0(multiplexer_22_out), .in1(1'b0), .out(multiplexer_26_out), .sel(C_IR3));
  Comparator #(.width(32), .mode("twosComplement")) comparator_6 (
    .a(JR_PC), .b(32'h22), .eq(comparator_6_eq));  // open: gt, lt
  assign bit_extender_3_out = {{24{multiplexer_27_out[7]}}, multiplexer_27_out};  // Bit_Extender bit_extender_3
  D_Flip_Flop #(.trigger("rising"), .Pre_Clr_Positions("LEGACY"), .NegatePresetClear("false"), .enable("true"), .NewFFLayout("false")) d_ff_2 (
    .clk(CLK), .D(multiplexer_24_out), .Q(d_ff_2_q), .en(or_14_out));  // open: Qn, preset, reset
  or or_14 (or_14_out, C_IR1, not_3_out);
  not not_3 (not_3_out, d_ff_2_q);
  D_Flip_Flop #(.trigger("rising"), .Pre_Clr_Positions("LEGACY"), .NegatePresetClear("false"), .enable("true"), .NewFFLayout("false")) d_ff_3 (
    .clk(CLK), .D(multiplexer_25_out), .Q(d_ff_3_q), .en(or_15_out));  // open: Qn, preset, reset
  or or_15 (or_15_out, C_IR2, not_4_out);
  not not_4 (not_4_out, d_ff_3_q);
  D_Flip_Flop #(.trigger("rising"), .Pre_Clr_Positions("LEGACY"), .NegatePresetClear("false"), .enable("true"), .NewFFLayout("false")) d_ff_4 (
    .clk(CLK), .D(multiplexer_26_out), .Q(d_ff_4_q), .en(or_16_out));  // open: Qn, preset, reset
  or or_16 (or_16_out, C_IR3, not_5_out);
  not not_5 (not_5_out, d_ff_4_q);
  RAM #(.addrWidth(10), .dataWidth(32), .bus("separate"), .Select("high")) ram_1 (
    .addr(mips_alu_1_result[11:2]), .din(MDin), .data(ram_1_data), .str(MemWrite), .clk(CLK));  // open: sel, ld, clr
  Multiplexer #(.select(2), .width(8), .disabled("Z"), .enable("false")) multiplexer_27 (
    .in0(multiplexer_28_out), .in1(multiplexer_28_out_2), .in2(multiplexer_28_out_3),
    .in3(multiplexer_28_out_4), .out(multiplexer_27_out), .sel(mips_alu_1_result[1:0]));
  and and_13 (and_13_out, ~d_ff_2_q, _1);  // AND_Gate
  and and_14 (and_14_out, ~d_ff_3_q, _2);  // AND_Gate
  and and_15 (and_15_out, ~d_ff_4_q, _3);  // AND_Gate
  Multiplexer #(.select(1), .width(32), .disabled("Z"), .enable("false")) multiplexer_28 (
    .in0(mips_alu_1_result), .in1(ram_1_data),
    .out({multiplexer_28_out_4, multiplexer_28_out_3, multiplexer_28_out_2, multiplexer_28_out}),
    .sel(\拓展单周期硬布线控制器_31_1_memtoreg ));
  Comparator #(.width(16), .mode("twosComplement")) comparator_7 (
    .a(16'h258), .b(\总周期数 ), .eq(comparator_7_eq));  // open: gt, lt
  Comparator #(.width(16), .mode("twosComplement")) comparator_8 (
    .a(\总周期数 ), .b(16'h1), .eq(comparator_8_eq));  // open: gt, lt
  Comparator #(.width(16), .mode("twosComplement")) comparator_9 (
    .a(\总周期数 ), .b(16'h4), .eq(comparator_9_eq));  // open: gt, lt
  Comparator #(.width(16), .mode("twosComplement")) comparator_10 (
    .a(\总周期数 ), .b(16'h7), .eq(comparator_10_eq));  // open: gt, lt
  or or_17 (or_17_out, comparator_10_eq, comparator_11_eq);
  Comparator #(.width(16), .mode("twosComplement")) comparator_11 (
    .a(\总周期数 ), .b(16'h241), .eq(comparator_11_eq));  // open: gt, lt
  Multiplexer #(.select(2), .width(1), .disabled("Z"), .enable("false")) multiplexer_29 (
    .in0(1'b1), .in1(and_13_out), .in2(and_14_out), .in3(and_15_out), .out(multiplexer_29_out), .sel(level));
  D_Flip_Flop #(.trigger("rising"), .Pre_Clr_Positions("LEGACY"), .NegatePresetClear("false"), .enable("true"), .NewFFLayout("false")) d_ff_5 (
    .clk(and_15_out), .D(1'b1));  // open: Q, Qn, preset, en, reset
  or or_18 (or_18_out, comparator_7_eq, comparator_8_eq);
  Pull_Resistor #(.pull(0)) pull_resistor_1 (.node(IRA));
  assign IRA = or_18_out ? ~CLK : 1'bz;  // Controlled_Inverter controlled_inverter_1
  Pull_Resistor #(.pull(0)) pull_resistor_2 (.node(IRB));
  assign IRB = comparator_9_eq ? ~CLK : 1'bz;  // Controlled_Inverter controlled_inverter_2
  Pull_Resistor #(.pull(0)) pull_resistor_3 (.node(IRC));
  assign IRC = or_17_out ? ~CLK : 1'bz;  // Controlled_Inverter controlled_inverter_3
  Multiplexer #(.select(1), .width(1), .disabled("Z"), .enable("false")) multiplexer_30 (
    .in0(1'b0), .in1(comparator_6_eq), .out(multiplexer_30_out), .sel(Syscall));
  Pull_Resistor #(.pull(0)) pull_resistor_4 (.node(level));
  or or_19 (\运行 , Go, multiplexer_30_out, ~Syscall);  // OR_Gate
  Register #(.width(32), .trigger("rising"), .Select("low")) register_3 (
    .D(MDin), .en(multiplexer_30_out), .Q(LedData), .clk(CLK));  // open: clr
  and and_16 (\优先级高的中断出现 , multiplexer_29_out, judge);

  // Other names for the same wires on the sheet: FUNC[5:0] = IR[5:0]; J_JAL_PC[27:2] = IR[25:0]; a0[31:0] = MDin;
  //   OP[5:0] = IR[31:26]; M[4:0] = IR[25:21]; Next_PC[31:28] = J_JAL_PC

  // Notes on the sheet:
  //   中断源
  //   中断等待指示
  //   总复位信号应将除ROM以外所有存储组件全部清零
  //   发生中断时，中断源的序号便存储到寄存器中
  //   数码管输出
  //   数码管输出应该用寄存器锁存，否则显示数据只能一闪而过
  //   指令存储器
  //   指令字
  //   contents of rom_1 (hex, n*v repeats v):
  //   201d07d0 20100001 109fc0 139fc3 8021 2012000c 24160008 26100001 3210000f 20080008 20090001 139900
  //   2709825 132020 20020022 c 1094022 1500fff9 22100001 2018000f 2188024 108700 20080008 20090001 139902
  //   2709825 132021 20020022 c 1094022 1500fff9 108702 2c9b022 12c00001 8000c07 4020 1084027 84400
  //   3508ffff 82021 20020022 c 8000c01 afa20000 23bd0004 afa40000 23bd0004 afb00000 23bd0004 afb30000
  //   23bd0004 afb40000 23bd0004 afb50000 23bd0004 afb60000 23bd0004 40000000 20160001 20140003 20150001
  //   168020 108100 2149825 132020 20020022 c 1600fffa 295a022 1680fff7 40800000 23bdfffc 8fb60000
  //   23bdfffc 8fb50000 23bdfffc 8fb40000 23bdfffc 8fb30000 23bdfffc 8fb00000 23bdfffc 8fa40000 23bdfffc
  //   8fa20000 42000018 afa20000 23bd0004 afa40000 23bd0004 afb00000 23bd0004 afb30000 23bd0004 afb40000
  //   23bd0004 afb50000 23bd0004 afb60000 23bd0004 40000000 20160002 20140003 20150001 168020 108100
  //   2149825 132020 20020022 c 1600fffa 295a022 1680fff7 40800000 23bdfffc 8fb60000 23bdfffc 8fb50000
  //   23bdfffc 8fb40000 23bdfffc 8fb30000 23bdfffc 8fb00000 23bdfffc 8fa40000 23bdfffc 8fa20000 42000018
  //   afa20000 23bd0004 afa40000 23bd0004 afb00000 23bd0004 afb30000 23bd0004 afb40000 23bd0004 afb50000
  //   23bd0004 afb60000 23bd0004 40000000 20160003 20140003 20150001 168020 108100 2149825 132020 20020022
  //   c 1600fffa 295a022 1680fff7 40800000 23bdfffc 8fb60000 23bdfffc 8fb50000 23bdfffc 8fb40000 23bdfffc
  //   8fb30000 23bdfffc 8fb00000 23bdfffc 8fa40000 23bdfffc 8fa20000 42000018
  //   OP
  //   Func
  //   rs
  //   rt
  //   rd
  //   OP
  //   Func
  //   JAL
  //   RegDst
  //   RegWrite
  //   为方便自动评测，需要输出PC，IR，寄存器堆写如数据RDin
  //   Beq
  //   Bne
  //   MemToReg
  //   MemWrite
  //   AluOP
  //   AluSrcB
  //   RAM写使能MemWrite、RAM写入数据MDin等信号
  //   多级中断信号产生
endmodule

module \重定向流水线_单级中断  (
  output RegWrite,
  output MemWrite,
  output [31:0] PC,
  output [31:0] IR,
  output [31:0] RDin,
  output [31:0] MDin
);

  wire and_1_out, and_6_out, and_7_out, and_8_out, and_9_out, and_11_out, B___De, BLEZ, BLEZ_DE,
       BracnhConflict, branch, C_IR1, C_IR2, C_IR3, CLK, comparator_1_gt, comparator_2_eq, comparator_3_eq,
       d_ff_1_qn, d_ff_2_q, DataConflict, decoder_1_out1, decoder_1_out2, decoder_1_out3, ERET, EX_Con,
       ex_mem_1_out_18, ex_mem_1_out_19, ex_mem_1_out_20, ex_mem_1_out_21, ex_mem_1_out_24, EX_RegWrite, Go,
       id_ex_1_out_31, id_ex_1_out_33, id_ex_1_out_34, id_ex_1_out_35, id_ex_1_out_36, id_ex_1_out_37,
       id_ex_1_out_39, id_ex_1_out_41, IR1, IR2, IR3, JAL_1, JAL_2, JAL_3, JAL_4, JMP, JR, LoadUse, LUI,
       MEM_RegWrite, mem_wb_1_out_19, mem_wb_1_out_20, mem_wb_1_out_23, mips_alu_1_equal, multiplexer_4_out,
       multiplexer_17_out, multiplexer_20_out, not_1_out, not_2_out, OK, or_3_out, or_4_out, or_5_out,
       or_6_out, or_8_out, or_11_out, or_12_out, or_13_out, or_14_out, priority_encoder_1_gs, R1_U, R2_U,
       register_1_q, RegWrite_1, RST, SignedExt, STALL, W1, W2, W3, \中断发生信号 , \中断按键参考电路_1_与中断屏蔽位与 ,
       \中断按键参考电路_2_与中断屏蔽位与 , \中断按键参考电路_3_与中断屏蔽位与 , \拓展单周期硬布线控制器_31_1_alu_src , \拓展单周期硬布线控制器_31_1_beq ,
       \拓展单周期硬布线控制器_31_1_blez , \拓展单周期硬布线控制器_31_1_bne , \拓展单周期硬布线控制器_31_1_jmp , \拓展单周期硬布线控制器_31_1_jr ,
       \拓展单周期硬布线控制器_31_1_lb , \拓展单周期硬布线控制器_31_1_lui , \拓展单周期硬布线控制器_31_1_memtoreg ,
       \拓展单周期硬布线控制器_31_1_memwrite , \拓展单周期硬布线控制器_31_1_regwrite , \拓展单周期硬布线控制器_31_1_syscall ,
       \数据相关检测_24_3_2_1_mem相关 , \运行 ;
  wire [0:0] or_1_out, \拓展单周期硬布线控制器_31_1_regdst ;
  wire [1:0] priority_encoder_1_out, register_2_q;
  wire [3:0] id_ex_1_out_38, relation, relation_1, \拓展单周期硬布线控制器_31_1_alu_op ;
  wire [4:0] EX_WriteReg_num, id_ex_1_out_47, MEM_WriteReg_num, multiplexer_8_out, R1_num, R2_num, W_num;
  wire [7:0] multiplexer_19_out;
  wire [15:0] \LoadUse次数 , \总周期数 , \插入气泡数 , \无条件分支数 , \条件分支成功数 ;
  wire [27:0] adder_2_out;
  wire [31:0] a0, adder_4_out, B___PC, bit_extender_1_out, bit_extender_2_out, bit_extender_3_out, Din,
       EPC__PC, ex_mem_1_out_23, ex_mem_1_out_28, ex_mem_1_out_30, EX_PC, id_ex_1_out_44, id_ex_1_out_45,
       id_ex_1_out_46, id_ex_1_out_49, ID_PC, IF_PC, IR_1, IR_2, IR_3, IR_4, JR_PC, LedData, MEM_AluR,
       MEM_PC, mem_wb_1_out_22, mem_wb_1_out_30, mips_alu_1_result, mips_regifile_1_r1, mips_regifile_1_r2,
       multiplexer_1_out, multiplexer_2_out, multiplexer_3_out, multiplexer_9_out, multiplexer_12_out,
       multiplexer_13_out, multiplexer_15_out, multiplexer_16_out, Next_PC, Next_PC_4, ram_1_data,
       rom_1_data, shifter_1_out, W, WB_AluR, WB_Read, \服务地址 ;
  wire [31:28] J_JAL_PC;

  Clock #(.highDuration(1), .lowDuration(1)) clock_1 (.out(CLK));
  Button _1 (.out(IR1));
  Button _2 (.out(IR2));
  Button _3 (.out(IR3));
  Button \u_继续运行  (.out(Go));
  LED #(.active("true")) led_1 (.in(W1));
  LED #(.active("true")) led_2 (.in(W2));
  LED #(.active("true")) led_3 (.in(W3));
  or or_1 (or_1_out[0], JR, BLEZ_DE, B___De);
  Multiplexer #(.select(2), .width(32), .disabled("Z"), .enable("false")) multiplexer_1 (
    .in0(Next_PC), .in1(B___PC), .in2({J_JAL_PC, IR_2[25:0], 2'b00}), .in3(JR_PC), .out(multiplexer_1_out),
    .sel({JMP, or_1_out[0]}));
  Hex_Digit_Display hex_digit_display_1 (.value(LedData[31:28]));  // open: dp
  Button \u_清零  (.out(RST));
  or or_2 (branch, BLEZ_DE, B___De);
  Hex_Digit_Display hex_digit_display_2 (.value(LedData[27:24]));  // open: dp
  Hex_Digit_Display hex_digit_display_3 (.value(LedData[23:20]));  // open: dp
  Multiplexer #(.select(1), .width(32), .disabled("Z"), .enable("false")) multiplexer_2 (
    .in0(multiplexer_1_out), .in1(\服务地址 ), .out(multiplexer_2_out), .sel(OK));
  \中断按键参考电路  \u_中断按键参考电路_1  (.\与中断屏蔽位与 (\中断按键参考电路_1_与中断屏蔽位与 ), .\同步清零信号 (C_IR1), .\中断输入 (IR1), .out_4(W1));
  \中断按键参考电路  \u_中断按键参考电路_2  (.\与中断屏蔽位与 (\中断按键参考电路_2_与中断屏蔽位与 ), .\同步清零信号 (C_IR2), .\中断输入 (IR2), .out_4(W2));
  \中断按键参考电路  \u_中断按键参考电路_3  (.\与中断屏蔽位与 (\中断按键参考电路_3_与中断屏蔽位与 ), .\同步清零信号 (C_IR3), .\中断输入 (IR3), .out_4(W3));
  Hex_Digit_Display hex_digit_display_4 (.value(LedData[19:16]));  // open: dp
  Hex_Digit_Display hex_digit_display_5 (.value(LedData[15:12]));  // open: dp
  // Probe on multiplexer_3_out
  Multiplexer #(.select(1), .width(32), .disabled("Z"), .enable("false")) multiplexer_3 (
    .in0(multiplexer_2_out), .in1(EPC__PC), .out(multiplexer_3_out), .sel(ERET));
  // Probe on EPC__PC
  Register #(.width(32), .trigger("rising"), .Select("low")) EPC (
    .D(MEM_PC), .en(OK), .Q(EPC__PC), .clk(CLK));  // open: clr
  Multiplexer #(.select(1), .width(1), .disabled("Z"), .enable("false")) multiplexer_4 (
    .in0(1'b0), .in1(1'b1), .out(multiplexer_4_out), .sel(or_3_out));
  or or_3 (or_3_out, d_ff_1_qn, ERET);
  D_Flip_Flop #(.trigger("rising"), .Pre_Clr_Positions("LEGACY"), .NegatePresetClear("false"), .enable("true"), .NewFFLayout("false")) d_ff_1 (
    .clk(CLK), .D(1'b1), .Qn(d_ff_1_qn));  // open: Q, preset, en, reset
  Hex_Digit_Display hex_digit_display_6 (.value(LedData[7:4]));  // open: dp
  Hex_Digit_Display hex_digit_display_7 (.value(LedData[11:8]));  // open: dp
  Register #(.width(32), .trigger("rising"), .Select("low")) u_PC (
    .D(multiplexer_3_out), .en(and_1_out), .Q(IF_PC), .clk(CLK));  // open: clr
  and and_1 (and_1_out, ~LoadUse, \运行 );  // AND_Gate
  Priority_Encoder #(.select(2), .disabled("Z")) priority_encoder_1 (
    .in0(1'b0), .in1(\中断按键参考电路_1_与中断屏蔽位与 ), .in2(\中断按键参考电路_2_与中断屏蔽位与 ), .in3(\中断按键参考电路_3_与中断屏蔽位与 ),
    .out(priority_encoder_1_out), .gs(priority_encoder_1_gs));  // open: en_out, en_in
  Register #(.width(1), .trigger("rising"), .Select("low")) register_1 (
    .D(multiplexer_4_out), .en(or_4_out), .Q(register_1_q), .clk(CLK));  // open: clr
  or or_4 (or_4_out, d_ff_1_qn, ERET, \中断发生信号 );
  Hex_Digit_Display hex_digit_display_8 (.value(LedData[3:0]));  // open: dp
  // Probe on \总周期数 
  Adder #(.width(32)) adder_1 (.a(IF_PC), .b(32'h4), .out(Next_PC));  // open: cin, cout
  Decoder #(.select(2), .tristate("false"), .disabled("Z"), .enable("false")) decoder_1 (
    .out1(decoder_1_out1), .out2(decoder_1_out2), .out3(decoder_1_out3), .sel(register_2_q));  // open: out0
  Register #(.width(2), .trigger("rising"), .Select("low")) register_2 (
    .D(priority_encoder_1_out), .en(\中断发生信号 ), .Q(register_2_q), .clk(CLK));  // open: clr
  and and_2 (\中断发生信号 , priority_encoder_1_gs, register_1_q);
  Counter #(.width(16), .max('hffff), .ongoal("wrap"), .trigger("rising"), .behavior("old")) counter_1 (
    .count(\运行 ), .Q(\总周期数 ), .clk(CLK));  // open: load, D, carry, clr, preset
  ROM #(.addrWidth(10), .dataWidth(32), .Select("high")) rom_1 (.addr(IF_PC[11:2]), .data(rom_1_data));
  or or_5 (or_5_out, RST, OK, ERET, BracnhConflict);
  IF_ID if_id_1 (
    .in_5(CLK), .in_2(rom_1_data), .in_1(IF_PC), .out_8(ID_PC), .out_9(IR_1), .in_7(or_5_out), .in_6(or_6_out));  // open: in_3, out_10, in_4, out_11
  or or_6 (or_6_out, STALL, LoadUse);
  and and_3 (C_IR1, decoder_1_out1, ERET);
  and and_4 (C_IR2, decoder_1_out2, ERET);
  and and_5 (C_IR3, decoder_1_out3, ERET);
  Multiplexer #(.select(2), .width(32), .disabled("Z"), .enable("false")) multiplexer_5 (
    .in1(32'h4), .in2(32'h120), .in3(32'h23c), .out(\服务地址 ), .sel(priority_encoder_1_out));  // open: in0
  \数据相关检测_24_3_2  \u_数据相关检测_24_3_2_1  (
    .EX_RegWrite(EX_RegWrite), .R1_num(R1_num), .EX_WriteReg_num(EX_WriteReg_num),
    .MEM_RegWrite(MEM_RegWrite), .R2_num(R2_num), .MEM_WriteReg_num(MEM_WriteReg_num), .R1_Used(R1_U),
    .R2_Used(R2_U), .\MEM相关 (\数据相关检测_24_3_2_1_mem相关 ), .\EX相关 (EX_Con), .R1_MEM(relation));
  \拓展单周期硬布线控制器_31  \u_拓展单周期硬布线控制器_31_1  (
    .OP(IR_1[31:26]), .Func(IR_1[5:0]), .ALU_OP(\拓展单周期硬布线控制器_31_1_alu_op ),
    .MemToReg(\拓展单周期硬布线控制器_31_1_memtoreg ), .MemWrite(\拓展单周期硬布线控制器_31_1_memwrite ),
    .ALU_SRC(\拓展单周期硬布线控制器_31_1_alu_src ), .RegWrite(\拓展单周期硬布线控制器_31_1_regwrite ),
    .SysCALL(\拓展单周期硬布线控制器_31_1_syscall ), .SignedExt(SignedExt), .RegDst(\拓展单周期硬布线控制器_31_1_regdst [0]),
    .Beq(\拓展单周期硬布线控制器_31_1_beq ), .Bne(\拓展单周期硬布线控制器_31_1_bne ), .JR(\拓展单周期硬布线控制器_31_1_jr ),
    .JMP(\拓展单周期硬布线控制器_31_1_jmp ), .JAL(JAL_1), .LUI(\拓展单周期硬布线控制器_31_1_lui ), .LB(\拓展单周期硬布线控制器_31_1_lb ),
    .BLEZ(\拓展单周期硬布线控制器_31_1_blez ), .R1_Used(R1_U), .R2_Used(R2_U), .ERET(ERET), .M(IR_1[25:21]));  // open: MFC0, MTC0
  or or_7 (DataConflict, EX_Con, \数据相关检测_24_3_2_1_mem相关 );
  Multiplexer #(.select(1), .width(5), .disabled("Z"), .enable("false")) multiplexer_6 (
    .in0(IR_1[25:21]), .in1(5'b00010), .out(R1_num), .sel(\拓展单周期硬布线控制器_31_1_syscall ));
  Multiplexer #(.select(1), .width(5), .disabled("Z"), .enable("false")) multiplexer_7 (
    .in0(IR_1[20:16]), .in1(5'b00100), .out(R2_num), .sel(\拓展单周期硬布线控制器_31_1_syscall ));
  assign bit_extender_1_out = {{16{1'b0}}, IR_1[15:0]};  // Bit_Extender bit_extender_1
  assign bit_extender_2_out = {{16{IR_1[15]}}, IR_1[15:0]};  // Bit_Extender bit_extender_2
  Multiplexer #(.select(2), .width(5), .disabled("Z"), .enable("false")) multiplexer_8 (
    .in0(IR_1[20:16]), .in1(IR_1[15:11]), .in2({5{1'b1}}), .out(multiplexer_8_out),
    .sel({JAL_1, \拓展单周期硬布线控制器_31_1_regdst [0]}));  // open: in3
  Multiplexer #(.select(1), .width(32), .disabled("Z"), .enable("false")) multiplexer_9 (
    .in0(bit_extender_1_out), .in1(bit_extender_2_out), .out(multiplexer_9_out), .sel(SignedExt));
  // Probe on \总周期数 
  // Probe on \无条件分支数 
  // Probe on \条件分支成功数 
  // Probe on \插入气泡数 
  // Probe on \LoadUse次数 
  MIPS_Regifile mips_regifile_1 (
    .Din(Din), .Clk(CLK), .R1(mips_regifile_1_r1), .R2(mips_regifile_1_r2), .WE(RegWrite_1), .W_num(W_num),
    .R1_num(R1_num), .R2_num(R2_num));
  // Probe on IF_PC[11:0]
  // Probe on EX_PC[11:0]
  // Probe on ID_PC[11:0]
  or or_8 (or_8_out, OK, RST, ERET, BracnhConflict, LoadUse);
  ID_EX id_ex_1 (
    .in_1(\拓展单周期硬布线控制器_31_1_jr ), .in_4(\拓展单周期硬布线控制器_31_1_blez ), .in_5(\拓展单周期硬布线控制器_31_1_lb ),
    .in_6(\拓展单周期硬布线控制器_31_1_beq ), .in_7(\拓展单周期硬布线控制器_31_1_bne ), .in_8(\拓展单周期硬布线控制器_31_1_memtoreg ),
    .in_9(\拓展单周期硬布线控制器_31_1_memwrite ), .in_10(\拓展单周期硬布线控制器_31_1_alu_op ),
    .in_11(\拓展单周期硬布线控制器_31_1_alu_src ), .in_12(\拓展单周期硬布线控制器_31_1_regwrite ),
    .in_13(\拓展单周期硬布线控制器_31_1_syscall ), .in_14(ID_PC), .in_15(IR_1), .in_16(mips_regifile_1_r1),
    .in_17(mips_regifile_1_r2), .in_18(multiplexer_9_out), .in_19(IR_1[10:6]), .in_20(multiplexer_8_out),
    .in_21({IR_1[15:0], {16{1'b0}}}), .out_29(JR), .out_30(JMP), .out_31(id_ex_1_out_31), .out_32(BLEZ),
    .out_33(id_ex_1_out_33), .out_34(id_ex_1_out_34), .out_35(id_ex_1_out_35), .out_36(id_ex_1_out_36),
    .out_37(id_ex_1_out_37), .out_40(EX_RegWrite), .out_41(id_ex_1_out_41), .out_42(EX_PC),
    .out_38(id_ex_1_out_38), .out_39(id_ex_1_out_39), .out_43(IR_2), .out_44(id_ex_1_out_44),
    .out_45(id_ex_1_out_45), .out_46(id_ex_1_out_46), .out_47(id_ex_1_out_47), .out_48(EX_WriteReg_num),
    .out_49(id_ex_1_out_49), .in_26(CLK), .in_3(\拓展单周期硬布线控制器_31_1_lui ), .in_2(\拓展单周期硬布线控制器_31_1_jmp ),
    .in_27(STALL), .in_28(or_8_out), .out_51(JAL_2), .in_23(JAL_1), .in_22(relation), .out_50(relation_1));  // open: in_24, out_52, in_25, out_53
  // Probe on MEM_PC[11:0]
  // Probe on Next_PC_4[11:0]
  Multiplexer #(.select(1), .width(1), .disabled("Z"), .enable("false")) multiplexer_10 (
    .in0(1'b0), .in1(id_ex_1_out_36), .out(LoadUse), .sel(EX_Con));
  Adder #(.width(32)) adder_2 (.a(EX_PC), .b(32'h4), .out({J_JAL_PC, adder_2_out}));  // open: cin, cout
  Multiplexer #(.select(2), .width(32), .disabled("Z"), .enable("false")) multiplexer_11 (
    .in0(id_ex_1_out_44), .in1(MEM_AluR), .in2(W), .in3(MEM_AluR), .out(JR_PC), .sel(relation_1[1:0]));
  Multiplexer #(.select(2), .width(32), .disabled("Z"), .enable("false")) multiplexer_12 (
    .in0(id_ex_1_out_45), .in1(MEM_AluR), .in2(W), .in3(MEM_AluR), .out(multiplexer_12_out),
    .sel(relation_1[3:2]));
  Multiplexer #(.select(1), .width(32), .disabled("Z"), .enable("false")) multiplexer_13 (
    .in0(multiplexer_12_out), .in1(id_ex_1_out_46), .out(multiplexer_13_out), .sel(id_ex_1_out_39));
  Shifter #(.width(32), .shift("ll")) shifter_1 (.in(id_ex_1_out_46), .\dist (5'b00010), .out(shifter_1_out));
  MIPS_ALU mips_alu_1 (
    .X(JR_PC), .Y(multiplexer_13_out), .AluOP(id_ex_1_out_38), .Equal(mips_alu_1_equal),
    .Result(mips_alu_1_result), .shamt(id_ex_1_out_47));  // open: Result_2
  or or_9 (BracnhConflict, JMP, JR, B___De, BLEZ_DE);
  not not_1 (not_1_out, mips_alu_1_equal);
  Adder #(.width(32)) adder_3 (.a(shifter_1_out), .b({J_JAL_PC, adder_2_out}), .out(B___PC));  // open: cin, cout
  and and_6 (and_6_out, mips_alu_1_equal, id_ex_1_out_34);
  and and_7 (and_7_out, not_1_out, id_ex_1_out_35);
  Comparator #(.width(32), .mode("twosComplement")) comparator_1 (
    .a(JR_PC), .b({32{1'b0}}), .gt(comparator_1_gt));  // open: eq, lt
  and and_8 (and_8_out, JMP, ~STALL);  // AND_Gate
  or or_10 (B___De, and_6_out, and_7_out);
  not not_2 (not_2_out, comparator_1_gt);
  Counter #(.width(16), .max('hffff), .ongoal("wrap"), .trigger("rising"), .behavior("new")) counter_2 (
    .count(and_8_out), .Q(\无条件分支数 ), .clk(CLK), .clr(RST));  // open: load, D, carry, preset, down
  and and_9 (and_9_out, branch, ~STALL);  // AND_Gate
  and and_10 (BLEZ_DE, BLEZ, not_2_out);
  // Probe on mips_alu_1_result
  Counter #(.width(16), .max('hffff), .ongoal("wrap"), .trigger("rising"), .behavior("new")) counter_3 (
    .count(and_9_out), .Q(\条件分支成功数 ), .clk(CLK), .clr(RST));  // open: load, D, carry, preset, down
  Counter #(.width(16), .max('hffff), .ongoal("wrap"), .trigger("rising"), .behavior("new")) counter_4 (
    .count(and_11_out), .Q(\插入气泡数 ), .clk(CLK), .clr(RST));  // open: load, D, carry, preset, down
  and and_11 (and_11_out, or_11_out, \运行 );
  or or_11 (or_11_out, STALL, LoadUse);
  Counter #(.width(16), .max('hffff), .ongoal("wrap"), .trigger("rising"), .behavior("new")) counter_5 (
    .count(and_11_out), .Q(\LoadUse次数 ), .clr(RST));  // open: load, D, carry, clk, preset, down
  or or_12 (or_12_out, RST, ERET, OK);
  EX_MEM ex_mem_1 (
    .in_1(id_ex_1_out_31), .out_18(ex_mem_1_out_18), .in_2(id_ex_1_out_33), .out_19(ex_mem_1_out_19),
    .in_3(id_ex_1_out_36), .out_20(ex_mem_1_out_20), .in_4(id_ex_1_out_37), .out_21(ex_mem_1_out_21),
    .in_8(EX_PC), .out_25(MEM_PC), .in_9(IR_2), .out_26(IR_3), .in_10(mips_alu_1_result), .out_27(MEM_AluR),
    .in_11(multiplexer_12_out), .out_28(ex_mem_1_out_28), .in_12(EX_WriteReg_num), .out_29(MEM_WriteReg_num),
    .in_13(id_ex_1_out_49), .out_30(ex_mem_1_out_30), .in_15(CLK), .in_5(EX_RegWrite), .out_22(MEM_RegWrite),
    .in_16(STALL), .in_17(or_12_out), .in_6(JR_PC), .out_23(ex_mem_1_out_23), .in_7(id_ex_1_out_41),
    .out_24(ex_mem_1_out_24), .in_14(JAL_2), .out_31(JAL_3));
  RAM #(.addrWidth(10), .dataWidth(32), .bus("separate"), .Select("high")) ram_1 (
    .addr(MEM_AluR[11:2]), .din(ex_mem_1_out_28), .data(ram_1_data), .str(ex_mem_1_out_21), .clk(CLK));  // open: sel, ld, clr
  Multiplexer #(.select(1), .width(32), .disabled("Z"), .enable("false")) multiplexer_14 (
    .in0(multiplexer_15_out), .in1(adder_4_out), .out(Din), .sel(JAL_4));
  Multiplexer #(.select(1), .width(32), .disabled("Z"), .enable("false")) multiplexer_15 (
    .in0(multiplexer_16_out), .in1(mem_wb_1_out_30), .out(multiplexer_15_out), .sel(LUI));
  Adder #(.width(32)) adder_4 (.a(Next_PC_4), .b(32'h4), .out(adder_4_out));  // open: cin, cout
  or or_13 (or_13_out, RST, ERET, OK);
  MEM_WB mem_wb_1 (
    .in_1(ex_mem_1_out_18), .out_18(LUI), .in_2(ex_mem_1_out_19), .out_19(mem_wb_1_out_19),
    .in_3(ex_mem_1_out_20), .out_20(mem_wb_1_out_20), .in_4(MEM_RegWrite), .out_21(RegWrite_1),
    .in_7(MEM_PC), .out_24(Next_PC_4), .in_8(IR_3), .out_25(IR_4), .in_9(MEM_AluR), .out_26(WB_AluR),
    .in_10(ram_1_data), .out_27(WB_Read), .in_12(MEM_WriteReg_num), .out_29(W_num), .in_13(ex_mem_1_out_30),
    .out_30(mem_wb_1_out_30), .in_15(CLK), .in_16(STALL), .in_5(ex_mem_1_out_23), .out_22(mem_wb_1_out_22),
    .in_6(ex_mem_1_out_24), .out_23(mem_wb_1_out_23), .in_11(ex_mem_1_out_28), .out_28(a0),
    .in_17(or_13_out), .in_14(JAL_3), .out_31(JAL_4));
  Multiplexer #(.select(1), .width(32), .disabled("Z"), .enable("false")) multiplexer_16 (
    .in0(W), .in1(bit_extender_3_out), .out(multiplexer_16_out), .sel(mem_wb_1_out_19));
  Multiplexer #(.select(1), .width(1), .disabled("Z"), .enable("false")) multiplexer_17 (
    .in0(1'b1), .in1(1'b0), .out(multiplexer_17_out), .sel(OK));
  or or_14 (or_14_out, OK, \中断发生信号 );
  Multiplexer #(.select(1), .width(32), .disabled("Z"), .enable("false")) multiplexer_18 (
    .in0(WB_AluR), .in1(WB_Read), .out(W), .sel(mem_wb_1_out_20));
  assign bit_extender_3_out = {{24{multiplexer_19_out[7]}}, multiplexer_19_out};  // Bit_Extender bit_extender_3
  D_Flip_Flop #(.trigger("rising"), .Pre_Clr_Positions("LEGACY"), .NegatePresetClear("false"), .enable("true"), .NewFFLayout("false")) d_ff_2 (
    .clk(CLK), .D(multiplexer_17_out), .Q(d_ff_2_q), .en(or_14_out));  // open: Qn, preset, reset
  Comparator #(.width(32), .mode("unsigned")) comparator_2 (
    .a({32{1'b0}}), .b(MEM_PC), .eq(comparator_2_eq));  // open: gt, lt
  Multiplexer #(.select(2), .width(8), .disabled("Z"), .enable("false")) multiplexer_19 (
    .in0(W[7:0]), .in1(W[15:8]), .in2(W[23:16]), .in3(W[31:24]), .out(multiplexer_19_out), .sel(WB_AluR[1:0]));
  and and_12 (OK, d_ff_2_q, ~comparator_2_eq);  // AND_Gate
  Comparator #(.width(32), .mode("twosComplement")) comparator_3 (
    .a(mem_wb_1_out_22), .b(32'h22), .eq(comparator_3_eq));  // open: gt, lt
  Multiplexer #(.select(1), .width(1), .disabled("Z"), .enable("false")) multiplexer_20 (
    .in0(1'b0), .in1(comparator_3_eq), .out(multiplexer_20_out), .sel(mem_wb_1_out_23));
  or or_15 (\运行 , Go, multiplexer_20_out, ~mem_wb_1_out_23);  // OR_Gate
  Register #(.width(32), .trigger("rising"), .Select("low")) register_3 (
    .D(a0), .en(multiplexer_20_out), .Q(LedData), .clk(CLK));  // open: clr
  not not_3 (STALL, \运行 );

  // Other names for the same wires on the sheet: J_JAL_PC[27:2] = IR_2[25:0]; Next_PC_1[31:0] = ID_PC;
  //   Next_PC_2[31:0] = EX_PC; Next_PC_3[31:0] = MEM_PC; PC__EPC[31:0] = MEM_PC; WB_PC[31:0] = Next_PC_4

  // Notes on the sheet:
  //   中断源
  //   中断等待指示
  //   总复位信号应将除ROM以外所有存储组件全部清零
  //   数码管输出
  //   数码管输出应该用寄存器锁存，否则显示数据只能一闪而过
  //   发生中断时，中断源的序号便存储到寄存器中
  //   指令存储器
  //   指令字
  //   contents of rom_1 (hex, n*v repeats v):
  //   80000d6 23bdfffc afa10000 23bdfffc afa20000 23bdfffc afa30000 23bdfffc afa40000 23bdfffc afa50000
  //   23bdfffc afa60000 23bdfffc afb00000 23bdfffc afb10000 23bdfffc afb30000 23bdfffc afb40000 23bdfffc
  //   afb50000 23bdfffc afb60000 23bdfffc afa10000 23bdfffc afa20000 20010003 20030001 20160001 20140006
  //   20150001 168020 108100 2149825 132020 20020022 c 1600fffa 295a022 1680fff7 8fa20000 23bd0004
  //   8fa10000 23bd0004 8fb60000 23bd0004 8fb50000 23bd0004 8fb40000 23bd0004 8fb30000 23bd0004 8fb10000
  //   23bd0004 8fb00000 23bd0004 8fa60000 23bd0004 8fa50000 23bd0004 8fa40000 23bd0004 8fa30000 23bd0004
  //   8fa20000 23bd0004 8fa10000 23bd0004 42000018 23bdfffc afa10000 23bdfffc afa20000 23bdfffc afa30000
  //   23bdfffc afa40000 23bdfffc afa50000 23bdfffc afa60000 23bdfffc afb00000 23bdfffc afb10000 23bdfffc
  //   afb30000 23bdfffc afb40000 23bdfffc afb50000 23bdfffc afb60000 23bdfffc afa10000 23bdfffc afa20000
  //   20010007 20030001 20160002 20140006 20150001 168020 108100 2149825 132020 20020022 c 1600fffa
  //   295a022 1680fff7 8fa20000 23bd0004 8fa10000 23bd0004 8fb60000 23bd0004 8fb50000 23bd0004 8fb40000
  //   23bd0004 8fb30000 23bd0004 8fb10000 23bd0004 8fb00000 23bd0004 8fa60000 23bd0004 8fa50000 23bd0004
  //   8fa40000 23bd0004 8fa30000 23bd0004 8fa20000 23bd0004 8fa10000 23bd0004 42000018 23bdfffc afa10000
  //   23bdfffc afa20000 23bdfffc afa30000 23bdfffc afa40000 23bdfffc afa50000 23bdfffc afa60000 23bdfffc
  //   afb00000 23bdfffc afb10000 23bdfffc afb30000 23bdfffc afb40000 23bdfffc afb50000 23bdfffc afb60000
  //   23bdfffc afa10000 23bdfffc afa20000 2001000f 20030001 20160003 20140006 20150001 168020 108100
  //   2149825 132020 20020022 c 1600fffa 295a022 1680fff7 8fa20000 23bd0004 8fa10000 23bd0004 8fb60000
  //   23bd0004 8fb50000 23bd0004 8fb40000 23bd0004 8fb30000 23bd0004 8fb10000 23bd0004 8fb00000 23bd0004
  //   8fa60000 23bd0004 8fa50000 23bd0004 8fa40000 23bd0004 8fa30000 23bd0004 8fa20000 23bd0004 8fa10000
  //   23bd0004 42000018 20110200 20020022 112020 c 2231ffff 1620fffc 4*0 2002000a c 2002000a c
  //   为方便自动评测，需要输出PC，IR，寄存器文件写入端口RDin，内存写入端口MDin等信号
  //   OP
  //   rs
  //   指令字
  //   rt
  //   Func
  //   rd
  //   JAL
  //   RegDst
  //   Syscall
  //   JR
  //   JMP
  //   LUI
  //   BLEZ
  //   LB
  //   Beq
  //   Bne
  //   MemToReg
  //   MemWrite
  //   AluOP
  //   AluSrcB
  //   RegWrite
  //   W#
  //   LUI
  //   BLEZ
  //   LB
  //   Beq
  //   Bne
  //   MemToReg
  //   MemWrite
  //   AluOP
  //   AluSrcB
  //   RegWrite
  //   W#
  //   流水调试日志用
  //   MemToReg
  //   MemWrite
  //   RegWrite
  //   LUI
  //   LUI
  //   LB
  //   LB
  //   W#
  //   W#
  //   LUI
  //   LB
  //   MemToReg
  //   RegWrite
  //   W#
endmodule

module \重定向流水线_动态分支预测  (
  output RegWrite,
  output MemWrite,
  output [31:0] PC,
  output [31:0] IR,
  output [31:0] RDin,
  output [31:0] MDin
);

  wire and_1_out, and_2_out, and_3_out, and_4_out, and_5_out, and_7_out, B___De, BLEZ, BLEZ_DE,
       BracnhConflict, branch, CLK, comparator_1_gt, comparator_2_eq, DataConflict, EX_CerJump, EX_Con,
       EX_Have, ex_mem_1_out_18, ex_mem_1_out_19, ex_mem_1_out_20, ex_mem_1_out_21, ex_mem_1_out_24,
       EX_ProJump, EX_RegWrite, \EX_条件跳转 , Go, id_ex_1_out_31, id_ex_1_out_33, id_ex_1_out_34,
       id_ex_1_out_35, id_ex_1_out_36, id_ex_1_out_37, id_ex_1_out_39, id_ex_1_out_41, ID_Have, IR1, IR2,
       IR3, JAL_1, JAL_2, JAL_3, JAL_4, JMP, JR, LoadUse, LUI, MEM_RegWrite, mem_wb_1_out_19,
       mem_wb_1_out_20, mem_wb_1_out_23, mips_alu_1_equal, multiplexer_23_out, NewClear, not_1_out,
       not_2_out, or_5_out, or_6_out, or_8_out, or_12_out, R1_U, R2_U, RegWrite_1, RST, SignedExt, STALL, W1,
       W2, W3, \拓展单周期硬布线控制器_31_1_alu_src , \拓展单周期硬布线控制器_31_1_beq , \拓展单周期硬布线控制器_31_1_blez ,
       \拓展单周期硬布线控制器_31_1_bne , \拓展单周期硬布线控制器_31_1_jmp , \拓展单周期硬布线控制器_31_1_jr , \拓展单周期硬布线控制器_31_1_lb ,
       \拓展单周期硬布线控制器_31_1_lui , \拓展单周期硬布线控制器_31_1_memtoreg , \拓展单周期硬布线控制器_31_1_memwrite ,
       \拓展单周期硬布线控制器_31_1_regwrite , \拓展单周期硬布线控制器_31_1_syscall , \数据相关检测_24_3_2_1_mem相关 , \运行 ;
  wire [0:0] or_2_out, \拓展单周期硬布线控制器_31_1_regdst ;
  wire [1:0] \bh表_1_双预测位输出 , \EX_双位预测 , \ID_双位预测 , multiplexer_3_out, multiplexer_4_out, \双位预测状态机_1_新的状态位 ;
  wire [2:0] if_id_1_out_11;
  wire [3:0] id_ex_1_out_38, relation, relation_1, \拓展单周期硬布线控制器_31_1_alu_op ;
  wire [4:0] EX_WriteReg_num, id_ex_1_out_47, MEM_WriteReg_num, multiplexer_11_out, R1_num, R2_num, W_num;
  wire [7:0] multiplexer_22_out;
  wire [15:0] \LoadUse次数 , \总周期数 , \插入气泡数 , \无条件分支数 , \条件分支成功数 ;
  wire [27:0] adder_4_out;
  wire [31:0] a0, adder_1_out, adder_3_out, adder_6_out, B___PC, \bh表_1_分支目标地址_2 , bit_extender_1_out,
       bit_extender_2_out, bit_extender_3_out, Din, ex_mem_1_out_23, ex_mem_1_out_28, ex_mem_1_out_30,
       EX_NPC, EX_PC, id_ex_1_out_44, id_ex_1_out_45, id_ex_1_out_46, id_ex_1_out_49, ID_NPC, ID_PC,
       if_id_1_out_10, IR_1, IR_2, IR_3, IR_4, JR_PC, LedData, MEM_AluR, MEM_PC, mem_wb_1_out_22,
       mem_wb_1_out_30, mips_alu_1_result, mips_regifile_1_r1, mips_regifile_1_r2, multiplexer_1_out,
       multiplexer_5_out, multiplexer_7_out, multiplexer_10_out, multiplexer_12_out, multiplexer_16_out,
       multiplexer_17_out, multiplexer_19_out, multiplexer_20_out, Next_PC, Next_PC_4, NPC_R, ram_1_data,
       rom_1_data, shifter_1_out, W, WB_AluR, WB_Read;
  wire [31:28] J_JAL_PC;

  Clock #(.highDuration(1), .lowDuration(1)) clock_1 (.out(CLK));
  Button _1 (.out(IR1));
  Button _2 (.out(IR2));
  Button _3 (.out(IR3));
  Button \u_继续运行  (.out(Go));
  LED #(.active("true")) led_1 (.in(W1));
  LED #(.active("true")) led_2 (.in(W2));
  LED #(.active("true")) led_3 (.in(W3));
  Hex_Digit_Display hex_digit_display_1 (.value(LedData[31:28]));  // open: dp
  Button \u_清零  (.out(RST));
  or or_1 (\EX_条件跳转 , BLEZ_DE, B___De);
  Multiplexer #(.select(1), .width(32), .disabled("Z"), .enable("false")) multiplexer_1 (
    .in0(Next_PC), .in1(adder_1_out), .out(multiplexer_1_out), .sel(NewClear));
  Adder #(.width(32)) adder_1 (.a(EX_PC), .b(32'h4), .out(adder_1_out));  // open: cin, cout
  Hex_Digit_Display hex_digit_display_2 (.value(LedData[23:20]));  // open: dp
  Hex_Digit_Display hex_digit_display_3 (.value(LedData[27:24]));  // open: dp
  or or_2 (or_2_out[0], JR, BLEZ_DE, B___De);
  Multiplexer #(.select(2), .width(32), .disabled("Z"), .enable("false")) multiplexer_2 (
    .in0(multiplexer_1_out), .in1(B___PC), .in2({J_JAL_PC, IR_2[25:0], 2'b00}), .in3(JR_PC), .out(NPC_R),
    .sel({JMP, or_2_out[0]}));
  Hex_Digit_Display hex_digit_display_4 (.value(LedData[15:12]));  // open: dp
  Hex_Digit_Display hex_digit_display_5 (.value(LedData[19:16]));  // open: dp
  or or_3 (branch, BLEZ_DE, B___De);
  or or_4 (EX_CerJump, JMP, or_2_out[0]);
  and and_1 (and_1_out, ~LoadUse, \运行 );  // AND_Gate
  Hex_Digit_Display hex_digit_display_6 (.value(LedData[7:4]));  // open: dp
  Hex_Digit_Display hex_digit_display_7 (.value(LedData[11:8]));  // open: dp
  Register #(.width(32), .trigger("rising"), .Select("low")) u_PC (
    .D(ID_NPC), .en(and_1_out), .Q(PC), .clk(CLK));  // open: clr
  Multiplexer #(.select(1), .width(2), .disabled("Z"), .enable("false")) multiplexer_3 (
    .in0(2'b10), .in1(2'b11), .out(multiplexer_3_out), .sel(\EX_条件跳转 ));
  Hex_Digit_Display hex_digit_display_8 (.value(LedData[3:0]));  // open: dp
  // Probe on \总周期数 
  Adder #(.width(32)) adder_2 (.a(PC), .b(32'h4), .out(Next_PC));  // open: cin, cout
  \双位预测状态机  \u_双位预测状态机_1  (.\新的状态位 (\双位预测状态机_1_新的状态位 ), .\初始预测位 (\EX_双位预测 ), .\实际跳转情况 (EX_CerJump));
  Counter #(.width(16), .max('hffff), .ongoal("wrap"), .trigger("rising"), .behavior("old")) counter_1 (
    .count(\运行 ), .Q(\总周期数 ), .clk(CLK));  // open: load, D, carry, clr, preset
  ROM #(.addrWidth(10), .dataWidth(32), .Select("high")) rom_1 (.addr(PC[11:2]), .data(rom_1_data));
  Multiplexer #(.select(1), .width(2), .disabled("Z"), .enable("false")) multiplexer_4 (
    .in0(multiplexer_3_out), .in1(\双位预测状态机_1_新的状态位 ), .out(multiplexer_4_out), .sel(EX_Have));
  or or_5 (or_5_out, RST, NewClear);
  IF_ID if_id_1 (
    .in_5(CLK), .in_2(rom_1_data), .in_1(PC), .out_8(ID_PC), .out_9(IR_1), .in_7(or_5_out), .in_6(or_6_out),
    .in_3(ID_NPC), .out_10(if_id_1_out_10), .in_4({ID_Have, \ID_双位预测 }), .out_11(if_id_1_out_11));
  or or_6 (or_6_out, STALL, LoadUse);
  Multiplexer #(.select(1), .width(32), .disabled("Z"), .enable("false")) multiplexer_5 (
    .in0(NPC_R), .in1(EX_NPC), .out(multiplexer_5_out), .sel(EX_Have));
  Adder #(.width(32)) adder_3 (.a(PC), .b(32'h4), .out(adder_3_out));  // open: cin, cout
  \BH表  \bh表_1  (
    .EX_PC(EX_PC), .\分支目标地址 (multiplexer_5_out), .IF_PC(PC), .\双预测位 (multiplexer_4_out), .CLK(CLK),
    .Have(ID_Have), .\分支目标地址_2 (\bh表_1_分支目标地址_2 ), .\双预测位输出 (\bh表_1_双预测位输出 ), .BlkDataReady(EX_ProJump));
  \数据相关检测_24_3_2  \u_数据相关检测_24_3_2_1  (
    .EX_RegWrite(EX_RegWrite), .R1_num(R1_num), .EX_WriteReg_num(EX_WriteReg_num),
    .MEM_RegWrite(MEM_RegWrite), .R2_num(R2_num), .MEM_WriteReg_num(MEM_WriteReg_num), .R1_Used(R1_U),
    .R2_Used(R2_U), .\MEM相关 (\数据相关检测_24_3_2_1_mem相关 ), .\EX相关 (EX_Con), .R1_MEM(relation));
  \拓展单周期硬布线控制器_31  \u_拓展单周期硬布线控制器_31_1  (
    .OP(IR_1[31:26]), .Func(IR_1[5:0]), .ALU_OP(\拓展单周期硬布线控制器_31_1_alu_op ),
    .MemToReg(\拓展单周期硬布线控制器_31_1_memtoreg ), .MemWrite(\拓展单周期硬布线控制器_31_1_memwrite ),
    .ALU_SRC(\拓展单周期硬布线控制器_31_1_alu_src ), .RegWrite(\拓展单周期硬布线控制器_31_1_regwrite ),
    .SysCALL(\拓展单周期硬布线控制器_31_1_syscall ), .SignedExt(SignedExt), .RegDst(\拓展单周期硬布线控制器_31_1_regdst [0]),
    .Beq(\拓展单周期硬布线控制器_31_1_beq ), .Bne(\拓展单周期硬布线控制器_31_1_bne ), .JR(\拓展单周期硬布线控制器_31_1_jr ),
    .JMP(\拓展单周期硬布线控制器_31_1_jmp ), .JAL(JAL_1), .LUI(\拓展单周期硬布线控制器_31_1_lui ), .LB(\拓展单周期硬布线控制器_31_1_lb ),
    .BLEZ(\拓展单周期硬布线控制器_31_1_blez ), .R1_Used(R1_U), .R2_Used(R2_U));  // open: MFC0, MTC0, ERET, M
  Multiplexer #(.select(1), .width(2), .disabled("Z"), .enable("false")) multiplexer_6 (
    .in0(2'b00), .in1(\bh表_1_双预测位输出 ), .out(\ID_双位预测 ), .sel(ID_Have));
  Multiplexer #(.select(2), .width(32), .disabled("Z"), .enable("false")) multiplexer_7 (
    .in0(adder_3_out), .in1(adder_3_out), .in2(\bh表_1_分支目标地址_2 ), .in3(\bh表_1_分支目标地址_2 ),
    .out(multiplexer_7_out), .sel(\bh表_1_双预测位输出 ));
  or or_7 (DataConflict, EX_Con, \数据相关检测_24_3_2_1_mem相关 );
  Multiplexer #(.select(1), .width(5), .disabled("Z"), .enable("false")) multiplexer_8 (
    .in0(IR_1[25:21]), .in1(5'b00010), .out(R1_num), .sel(\拓展单周期硬布线控制器_31_1_syscall ));
  Multiplexer #(.select(1), .width(5), .disabled("Z"), .enable("false")) multiplexer_9 (
    .in0(IR_1[20:16]), .in1(5'b00100), .out(R2_num), .sel(\拓展单周期硬布线控制器_31_1_syscall ));
  assign bit_extender_1_out = {{16{1'b0}}, IR_1[15:0]};  // Bit_Extender bit_extender_1
  assign bit_extender_2_out = {{16{IR_1[15]}}, IR_1[15:0]};  // Bit_Extender bit_extender_2
  Multiplexer #(.select(1), .width(32), .disabled("Z"), .enable("false")) multiplexer_10 (
    .in0(adder_3_out), .in1(multiplexer_7_out), .out(multiplexer_10_out), .sel(ID_Have));
  Multiplexer #(.select(2), .width(5), .disabled("Z"), .enable("false")) multiplexer_11 (
    .in0(IR_1[20:16]), .in1(IR_1[15:11]), .in2({5{1'b1}}), .out(multiplexer_11_out),
    .sel({JAL_1, \拓展单周期硬布线控制器_31_1_regdst [0]}));  // open: in3
  Multiplexer #(.select(1), .width(32), .disabled("Z"), .enable("false")) multiplexer_12 (
    .in0(bit_extender_1_out), .in1(bit_extender_2_out), .out(multiplexer_12_out), .sel(SignedExt));
  Multiplexer #(.select(1), .width(32), .disabled("Z"), .enable("false")) multiplexer_13 (
    .in0(multiplexer_10_out), .in1(NPC_R), .out(ID_NPC), .sel(NewClear));
  xor xor_1 (NewClear, \EX_双位预测 [1], EX_CerJump);
  // Probe on \总周期数 
  // Probe on \无条件分支数 
  // Probe on \条件分支成功数 
  // Probe on \插入气泡数 
  // Probe on \LoadUse次数 
  MIPS_Regifile mips_regifile_1 (
    .Din(Din), .Clk(CLK), .R1(mips_regifile_1_r1), .R2(mips_regifile_1_r2), .WE(RegWrite_1), .W_num(W_num),
    .R1_num(R1_num), .R2_num(R2_num));
  // Probe on PC[11:0]
  // Probe on EX_PC[11:0]
  // Probe on ID_PC[11:0]
  or or_8 (or_8_out, RST, NewClear, LoadUse);
  ID_EX id_ex_1 (
    .in_1(\拓展单周期硬布线控制器_31_1_jr ), .in_4(\拓展单周期硬布线控制器_31_1_blez ), .in_5(\拓展单周期硬布线控制器_31_1_lb ),
    .in_6(\拓展单周期硬布线控制器_31_1_beq ), .in_7(\拓展单周期硬布线控制器_31_1_bne ), .in_8(\拓展单周期硬布线控制器_31_1_memtoreg ),
    .in_9(\拓展单周期硬布线控制器_31_1_memwrite ), .in_10(\拓展单周期硬布线控制器_31_1_alu_op ),
    .in_11(\拓展单周期硬布线控制器_31_1_alu_src ), .in_12(\拓展单周期硬布线控制器_31_1_regwrite ),
    .in_13(\拓展单周期硬布线控制器_31_1_syscall ), .in_14(ID_PC), .in_15(IR_1), .in_16(mips_regifile_1_r1),
    .in_17(mips_regifile_1_r2), .in_18(multiplexer_12_out), .in_19(IR_1[10:6]), .in_20(multiplexer_11_out),
    .in_21({IR_1[15:0], {16{1'b0}}}), .out_29(JR), .out_30(JMP), .out_31(id_ex_1_out_31), .out_32(BLEZ),
    .out_33(id_ex_1_out_33), .out_34(id_ex_1_out_34), .out_35(id_ex_1_out_35), .out_36(id_ex_1_out_36),
    .out_37(id_ex_1_out_37), .out_40(EX_RegWrite), .out_41(id_ex_1_out_41), .out_42(EX_PC),
    .out_38(id_ex_1_out_38), .out_39(id_ex_1_out_39), .out_43(IR_2), .out_44(id_ex_1_out_44),
    .out_45(id_ex_1_out_45), .out_46(id_ex_1_out_46), .out_47(id_ex_1_out_47), .out_48(EX_WriteReg_num),
    .out_49(id_ex_1_out_49), .in_26(CLK), .in_3(\拓展单周期硬布线控制器_31_1_lui ), .in_2(\拓展单周期硬布线控制器_31_1_jmp ),
    .in_27(STALL), .in_28(or_8_out), .out_51(JAL_2), .in_23(JAL_1), .in_22(relation), .out_50(relation_1),
    .in_24(if_id_1_out_10), .out_52(EX_NPC), .in_25(if_id_1_out_11), .out_53({EX_Have, \EX_双位预测 }));
  // Probe on MEM_PC[11:0]
  or or_9 (EX_ProJump, JR, JMP, BLEZ, id_ex_1_out_34, id_ex_1_out_35, JAL_2);
  // Probe on Next_PC_4[11:0]
  Multiplexer #(.select(1), .width(1), .disabled("Z"), .enable("false")) multiplexer_14 (
    .in0(1'b0), .in1(id_ex_1_out_36), .out(LoadUse), .sel(EX_Con));
  Adder #(.width(32)) adder_4 (.a(EX_PC), .b(32'h4), .out({J_JAL_PC, adder_4_out}));  // open: cin, cout
  Multiplexer #(.select(2), .width(32), .disabled("Z"), .enable("false")) multiplexer_15 (
    .in0(id_ex_1_out_44), .in1(MEM_AluR), .in2(W), .in3(MEM_AluR), .out(JR_PC), .sel(relation_1[1:0]));
  Multiplexer #(.select(2), .width(32), .disabled("Z"), .enable("false")) multiplexer_16 (
    .in0(id_ex_1_out_45), .in1(MEM_AluR), .in2(W), .in3(MEM_AluR), .out(multiplexer_16_out),
    .sel(relation_1[3:2]));
  Multiplexer #(.select(1), .width(32), .disabled("Z"), .enable("false")) multiplexer_17 (
    .in0(multiplexer_16_out), .in1(id_ex_1_out_46), .out(multiplexer_17_out), .sel(id_ex_1_out_39));
  Shifter #(.width(32), .shift("ll")) shifter_1 (.in(id_ex_1_out_46), .\dist (5'b00010), .out(shifter_1_out));
  MIPS_ALU mips_alu_1 (
    .X(JR_PC), .Y(multiplexer_17_out), .AluOP(id_ex_1_out_38), .Equal(mips_alu_1_equal),
    .Result(mips_alu_1_result), .shamt(id_ex_1_out_47));  // open: Result_2
  or or_10 (BracnhConflict, JMP, JR, B___De, BLEZ_DE);
  not not_1 (not_1_out, mips_alu_1_equal);
  Adder #(.width(32)) adder_5 (.a(shifter_1_out), .b({J_JAL_PC, adder_4_out}), .out(B___PC));  // open: cin, cout
  and and_2 (and_2_out, mips_alu_1_equal, id_ex_1_out_34);
  and and_3 (and_3_out, not_1_out, id_ex_1_out_35);
  Comparator #(.width(32), .mode("twosComplement")) comparator_1 (
    .a(JR_PC), .b({32{1'b0}}), .gt(comparator_1_gt));  // open: eq, lt
  and and_4 (and_4_out, JMP, ~STALL);  // AND_Gate
  or or_11 (B___De, and_2_out, and_3_out);
  not not_2 (not_2_out, comparator_1_gt);
  Counter #(.width(16), .max('hffff), .ongoal("wrap"), .trigger("rising"), .behavior("new")) counter_2 (
    .count(and_4_out), .Q(\无条件分支数 ), .clk(CLK), .clr(RST));  // open: load, D, carry, preset, down
  and and_5 (and_5_out, branch, ~STALL);  // AND_Gate
  and and_6 (BLEZ_DE, BLEZ, not_2_out);
  // Probe on mips_alu_1_result
  Counter #(.width(16), .max('hffff), .ongoal("wrap"), .trigger("rising"), .behavior("new")) counter_3 (
    .count(and_5_out), .Q(\条件分支成功数 ), .clk(CLK), .clr(RST));  // open: load, D, carry, preset, down
  Counter #(.width(16), .max('hffff), .ongoal("wrap"), .trigger("rising"), .behavior("new")) counter_4 (
    .count(and_7_out), .Q(\插入气泡数 ), .clk(CLK), .clr(RST));  // open: load, D, carry, preset, down
  and and_7 (and_7_out, or_12_out, \运行 );
  or or_12 (or_12_out, STALL, LoadUse);
  Counter #(.width(16), .max('hffff), .ongoal("wrap"), .trigger("rising"), .behavior("new")) counter_5 (
    .count(and_7_out), .Q(\LoadUse次数 ), .clr(RST));  // open: load, D, carry, clk, preset, down
  EX_MEM ex_mem_1 (
    .in_1(id_ex_1_out_31), .out_18(ex_mem_1_out_18), .in_2(id_ex_1_out_33), .out_19(ex_mem_1_out_19),
    .in_3(id_ex_1_out_36), .out_20(ex_mem_1_out_20), .in_4(id_ex_1_out_37), .out_21(ex_mem_1_out_21),
    .in_8(EX_PC), .out_25(MEM_PC), .in_9(IR_2), .out_26(IR_3), .in_10(mips_alu_1_result), .out_27(MEM_AluR),
    .in_11(multiplexer_16_out), .out_28(ex_mem_1_out_28), .in_12(EX_WriteReg_num), .out_29(MEM_WriteReg_num),
    .in_13(id_ex_1_out_49), .out_30(ex_mem_1_out_30), .in_15(CLK), .in_5(EX_RegWrite), .out_22(MEM_RegWrite),
    .in_16(STALL), .in_17(RST), .in_6(JR_PC), .out_23(ex_mem_1_out_23), .in_7(id_ex_1_out_41),
    .out_24(ex_mem_1_out_24), .in_14(JAL_2), .out_31(JAL_3));
  RAM #(.addrWidth(10), .dataWidth(32), .bus("separate"), .Select("high")) ram_1 (
    .addr(MEM_AluR[11:2]), .din(ex_mem_1_out_28), .data(ram_1_data), .str(ex_mem_1_out_21), .clk(CLK));  // open: sel, ld, clr
  Multiplexer #(.select(1), .width(32), .disabled("Z"), .enable("false")) multiplexer_18 (
    .in0(multiplexer_19_out), .in1(adder_6_out), .out(Din), .sel(JAL_4));
  Multiplexer #(.select(1), .width(32), .disabled("Z"), .enable("false")) multiplexer_19 (
    .in0(multiplexer_20_out), .in1(mem_wb_1_out_30), .out(multiplexer_19_out), .sel(LUI));
  Adder #(.width(32)) adder_6 (.a(Next_PC_4), .b(32'h4), .out(adder_6_out));  // open: cin, cout
  MEM_WB mem_wb_1 (
    .in_1(ex_mem_1_out_18), .out_18(LUI), .in_2(ex_mem_1_out_19), .out_19(mem_wb_1_out_19),
    .in_3(ex_mem_1_out_20), .out_20(mem_wb_1_out_20), .in_4(MEM_RegWrite), .out_21(RegWrite_1),
    .in_7(MEM_PC), .out_24(Next_PC_4), .in_8(IR_3), .out_25(IR_4), .in_9(MEM_AluR), .out_26(WB_AluR),
    .in_10(ram_1_data), .out_27(WB_Read), .in_12(MEM_WriteReg_num), .out_29(W_num), .in_13(ex_mem_1_out_30),
    .out_30(mem_wb_1_out_30), .in_15(CLK), .in_16(STALL), .in_5(ex_mem_1_out_23), .out_22(mem_wb_1_out_22),
    .in_6(ex_mem_1_out_24), .out_23(mem_wb_1_out_23), .in_11(ex_mem_1_out_28), .out_28(a0), .in_17(RST),
    .in_14(JAL_3), .out_31(JAL_4));
  Multiplexer #(.select(1), .width(32), .disabled("Z"), .enable("false")) multiplexer_20 (
    .in0(W), .in1(bit_extender_3_out), .out(multiplexer_20_out), .sel(mem_wb_1_out_19));
  Multiplexer #(.select(1), .width(32), .disabled("Z"), .enable("false")) multiplexer_21 (
    .in0(WB_AluR), .in1(WB_Read), .out(W), .sel(mem_wb_1_out_20));
  assign bit_extender_3_out = {{24{multiplexer_22_out[7]}}, multiplexer_22_out};  // Bit_Extender bit_extender_3
  Multiplexer #(.select(2), .width(8), .disabled("Z"), .enable("false")) multiplexer_22 (
    .in0(W[7:0]), .in1(W[15:8]), .in2(W[23:16]), .in3(W[31:24]), .out(multiplexer_22_out), .sel(WB_AluR[1:0]));
  Comparator #(.width(32), .mode("twosComplement")) comparator_2 (
    .a(mem_wb_1_out_22), .b(32'h22), .eq(comparator_2_eq));  // open: gt, lt
  Multiplexer #(.select(1), .width(1), .disabled("Z"), .enable("false")) multiplexer_23 (
    .in0(1'b0), .in1(comparator_2_eq), .out(multiplexer_23_out), .sel(mem_wb_1_out_23));
  or or_13 (\运行 , Go, multiplexer_23_out, ~mem_wb_1_out_23);  // OR_Gate
  Register #(.width(32), .trigger("rising"), .Select("low")) register_1 (
    .D(a0), .en(multiplexer_23_out), .Q(LedData), .clk(CLK));  // open: clr
  not not_3 (STALL, \运行 );

  // Other names for the same wires on the sheet: IF_PC[31:0] = PC; J_JAL_PC[27:2] = IR_2[25:0];
  //   Next_PC_1[31:0] = ID_PC; Next_PC_2[31:0] = EX_PC; Next_PC_3[31:0] = MEM_PC; WB_PC[31:0] = Next_PC_4

  // Notes on the sheet:
  //   中断源
  //   中断等待指示
  //   总复位信号应将除ROM以外所有存储组件全部清零
  //   数码管输出
  //   数码管输出应该用寄存器锁存，否则显示数据只能一闪而过
  //   指令存储器
  //   指令字
  //   contents of rom_1 (hex, n*v repeats v):
  //   20110001 8000c05 20110001 20120002 20130003 8000c09 20110001 20120002 20130003 8000c0d 20110001
  //   20120002 20130003 8000c11 20110001 20120002 20130003 c000cb8 20100001 20110001 118fc0 112020
  //   20020022 c 118882 12200001 8000c15 112020 20020022 c 20110001 118880 112020 20020022 c 12200001
  //   8000c1f 20110001 118fc0 112020 20020022 c 1188c3 112020 20020022 c 118903 112020 20020022 c 118903
  //   112020 20020022 c 118903 112020 20020022 c 118903 112020 20020022 c 118903 112020 20020022 c 118903
  //   112020 20020022 c 118903 112020 20020022 c 20100001 109fc0 139fc3 8021 2012000c 24160003 26100001
  //   3210000f 20080008 20090001 139900 2709825 132020 20020022 c 1094022 1500fff9 22100001 2018000f
  //   2188024 108700 20080008 20090001 139902 2709825 132021 20020022 c 1094022 1500fff9 108702 2c9b022
  //   12c00001 8000c50 4020 1084027 84400 3508ffff 82021 20020022 c 2010ffff 20110000 ae300000 22100001
  //   22310004 ae300000 22100001 22310004 ae300000 22100001 22310004 ae300000 22100001 22310004 ae300000
  //   22100001 22310004 ae300000 22100001 22310004 ae300000 22100001 22310004 ae300000 22100001 22310004
  //   ae300000 22100001 22310004 ae300000 22100001 22310004 ae300000 22100001 22310004 ae300000 22100001
  //   22310004 ae300000 22100001 22310004 ae300000 22100001 22310004 ae300000 22100001 22310004 ae300000
  //   22100001 22310004 22100001 8020 2011003c 8e130000 8e340000 274402a 11000002 ae330000 ae140000
  //   2231fffc 1611fff8 102020 20020022 c 22100004 2011003c 1611fff2 20020032 c 20100000 22100001 102020
  //   20020022 c 22100002 102020 20020022 c 22100003 102020 20020022 c 22100004 102020 20020022 c 22100005
  //   102020 20020022 c 22100006 102020 20020022 c 22100007 102020 20020022 c 22100008 102020 20020022
  //   20020022 c 3e00008
  //   为方便自动评测，需要输出PC，IR，寄存器文件写入端口RDin，内存写入端口MDin等信号
  //   OP
  //   rs
  //   指令字
  //   rt
  //   Func
  //   rd
  //   避免取Cache的第一行双位预测
  //   JAL
  //   RegDst
  //   Syscall
  //   预测情况与实际情况相反
  //   JR
  //   JMP
  //   LUI
  //   BLEZ
  //   LB
  //   Beq
  //   Bne
  //   MemToReg
  //   MemWrite
  //   AluOP
  //   AluSrcB
  //   RegWrite
  //   W#
  //   JR
  //   JMP
  //   LUI
  //   BLEZ
  //   LB
  //   Beq
  //   Bne
  //   MemToReg
  //   MemWrite
  //   AluOP
  //   AluSrcB
  //   RegWrite
  //   W#
  //   流水调试日志用
  //   MemToReg
  //   MemWrite
  //   RegWrite
  //   LUI
  //   LUI
  //   LB
  //   LB
  //   W#
  //   W#
  //   LUI
  //   LB
  //   MemToReg
  //   RegWrite
  //   W#
endmodule

module \BH表  (
  input  [31:0] EX_PC,
  input  [31:0] \分支目标地址 ,
  input  [31:0] IF_PC,
  input  [1:0] \双预测位 ,
  input  BlkDataReady,
  input  CLK,
  output Have,
  output [31:0] \分支目标地址_2 ,
  output [1:0] \双预测位输出 
);

  wire and_9_out, comparator_1_eq, comparator_2_eq, comparator_3_eq, comparator_4_eq, comparator_5_eq,
       comparator_6_eq, comparator_7_eq, comparator_8_eq, comparator_9_eq, comparator_10_eq,
       comparator_11_eq, comparator_12_eq, comparator_13_eq, comparator_14_eq, comparator_15_eq,
       comparator_16_eq, decoder_1_out0, decoder_1_out1, decoder_1_out2, decoder_1_out3, decoder_1_out4,
       decoder_1_out5, decoder_1_out6, decoder_1_out7, not_1_out, not_2_out, not_3_out, not_4_out, not_5_out,
       not_6_out, not_7_out, not_8_out, priority_encoder_1_gs, priority_encoder_2_gs, S0, S1, S2, S3, S4, S5,
       S6, S7, Shoot, V0, V1, V2, V3, V4, V5, V6, V7, W0, W1, W2, W3, W4, W5, W6, W7, Write0, Write1, Write2,
       Write3, Write4, Write5, Write6, Write7;
  wire [1:0] \双预测位输出0 , \双预测位输出1 , \双预测位输出2 , \双预测位输出3 , \双预测位输出4 , \双预测位输出5 , \双预测位输出6 , \双预测位输出7 ;
  wire [2:0] \max2_归并比较_1_max_num , \max2_归并比较_2_max_num , \max2_归并比较_3_max_num , \max2_归并比较_4_max_num ,
       \max2_归并比较_5_max_num , \max2_归并比较_6_max_num , \max2_归并比较_7_max_num , multiplexer_1_out,
       multiplexer_2_out, priority_encoder_1_out, priority_encoder_2_out;
  wire [15:0] LRU0, LRU1, LRU2, LRU3, LRU4, LRU5, LRU6, LRU7, \max2_归并比较_1_max , \max2_归并比较_2_max ,
       \max2_归并比较_3_max , \max2_归并比较_4_max , \max2_归并比较_5_max , \max2_归并比较_6_max ;
  wire [31:0] Tag0, Tag1, Tag2, Tag3, Tag4, Tag5, Tag6, Tag7, \分支地址输出0 , \分支地址输出1 , \分支地址输出2 , \分支地址输出3 ,
       \分支地址输出4 , \分支地址输出5 , \分支地址输出6 , \分支地址输出7 ;

  Register #(.width(1), .trigger("rising"), .Select("low")) valid (
    .D(1'b1), .en(Write0), .Q(V0), .clk(CLK));  // open: clr
  Register #(.width(1), .trigger("rising"), .Select("low")) valid_2 (
    .D(1'b1), .en(Write1), .Q(V1), .clk(CLK));  // open: clr
  Register #(.width(1), .trigger("rising"), .Select("low")) valid_3 (
    .D(1'b1), .en(Write2), .Q(V2), .clk(CLK));  // open: clr
  Register #(.width(1), .trigger("rising"), .Select("low")) valid_4 (
    .D(1'b1), .en(Write3), .Q(V3), .clk(CLK));  // open: clr
  Register #(.width(1), .trigger("rising"), .Select("low")) valid_5 (
    .D(1'b1), .en(Write4), .Q(V4), .clk(CLK));  // open: clr
  Register #(.width(1), .trigger("rising"), .Select("low")) valid_6 (
    .D(1'b1), .en(Write5), .Q(V5), .clk(CLK));  // open: clr
  Register #(.width(1), .trigger("rising"), .Select("low")) valid_7 (
    .D(1'b1), .en(Write6), .Q(V6), .clk(CLK));  // open: clr
  Register #(.width(1), .trigger("rising"), .Select("low")) valid_8 (
    .D(1'b1), .en(Write7), .Q(V7), .clk(CLK));  // open: clr
  Register #(.width(32), .trigger("rising"), .Select("low")) \u_分支指令地址  (
    .D(EX_PC), .en(Write0), .Q(Tag0), .clk(CLK));  // open: clr
  Register #(.width(32), .trigger("rising"), .Select("low")) \u_分支指令地址_2  (
    .D(EX_PC), .en(Write1), .Q(Tag1), .clk(CLK));  // open: clr
  Register #(.width(32), .trigger("rising"), .Select("low")) \u_分支指令地址_3  (
    .D(EX_PC), .en(Write2), .Q(Tag2), .clk(CLK));  // open: clr
  Register #(.width(32), .trigger("rising"), .Select("low")) \u_分支指令地址_4  (
    .D(EX_PC), .en(Write3), .Q(Tag3), .clk(CLK));  // open: clr
  Register #(.width(32), .trigger("rising"), .Select("low")) \u_分支指令地址_5  (
    .D(EX_PC), .en(Write4), .Q(Tag4), .clk(CLK));  // open: clr
  Register #(.width(32), .trigger("rising"), .Select("low")) \u_分支指令地址_6  (
    .D(EX_PC), .en(Write5), .Q(Tag5), .clk(CLK));  // open: clr
  Register #(.width(32), .trigger("rising"), .Select("low")) \u_分支指令地址_7  (
    .D(EX_PC), .en(Write6), .Q(Tag6), .clk(CLK));  // open: clr
  Register #(.width(32), .trigger("rising"), .Select("low")) \u_分支指令地址_8  (
    .D(EX_PC), .en(Write7), .Q(Tag7), .clk(CLK));  // open: clr
  Register #(.width(32), .trigger("rising"), .Select("low")) \u_分支目标地址  (
    .D(\分支目标地址 ), .en(Write0), .Q(\分支地址输出0 ), .clk(CLK));  // open: clr
  Register #(.width(32), .trigger("rising"), .Select("low")) \u_分支目标地址_2  (
    .D(\分支目标地址 ), .en(Write1), .Q(\分支地址输出1 ), .clk(CLK));  // open: clr
  Register #(.width(32), .trigger("rising"), .Select("low")) \u_分支目标地址_3  (
    .D(\分支目标地址 ), .en(Write2), .Q(\分支地址输出2 ), .clk(CLK));  // open: clr
  Register #(.width(32), .trigger("rising"), .Select("low")) \u_分支目标地址_4  (
    .D(\分支目标地址 ), .en(Write3), .Q(\分支地址输出3 ), .clk(CLK));  // open: clr
  Register #(.width(32), .trigger("rising"), .Select("low")) \u_分支目标地址_5  (
    .D(\分支目标地址 ), .en(Write4), .Q(\分支地址输出4 ), .clk(CLK));  // open: clr
  Register #(.width(32), .trigger("rising"), .Select("low")) \u_分支目标地址_6  (
    .D(\分支目标地址 ), .en(Write5), .Q(\分支地址输出5 ), .clk(CLK));  // open: clr
  Register #(.width(32), .trigger("rising"), .Select("low")) \u_分支目标地址_7  (
    .D(\分支目标地址 ), .en(Write6), .Q(\分支地址输出6 ), .clk(CLK));  // open: clr
  Register #(.width(32), .trigger("rising"), .Select("low")) \u_分支目标地址_8  (
    .D(\分支目标地址 ), .en(Write7), .Q(\分支地址输出7 ), .clk(CLK));  // open: clr
  Register #(.width(2), .trigger("rising"), .Select("low")) \u_双预测位  (
    .D(\双预测位 ), .en(Write0), .Q(\双预测位输出0 ), .clk(CLK));  // open: clr
  Register #(.width(2), .trigger("rising"), .Select("low")) \u_双预测位_2  (
    .D(\双预测位 ), .en(Write1), .Q(\双预测位输出1 ), .clk(CLK));  // open: clr
  Register #(.width(2), .trigger("rising"), .Select("low")) \u_双预测位_3  (
    .D(\双预测位 ), .en(Write2), .Q(\双预测位输出2 ), .clk(CLK));  // open: clr
  Register #(.width(2), .trigger("rising"), .Select("low")) \u_双预测位_4  (
    .D(\双预测位 ), .en(Write3), .Q(\双预测位输出3 ), .clk(CLK));  // open: clr
  Register #(.width(2), .trigger("rising"), .Select("low")) \u_双预测位_5  (
    .D(\双预测位 ), .en(Write4), .Q(\双预测位输出4 ), .clk(CLK));  // open: clr
  Register #(.width(2), .trigger("rising"), .Select("low")) \u_双预测位_6  (
    .D(\双预测位 ), .en(Write5), .Q(\双预测位输出5 ), .clk(CLK));  // open: clr
  Register #(.width(2), .trigger("rising"), .Select("low")) \u_双预测位_7  (
    .D(\双预测位 ), .en(Write6), .Q(\双预测位输出6 ), .clk(CLK));  // open: clr
  Register #(.width(2), .trigger("rising"), .Select("low")) \u_双预测位_8  (
    .D(\双预测位 ), .en(Write7), .Q(\双预测位输出7 ), .clk(CLK));  // open: clr
  not not_1 (not_1_out, W0);
  not not_2 (not_2_out, W1);
  not not_3 (not_3_out, W2);
  not not_4 (not_4_out, W3);
  not not_5 (not_5_out, W4);
  not not_6 (not_6_out, W5);
  not not_7 (not_7_out, W6);
  not not_8 (not_8_out, W7);
  Counter #(.width(16), .max('hffff), .ongoal("wrap"), .trigger("rising"), .behavior("old")) \u_淘汰标志位  (
    .count(not_1_out), .Q(LRU0), .clk(CLK), .clr(W0));  // open: load, D, carry, preset
  Counter #(.width(16), .max('hffff), .ongoal("wrap"), .trigger("rising"), .behavior("old")) \u_淘汰标志位_2  (
    .count(not_2_out), .Q(LRU1), .clk(CLK), .clr(W1));  // open: load, D, carry, preset
  Counter #(.width(16), .max('hffff), .ongoal("wrap"), .trigger("rising"), .behavior("old")) \u_淘汰标志位_3  (
    .count(not_3_out), .Q(LRU2), .clk(CLK), .clr(W2));  // open: load, D, carry, preset
  Counter #(.width(16), .max('hffff), .ongoal("wrap"), .trigger("rising"), .behavior("old")) \u_淘汰标志位_4  (
    .count(not_4_out), .Q(LRU3), .clk(CLK), .clr(W3));  // open: load, D, carry, preset
  Counter #(.width(16), .max('hffff), .ongoal("wrap"), .trigger("rising"), .behavior("old")) \u_淘汰标志位_5  (
    .count(not_5_out), .Q(LRU4), .clk(CLK), .clr(W4));  // open: load, D, carry, preset
  Counter #(.width(16), .max('hffff), .ongoal("wrap"), .trigger("rising"), .behavior("old")) \u_淘汰标志位_6  (
    .count(not_6_out), .Q(LRU5), .clk(CLK), .clr(W5));  // open: load, D, carry, preset
  Counter #(.width(16), .max('hffff), .ongoal("wrap"), .trigger("rising"), .behavior("old")) \u_淘汰标志位_7  (
    .count(not_7_out), .Q(LRU6), .clk(CLK), .clr(W6));  // open: load, D, carry, preset
  Counter #(.width(16), .max('hffff), .ongoal("wrap"), .trigger("rising"), .behavior("old")) \u_淘汰标志位_8  (
    .count(not_8_out), .Q(LRU7), .clk(CLK), .clr(W7));  // open: load, D, carry, preset
  \Max2_归并比较  \max2_归并比较_1  (
    .Y(LRU1), .X(LRU0), .Y_num(3'b001), .X_num(3'b000), .MAX(\max2_归并比较_1_max ),
    .Max_num(\max2_归并比较_1_max_num ));
  \Max2_归并比较  \max2_归并比较_2  (
    .Y(LRU3), .X(LRU2), .Y_num(3'b011), .X_num(3'b010), .MAX(\max2_归并比较_2_max ),
    .Max_num(\max2_归并比较_2_max_num ));
  \Max2_归并比较  \max2_归并比较_3  (
    .Y(LRU5), .X(LRU4), .Y_num(3'b101), .X_num(3'b100), .MAX(\max2_归并比较_3_max ),
    .Max_num(\max2_归并比较_3_max_num ));
  \Max2_归并比较  \max2_归并比较_4  (
    .Y(LRU7), .X(LRU6), .Y_num(3'b111), .X_num(3'b110), .MAX(\max2_归并比较_4_max ),
    .Max_num(\max2_归并比较_4_max_num ));
  \Max2_归并比较  \max2_归并比较_5  (
    .Y(\max2_归并比较_2_max ), .X(\max2_归并比较_1_max ), .Y_num(\max2_归并比较_2_max_num ),
    .X_num(\max2_归并比较_1_max_num ), .MAX(\max2_归并比较_5_max ), .Max_num(\max2_归并比较_5_max_num ));
  \Max2_归并比较  \max2_归并比较_6  (
    .Y(\max2_归并比较_4_max ), .X(\max2_归并比较_3_max ), .Y_num(\max2_归并比较_4_max_num ),
    .X_num(\max2_归并比较_3_max_num ), .MAX(\max2_归并比较_6_max ), .Max_num(\max2_归并比较_6_max_num ));
  and and_1 (W0, V0, comparator_1_eq);
  Comparator #(.width(32), .mode("twosComplement")) comparator_1 (
    .a(Tag0), .b(EX_PC), .eq(comparator_1_eq));  // open: gt, lt
  and and_2 (W1, V1, comparator_2_eq);
  Comparator #(.width(32), .mode("twosComplement")) comparator_2 (
    .a(Tag1), .b(EX_PC), .eq(comparator_2_eq));  // open: gt, lt
  and and_3 (W2, V2, comparator_3_eq);
  Comparator #(.width(32), .mode("twosComplement")) comparator_3 (
    .a(Tag2), .b(EX_PC), .eq(comparator_3_eq));  // open: gt, lt
  and and_4 (W3, V3, comparator_4_eq);
  Comparator #(.width(32), .mode("twosComplement")) comparator_4 (
    .a(Tag3), .b(EX_PC), .eq(comparator_4_eq));  // open: gt, lt
  and and_5 (W4, V4, comparator_5_eq);
  Comparator #(.width(32), .mode("twosComplement")) comparator_5 (
    .a(Tag4), .b(EX_PC), .eq(comparator_5_eq));  // open: gt, lt
  and and_6 (W5, V5, comparator_6_eq);
  Comparator #(.width(32), .mode("twosComplement")) comparator_6 (
    .a(Tag5), .b(EX_PC), .eq(comparator_6_eq));  // open: gt, lt
  and and_7 (W6, V6, comparator_7_eq);
  Comparator #(.width(32), .mode("twosComplement")) comparator_7 (
    .a(Tag6), .b(EX_PC), .eq(comparator_7_eq));  // open: gt, lt
  and and_8 (W7, V7, comparator_8_eq);
  Comparator #(.width(32), .mode("twosComplement")) comparator_8 (
    .a(Tag7), .b(EX_PC), .eq(comparator_8_eq));  // open: gt, lt
  \Max2_归并比较  \max2_归并比较_7  (
    .Y(\max2_归并比较_6_max ), .X(\max2_归并比较_5_max ), .Y_num(\max2_归并比较_6_max_num ),
    .X_num(\max2_归并比较_5_max_num ), .Max_num(\max2_归并比较_7_max_num ));  // open: MAX
  and and_9 (and_9_out, priority_encoder_1_gs, Shoot);
  Priority_Encoder #(.select(3), .disabled("Z")) priority_encoder_1 (
    .in0(W0), .in1(W1), .in2(W2), .in3(W3), .in4(W4), .in5(W5), .in6(W6), .in7(W7),
    .out(priority_encoder_1_out), .gs(priority_encoder_1_gs));  // open: en_out, en_in
  Decoder #(.select(3), .tristate("false"), .disabled("Z"), .enable("false")) decoder_1 (
    .out0(decoder_1_out0), .out1(decoder_1_out1), .out2(decoder_1_out2), .out3(decoder_1_out3),
    .out4(decoder_1_out4), .out5(decoder_1_out5), .out6(decoder_1_out6), .out7(decoder_1_out7),
    .sel(multiplexer_1_out));
  Multiplexer #(.select(1), .width(3), .disabled("Z"), .enable("false")) multiplexer_1 (
    .in0(\max2_归并比较_7_max_num ), .in1(priority_encoder_1_out), .out(multiplexer_1_out), .sel(and_9_out));
  or or_1 (Shoot, W0, W1, W2, W3, W4, W5, W6, W7);
  and and_10 (Write0, BlkDataReady, decoder_1_out0);
  and and_11 (Write1, BlkDataReady, decoder_1_out1);
  and and_12 (Write2, BlkDataReady, decoder_1_out2);
  and and_13 (Write5, decoder_1_out5, BlkDataReady);
  and and_14 (Write6, decoder_1_out6, BlkDataReady);
  and and_15 (Write7, decoder_1_out7, BlkDataReady);
  and and_16 (Write3, BlkDataReady, decoder_1_out3);
  and and_17 (Write4, decoder_1_out4, BlkDataReady);
  and and_18 (S0, V0, comparator_9_eq);
  Comparator #(.width(32), .mode("twosComplement")) comparator_9 (
    .a(Tag0), .b(IF_PC), .eq(comparator_9_eq));  // open: gt, lt
  and and_19 (S1, V1, comparator_10_eq);
  Comparator #(.width(32), .mode("twosComplement")) comparator_10 (
    .a(Tag1), .b(IF_PC), .eq(comparator_10_eq));  // open: gt, lt
  and and_20 (S2, V2, comparator_11_eq);
  Comparator #(.width(32), .mode("twosComplement")) comparator_11 (
    .a(Tag2), .b(IF_PC), .eq(comparator_11_eq));  // open: gt, lt
  and and_21 (S3, V3, comparator_12_eq);
  Comparator #(.width(32), .mode("twosComplement")) comparator_12 (
    .a(Tag3), .b(IF_PC), .eq(comparator_12_eq));  // open: gt, lt
  and and_22 (S4, V4, comparator_13_eq);
  Comparator #(.width(32), .mode("twosComplement")) comparator_13 (
    .a(Tag4), .b(IF_PC), .eq(comparator_13_eq));  // open: gt, lt
  and and_23 (S5, V5, comparator_14_eq);
  Comparator #(.width(32), .mode("twosComplement")) comparator_14 (
    .a(Tag5), .b(IF_PC), .eq(comparator_14_eq));  // open: gt, lt
  and and_24 (S6, V6, comparator_15_eq);
  Comparator #(.width(32), .mode("twosComplement")) comparator_15 (
    .a(Tag6), .b(IF_PC), .eq(comparator_15_eq));  // open: gt, lt
  and and_25 (S7, V7, comparator_16_eq);
  Comparator #(.width(32), .mode("twosComplement")) comparator_16 (
    .a(Tag7), .b(IF_PC), .eq(comparator_16_eq));  // open: gt, lt
  or or_2 (Have, S0, S1, S2, S3, S4, S5, S6, S7);
  Priority_Encoder #(.select(3), .disabled("Z")) priority_encoder_2 (
    .in0(S0), .in1(S1), .in2(S2), .in3(S3), .in4(S4), .in5(S5), .in6(S6), .in7(S7),
    .out(priority_encoder_2_out), .gs(priority_encoder_2_gs));  // open: en_out, en_in
  Multiplexer #(.select(1), .width(3), .disabled("Z"), .enable("false")) multiplexer_2 (
    .in0(3'b000), .in1(priority_encoder_2_out), .out(multiplexer_2_out), .sel(priority_encoder_2_gs));
  Multiplexer #(.select(3), .width(32), .disabled("Z"), .enable("false")) multiplexer_3 (
    .in0(\分支地址输出0 ), .in1(\分支地址输出1 ), .in2(\分支地址输出2 ), .in3(\分支地址输出3 ), .in4(\分支地址输出4 ), .in5(\分支地址输出5 ),
    .in6(\分支地址输出6 ), .in7(\分支地址输出7 ), .out(\分支目标地址_2 ), .sel(multiplexer_2_out));
  Multiplexer #(.select(3), .width(2), .disabled("Z"), .enable("false")) multiplexer_4 (
    .in0(\双预测位输出0 ), .in1(\双预测位输出1 ), .in2(\双预测位输出2 ), .in3(\双预测位输出3 ), .in4(\双预测位输出4 ), .in5(\双预测位输出5 ),
    .in6(\双预测位输出6 ), .in7(\双预测位输出7 ), .out(\双预测位输出 ), .sel(multiplexer_2_out));

  // Other names for the same wires on the sheet: Blk[31:0] = \分支目标地址 ; BlkReady = BlkDataReady;
  //   分支地址输出[31:0] = \分支目标地址_2 ; 分支指令地址Search[31:0] = IF_PC; 分支指令地址Write[31:0] = EX_PC

  // Notes on the sheet:
  //   输入引脚区
  //   (用于区分查找和写入)
  //   输出引脚区
  //   写阶段/命中阶段
  //   读阶段
  //   查
endmodule

// 状态
module \双位预测状态机  (
  input  [1:0] \初始预测位 ,
  input  \实际跳转情况 ,
  output [1:0] \新的状态位 
);

  wire [1:0] multiplexer_1_out, multiplexer_2_out;

  Multiplexer #(.select(2), .width(2), .disabled("Z"), .enable("false")) multiplexer_1 (
    .in0(2'b00), .in1(2'b00), .in2(2'b11), .in3(2'b00), .out(multiplexer_1_out), .sel(\初始预测位 ));
  Multiplexer #(.select(2), .width(2), .disabled("Z"), .enable("false")) multiplexer_2 (
    .in0(2'b01), .in1(2'b10), .in2(2'b10), .in3(2'b10), .out(multiplexer_2_out), .sel(\初始预测位 ));
  Multiplexer #(.select(1), .width(2), .disabled("Z"), .enable("false")) multiplexer_3 (
    .in0(multiplexer_1_out), .in1(multiplexer_2_out), .out(\新的状态位 ), .sel(\实际跳转情况 ));
endmodule

// Max2
module \Max2_归并比较  (
  input  [15:0] Y,
  input  [15:0] X,
  input  [2:0] Y_num,
  input  [2:0] X_num,
  output [15:0] MAX,
  output [2:0] Max_num
);

  wire comparator_1_eq, comparator_1_gt, or_1_out;

  Multiplexer #(.select(1), .width(16), .disabled("Z"), .enable("false")) multiplexer_1 (
    .in0(Y), .in1(X), .out(MAX), .sel(or_1_out));
  Comparator #(.width(16), .mode("unsigned")) comparator_1 (
    .a(X), .b(Y), .gt(comparator_1_gt), .eq(comparator_1_eq));  // open: lt
  or or_1 (or_1_out, comparator_1_gt, comparator_1_eq);
  Multiplexer #(.select(1), .width(3), .disabled("Z"), .enable("false")) multiplexer_2 (
    .in0(Y_num), .in1(X_num), .out(Max_num), .sel(or_1_out));

  // Notes on the sheet:
  //   输出两个输入中的较大值，并输出较大值的3位编号
endmodule
module \BHT表_劣质  (
  input  [31:0] EX_PC,
  input  [31:0] \分支目标地址 ,
  input  [31:0] IF_PC,
  input  BlkReady,
  input  [1:0] \双预测位 ,
  input  CLK,
  output Have,
  output [31:0] \分支目标地址_2 ,
  output [1:0] \双预测位输出 
);

  wire and_9_out, comparator_1_eq, comparator_2_eq, comparator_3_eq, comparator_4_eq, comparator_5_eq,
       comparator_6_eq, comparator_7_eq, comparator_8_eq, comparator_9_eq, comparator_10_eq,
       comparator_11_eq, comparator_12_eq, comparator_13_eq, comparator_14_eq, comparator_15_eq,
       comparator_16_eq, decoder_1_out0, decoder_1_out1, decoder_1_out2, decoder_1_out3, decoder_1_out4,
       decoder_1_out5, decoder_1_out6, decoder_1_out7, not_1_out, not_2_out, not_3_out, not_4_out, not_5_out,
       not_6_out, not_7_out, not_8_out, priority_encoder_1_gs, priority_encoder_2_gs, S0, S1, S2, S3, S4, S5,
       S6, S7, Shoot, V0, V1, V2, V3, V4, V5, V6, V7, W0, W1, W2, W3, W4, W5, W6, W7, Write0, Write1, Write2,
       Write3, Write4, Write5, Write6, Write7;
  wire [1:0] \预输0 , \预输1 , \预输2 , \预输3 , \预输4 , \预输5 , \预输6 , \预输7 ;
  wire [2:0] \max2_归并比较_1_max_num , \max2_归并比较_2_max_num , \max2_归并比较_3_max_num , \max2_归并比较_4_max_num ,
       \max2_归并比较_5_max_num , \max2_归并比较_6_max_num , \max2_归并比较_7_max_num , multiplexer_1_out,
       multiplexer_2_out, priority_encoder_1_out, priority_encoder_2_out;
  wire [15:0] LRU0, LRU1, LRU2, LRU3, LRU4, LRU5, LRU6, LRU7, \max2_归并比较_1_max , \max2_归并比较_2_max ,
       \max2_归并比较_3_max , \max2_归并比较_4_max , \max2_归并比较_5_max , \max2_归并比较_6_max ;
  wire [31:0] Tag0, Tag1, Tag2, Tag3, Tag4, Tag5, Tag6, Tag7, \分支PCAimAddrOut0 , \分支PCAimAddrOut1 ,
       \分支PCAimAddrOut2 , \分支PCAimAddrOut3 , \分支PCAimAddrOut4 , \分支PCAimAddrOut5 , \分支PCAimAddrOut6 ,
       \分支PCAimAddrOut7 ;

  Register #(.width(1), .trigger("rising"), .Select("low")) Valid (
    .D(1'b1), .en(Write0), .Q(V0), .clk(CLK));  // open: clr
  Register #(.width(1), .trigger("rising"), .Select("low")) Valid_2 (
    .D(1'b1), .en(Write1), .Q(V1), .clk(CLK));  // open: clr
  Register #(.width(1), .trigger("rising"), .Select("low")) Valid_3 (
    .D(1'b1), .en(Write2), .Q(V2), .clk(CLK));  // open: clr
  Register #(.width(1), .trigger("rising"), .Select("low")) Valid_4 (
    .D(1'b1), .en(Write3), .Q(V3), .clk(CLK));  // open: clr
  Register #(.width(1), .trigger("rising"), .Select("low")) Valid_5 (
    .D(1'b1), .en(Write4), .Q(V4), .clk(CLK));  // open: clr
  Register #(.width(1), .trigger("rising"), .Select("low")) Valid_6 (
    .D(1'b1), .en(Write5), .Q(V5), .clk(CLK));  // open: clr
  Register #(.width(1), .trigger("rising"), .Select("low")) Valid_7 (
    .D(1'b1), .en(Write6), .Q(V6), .clk(CLK));  // open: clr
  Register #(.width(1), .trigger("rising"), .Select("low")) Valid_8 (
    .D(1'b1), .en(Write7), .Q(V7), .clk(CLK));  // open: clr
  Register #(.width(32), .trigger("rising"), .Select("low")) \u_分支指令地址  (
    .D(EX_PC), .en(Write0), .Q(Tag0), .clk(CLK));  // open: clr
  Register #(.width(32), .trigger("rising"), .Select("low")) \u_分支指令地址_2  (
    .D(EX_PC), .en(Write1), .Q(Tag1), .clk(CLK));  // open: clr
  Register #(.width(32), .trigger("rising"), .Select("low")) \u_分支指令地址_3  (
    .D(EX_PC), .en(Write2), .Q(Tag2), .clk(CLK));  // open: clr
  Register #(.width(32), .trigger("rising"), .Select("low")) \u_分支指令地址_4  (
    .D(EX_PC), .en(Write3), .Q(Tag3), .clk(CLK));  // open: clr
  Register #(.width(32), .trigger("rising"), .Select("low")) \u_分支指令地址_5  (
    .D(EX_PC), .en(Write4), .Q(Tag4), .clk(CLK));  // open: clr
  Register #(.width(32), .trigger("rising"), .Select("low")) \u_分支指令地址_6  (
    .D(EX_PC), .en(Write5), .Q(Tag5), .clk(CLK));  // open: clr
  Register #(.width(32), .trigger("rising"), .Select("low")) \u_分支指令地址_7  (
    .D(EX_PC), .en(Write6), .Q(Tag6), .clk(CLK));  // open: clr
  Register #(.width(32), .trigger("rising"), .Select("low")) \u_分支指令地址_8  (
    .D(EX_PC), .en(Write7), .Q(Tag7), .clk(CLK));  // open: clr
  Register #(.width(32), .trigger("rising"), .Select("low")) \u_分支目标地址  (
    .D(\分支目标地址 ), .en(Write0), .Q(\分支PCAimAddrOut0 ), .clk(CLK));  // open: clr
  Register #(.width(32), .trigger("rising"), .Select("low")) \u_分支目标地址_2  (
    .D(\分支目标地址 ), .en(Write1), .Q(\分支PCAimAddrOut1 ), .clk(CLK));  // open: clr
  Register #(.width(32), .trigger("rising"), .Select("low")) \u_分支目标地址_3  (
    .D(\分支目标地址 ), .en(Write2), .Q(\分支PCAimAddrOut2 ), .clk(CLK));  // open: clr
  Register #(.width(32), .trigger("rising"), .Select("low")) \u_分支目标地址_4  (
    .D(\分支目标地址 ), .en(Write3), .Q(\分支PCAimAddrOut3 ), .clk(CLK), .clr(CLK));
  Register #(.width(32), .trigger("rising"), .Select("low")) \u_分支目标地址_5  (
    .D(\分支目标地址 ), .en(Write5), .Q(\分支PCAimAddrOut5 ), .clk(CLK), .clr(CLK));
  Register #(.width(32), .trigger("rising"), .Select("low")) \u_分支目标地址_6  (
    .D(\分支目标地址 ), .en(Write6), .Q(\分支PCAimAddrOut6 ), .clk(CLK), .clr(CLK));
  Register #(.width(32), .trigger("rising"), .Select("low")) \u_分支目标地址_7  (
    .D(\分支目标地址 ), .en(Write4), .Q(\分支PCAimAddrOut4 ), .clk(CLK), .clr(CLK));
  Register #(.width(32), .trigger("rising"), .Select("low")) \u_分支目标地址_8  (
    .D(\分支目标地址 ), .en(Write7), .Q(\分支PCAimAddrOut7 ), .clk(CLK), .clr(CLK));
  Register #(.width(2), .trigger("rising"), .Select("low")) \u_双预测位  (
    .D(\双预测位 ), .en(Write0), .Q(\预输0 ), .clk(CLK));  // open: clr
  Register #(.width(2), .trigger("rising"), .Select("low")) \u_双预测位_2  (
    .D(\双预测位 ), .en(Write1), .Q(\预输1 ), .clk(CLK));  // open: clr
  Register #(.width(2), .trigger("rising"), .Select("low")) \u_双预测位_3  (
    .D(\双预测位 ), .en(Write2), .Q(\预输2 ), .clk(CLK));  // open: clr
  Register #(.width(2), .trigger("rising"), .Select("low")) \u_双预测位_4  (
    .D(\双预测位 ), .en(Write3), .Q(\预输3 ), .clk(CLK));  // open: clr
  not not_1 (not_1_out, W0);
  not not_2 (not_2_out, W1);
  not not_3 (not_3_out, W2);
  not not_4 (not_4_out, W3);
  Register #(.width(2), .trigger("rising"), .Select("low")) \u_双预测位_5  (
    .D(\双预测位 ), .en(Write4), .Q(\预输4 ), .clk(CLK));  // open: clr
  not not_5 (not_5_out, W4);
  Register #(.width(2), .trigger("rising"), .Select("low")) \u_双预测位_6  (
    .D(\双预测位 ), .en(Write5), .Q(\预输5 ), .clk(CLK));  // open: clr
  not not_6 (not_6_out, W5);
  Register #(.width(2), .trigger("rising"), .Select("low")) \u_双预测位_7  (
    .D(\双预测位 ), .en(Write6), .Q(\预输6 ), .clk(CLK));  // open: clr
  not not_7 (not_7_out, W6);
  Register #(.width(2), .trigger("rising"), .Select("low")) \u_双预测位_8  (
    .D(\双预测位 ), .en(Write7), .Q(\预输7 ), .clk(CLK));  // open: clr
  not not_8 (not_8_out, W7);
  Counter #(.width(16), .max('hffff), .ongoal("stay"), .trigger("rising"), .behavior("old")) counter_1 (
    .count(not_1_out), .Q(LRU0), .clk(CLK), .clr(W0));  // open: load, D, carry, preset
  Counter #(.width(16), .max('hffff), .ongoal("stay"), .trigger("rising"), .behavior("old")) counter_2 (
    .count(not_2_out), .Q(LRU1), .clk(CLK), .clr(W1));  // open: load, D, carry, preset
  Counter #(.width(16), .max('hffff), .ongoal("stay"), .trigger("rising"), .behavior("old")) counter_3 (
    .count(not_3_out), .Q(LRU2), .clk(CLK), .clr(W2));  // open: load, D, carry, preset
  Counter #(.width(16), .max('hffff), .ongoal("stay"), .trigger("rising"), .behavior("old")) counter_4 (
    .count(not_4_out), .Q(LRU3), .clk(CLK), .clr(W3));  // open: load, D, carry, preset
  Counter #(.width(16), .max('hffff), .ongoal("stay"), .trigger("rising"), .behavior("old")) counter_5 (
    .count(not_5_out), .Q(LRU4), .clk(CLK), .clr(W4));  // open: load, D, carry, preset
  Counter #(.width(16), .max('hffff), .ongoal("stay"), .trigger("rising"), .behavior("old")) counter_6 (
    .count(not_6_out), .Q(LRU5), .clk(CLK), .clr(W5));  // open: load, D, carry, preset
  Counter #(.width(16), .max('hffff), .ongoal("stay"), .trigger("rising"), .behavior("old")) counter_7 (
    .count(not_7_out), .Q(LRU6), .clk(CLK), .clr(W6));  // open: load, D, carry, preset
  Counter #(.width(16), .max('hffff), .ongoal("stay"), .trigger("rising"), .behavior("old")) counter_8 (
    .count(not_8_out), .Q(LRU7), .clk(CLK), .clr(W7));  // open: load, D, carry, preset
  Comparator #(.width(32), .mode("twosComplement")) comparator_1 (
    .a(Tag0), .b(EX_PC), .eq(comparator_1_eq));  // open: gt, lt
  Comparator #(.width(32), .mode("twosComplement")) comparator_2 (
    .a(Tag1), .b(EX_PC), .eq(comparator_2_eq));  // open: gt, lt
  Comparator #(.width(32), .mode("twosComplement")) comparator_3 (
    .a(Tag2), .b(EX_PC), .eq(comparator_3_eq));  // open: gt, lt
  Comparator #(.width(32), .mode("twosComplement")) comparator_4 (
    .a(Tag3), .b(EX_PC), .eq(comparator_4_eq));  // open: gt, lt
  Comparator #(.width(32), .mode("twosComplement")) comparator_5 (
    .a(Tag4), .b(EX_PC), .eq(comparator_5_eq));  // open: gt, lt
  Comparator #(.width(32), .mode("twosComplement")) comparator_6 (
    .a(Tag5), .b(EX_PC), .eq(comparator_6_eq));  // open: gt, lt
  Comparator #(.width(32), .mode("twosComplement")) comparator_7 (
    .a(Tag6), .b(EX_PC), .eq(comparator_7_eq));  // open: gt, lt
  Comparator #(.width(32), .mode("twosComplement")) comparator_8 (
    .a(Tag7), .b(EX_PC), .eq(comparator_8_eq));  // open: gt, lt
  \Max2_归并比较  \max2_归并比较_1  (
    .Y(LRU1), .X(LRU0), .Y_num(3'b001), .X_num(3'b000), .MAX(\max2_归并比较_1_max ),
    .Max_num(\max2_归并比较_1_max_num ));
  \Max2_归并比较  \max2_归并比较_2  (
    .Y(LRU3), .X(LRU2), .Y_num(3'b011), .X_num(3'b010), .MAX(\max2_归并比较_2_max ),
    .Max_num(\max2_归并比较_2_max_num ));
  \Max2_归并比较  \max2_归并比较_3  (
    .Y(LRU5), .X(LRU4), .Y_num(3'b101), .X_num(3'b100), .MAX(\max2_归并比较_3_max ),
    .Max_num(\max2_归并比较_3_max_num ));
  \Max2_归并比较  \max2_归并比较_4  (
    .Y(LRU7), .X(LRU6), .Y_num(3'b111), .X_num(3'b110), .MAX(\max2_归并比较_4_max ),
    .Max_num(\max2_归并比较_4_max_num ));
  and and_1 (W0, V0, comparator_1_eq);
  and and_2 (W1, V1, comparator_2_eq);
  and and_3 (W2, V2, comparator_3_eq);
  and and_4 (W3, V3, comparator_4_eq);
  and and_5 (W4, V4, comparator_5_eq);
  and and_6 (W5, V5, comparator_6_eq);
  and and_7 (W6, V6, comparator_7_eq);
  and and_8 (W7, V7, comparator_8_eq);
  \Max2_归并比较  \max2_归并比较_5  (
    .Y(\max2_归并比较_2_max ), .X(\max2_归并比较_1_max ), .Y_num(\max2_归并比较_2_max_num ),
    .X_num(\max2_归并比较_1_max_num ), .MAX(\max2_归并比较_5_max ), .Max_num(\max2_归并比较_5_max_num ));
  \Max2_归并比较  \max2_归并比较_6  (
    .Y(\max2_归并比较_4_max ), .X(\max2_归并比较_3_max ), .Y_num(\max2_归并比较_4_max_num ),
    .X_num(\max2_归并比较_3_max_num ), .MAX(\max2_归并比较_6_max ), .Max_num(\max2_归并比较_6_max_num ));
  \Max2_归并比较  \max2_归并比较_7  (
    .Y(\max2_归并比较_6_max ), .X(\max2_归并比较_5_max ), .Y_num(\max2_归并比较_6_max_num ),
    .X_num(\max2_归并比较_5_max_num ), .Max_num(\max2_归并比较_7_max_num ));  // open: MAX
  Priority_Encoder #(.select(3), .disabled("Z")) priority_encoder_1 (
    .in0(W0), .in1(W1), .in2(W2), .in3(W3), .in4(W4), .in5(W5), .in6(W6), .in7(W7),
    .out(priority_encoder_1_out), .gs(priority_encoder_1_gs));  // open: en_out, en_in
  or or_1 (Shoot, W0, W1, W2, W3, W4, W5, W6, W7);
  Decoder #(.select(3), .tristate("false"), .disabled("Z"), .enable("false")) decoder_1 (
    .out0(decoder_1_out0), .out1(decoder_1_out1), .out2(decoder_1_out2), .out3(decoder_1_out3),
    .out4(decoder_1_out4), .out5(decoder_1_out5), .out6(decoder_1_out6), .out7(decoder_1_out7),
    .sel(multiplexer_1_out));
  Multiplexer #(.select(1), .width(3), .disabled("Z"), .enable("false")) multiplexer_1 (
    .in0(\max2_归并比较_7_max_num ), .in1(priority_encoder_1_out), .out(multiplexer_1_out), .sel(and_9_out));
  and and_9 (and_9_out, priority_encoder_1_gs, Shoot);
  and and_10 (Write0, BlkReady, decoder_1_out0);
  and and_11 (Write1, BlkReady, decoder_1_out1);
  and and_12 (Write6, decoder_1_out6, BlkReady);
  and and_13 (Write7, decoder_1_out7, BlkReady);
  and and_14 (Write2, BlkReady, decoder_1_out2);
  and and_15 (Write3, BlkReady, decoder_1_out3);
  and and_16 (Write4, decoder_1_out4, BlkReady);
  and and_17 (Write5, decoder_1_out5, BlkReady);
  and and_18 (S0, V0, comparator_9_eq);
  Comparator #(.width(32), .mode("twosComplement")) comparator_9 (
    .a(Tag0), .b(IF_PC), .eq(comparator_9_eq));  // open: gt, lt
  and and_19 (S1, V1, comparator_10_eq);
  Comparator #(.width(32), .mode("twosComplement")) comparator_10 (
    .a(Tag1), .b(IF_PC), .eq(comparator_10_eq));  // open: gt, lt
  and and_20 (S2, V2, comparator_11_eq);
  Comparator #(.width(32), .mode("twosComplement")) comparator_11 (
    .a(Tag2), .b(IF_PC), .eq(comparator_11_eq));  // open: gt, lt
  and and_21 (S3, V3, comparator_12_eq);
  Comparator #(.width(32), .mode("twosComplement")) comparator_12 (
    .a(Tag3), .b(IF_PC), .eq(comparator_12_eq));  // open: gt, lt
  and and_22 (S4, V4, comparator_13_eq);
  Comparator #(.width(32), .mode("twosComplement")) comparator_13 (
    .a(Tag4), .b(IF_PC), .eq(comparator_13_eq));  // open: gt, lt
  and and_23 (S5, V5, comparator_14_eq);
  Comparator #(.width(32), .mode("twosComplement")) comparator_14 (
    .a(Tag5), .b(IF_PC), .eq(comparator_14_eq));  // open: gt, lt
  and and_24 (S6, V6, comparator_15_eq);
  Comparator #(.width(32), .mode("twosComplement")) comparator_15 (
    .a(Tag6), .b(IF_PC), .eq(comparator_15_eq));  // open: gt, lt
  and and_25 (S7, V7, comparator_16_eq);
  Comparator #(.width(32), .mode("twosComplement")) comparator_16 (
    .a(Tag7), .b(IF_PC), .eq(comparator_16_eq));  // open: gt, lt
  or or_2 (Have, S0, S1, S2, S3, S4, S5, S6, S7);
  Priority_Encoder #(.select(3), .disabled("Z")) priority_encoder_2 (
    .in0(S0), .in1(S1), .in2(S2), .in3(S3), .in4(S4), .in5(S5), .in6(S6), .in7(S7),
    .out(priority_encoder_2_out), .gs(priority_encoder_2_gs));  // open: en_out, en_in
  Multiplexer #(.select(1), .width(3), .disabled("Z"), .enable("false")) multiplexer_2 (
    .in0(3'b000), .in1(priority_encoder_2_out), .out(multiplexer_2_out), .sel(priority_encoder_2_gs));
  Multiplexer #(.select(3), .width(32), .disabled("Z"), .enable("false")) multiplexer_3 (
    .in0(\分支PCAimAddrOut0 ), .in1(\分支PCAimAddrOut1 ), .in2(\分支PCAimAddrOut2 ), .in3(\分支PCAimAddrOut3 ),
    .in4(\分支PCAimAddrOut4 ), .in5(\分支PCAimAddrOut5 ), .in6(\分支PCAimAddrOut6 ), .in7(\分支PCAimAddrOut7 ),
    .out(\分支目标地址_2 ), .sel(multiplexer_2_out));
  Multiplexer #(.select(3), .width(2), .disabled("Z"), .enable("false")) multiplexer_4 (
    .in0(\预输0 ), .in1(\预输1 ), .in2(\预输2 ), .in3(\预输3 ), .in4(\预输4 ), .in5(\预输5 ), .in6(\预输6 ), .in7(\预输7 ),
    .out(\双预测位输出 ), .sel(multiplexer_2_out));

  // Other names for the same wires on the sheet: 分支PCAddrSearch[31:0] = IF_PC; 分支PCAddrWrite[31:0] = EX_PC;
  //   分支PCAimAddr[31:0] = \分支目标地址 ; 分支地址输出[31:0] = \分支目标地址_2 

  // Notes on the sheet:
  //   (用于区分查找和写入)
  //   输入引脚区
  //   输出引脚区
  //   写阶段/命中
  //   查阶段
endmodule
